// Logisim project Branch Instructions.circ as structural Verilog: 6 circuits, main circuit beq
module beq (
  input  A0,
  input  A1,
  input  A2,
  input  A3,
  input  A4,
  input  A5,
  input  A6,
  input  A7,
  input  A8,
  input  A9,
  input  A10,
  input  A11,
  input  A12,
  input  A13,
  input  A14,
  input  A15,
  input  A16,
  input  A17,
  input  A18,
  input  A19,
  input  A20,
  input  A21,
  input  A22,
  input  A23,
  input  A24,
  input  A25,
  input  A26,
  input  A27,
  input  A28,
  input  A29,
  input  A30,
  input  A31,
  input  A0_2,
  input  A1_2,
  input  A2_2,
  input  A3_2,
  input  A4_2,
  input  A5_2,
  input  A6_2,
  input  A7_2,
  input  A8_2,
  input  A9_2,
  input  A10_2,
  input  A11_2,
  input  A12_2,
  input  A13_2,
  input  A14_2,
  input  A15_2,
  input  A16_2,
  input  A17_2,
  input  A18_2,
  input  A19_2,
  input  A20_2,
  input  A21_2,
  input  A22_2,
  input  A23_2,
  input  A24_2,
  input  A25_2,
  input  A26_2,
  input  A27_2,
  input  A28_2,
  input  A29_2,
  input  A30_2,
  input  A31_2,
  input  A0_3,
  input  A1_3,
  input  A2_3,
  input  A3_3,
  input  A4_3,
  input  A5_3,
  input  A6_3,
  input  A7_3,
  input  A8_3,
  input  A9_3,
  input  A10_3,
  input  A11_3,
  input  A12_3,
  input  A13_3,
  input  A14_3,
  input  A15_3,
  input  E,
  output out_82,
  output out_83,
  output out_84,
  output out_85,
  output out_86,
  output out_87,
  output out_88,
  output out_89,
  output out_90,
  output out_91,
  output out_92,
  output out_93,
  output out_94,
  output out_95,
  output out_96,
  output out_97,
  output out_98,
  output out_99,
  output out_100,
  output out_101,
  output out_102,
  output out_103,
  output out_104,
  output out_105,
  output out_106,
  output out_107,
  output out_108,
  output out_109,
  output out_110,
  output out_111,
  output out_112,
  output out_113
);

  wire and_1_out, and_2_out, and_3_out, and_4_out, and_5_out, and_6_out, and_7_out, and_8_out, and_9_out,
       and_10_out, and_11_out, and_12_out, and_13_out, and_14_out, and_15_out, and_16_out, and_17_out,
       and_18_out, and_19_out, and_20_out, and_21_out, and_22_out, and_23_out, and_24_out, and_25_out,
       and_26_out, and_27_out, and_28_out, and_29_out, and_30_out, and_31_out, n16_bit_general_register_1_q0,
       n16_bit_general_register_1_q1, n16_bit_general_register_1_q2, n16_bit_general_register_1_q3,
       n16_bit_general_register_1_q4, n16_bit_general_register_1_q5, n16_bit_general_register_1_q6,
       n16_bit_general_register_1_q7, n16_bit_general_register_1_q8, n16_bit_general_register_1_q9,
       n16_bit_general_register_1_q10, n16_bit_general_register_1_q11, n16_bit_general_register_1_q12,
       n16_bit_general_register_1_q13, n16_bit_general_register_1_q14, n16_bit_general_register_1_q15,
       xnor_1__0, xnor_1__1, xnor_1__2, xnor_1__3, xnor_1__4, xnor_1__5, xnor_1__6, xnor_1__7, xnor_1__8,
       xnor_1__9, xnor_1__10, xnor_1__11, xnor_1__12, xnor_1__13, xnor_1__14, xnor_1__15, xnor_1__16,
       xnor_1__17, xnor_1__18, xnor_1__19, xnor_1__20, xnor_1__21, xnor_1__22, xnor_1__23, xnor_1__24,
       xnor_1__25, xnor_1__26, xnor_1__27, xnor_1__28, xnor_1__29, xnor_1__30, xnor_1__31;

  _16_Bit_General_Register u_16_bit_general_register_1 (
    .E(E), .D0(A0_3), .Q0(n16_bit_general_register_1_q0), .D1(A1_3), .Q1(n16_bit_general_register_1_q1),
    .D2(A2_3), .Q2(n16_bit_general_register_1_q2), .D3(A3_3), .Q3(n16_bit_general_register_1_q3), .D4(A4_3),
    .Q4(n16_bit_general_register_1_q4), .D5(A5_3), .Q5(n16_bit_general_register_1_q5), .D6(A6_3),
    .Q6(n16_bit_general_register_1_q6), .D7(A7_3), .Q7(n16_bit_general_register_1_q7), .D8(A8_3),
    .Q8(n16_bit_general_register_1_q8), .D9(A9_3), .Q9(n16_bit_general_register_1_q9), .D10(A10_3),
    .Q10(n16_bit_general_register_1_q10), .D11(A11_3), .Q11(n16_bit_general_register_1_q11), .D12(A12_3),
    .Q12(n16_bit_general_register_1_q12), .D13(A13_3), .Q13(n16_bit_general_register_1_q13), .D14(A14_3),
    .Q14(n16_bit_general_register_1_q14), .D15(A15_3), .Q15(n16_bit_general_register_1_q15));
  \xnor  xnor_1 (
    .A0(A0_2), .B0(A0), .A1(A1_2), .B1(A1), .A2(A2_2), .B2(A2), .A3(A3_2), .B3(A3), .A4(A4_2), .B4(A4),
    .A5(A5_2), .B5(A5), .A6(A6_2), .B6(A6), .A7(A7_2), .B7(A7), .A8(A8_2), .B8(A8), .A9(A9_2), .B9(A9),
    .A10(A10_2), .B10(A10), .A11(A11_2), .B11(A11), .A12(A12_2), .B12(A12), .A13(A13_2), .B13(A13),
    .A14(A14_2), .B14(A14), .A15(A15_2), .B15(A15), .A16(A16_2), .B16(A16), .A17(A17_2), .B17(A17),
    .A18(A18_2), .B18(A18), .A19(A19_2), .B19(A19), .A20(A20_2), .B20(A20), .A21(A21_2), .B21(A21),
    .A22(A22_2), .B22(A22), .A23(A23_2), .B23(A23), .A24(A24_2), .B24(A24), .A25(A25_2), .B25(A25),
    .A26(A26_2), .B26(A26), .A27(A27_2), .B27(A27), .A28(A28_2), .B28(A28), .A29(A29_2), .B29(A29),
    .A30(A30_2), .B30(A30), .A31(A31_2), .B31(A31), ._0(xnor_1__0), ._1(xnor_1__1), ._2(xnor_1__2),
    ._3(xnor_1__3), ._4(xnor_1__4), ._5(xnor_1__5), ._6(xnor_1__6), ._7(xnor_1__7), ._8(xnor_1__8),
    ._9(xnor_1__9), ._10(xnor_1__10), ._11(xnor_1__11), ._12(xnor_1__12), ._13(xnor_1__13), ._14(xnor_1__14),
    ._15(xnor_1__15), ._16(xnor_1__16), ._17(xnor_1__17), ._18(xnor_1__18), ._19(xnor_1__19),
    ._20(xnor_1__20), ._21(xnor_1__21), ._22(xnor_1__22), ._23(xnor_1__23), ._24(xnor_1__24),
    ._25(xnor_1__25), ._26(xnor_1__26), ._27(xnor_1__27), ._28(xnor_1__28), ._29(xnor_1__29),
    ._30(xnor_1__30), ._31(xnor_1__31));
  sll sll_1 (
    .B0(1'b0), .B1(and_30_out), .B2(1'b0), .B3(1'b0), .B4(1'b0), .A0(n16_bit_general_register_1_q0),
    .A1(n16_bit_general_register_1_q1), .A2(n16_bit_general_register_1_q2),
    .A3(n16_bit_general_register_1_q3), .A4(n16_bit_general_register_1_q4),
    .A5(n16_bit_general_register_1_q5), .A6(n16_bit_general_register_1_q6),
    .A7(n16_bit_general_register_1_q7), .A8(n16_bit_general_register_1_q8),
    .A9(n16_bit_general_register_1_q9), .A10(n16_bit_general_register_1_q10),
    .A11(n16_bit_general_register_1_q11), .A12(n16_bit_general_register_1_q12),
    .A13(n16_bit_general_register_1_q13), .A14(n16_bit_general_register_1_q14),
    .A15(n16_bit_general_register_1_q15), .A16(1'b0), .A17(1'b0), .A18(1'b0), .A19(1'b0), .A20(1'b0),
    .A21(1'b0), .A22(1'b0), .A23(1'b0), .A24(1'b0), .A25(1'b0), .A26(1'b0), .A27(1'b0), .A28(1'b0),
    .A29(1'b0), .A30(1'b0), .A31(1'b0), ._0(out_82), ._1(out_83), ._2(out_84), ._3(out_85), ._4(out_86),
    ._5(out_87), ._6(out_88), ._7(out_89), ._8(out_90), ._9(out_91), ._10(out_92), ._11(out_93),
    ._12(out_94), ._13(out_95), ._14(out_96), ._15(out_97), ._16(out_98), ._17(out_99), ._18(out_100),
    ._19(out_101), ._20(out_102), ._21(out_103), ._22(out_104), ._23(out_105), ._24(out_106), ._25(out_107),
    ._26(out_108), ._27(out_109), ._28(out_110), ._29(out_111), ._30(out_112), ._31(out_113));
  and and_1 (and_1_out, xnor_1__0, xnor_1__1);
  and and_2 (and_2_out, and_1_out, and_3_out);
  and and_3 (and_3_out, xnor_1__2, xnor_1__3);
  and and_4 (and_4_out, xnor_1__4, xnor_1__5);
  and and_5 (and_5_out, and_4_out, and_6_out);
  and and_6 (and_6_out, xnor_1__6, xnor_1__7);
  and and_7 (and_7_out, xnor_1__8, xnor_1__9);
  and and_8 (and_8_out, and_7_out, and_9_out);
  and and_9 (and_9_out, xnor_1__10, xnor_1__11);
  and and_10 (and_10_out, xnor_1__12, xnor_1__13);
  and and_11 (and_11_out, and_10_out, and_12_out);
  and and_12 (and_12_out, xnor_1__14, xnor_1__15);
  and and_13 (and_13_out, xnor_1__16, xnor_1__17);
  and and_14 (and_14_out, and_13_out, and_15_out);
  and and_15 (and_15_out, xnor_1__18, xnor_1__19);
  and and_16 (and_16_out, xnor_1__20, xnor_1__21);
  and and_17 (and_17_out, and_16_out, and_18_out);
  and and_18 (and_18_out, xnor_1__22, xnor_1__23);
  and and_19 (and_19_out, xnor_1__24, xnor_1__25);
  and and_20 (and_20_out, and_19_out, and_21_out);
  and and_21 (and_21_out, xnor_1__26, xnor_1__27);
  and and_22 (and_22_out, xnor_1__28, xnor_1__29);
  and and_23 (and_23_out, and_22_out, and_24_out);
  and and_24 (and_24_out, xnor_1__30, xnor_1__31);
  and and_25 (and_25_out, and_2_out, and_5_out);
  and and_26 (and_26_out, and_8_out, and_11_out);
  and and_27 (and_27_out, and_14_out, and_17_out);
  and and_28 (and_28_out, and_20_out, and_23_out);
  and and_29 (and_29_out, and_25_out, and_26_out);
  and and_30 (and_30_out, and_29_out, and_31_out);
  and and_31 (and_31_out, and_27_out, and_28_out);

  // Notes on the sheet:
  //   INPUT A
  //   OFFSET (IMMEDIATE)
  //   INPUT B
endmodule

module bgez_bgezal (
  input  A0,
  input  A1,
  input  A2,
  input  A3,
  input  A4,
  input  A5,
  input  A6,
  input  A7,
  input  A8,
  input  A9,
  input  A10,
  input  A11,
  input  A12,
  input  A13,
  input  A14,
  input  A15,
  input  A16,
  input  A17,
  input  A18,
  input  A19,
  input  A20,
  input  A21,
  input  A22,
  input  A23,
  input  A24,
  input  A25,
  input  A26,
  input  A27,
  input  A28,
  input  A29,
  input  A30,
  input  A31,
  input  A0_2,
  input  A1_2,
  input  A2_2,
  input  A3_2,
  input  A4_2,
  input  A5_2,
  input  A6_2,
  input  A7_2,
  input  A8_2,
  input  A9_2,
  input  A10_2,
  input  A11_2,
  input  A12_2,
  input  A13_2,
  input  A14_2,
  input  A15_2,
  input  E,
  output out_50,
  output out_51,
  output out_52,
  output out_53,
  output out_54,
  output out_55,
  output out_56,
  output out_57,
  output out_58,
  output out_59,
  output out_60,
  output out_61,
  output out_62,
  output out_63,
  output out_64,
  output out_65,
  output out_66,
  output out_67,
  output out_68,
  output out_69,
  output out_70,
  output out_71,
  output out_72,
  output out_73,
  output out_74,
  output out_75,
  output out_76,
  output out_77,
  output out_78,
  output out_79,
  output out_80,
  output out_81
);

  wire and_1_out, and_2_out, and_3_out, and_4_out, and_5_out, and_6_out, and_7_out, and_8_out, and_9_out,
       and_10_out, and_11_out, and_12_out, and_13_out, and_14_out, and_15_out, and_16_out, and_17_out,
       and_18_out, and_19_out, and_20_out, and_21_out, and_22_out, and_23_out, and_24_out, and_25_out,
       and_26_out, and_27_out, and_28_out, and_29_out, and_30_out, and_31_out, n16_bit_general_register_1_q0,
       n16_bit_general_register_1_q1, n16_bit_general_register_1_q2, n16_bit_general_register_1_q3,
       n16_bit_general_register_1_q4, n16_bit_general_register_1_q5, n16_bit_general_register_1_q6,
       n16_bit_general_register_1_q7, n16_bit_general_register_1_q8, n16_bit_general_register_1_q9,
       n16_bit_general_register_1_q10, n16_bit_general_register_1_q11, n16_bit_general_register_1_q12,
       n16_bit_general_register_1_q13, n16_bit_general_register_1_q14, n16_bit_general_register_1_q15,
       nor_1_out, or_1_out, or_2_out, or_3_out, or_4_out, or_5_out, or_6_out, or_7_out, or_8_out, or_9_out,
       or_10_out, or_11_out, or_12_out, or_13_out, or_14_out, or_15_out, or_16_out, or_17_out, or_18_out,
       or_19_out, or_20_out, or_21_out, or_22_out, or_23_out, or_24_out, or_25_out, or_26_out, or_27_out,
       or_28_out, or_29_out, or_30_out, or_31_out, slt_1__0, slt_1__1, slt_1__2, slt_1__3, slt_1__4,
       slt_1__5, slt_1__6, slt_1__7, slt_1__8, slt_1__9, slt_1__10, slt_1__11, slt_1__12, slt_1__13,
       slt_1__14, slt_1__15, slt_1__16, slt_1__17, slt_1__18, slt_1__19, slt_1__20, slt_1__21, slt_1__22,
       slt_1__23, slt_1__24, slt_1__25, slt_1__26, slt_1__27, slt_1__28, slt_1__29, slt_1__30, slt_1__31,
       xnor_1__0, xnor_1__1, xnor_1__2, xnor_1__3, xnor_1__4, xnor_1__5, xnor_1__6, xnor_1__7, xnor_1__8,
       xnor_1__9, xnor_1__10, xnor_1__11, xnor_1__12, xnor_1__13, xnor_1__14, xnor_1__15, xnor_1__16,
       xnor_1__17, xnor_1__18, xnor_1__19, xnor_1__20, xnor_1__21, xnor_1__22, xnor_1__23, xnor_1__24,
       xnor_1__25, xnor_1__26, xnor_1__27, xnor_1__28, xnor_1__29, xnor_1__30, xnor_1__31;

  _16_Bit_General_Register u_16_bit_general_register_1 (
    .E(E), .D0(A0_2), .Q0(n16_bit_general_register_1_q0), .D1(A1_2), .Q1(n16_bit_general_register_1_q1),
    .D2(A2_2), .Q2(n16_bit_general_register_1_q2), .D3(A3_2), .Q3(n16_bit_general_register_1_q3), .D4(A4_2),
    .Q4(n16_bit_general_register_1_q4), .D5(A5_2), .Q5(n16_bit_general_register_1_q5), .D6(A6_2),
    .Q6(n16_bit_general_register_1_q6), .D7(A7_2), .Q7(n16_bit_general_register_1_q7), .D8(A8_2),
    .Q8(n16_bit_general_register_1_q8), .D9(A9_2), .Q9(n16_bit_general_register_1_q9), .D10(A10_2),
    .Q10(n16_bit_general_register_1_q10), .D11(A11_2), .Q11(n16_bit_general_register_1_q11), .D12(A12_2),
    .Q12(n16_bit_general_register_1_q12), .D13(A13_2), .Q13(n16_bit_general_register_1_q13), .D14(A14_2),
    .Q14(n16_bit_general_register_1_q14), .D15(A15_2), .Q15(n16_bit_general_register_1_q15));
  slt slt_1 (
    .A0(A0), .A1(A1), .A2(A2), .A3(A3), .A4(A4), .A5(A5), .A6(A6), .A7(A7), .A8(A8), .A9(A9), .A10(A10),
    .A11(A11), .A12(A12), .A13(A13), .A14(A14), .A15(A15), .A16(A16), .A17(A17), .A18(A18), .A19(A19),
    .A20(A20), .A21(A21), .A22(A22), .A23(A23), .A24(A24), .A25(A25), .A26(A26), .A27(A27), .A28(A28),
    .A29(A29), .A30(A30), .A31(A31), ._0(slt_1__0), ._1(slt_1__1), ._2(slt_1__2), ._3(slt_1__3),
    ._4(slt_1__4), ._5(slt_1__5), ._6(slt_1__6), ._7(slt_1__7), ._8(slt_1__8), ._9(slt_1__9),
    ._10(slt_1__10), ._11(slt_1__11), ._12(slt_1__12), ._13(slt_1__13), ._14(slt_1__14), ._15(slt_1__15),
    ._16(slt_1__16), ._17(slt_1__17), ._18(slt_1__18), ._19(slt_1__19), ._20(slt_1__20), ._21(slt_1__21),
    ._22(slt_1__22), ._23(slt_1__23), ._24(slt_1__24), ._25(slt_1__25), ._26(slt_1__26), ._27(slt_1__27),
    ._28(slt_1__28), ._29(slt_1__29), ._30(slt_1__30), ._31(slt_1__31), .B0(1'b0), .B1(1'b0), .B2(1'b0),
    .B3(1'b0), .B4(1'b0), .B5(1'b0), .B6(1'b0), .B7(1'b0), .B8(1'b0), .B9(1'b0), .B10(1'b0), .B11(1'b0),
    .B12(1'b0), .B13(1'b0), .B14(1'b0), .B15(1'b0), .B16(1'b0), .B17(1'b0), .B18(1'b0), .B19(1'b0),
    .B20(1'b0), .B21(1'b0), .B22(1'b0), .B23(1'b0), .B24(1'b0), .B25(1'b0), .B26(1'b0), .B27(1'b0),
    .B28(1'b0), .B29(1'b0), .B30(1'b0), .B31(1'b0));
  \xnor  xnor_1 (
    .A0(A0), .B0(1'b0), .A1(A1), .B1(1'b0), .A2(A2), .B2(1'b0), .A3(A3), .B3(1'b0), .A4(A4), .B4(1'b0),
    .A5(A5), .B5(1'b0), .A6(A6), .B6(1'b0), .A7(A7), .B7(1'b0), .A8(A8), .B8(1'b0), .A9(A9), .B9(1'b0),
    .A10(A10), .B10(1'b0), .A11(A11), .B11(1'b0), .A12(A12), .B12(1'b0), .A13(A13), .B13(1'b0), .A14(A14),
    .B14(1'b0), .A15(A15), .B15(1'b0), .A16(A16), .B16(1'b0), .A17(A17), .B17(1'b0), .A18(A18), .B18(1'b0),
    .A19(A19), .B19(1'b0), .A20(A20), .B20(1'b0), .A21(A21), .B21(1'b0), .A22(A22), .B22(1'b0), .A23(A23),
    .B23(1'b0), .A24(A24), .B24(1'b0), .A25(A25), .B25(1'b0), .A26(A26), .B26(1'b0), .A27(A27), .B27(1'b0),
    .A28(A28), .B28(1'b0), .A29(A29), .B29(1'b0), .A30(A30), .B30(1'b0), .A31(A31), .B31(1'b0),
    ._0(xnor_1__0), ._1(xnor_1__1), ._2(xnor_1__2), ._3(xnor_1__3), ._4(xnor_1__4), ._5(xnor_1__5),
    ._6(xnor_1__6), ._7(xnor_1__7), ._8(xnor_1__8), ._9(xnor_1__9), ._10(xnor_1__10), ._11(xnor_1__11),
    ._12(xnor_1__12), ._13(xnor_1__13), ._14(xnor_1__14), ._15(xnor_1__15), ._16(xnor_1__16),
    ._17(xnor_1__17), ._18(xnor_1__18), ._19(xnor_1__19), ._20(xnor_1__20), ._21(xnor_1__21),
    ._22(xnor_1__22), ._23(xnor_1__23), ._24(xnor_1__24), ._25(xnor_1__25), ._26(xnor_1__26),
    ._27(xnor_1__27), ._28(xnor_1__28), ._29(xnor_1__29), ._30(xnor_1__30), ._31(xnor_1__31));
  sll sll_1 (
    .B0(1'b0), .B1(or_31_out), .B2(1'b0), .B3(1'b0), .B4(1'b0), .A0(n16_bit_general_register_1_q0),
    .A1(n16_bit_general_register_1_q1), .A2(n16_bit_general_register_1_q2),
    .A3(n16_bit_general_register_1_q3), .A4(n16_bit_general_register_1_q4),
    .A5(n16_bit_general_register_1_q5), .A6(n16_bit_general_register_1_q6),
    .A7(n16_bit_general_register_1_q7), .A8(n16_bit_general_register_1_q8),
    .A9(n16_bit_general_register_1_q9), .A10(n16_bit_general_register_1_q10),
    .A11(n16_bit_general_register_1_q11), .A12(n16_bit_general_register_1_q12),
    .A13(n16_bit_general_register_1_q13), .A14(n16_bit_general_register_1_q14),
    .A15(n16_bit_general_register_1_q15), .A16(1'b0), .A17(1'b0), .A18(1'b0), .A19(1'b0), .A20(1'b0),
    .A21(1'b0), .A22(1'b0), .A23(1'b0), .A24(1'b0), .A25(1'b0), .A26(1'b0), .A27(1'b0), .A28(1'b0),
    .A29(1'b0), .A30(1'b0), .A31(1'b0), ._0(out_50), ._1(out_51), ._2(out_52), ._3(out_53), ._4(out_54),
    ._5(out_55), ._6(out_56), ._7(out_57), ._8(out_58), ._9(out_59), ._10(out_60), ._11(out_61),
    ._12(out_62), ._13(out_63), ._14(out_64), ._15(out_65), ._16(out_66), ._17(out_67), ._18(out_68),
    ._19(out_69), ._20(out_70), ._21(out_71), ._22(out_72), ._23(out_73), ._24(out_74), ._25(out_75),
    ._26(out_76), ._27(out_77), ._28(out_78), ._29(out_79), ._30(out_80), ._31(out_81));
  or or_1 (or_1_out, slt_1__0, slt_1__1);
  or or_2 (or_2_out, or_1_out, or_3_out);
  or or_3 (or_3_out, slt_1__2, slt_1__3);
  or or_4 (or_4_out, slt_1__4, slt_1__5);
  or or_5 (or_5_out, or_4_out, or_6_out);
  or or_6 (or_6_out, slt_1__6, slt_1__7);
  or or_7 (or_7_out, slt_1__8, slt_1__9);
  or or_8 (or_8_out, or_7_out, or_9_out);
  or or_9 (or_9_out, slt_1__10, slt_1__11);
  or or_10 (or_10_out, slt_1__12, slt_1__13);
  or or_11 (or_11_out, or_10_out, or_12_out);
  or or_12 (or_12_out, slt_1__14, slt_1__15);
  or or_13 (or_13_out, slt_1__16, slt_1__17);
  or or_14 (or_14_out, or_13_out, or_15_out);
  or or_15 (or_15_out, slt_1__18, slt_1__19);
  or or_16 (or_16_out, slt_1__20, slt_1__21);
  or or_17 (or_17_out, or_16_out, or_18_out);
  or or_18 (or_18_out, slt_1__22, slt_1__23);
  or or_19 (or_19_out, slt_1__24, slt_1__25);
  or or_20 (or_20_out, or_19_out, or_21_out);
  or or_21 (or_21_out, slt_1__26, slt_1__27);
  or or_22 (or_22_out, slt_1__28, slt_1__29);
  or or_23 (or_23_out, or_22_out, or_24_out);
  or or_24 (or_24_out, slt_1__30, slt_1__31);
  and and_1 (and_1_out, xnor_1__0, xnor_1__1);
  and and_2 (and_2_out, and_1_out, and_3_out);
  and and_3 (and_3_out, xnor_1__2, xnor_1__3);
  and and_4 (and_4_out, xnor_1__4, xnor_1__5);
  and and_5 (and_5_out, and_4_out, and_6_out);
  and and_6 (and_6_out, xnor_1__6, xnor_1__7);
  and and_7 (and_7_out, xnor_1__8, xnor_1__9);
  and and_8 (and_8_out, and_7_out, and_9_out);
  and and_9 (and_9_out, xnor_1__10, xnor_1__11);
  and and_10 (and_10_out, xnor_1__12, xnor_1__13);
  and and_11 (and_11_out, and_10_out, and_12_out);
  and and_12 (and_12_out, xnor_1__14, xnor_1__15);
  and and_13 (and_13_out, xnor_1__16, xnor_1__17);
  and and_14 (and_14_out, and_13_out, and_15_out);
  and and_15 (and_15_out, xnor_1__18, xnor_1__19);
  and and_16 (and_16_out, xnor_1__20, xnor_1__21);
  and and_17 (and_17_out, and_16_out, and_18_out);
  and and_18 (and_18_out, xnor_1__22, xnor_1__23);
  and and_19 (and_19_out, xnor_1__24, xnor_1__25);
  and and_20 (and_20_out, and_19_out, and_21_out);
  and and_21 (and_21_out, xnor_1__26, xnor_1__27);
  and and_22 (and_22_out, xnor_1__28, xnor_1__29);
  and and_23 (and_23_out, and_22_out, and_24_out);
  and and_24 (and_24_out, xnor_1__30, xnor_1__31);
  or or_25 (or_25_out, or_2_out, or_5_out);
  or or_26 (or_26_out, or_8_out, or_11_out);
  or or_27 (or_27_out, or_14_out, or_17_out);
  or or_28 (or_28_out, or_20_out, or_23_out);
  and and_25 (and_25_out, and_2_out, and_5_out);
  and and_26 (and_26_out, and_8_out, and_11_out);
  and and_27 (and_27_out, and_14_out, and_17_out);
  and and_28 (and_28_out, and_20_out, and_23_out);
  or or_29 (or_29_out, or_25_out, or_26_out);
  nor nor_1 (nor_1_out, or_29_out, or_30_out);
  or or_30 (or_30_out, or_27_out, or_28_out);
  and and_29 (and_29_out, and_25_out, and_26_out);
  and and_30 (and_30_out, and_29_out, and_31_out);
  and and_31 (and_31_out, and_27_out, and_28_out);
  or or_31 (or_31_out, and_30_out, nor_1_out);

  // Notes on the sheet:
  //   INPUT A
  //   OFFSET (IMMEDIATE)
endmodule

module bgtz (
  input  A0,
  input  A1,
  input  A2,
  input  A3,
  input  A4,
  input  A5,
  input  A6,
  input  A7,
  input  A8,
  input  A9,
  input  A10,
  input  A11,
  input  A12,
  input  A13,
  input  A14,
  input  A15,
  input  A16,
  input  A17,
  input  A18,
  input  A19,
  input  A20,
  input  A21,
  input  A22,
  input  A23,
  input  A24,
  input  A25,
  input  A26,
  input  A27,
  input  A28,
  input  A29,
  input  A30,
  input  A31,
  input  A0_2,
  input  A1_2,
  input  A2_2,
  input  A3_2,
  input  A4_2,
  input  A5_2,
  input  A6_2,
  input  A7_2,
  input  A8_2,
  input  A9_2,
  input  A10_2,
  input  A11_2,
  input  A12_2,
  input  A13_2,
  input  A14_2,
  input  A15_2,
  input  E,
  output out_50,
  output out_51,
  output out_52,
  output out_53,
  output out_54,
  output out_55,
  output out_56,
  output out_57,
  output out_58,
  output out_59,
  output out_60,
  output out_61,
  output out_62,
  output out_63,
  output out_64,
  output out_65,
  output out_66,
  output out_67,
  output out_68,
  output out_69,
  output out_70,
  output out_71,
  output out_72,
  output out_73,
  output out_74,
  output out_75,
  output out_76,
  output out_77,
  output out_78,
  output out_79,
  output out_80,
  output out_81
);

  wire and_1_out, and_2_out, and_3_out, and_4_out, and_5_out, and_6_out, and_7_out, and_8_out, and_9_out,
       and_10_out, and_11_out, and_12_out, and_13_out, and_14_out, and_15_out, and_16_out, and_17_out,
       and_18_out, and_19_out, and_20_out, and_21_out, and_22_out, and_23_out, and_24_out, and_25_out,
       and_26_out, and_27_out, and_28_out, and_29_out, and_30_out, and_31_out, n16_bit_general_register_1_q0,
       n16_bit_general_register_1_q1, n16_bit_general_register_1_q2, n16_bit_general_register_1_q3,
       n16_bit_general_register_1_q4, n16_bit_general_register_1_q5, n16_bit_general_register_1_q6,
       n16_bit_general_register_1_q7, n16_bit_general_register_1_q8, n16_bit_general_register_1_q9,
       n16_bit_general_register_1_q10, n16_bit_general_register_1_q11, n16_bit_general_register_1_q12,
       n16_bit_general_register_1_q13, n16_bit_general_register_1_q14, n16_bit_general_register_1_q15,
       slt_1__0, slt_1__1, slt_1__2, slt_1__3, slt_1__4, slt_1__5, slt_1__6, slt_1__7, slt_1__8, slt_1__9,
       slt_1__10, slt_1__11, slt_1__12, slt_1__13, slt_1__14, slt_1__15, slt_1__16, slt_1__17, slt_1__18,
       slt_1__19, slt_1__20, slt_1__21, slt_1__22, slt_1__23, slt_1__24, slt_1__25, slt_1__26, slt_1__27,
       slt_1__28, slt_1__29, slt_1__30, slt_1__31;

  _16_Bit_General_Register u_16_bit_general_register_1 (
    .E(E), .D0(A0_2), .Q0(n16_bit_general_register_1_q0), .D1(A1_2), .Q1(n16_bit_general_register_1_q1),
    .D2(A2_2), .Q2(n16_bit_general_register_1_q2), .D3(A3_2), .Q3(n16_bit_general_register_1_q3), .D4(A4_2),
    .Q4(n16_bit_general_register_1_q4), .D5(A5_2), .Q5(n16_bit_general_register_1_q5), .D6(A6_2),
    .Q6(n16_bit_general_register_1_q6), .D7(A7_2), .Q7(n16_bit_general_register_1_q7), .D8(A8_2),
    .Q8(n16_bit_general_register_1_q8), .D9(A9_2), .Q9(n16_bit_general_register_1_q9), .D10(A10_2),
    .Q10(n16_bit_general_register_1_q10), .D11(A11_2), .Q11(n16_bit_general_register_1_q11), .D12(A12_2),
    .Q12(n16_bit_general_register_1_q12), .D13(A13_2), .Q13(n16_bit_general_register_1_q13), .D14(A14_2),
    .Q14(n16_bit_general_register_1_q14), .D15(A15_2), .Q15(n16_bit_general_register_1_q15));
  slt slt_1 (
    .A0(1'b0), .A1(1'b0), .A2(1'b0), .A3(1'b0), .A4(1'b0), .A5(1'b0), .A6(1'b0), .A7(1'b0), .A8(1'b0),
    .A9(1'b0), .A10(1'b0), .A11(1'b0), .A12(1'b0), .A13(1'b0), .A14(1'b0), .A15(1'b0), .A16(1'b0),
    .A17(1'b0), .A18(1'b0), .A19(1'b0), .A20(1'b0), .A21(1'b0), .A22(1'b0), .A23(1'b0), .A24(1'b0),
    .A25(1'b0), .A26(1'b0), .A27(1'b0), .A28(1'b0), .A29(1'b0), .A30(1'b0), .A31(1'b0), ._0(slt_1__0),
    ._1(slt_1__1), ._2(slt_1__2), ._3(slt_1__3), ._4(slt_1__4), ._5(slt_1__5), ._6(slt_1__6), ._7(slt_1__7),
    ._8(slt_1__8), ._9(slt_1__9), ._10(slt_1__10), ._11(slt_1__11), ._12(slt_1__12), ._13(slt_1__13),
    ._14(slt_1__14), ._15(slt_1__15), ._16(slt_1__16), ._17(slt_1__17), ._18(slt_1__18), ._19(slt_1__19),
    ._20(slt_1__20), ._21(slt_1__21), ._22(slt_1__22), ._23(slt_1__23), ._24(slt_1__24), ._25(slt_1__25),
    ._26(slt_1__26), ._27(slt_1__27), ._28(slt_1__28), ._29(slt_1__29), ._30(slt_1__30), ._31(slt_1__31),
    .B0(A0), .B1(A1), .B2(A2), .B3(A3), .B4(A4), .B5(A5), .B6(A6), .B7(A7), .B8(A8), .B9(A9), .B10(A10),
    .B11(A11), .B12(A12), .B13(A13), .B14(A14), .B15(A15), .B16(A16), .B17(A17), .B18(A18), .B19(A19),
    .B20(A20), .B21(A21), .B22(A22), .B23(A23), .B24(A24), .B25(A25), .B26(A26), .B27(A27), .B28(A28),
    .B29(A29), .B30(A30), .B31(A31));
  sll sll_1 (
    .B0(1'b0), .B1(and_31_out), .B2(1'b0), .B3(1'b0), .B4(1'b0), .A0(n16_bit_general_register_1_q0),
    .A1(n16_bit_general_register_1_q1), .A2(n16_bit_general_register_1_q2),
    .A3(n16_bit_general_register_1_q3), .A4(n16_bit_general_register_1_q4),
    .A5(n16_bit_general_register_1_q5), .A6(n16_bit_general_register_1_q6),
    .A7(n16_bit_general_register_1_q7), .A8(n16_bit_general_register_1_q8),
    .A9(n16_bit_general_register_1_q9), .A10(n16_bit_general_register_1_q10),
    .A11(n16_bit_general_register_1_q11), .A12(n16_bit_general_register_1_q12),
    .A13(n16_bit_general_register_1_q13), .A14(n16_bit_general_register_1_q14),
    .A15(n16_bit_general_register_1_q15), .A16(1'b0), .A17(1'b0), .A18(1'b0), .A19(1'b0), .A20(1'b0),
    .A21(1'b0), .A22(1'b0), .A23(1'b0), .A24(1'b0), .A25(1'b0), .A26(1'b0), .A27(1'b0), .A28(1'b0),
    .A29(1'b0), .A30(1'b0), .A31(1'b0), ._0(out_50), ._1(out_51), ._2(out_52), ._3(out_53), ._4(out_54),
    ._5(out_55), ._6(out_56), ._7(out_57), ._8(out_58), ._9(out_59), ._10(out_60), ._11(out_61),
    ._12(out_62), ._13(out_63), ._14(out_64), ._15(out_65), ._16(out_66), ._17(out_67), ._18(out_68),
    ._19(out_69), ._20(out_70), ._21(out_71), ._22(out_72), ._23(out_73), ._24(out_74), ._25(out_75),
    ._26(out_76), ._27(out_77), ._28(out_78), ._29(out_79), ._30(out_80), ._31(out_81));
  and and_1 (and_1_out, slt_1__0, slt_1__1);
  and and_2 (and_2_out, slt_1__2, slt_1__3);
  and and_3 (and_3_out, slt_1__4, slt_1__5);
  and and_4 (and_4_out, slt_1__6, slt_1__7);
  and and_5 (and_5_out, slt_1__8, slt_1__9);
  and and_6 (and_6_out, slt_1__10, slt_1__11);
  and and_7 (and_7_out, slt_1__12, slt_1__13);
  and and_8 (and_8_out, slt_1__14, slt_1__15);
  and and_9 (and_9_out, slt_1__16, slt_1__17);
  and and_10 (and_10_out, slt_1__18, slt_1__19);
  and and_11 (and_11_out, slt_1__20, slt_1__21);
  and and_12 (and_12_out, slt_1__22, slt_1__23);
  and and_13 (and_13_out, slt_1__24, slt_1__25);
  and and_14 (and_14_out, slt_1__26, slt_1__27);
  and and_15 (and_15_out, slt_1__28, slt_1__29);
  and and_16 (and_16_out, slt_1__30, slt_1__31);
  and and_17 (and_17_out, and_1_out, and_2_out);
  and and_18 (and_18_out, and_3_out, and_4_out);
  and and_19 (and_19_out, and_5_out, and_6_out);
  and and_20 (and_20_out, and_7_out, and_8_out);
  and and_21 (and_21_out, and_9_out, and_10_out);
  and and_22 (and_22_out, and_11_out, and_12_out);
  and and_23 (and_23_out, and_13_out, and_14_out);
  and and_24 (and_24_out, and_15_out, and_16_out);
  and and_25 (and_25_out, and_17_out, and_18_out);
  and and_26 (and_26_out, and_25_out, and_27_out);
  and and_27 (and_27_out, and_19_out, and_20_out);
  and and_28 (and_28_out, and_21_out, and_22_out);
  and and_29 (and_29_out, and_28_out, and_30_out);
  and and_30 (and_30_out, and_23_out, and_24_out);
  and and_31 (and_31_out, and_26_out, and_29_out);

  // Notes on the sheet:
  //   OFFSET (IMMEDIATE)
endmodule

module blez (
  input  A0,
  input  A1,
  input  A2,
  input  A3,
  input  A4,
  input  A5,
  input  A6,
  input  A7,
  input  A8,
  input  A9,
  input  A10,
  input  A11,
  input  A12,
  input  A13,
  input  A14,
  input  A15,
  input  A16,
  input  A17,
  input  A18,
  input  A19,
  input  A20,
  input  A21,
  input  A22,
  input  A23,
  input  A24,
  input  A25,
  input  A26,
  input  A27,
  input  A28,
  input  A29,
  input  A30,
  input  A31,
  input  A0_2,
  input  A1_2,
  input  A2_2,
  input  A3_2,
  input  A4_2,
  input  A5_2,
  input  A6_2,
  input  A7_2,
  input  A8_2,
  input  A9_2,
  input  A10_2,
  input  A11_2,
  input  A12_2,
  input  A13_2,
  input  A14_2,
  input  A15_2,
  input  E,
  output out_50,
  output out_51,
  output out_52,
  output out_53,
  output out_54,
  output out_55,
  output out_56,
  output out_57,
  output out_58,
  output out_59,
  output out_60,
  output out_61,
  output out_62,
  output out_63,
  output out_64,
  output out_65,
  output out_66,
  output out_67,
  output out_68,
  output out_69,
  output out_70,
  output out_71,
  output out_72,
  output out_73,
  output out_74,
  output out_75,
  output out_76,
  output out_77,
  output out_78,
  output out_79,
  output out_80,
  output out_81
);

  wire and_1_out, and_2_out, and_3_out, and_4_out, and_5_out, and_6_out, and_7_out, and_8_out, and_9_out,
       and_10_out, and_11_out, and_12_out, and_13_out, and_14_out, and_15_out, and_16_out, and_17_out,
       and_18_out, and_19_out, and_20_out, and_21_out, and_22_out, and_23_out, and_24_out, and_25_out,
       and_26_out, and_27_out, and_28_out, and_29_out, and_30_out, and_31_out, n16_bit_general_register_1_q0,
       n16_bit_general_register_1_q1, n16_bit_general_register_1_q2, n16_bit_general_register_1_q3,
       n16_bit_general_register_1_q4, n16_bit_general_register_1_q5, n16_bit_general_register_1_q6,
       n16_bit_general_register_1_q7, n16_bit_general_register_1_q8, n16_bit_general_register_1_q9,
       n16_bit_general_register_1_q10, n16_bit_general_register_1_q11, n16_bit_general_register_1_q12,
       n16_bit_general_register_1_q13, n16_bit_general_register_1_q14, n16_bit_general_register_1_q15,
       or_1_out, or_2_out, or_3_out, or_4_out, or_5_out, or_6_out, or_7_out, or_8_out, or_9_out, or_10_out,
       or_11_out, or_12_out, or_13_out, or_14_out, or_15_out, or_16_out, or_17_out, or_18_out, or_19_out,
       or_20_out, or_21_out, or_22_out, or_23_out, or_24_out, or_25_out, or_26_out, or_27_out, or_28_out,
       or_29_out, or_30_out, or_31_out, or_32_out, slt_1__0, slt_1__1, slt_1__2, slt_1__3, slt_1__4,
       slt_1__5, slt_1__6, slt_1__7, slt_1__8, slt_1__9, slt_1__10, slt_1__11, slt_1__12, slt_1__13,
       slt_1__14, slt_1__15, slt_1__16, slt_1__17, slt_1__18, slt_1__19, slt_1__20, slt_1__21, slt_1__22,
       slt_1__23, slt_1__24, slt_1__25, slt_1__26, slt_1__27, slt_1__28, slt_1__29, slt_1__30, slt_1__31,
       xnor_1__0, xnor_1__1, xnor_1__2, xnor_1__3, xnor_1__4, xnor_1__5, xnor_1__6, xnor_1__7, xnor_1__8,
       xnor_1__9, xnor_1__10, xnor_1__11, xnor_1__12, xnor_1__13, xnor_1__14, xnor_1__15, xnor_1__16,
       xnor_1__17, xnor_1__18, xnor_1__19, xnor_1__20, xnor_1__21, xnor_1__22, xnor_1__23, xnor_1__24,
       xnor_1__25, xnor_1__26, xnor_1__27, xnor_1__28, xnor_1__29, xnor_1__30, xnor_1__31;

  _16_Bit_General_Register u_16_bit_general_register_1 (
    .E(E), .D0(A0_2), .Q0(n16_bit_general_register_1_q0), .D1(A1_2), .Q1(n16_bit_general_register_1_q1),
    .D2(A2_2), .Q2(n16_bit_general_register_1_q2), .D3(A3_2), .Q3(n16_bit_general_register_1_q3), .D4(A4_2),
    .Q4(n16_bit_general_register_1_q4), .D5(A5_2), .Q5(n16_bit_general_register_1_q5), .D6(A6_2),
    .Q6(n16_bit_general_register_1_q6), .D7(A7_2), .Q7(n16_bit_general_register_1_q7), .D8(A8_2),
    .Q8(n16_bit_general_register_1_q8), .D9(A9_2), .Q9(n16_bit_general_register_1_q9), .D10(A10_2),
    .Q10(n16_bit_general_register_1_q10), .D11(A11_2), .Q11(n16_bit_general_register_1_q11), .D12(A12_2),
    .Q12(n16_bit_general_register_1_q12), .D13(A13_2), .Q13(n16_bit_general_register_1_q13), .D14(A14_2),
    .Q14(n16_bit_general_register_1_q14), .D15(A15_2), .Q15(n16_bit_general_register_1_q15));
  slt slt_1 (
    .A0(A0), .A1(A1), .A2(A2), .A3(A3), .A4(A4), .A5(A5), .A6(A6), .A7(A7), .A8(A8), .A9(A9), .A10(A10),
    .A11(A11), .A12(A12), .A13(A13), .A14(A14), .A15(A15), .A16(A16), .A17(A17), .A18(A18), .A19(A19),
    .A20(A20), .A21(A21), .A22(A22), .A23(A23), .A24(A24), .A25(A25), .A26(A26), .A27(A27), .A28(A28),
    .A29(A29), .A30(A30), .A31(A31), ._0(slt_1__0), ._1(slt_1__1), ._2(slt_1__2), ._3(slt_1__3),
    ._4(slt_1__4), ._5(slt_1__5), ._6(slt_1__6), ._7(slt_1__7), ._8(slt_1__8), ._9(slt_1__9),
    ._10(slt_1__10), ._11(slt_1__11), ._12(slt_1__12), ._13(slt_1__13), ._14(slt_1__14), ._15(slt_1__15),
    ._16(slt_1__16), ._17(slt_1__17), ._18(slt_1__18), ._19(slt_1__19), ._20(slt_1__20), ._21(slt_1__21),
    ._22(slt_1__22), ._23(slt_1__23), ._24(slt_1__24), ._25(slt_1__25), ._26(slt_1__26), ._27(slt_1__27),
    ._28(slt_1__28), ._29(slt_1__29), ._30(slt_1__30), ._31(slt_1__31), .B0(1'b0), .B1(1'b0), .B2(1'b0),
    .B3(1'b0), .B4(1'b0), .B5(1'b0), .B6(1'b0), .B7(1'b0), .B8(1'b0), .B9(1'b0), .B10(1'b0), .B11(1'b0),
    .B12(1'b0), .B13(1'b0), .B14(1'b0), .B15(1'b0), .B16(1'b0), .B17(1'b0), .B18(1'b0), .B19(1'b0),
    .B20(1'b0), .B21(1'b0), .B22(1'b0), .B23(1'b0), .B24(1'b0), .B25(1'b0), .B26(1'b0), .B27(1'b0),
    .B28(1'b0), .B29(1'b0), .B30(1'b0), .B31(1'b0));
  \xnor  xnor_1 (
    .A0(A0), .B0(1'b0), .A1(A1), .B1(1'b0), .A2(A2), .B2(1'b0), .A3(A3), .B3(1'b0), .A4(A4), .B4(1'b0),
    .A5(A5), .B5(1'b0), .A6(A6), .B6(1'b0), .A7(A7), .B7(1'b0), .A8(A8), .B8(1'b0), .A9(A9), .B9(1'b0),
    .A10(A10), .B10(1'b0), .A11(A11), .B11(1'b0), .A12(A12), .B12(1'b0), .A13(A13), .B13(1'b0), .A14(A14),
    .B14(1'b0), .A15(A15), .B15(1'b0), .A16(A16), .B16(1'b0), .A17(A17), .B17(1'b0), .A18(A18), .B18(1'b0),
    .A19(A19), .B19(1'b0), .A20(A20), .B20(1'b0), .A21(A21), .B21(1'b0), .A22(A22), .B22(1'b0), .A23(A23),
    .B23(1'b0), .A24(A24), .B24(1'b0), .A25(A25), .B25(1'b0), .A26(A26), .B26(1'b0), .A27(A27), .B27(1'b0),
    .A28(A28), .B28(1'b0), .A29(A29), .B29(1'b0), .A30(A30), .B30(1'b0), .A31(A31), .B31(1'b0),
    ._0(xnor_1__0), ._1(xnor_1__1), ._2(xnor_1__2), ._3(xnor_1__3), ._4(xnor_1__4), ._5(xnor_1__5),
    ._6(xnor_1__6), ._7(xnor_1__7), ._8(xnor_1__8), ._9(xnor_1__9), ._10(xnor_1__10), ._11(xnor_1__11),
    ._12(xnor_1__12), ._13(xnor_1__13), ._14(xnor_1__14), ._15(xnor_1__15), ._16(xnor_1__16),
    ._17(xnor_1__17), ._18(xnor_1__18), ._19(xnor_1__19), ._20(xnor_1__20), ._21(xnor_1__21),
    ._22(xnor_1__22), ._23(xnor_1__23), ._24(xnor_1__24), ._25(xnor_1__25), ._26(xnor_1__26),
    ._27(xnor_1__27), ._28(xnor_1__28), ._29(xnor_1__29), ._30(xnor_1__30), ._31(xnor_1__31));
  sll sll_1 (
    .B0(1'b0), .B1(or_32_out), .B2(1'b0), .B3(1'b0), .B4(1'b0), .A0(n16_bit_general_register_1_q0),
    .A1(n16_bit_general_register_1_q1), .A2(n16_bit_general_register_1_q2),
    .A3(n16_bit_general_register_1_q3), .A4(n16_bit_general_register_1_q4),
    .A5(n16_bit_general_register_1_q5), .A6(n16_bit_general_register_1_q6),
    .A7(n16_bit_general_register_1_q7), .A8(n16_bit_general_register_1_q8),
    .A9(n16_bit_general_register_1_q9), .A10(n16_bit_general_register_1_q10),
    .A11(n16_bit_general_register_1_q11), .A12(n16_bit_general_register_1_q12),
    .A13(n16_bit_general_register_1_q13), .A14(n16_bit_general_register_1_q14),
    .A15(n16_bit_general_register_1_q15), .A16(1'b0), .A17(1'b0), .A18(1'b0), .A19(1'b0), .A20(1'b0),
    .A21(1'b0), .A22(1'b0), .A23(1'b0), .A24(1'b0), .A25(1'b0), .A26(1'b0), .A27(1'b0), .A28(1'b0),
    .A29(1'b0), .A30(1'b0), .A31(1'b0), ._0(out_50), ._1(out_51), ._2(out_52), ._3(out_53), ._4(out_54),
    ._5(out_55), ._6(out_56), ._7(out_57), ._8(out_58), ._9(out_59), ._10(out_60), ._11(out_61),
    ._12(out_62), ._13(out_63), ._14(out_64), ._15(out_65), ._16(out_66), ._17(out_67), ._18(out_68),
    ._19(out_69), ._20(out_70), ._21(out_71), ._22(out_72), ._23(out_73), ._24(out_74), ._25(out_75),
    ._26(out_76), ._27(out_77), ._28(out_78), ._29(out_79), ._30(out_80), ._31(out_81));
  or or_1 (or_1_out, slt_1__0, slt_1__1);
  or or_2 (or_2_out, or_1_out, or_3_out);
  or or_3 (or_3_out, slt_1__2, slt_1__3);
  or or_4 (or_4_out, slt_1__4, slt_1__5);
  or or_5 (or_5_out, or_4_out, or_6_out);
  or or_6 (or_6_out, slt_1__6, slt_1__7);
  or or_7 (or_7_out, slt_1__8, slt_1__9);
  or or_8 (or_8_out, or_7_out, or_9_out);
  or or_9 (or_9_out, slt_1__10, slt_1__11);
  or or_10 (or_10_out, slt_1__12, slt_1__13);
  or or_11 (or_11_out, or_10_out, or_12_out);
  or or_12 (or_12_out, slt_1__14, slt_1__15);
  or or_13 (or_13_out, slt_1__16, slt_1__17);
  or or_14 (or_14_out, or_13_out, or_15_out);
  or or_15 (or_15_out, slt_1__18, slt_1__19);
  or or_16 (or_16_out, slt_1__20, slt_1__21);
  or or_17 (or_17_out, or_16_out, or_18_out);
  or or_18 (or_18_out, slt_1__22, slt_1__23);
  or or_19 (or_19_out, slt_1__24, slt_1__25);
  or or_20 (or_20_out, or_19_out, or_21_out);
  or or_21 (or_21_out, slt_1__26, slt_1__27);
  or or_22 (or_22_out, slt_1__28, slt_1__29);
  or or_23 (or_23_out, or_22_out, or_24_out);
  or or_24 (or_24_out, slt_1__30, slt_1__31);
  and and_1 (and_1_out, xnor_1__0, xnor_1__1);
  and and_2 (and_2_out, and_1_out, and_3_out);
  and and_3 (and_3_out, xnor_1__2, xnor_1__3);
  and and_4 (and_4_out, xnor_1__4, xnor_1__5);
  and and_5 (and_5_out, and_4_out, and_6_out);
  and and_6 (and_6_out, xnor_1__6, xnor_1__7);
  and and_7 (and_7_out, xnor_1__8, xnor_1__9);
  and and_8 (and_8_out, and_7_out, and_9_out);
  and and_9 (and_9_out, xnor_1__10, xnor_1__11);
  and and_10 (and_10_out, xnor_1__12, xnor_1__13);
  and and_11 (and_11_out, and_10_out, and_12_out);
  and and_12 (and_12_out, xnor_1__14, xnor_1__15);
  and and_13 (and_13_out, xnor_1__16, xnor_1__17);
  and and_14 (and_14_out, and_13_out, and_15_out);
  and and_15 (and_15_out, xnor_1__18, xnor_1__19);
  and and_16 (and_16_out, xnor_1__20, xnor_1__21);
  and and_17 (and_17_out, and_16_out, and_18_out);
  and and_18 (and_18_out, xnor_1__22, xnor_1__23);
  and and_19 (and_19_out, xnor_1__24, xnor_1__25);
  and and_20 (and_20_out, and_19_out, and_21_out);
  and and_21 (and_21_out, xnor_1__26, xnor_1__27);
  and and_22 (and_22_out, xnor_1__28, xnor_1__29);
  and and_23 (and_23_out, and_22_out, and_24_out);
  and and_24 (and_24_out, xnor_1__30, xnor_1__31);
  or or_25 (or_25_out, or_2_out, or_5_out);
  or or_26 (or_26_out, or_8_out, or_11_out);
  or or_27 (or_27_out, or_14_out, or_17_out);
  or or_28 (or_28_out, or_20_out, or_23_out);
  and and_25 (and_25_out, and_2_out, and_5_out);
  and and_26 (and_26_out, and_8_out, and_11_out);
  and and_27 (and_27_out, and_14_out, and_17_out);
  and and_28 (and_28_out, and_20_out, and_23_out);
  or or_29 (or_29_out, or_25_out, or_26_out);
  or or_30 (or_30_out, or_29_out, or_31_out);
  or or_31 (or_31_out, or_27_out, or_28_out);
  and and_29 (and_29_out, and_25_out, and_26_out);
  and and_30 (and_30_out, and_29_out, and_31_out);
  and and_31 (and_31_out, and_27_out, and_28_out);
  or or_32 (or_32_out, and_30_out, or_30_out);

  // Notes on the sheet:
  //   INPUT A
  //   OFFSET (IMMEDIATE)
endmodule

module bltz_bltzal (
  input  A0,
  input  A1,
  input  A2,
  input  A3,
  input  A4,
  input  A5,
  input  A6,
  input  A7,
  input  A8,
  input  A9,
  input  A10,
  input  A11,
  input  A12,
  input  A13,
  input  A14,
  input  A15,
  input  A16,
  input  A17,
  input  A18,
  input  A19,
  input  A20,
  input  A21,
  input  A22,
  input  A23,
  input  A24,
  input  A25,
  input  A26,
  input  A27,
  input  A28,
  input  A29,
  input  A30,
  input  A31,
  input  A0_2,
  input  A1_2,
  input  A2_2,
  input  A3_2,
  input  A4_2,
  input  A5_2,
  input  A6_2,
  input  A7_2,
  input  A8_2,
  input  A9_2,
  input  A10_2,
  input  A11_2,
  input  A12_2,
  input  A13_2,
  input  A14_2,
  input  A15_2,
  input  E,
  output out_50,
  output out_51,
  output out_52,
  output out_53,
  output out_54,
  output out_55,
  output out_56,
  output out_57,
  output out_58,
  output out_59,
  output out_60,
  output out_61,
  output out_62,
  output out_63,
  output out_64,
  output out_65,
  output out_66,
  output out_67,
  output out_68,
  output out_69,
  output out_70,
  output out_71,
  output out_72,
  output out_73,
  output out_74,
  output out_75,
  output out_76,
  output out_77,
  output out_78,
  output out_79,
  output out_80,
  output out_81
);

  wire and_1_out, and_2_out, and_3_out, and_4_out, and_5_out, and_6_out, and_7_out, and_8_out, and_9_out,
       and_10_out, and_11_out, and_12_out, and_13_out, and_14_out, and_15_out, and_16_out, and_17_out,
       and_18_out, and_19_out, and_20_out, and_21_out, and_22_out, and_23_out, and_24_out, and_25_out,
       and_26_out, and_27_out, and_28_out, and_29_out, and_30_out, and_31_out, n16_bit_general_register_1_q0,
       n16_bit_general_register_1_q1, n16_bit_general_register_1_q2, n16_bit_general_register_1_q3,
       n16_bit_general_register_1_q4, n16_bit_general_register_1_q5, n16_bit_general_register_1_q6,
       n16_bit_general_register_1_q7, n16_bit_general_register_1_q8, n16_bit_general_register_1_q9,
       n16_bit_general_register_1_q10, n16_bit_general_register_1_q11, n16_bit_general_register_1_q12,
       n16_bit_general_register_1_q13, n16_bit_general_register_1_q14, n16_bit_general_register_1_q15,
       slt_1__0, slt_1__1, slt_1__2, slt_1__3, slt_1__4, slt_1__5, slt_1__6, slt_1__7, slt_1__8, slt_1__9,
       slt_1__10, slt_1__11, slt_1__12, slt_1__13, slt_1__14, slt_1__15, slt_1__16, slt_1__17, slt_1__18,
       slt_1__19, slt_1__20, slt_1__21, slt_1__22, slt_1__23, slt_1__24, slt_1__25, slt_1__26, slt_1__27,
       slt_1__28, slt_1__29, slt_1__30, slt_1__31;

  _16_Bit_General_Register u_16_bit_general_register_1 (
    .E(E), .D0(A0_2), .Q0(n16_bit_general_register_1_q0), .D1(A1_2), .Q1(n16_bit_general_register_1_q1),
    .D2(A2_2), .Q2(n16_bit_general_register_1_q2), .D3(A3_2), .Q3(n16_bit_general_register_1_q3), .D4(A4_2),
    .Q4(n16_bit_general_register_1_q4), .D5(A5_2), .Q5(n16_bit_general_register_1_q5), .D6(A6_2),
    .Q6(n16_bit_general_register_1_q6), .D7(A7_2), .Q7(n16_bit_general_register_1_q7), .D8(A8_2),
    .Q8(n16_bit_general_register_1_q8), .D9(A9_2), .Q9(n16_bit_general_register_1_q9), .D10(A10_2),
    .Q10(n16_bit_general_register_1_q10), .D11(A11_2), .Q11(n16_bit_general_register_1_q11), .D12(A12_2),
    .Q12(n16_bit_general_register_1_q12), .D13(A13_2), .Q13(n16_bit_general_register_1_q13), .D14(A14_2),
    .Q14(n16_bit_general_register_1_q14), .D15(A15_2), .Q15(n16_bit_general_register_1_q15));
  slt slt_1 (
    .A0(A0), .A1(A1), .A2(A2), .A3(A3), .A4(A4), .A5(A5), .A6(A6), .A7(A7), .A8(A8), .A9(A9), .A10(A10),
    .A11(A11), .A12(A12), .A13(A13), .A14(A14), .A15(A15), .A16(A16), .A17(A17), .A18(A18), .A19(A19),
    .A20(A20), .A21(A21), .A22(A22), .A23(A23), .A24(A24), .A25(A25), .A26(A26), .A27(A27), .A28(A28),
    .A29(A29), .A30(A30), .A31(A31), ._0(slt_1__0), ._1(slt_1__1), ._2(slt_1__2), ._3(slt_1__3),
    ._4(slt_1__4), ._5(slt_1__5), ._6(slt_1__6), ._7(slt_1__7), ._8(slt_1__8), ._9(slt_1__9),
    ._10(slt_1__10), ._11(slt_1__11), ._12(slt_1__12), ._13(slt_1__13), ._14(slt_1__14), ._15(slt_1__15),
    ._16(slt_1__16), ._17(slt_1__17), ._18(slt_1__18), ._19(slt_1__19), ._20(slt_1__20), ._21(slt_1__21),
    ._22(slt_1__22), ._23(slt_1__23), ._24(slt_1__24), ._25(slt_1__25), ._26(slt_1__26), ._27(slt_1__27),
    ._28(slt_1__28), ._29(slt_1__29), ._30(slt_1__30), ._31(slt_1__31), .B0(1'b0), .B1(1'b0), .B2(1'b0),
    .B3(1'b0), .B4(1'b0), .B5(1'b0), .B6(1'b0), .B7(1'b0), .B8(1'b0), .B9(1'b0), .B10(1'b0), .B11(1'b0),
    .B12(1'b0), .B13(1'b0), .B14(1'b0), .B15(1'b0), .B16(1'b0), .B17(1'b0), .B18(1'b0), .B19(1'b0),
    .B20(1'b0), .B21(1'b0), .B22(1'b0), .B23(1'b0), .B24(1'b0), .B25(1'b0), .B26(1'b0), .B27(1'b0),
    .B28(1'b0), .B29(1'b0), .B30(1'b0), .B31(1'b0));
  sll sll_1 (
    .B0(1'b0), .B1(and_30_out), .B2(1'b0), .B3(1'b0), .B4(1'b0), .A0(n16_bit_general_register_1_q0),
    .A1(n16_bit_general_register_1_q1), .A2(n16_bit_general_register_1_q2),
    .A3(n16_bit_general_register_1_q3), .A4(n16_bit_general_register_1_q4),
    .A5(n16_bit_general_register_1_q5), .A6(n16_bit_general_register_1_q6),
    .A7(n16_bit_general_register_1_q7), .A8(n16_bit_general_register_1_q8),
    .A9(n16_bit_general_register_1_q9), .A10(n16_bit_general_register_1_q10),
    .A11(n16_bit_general_register_1_q11), .A12(n16_bit_general_register_1_q12),
    .A13(n16_bit_general_register_1_q13), .A14(n16_bit_general_register_1_q14),
    .A15(n16_bit_general_register_1_q15), .A16(1'b0), .A17(1'b0), .A18(1'b0), .A19(1'b0), .A20(1'b0),
    .A21(1'b0), .A22(1'b0), .A23(1'b0), .A24(1'b0), .A25(1'b0), .A26(1'b0), .A27(1'b0), .A28(1'b0),
    .A29(1'b0), .A30(1'b0), .A31(1'b0), ._0(out_50), ._1(out_51), ._2(out_52), ._3(out_53), ._4(out_54),
    ._5(out_55), ._6(out_56), ._7(out_57), ._8(out_58), ._9(out_59), ._10(out_60), ._11(out_61),
    ._12(out_62), ._13(out_63), ._14(out_64), ._15(out_65), ._16(out_66), ._17(out_67), ._18(out_68),
    ._19(out_69), ._20(out_70), ._21(out_71), ._22(out_72), ._23(out_73), ._24(out_74), ._25(out_75),
    ._26(out_76), ._27(out_77), ._28(out_78), ._29(out_79), ._30(out_80), ._31(out_81));
  and and_1 (and_1_out, slt_1__0, slt_1__1);
  and and_2 (and_2_out, and_1_out, and_3_out);
  and and_3 (and_3_out, slt_1__2, slt_1__3);
  and and_4 (and_4_out, slt_1__4, slt_1__5);
  and and_5 (and_5_out, and_4_out, and_6_out);
  and and_6 (and_6_out, slt_1__6, slt_1__7);
  and and_7 (and_7_out, slt_1__8, slt_1__9);
  and and_8 (and_8_out, and_7_out, and_9_out);
  and and_9 (and_9_out, slt_1__10, slt_1__11);
  and and_10 (and_10_out, slt_1__12, slt_1__13);
  and and_11 (and_11_out, and_10_out, and_12_out);
  and and_12 (and_12_out, slt_1__14, slt_1__15);
  and and_13 (and_13_out, slt_1__16, slt_1__17);
  and and_14 (and_14_out, and_13_out, and_15_out);
  and and_15 (and_15_out, slt_1__18, slt_1__19);
  and and_16 (and_16_out, slt_1__20, slt_1__21);
  and and_17 (and_17_out, and_16_out, and_18_out);
  and and_18 (and_18_out, slt_1__22, slt_1__23);
  and and_19 (and_19_out, slt_1__24, slt_1__25);
  and and_20 (and_20_out, and_19_out, and_21_out);
  and and_21 (and_21_out, slt_1__26, slt_1__27);
  and and_22 (and_22_out, slt_1__28, slt_1__29);
  and and_23 (and_23_out, and_22_out, and_24_out);
  and and_24 (and_24_out, slt_1__30, slt_1__31);
  and and_25 (and_25_out, and_2_out, and_5_out);
  and and_26 (and_26_out, and_8_out, and_11_out);
  and and_27 (and_27_out, and_14_out, and_17_out);
  and and_28 (and_28_out, and_20_out, and_23_out);
  and and_29 (and_29_out, and_25_out, and_26_out);
  and and_30 (and_30_out, and_29_out, and_31_out);
  and and_31 (and_31_out, and_27_out, and_28_out);

  // Notes on the sheet:
  //   OFFSET (IMMEDIATE)
endmodule

module bne (
  input  A0,
  input  A1,
  input  A2,
  input  A3,
  input  A4,
  input  A5,
  input  A6,
  input  A7,
  input  A8,
  input  A9,
  input  A10,
  input  A11,
  input  A12,
  input  A13,
  input  A14,
  input  A15,
  input  A16,
  input  A17,
  input  A18,
  input  A19,
  input  A20,
  input  A21,
  input  A22,
  input  A23,
  input  A24,
  input  A25,
  input  A26,
  input  A27,
  input  A28,
  input  A29,
  input  A30,
  input  A31,
  input  A0_2,
  input  A1_2,
  input  A2_2,
  input  A3_2,
  input  A4_2,
  input  A5_2,
  input  A6_2,
  input  A7_2,
  input  A8_2,
  input  A9_2,
  input  A10_2,
  input  A11_2,
  input  A12_2,
  input  A13_2,
  input  A14_2,
  input  A15_2,
  input  A16_2,
  input  A17_2,
  input  A18_2,
  input  A19_2,
  input  A20_2,
  input  A21_2,
  input  A22_2,
  input  A23_2,
  input  A24_2,
  input  A25_2,
  input  A26_2,
  input  A27_2,
  input  A28_2,
  input  A29_2,
  input  A30_2,
  input  A31_2,
  input  A0_3,
  input  A1_3,
  input  A2_3,
  input  A3_3,
  input  A4_3,
  input  A5_3,
  input  A6_3,
  input  A7_3,
  input  A8_3,
  input  A9_3,
  input  A10_3,
  input  A11_3,
  input  A12_3,
  input  A13_3,
  input  A14_3,
  input  A15_3,
  input  E,
  output out_82,
  output out_83,
  output out_84,
  output out_85,
  output out_86,
  output out_87,
  output out_88,
  output out_89,
  output out_90,
  output out_91,
  output out_92,
  output out_93,
  output out_94,
  output out_95,
  output out_96,
  output out_97,
  output out_98,
  output out_99,
  output out_100,
  output out_101,
  output out_102,
  output out_103,
  output out_104,
  output out_105,
  output out_106,
  output out_107,
  output out_108,
  output out_109,
  output out_110,
  output out_111,
  output out_112,
  output out_113
);

  wire and_1_out, and_2_out, and_3_out, and_4_out, and_5_out, and_6_out, and_7_out, and_8_out, and_9_out,
       and_10_out, and_11_out, and_12_out, and_13_out, and_14_out, and_15_out, and_16_out, and_17_out,
       and_18_out, and_19_out, and_20_out, and_21_out, and_22_out, and_23_out, and_24_out, and_25_out,
       and_26_out, and_27_out, and_28_out, and_29_out, and_30_out, n16_bit_general_register_1_q0,
       n16_bit_general_register_1_q1, n16_bit_general_register_1_q2, n16_bit_general_register_1_q3,
       n16_bit_general_register_1_q4, n16_bit_general_register_1_q5, n16_bit_general_register_1_q6,
       n16_bit_general_register_1_q7, n16_bit_general_register_1_q8, n16_bit_general_register_1_q9,
       n16_bit_general_register_1_q10, n16_bit_general_register_1_q11, n16_bit_general_register_1_q12,
       n16_bit_general_register_1_q13, n16_bit_general_register_1_q14, n16_bit_general_register_1_q15,
       nand_1_out, xnor_1__0, xnor_1__1, xnor_1__2, xnor_1__3, xnor_1__4, xnor_1__5, xnor_1__6, xnor_1__7,
       xnor_1__8, xnor_1__9, xnor_1__10, xnor_1__11, xnor_1__12, xnor_1__13, xnor_1__14, xnor_1__15,
       xnor_1__16, xnor_1__17, xnor_1__18, xnor_1__19, xnor_1__20, xnor_1__21, xnor_1__22, xnor_1__23,
       xnor_1__24, xnor_1__25, xnor_1__26, xnor_1__27, xnor_1__28, xnor_1__29, xnor_1__30, xnor_1__31;

  _16_Bit_General_Register u_16_bit_general_register_1 (
    .E(E), .D0(A0_3), .Q0(n16_bit_general_register_1_q0), .D1(A1_3), .Q1(n16_bit_general_register_1_q1),
    .D2(A2_3), .Q2(n16_bit_general_register_1_q2), .D3(A3_3), .Q3(n16_bit_general_register_1_q3), .D4(A4_3),
    .Q4(n16_bit_general_register_1_q4), .D5(A5_3), .Q5(n16_bit_general_register_1_q5), .D6(A6_3),
    .Q6(n16_bit_general_register_1_q6), .D7(A7_3), .Q7(n16_bit_general_register_1_q7), .D8(A8_3),
    .Q8(n16_bit_general_register_1_q8), .D9(A9_3), .Q9(n16_bit_general_register_1_q9), .D10(A10_3),
    .Q10(n16_bit_general_register_1_q10), .D11(A11_3), .Q11(n16_bit_general_register_1_q11), .D12(A12_3),
    .Q12(n16_bit_general_register_1_q12), .D13(A13_3), .Q13(n16_bit_general_register_1_q13), .D14(A14_3),
    .Q14(n16_bit_general_register_1_q14), .D15(A15_3), .Q15(n16_bit_general_register_1_q15));
  \xnor  xnor_1 (
    .A0(A0_2), .B0(A0), .A1(A1_2), .B1(A1), .A2(A2_2), .B2(A2), .A3(A3_2), .B3(A3), .A4(A4_2), .B4(A4),
    .A5(A5_2), .B5(A5), .A6(A6_2), .B6(A6), .A7(A7_2), .B7(A7), .A8(A8_2), .B8(A8), .A9(A9_2), .B9(A9),
    .A10(A10_2), .B10(A10), .A11(A11_2), .B11(A11), .A12(A12_2), .B12(A12), .A13(A13_2), .B13(A13),
    .A14(A14_2), .B14(A14), .A15(A15_2), .B15(A15), .A16(A16_2), .B16(A16), .A17(A17_2), .B17(A17),
    .A18(A18_2), .B18(A18), .A19(A19_2), .B19(A19), .A20(A20_2), .B20(A20), .A21(A21_2), .B21(A21),
    .A22(A22_2), .B22(A22), .A23(A23_2), .B23(A23), .A24(A24_2), .B24(A24), .A25(A25_2), .B25(A25),
    .A26(A26_2), .B26(A26), .A27(A27_2), .B27(A27), .A28(A28_2), .B28(A28), .A29(A29_2), .B29(A29),
    .A30(A30_2), .B30(A30), .A31(A31_2), .B31(A31), ._0(xnor_1__0), ._1(xnor_1__1), ._2(xnor_1__2),
    ._3(xnor_1__3), ._4(xnor_1__4), ._5(xnor_1__5), ._6(xnor_1__6), ._7(xnor_1__7), ._8(xnor_1__8),
    ._9(xnor_1__9), ._10(xnor_1__10), ._11(xnor_1__11), ._12(xnor_1__12), ._13(xnor_1__13), ._14(xnor_1__14),
    ._15(xnor_1__15), ._16(xnor_1__16), ._17(xnor_1__17), ._18(xnor_1__18), ._19(xnor_1__19),
    ._20(xnor_1__20), ._21(xnor_1__21), ._22(xnor_1__22), ._23(xnor_1__23), ._24(xnor_1__24),
    ._25(xnor_1__25), ._26(xnor_1__26), ._27(xnor_1__27), ._28(xnor_1__28), ._29(xnor_1__29),
    ._30(xnor_1__30), ._31(xnor_1__31));
  sll sll_1 (
    .B0(1'b0), .B1(nand_1_out), .B2(1'b0), .B3(1'b0), .B4(1'b0), .A0(n16_bit_general_register_1_q0),
    .A1(n16_bit_general_register_1_q1), .A2(n16_bit_general_register_1_q2),
    .A3(n16_bit_general_register_1_q3), .A4(n16_bit_general_register_1_q4),
    .A5(n16_bit_general_register_1_q5), .A6(n16_bit_general_register_1_q6),
    .A7(n16_bit_general_register_1_q7), .A8(n16_bit_general_register_1_q8),
    .A9(n16_bit_general_register_1_q9), .A10(n16_bit_general_register_1_q10),
    .A11(n16_bit_general_register_1_q11), .A12(n16_bit_general_register_1_q12),
    .A13(n16_bit_general_register_1_q13), .A14(n16_bit_general_register_1_q14),
    .A15(n16_bit_general_register_1_q15), .A16(1'b0), .A17(1'b0), .A18(1'b0), .A19(1'b0), .A20(1'b0),
    .A21(1'b0), .A22(1'b0), .A23(1'b0), .A24(1'b0), .A25(1'b0), .A26(1'b0), .A27(1'b0), .A28(1'b0),
    .A29(1'b0), .A30(1'b0), .A31(1'b0), ._0(out_82), ._1(out_83), ._2(out_84), ._3(out_85), ._4(out_86),
    ._5(out_87), ._6(out_88), ._7(out_89), ._8(out_90), ._9(out_91), ._10(out_92), ._11(out_93),
    ._12(out_94), ._13(out_95), ._14(out_96), ._15(out_97), ._16(out_98), ._17(out_99), ._18(out_100),
    ._19(out_101), ._20(out_102), ._21(out_103), ._22(out_104), ._23(out_105), ._24(out_106), ._25(out_107),
    ._26(out_108), ._27(out_109), ._28(out_110), ._29(out_111), ._30(out_112), ._31(out_113));
  and and_1 (and_1_out, xnor_1__0, xnor_1__1);
  and and_2 (and_2_out, and_1_out, and_3_out);
  and and_3 (and_3_out, xnor_1__2, xnor_1__3);
  and and_4 (and_4_out, xnor_1__4, xnor_1__5);
  and and_5 (and_5_out, and_4_out, and_6_out);
  and and_6 (and_6_out, xnor_1__6, xnor_1__7);
  and and_7 (and_7_out, xnor_1__8, xnor_1__9);
  and and_8 (and_8_out, and_7_out, and_9_out);
  and and_9 (and_9_out, xnor_1__10, xnor_1__11);
  and and_10 (and_10_out, xnor_1__12, xnor_1__13);
  and and_11 (and_11_out, and_10_out, and_12_out);
  and and_12 (and_12_out, xnor_1__14, xnor_1__15);
  and and_13 (and_13_out, xnor_1__16, xnor_1__17);
  and and_14 (and_14_out, and_13_out, and_15_out);
  and and_15 (and_15_out, xnor_1__18, xnor_1__19);
  and and_16 (and_16_out, xnor_1__20, xnor_1__21);
  and and_17 (and_17_out, and_16_out, and_18_out);
  and and_18 (and_18_out, xnor_1__22, xnor_1__23);
  and and_19 (and_19_out, xnor_1__24, xnor_1__25);
  and and_20 (and_20_out, and_19_out, and_21_out);
  and and_21 (and_21_out, xnor_1__26, xnor_1__27);
  and and_22 (and_22_out, xnor_1__28, xnor_1__29);
  and and_23 (and_23_out, and_22_out, and_24_out);
  and and_24 (and_24_out, xnor_1__30, xnor_1__31);
  and and_25 (and_25_out, and_2_out, and_5_out);
  and and_26 (and_26_out, and_8_out, and_11_out);
  and and_27 (and_27_out, and_14_out, and_17_out);
  and and_28 (and_28_out, and_20_out, and_23_out);
  and and_29 (and_29_out, and_25_out, and_26_out);
  nand nand_1 (nand_1_out, and_29_out, and_30_out);
  and and_30 (and_30_out, and_27_out, and_28_out);

  // Notes on the sheet:
  //   INPUT A
  //   OFFSET (IMMEDIATE)
  //   INPUT B
endmodule
