// Logisim project MIPS.circ as structural Verilog
// D Latch
module Gated_D_Latch (
  input  D,
  input  E,
  output Q,
  output nQ
);

  wire nand_1_out, nand_2_out;

  nand nand_1 (nand_1_out, D, E);
  nand nand_2 (nand_2_out, nand_1_out, E);
  nand nand_3 (Q, nand_1_out, nQ);
  nand nand_4 (nQ, Q, nand_2_out);
endmodule

module _32_Bit_General_Register (
  input  E,
  input  D0,
  input  D1,
  input  D2,
  input  D3,
  input  D4,
  input  D5,
  input  D6,
  input  D7,
  input  D8,
  input  D9,
  input  D10,
  input  D11,
  input  D12,
  input  D13,
  input  D14,
  input  D15,
  input  D16,
  input  D17,
  input  D18,
  input  D19,
  input  D20,
  input  D21,
  input  D22,
  input  D23,
  input  D24,
  input  D25,
  input  D26,
  input  D27,
  input  D28,
  input  D29,
  input  D30,
  input  D31,
  output Q0,
  output Q1,
  output Q2,
  output Q3,
  output Q4,
  output Q5,
  output Q6,
  output Q7,
  output Q8,
  output Q9,
  output Q10,
  output Q11,
  output Q12,
  output Q13,
  output Q14,
  output Q15,
  output Q16,
  output Q17,
  output Q18,
  output D19_2,
  output D20_2,
  output D21_2,
  output D22_2,
  output D23_2,
  output D24_2,
  output D25_2,
  output D26_2,
  output D27_2,
  output D28_2,
  output D29_2,
  output D30_2,
  output D31_2
);

  Gated_D_Latch gated_d_latch_1 (.E(E), .D(D0), .Q(Q0));  // open: nQ
  Gated_D_Latch gated_d_latch_2 (.E(E), .D(D1), .Q(Q1));  // open: nQ
  Gated_D_Latch gated_d_latch_3 (.E(E), .D(D2), .Q(Q2));  // open: nQ
  Gated_D_Latch gated_d_latch_4 (.E(E), .D(D3), .Q(Q3));  // open: nQ
  Gated_D_Latch gated_d_latch_5 (.E(E), .D(D4), .Q(Q4));  // open: nQ
  Gated_D_Latch gated_d_latch_6 (.E(E), .D(D5), .Q(Q5));  // open: nQ
  Gated_D_Latch gated_d_latch_7 (.E(E), .D(D6), .Q(Q6));  // open: nQ
  Gated_D_Latch gated_d_latch_8 (.E(E), .D(D7), .Q(Q7));  // open: nQ
  Gated_D_Latch gated_d_latch_9 (.E(E), .D(D8), .Q(Q8));  // open: nQ
  Gated_D_Latch gated_d_latch_10 (.E(E), .D(D9), .Q(Q9));  // open: nQ
  Gated_D_Latch gated_d_latch_11 (.E(E), .D(D10), .Q(Q10));  // open: nQ
  Gated_D_Latch gated_d_latch_12 (.E(E), .D(D11), .Q(Q11));  // open: nQ
  Gated_D_Latch gated_d_latch_13 (.E(E), .D(D12), .Q(Q12));  // open: nQ
  Gated_D_Latch gated_d_latch_14 (.E(E), .D(D13), .Q(Q13));  // open: nQ
  Gated_D_Latch gated_d_latch_15 (.E(E), .D(D14), .Q(Q14));  // open: nQ
  Gated_D_Latch gated_d_latch_16 (.E(E), .D(D15), .Q(Q15));  // open: nQ
  Gated_D_Latch gated_d_latch_17 (.E(E), .D(D16), .Q(Q16));  // open: nQ
  Gated_D_Latch gated_d_latch_18 (.E(E), .D(D17), .Q(Q17));  // open: nQ
  Gated_D_Latch gated_d_latch_19 (.E(E), .D(D18), .Q(Q18));  // open: nQ
  Gated_D_Latch gated_d_latch_20 (.E(E), .D(D19), .Q(D19_2));  // open: nQ
  Gated_D_Latch gated_d_latch_21 (.E(E), .D(D20), .Q(D20_2));  // open: nQ
  Gated_D_Latch gated_d_latch_22 (.E(E), .D(D21), .Q(D21_2));  // open: nQ
  Gated_D_Latch gated_d_latch_23 (.E(E), .D(D22), .Q(D22_2));  // open: nQ
  Gated_D_Latch gated_d_latch_24 (.E(E), .D(D23), .Q(D23_2));  // open: nQ
  Gated_D_Latch gated_d_latch_25 (.E(E), .D(D24), .Q(D24_2));  // open: nQ
  Gated_D_Latch gated_d_latch_26 (.E(E), .D(D25), .Q(D25_2));  // open: nQ
  Gated_D_Latch gated_d_latch_27 (.E(E), .D(D26), .Q(D26_2));  // open: nQ
  Gated_D_Latch gated_d_latch_28 (.E(E), .D(D27), .Q(D27_2));  // open: nQ
  Gated_D_Latch gated_d_latch_29 (.E(E), .D(D28), .Q(D28_2));  // open: nQ
  Gated_D_Latch gated_d_latch_30 (.E(E), .D(D29), .Q(D29_2));  // open: nQ
  Gated_D_Latch gated_d_latch_31 (.E(E), .D(D30), .Q(D30_2));  // open: nQ
  Gated_D_Latch gated_d_latch_32 (.E(E), .D(D31), .Q(D31_2));  // open: nQ
endmodule

module _16_Bit_General_Register (
  input  E,
  input  D0,
  input  D1,
  input  D2,
  input  D3,
  input  D4,
  input  D5,
  input  D6,
  input  D7,
  input  D8,
  input  D9,
  input  D10,
  input  D11,
  input  D12,
  input  D13,
  input  D14,
  input  D15,
  output Q0,
  output Q1,
  output Q2,
  output Q3,
  output Q4,
  output Q5,
  output Q6,
  output Q7,
  output Q8,
  output Q9,
  output Q10,
  output Q11,
  output Q12,
  output Q13,
  output Q14,
  output Q15
);

  Gated_D_Latch gated_d_latch_1 (.E(E), .D(D0), .Q(Q0));  // open: nQ
  Gated_D_Latch gated_d_latch_2 (.E(E), .D(D1), .Q(Q1));  // open: nQ
  Gated_D_Latch gated_d_latch_3 (.E(E), .D(D2), .Q(Q2));  // open: nQ
  Gated_D_Latch gated_d_latch_4 (.E(E), .D(D3), .Q(Q3));  // open: nQ
  Gated_D_Latch gated_d_latch_5 (.E(E), .D(D4), .Q(Q4));  // open: nQ
  Gated_D_Latch gated_d_latch_6 (.E(E), .D(D5), .Q(Q5));  // open: nQ
  Gated_D_Latch gated_d_latch_7 (.E(E), .D(D6), .Q(Q6));  // open: nQ
  Gated_D_Latch gated_d_latch_8 (.E(E), .D(D7), .Q(Q7));  // open: nQ
  Gated_D_Latch gated_d_latch_9 (.E(E), .D(D8), .Q(Q8));  // open: nQ
  Gated_D_Latch gated_d_latch_10 (.E(E), .D(D9), .Q(Q9));  // open: nQ
  Gated_D_Latch gated_d_latch_11 (.E(E), .D(D10), .Q(Q10));  // open: nQ
  Gated_D_Latch gated_d_latch_12 (.E(E), .D(D11), .Q(Q11));  // open: nQ
  Gated_D_Latch gated_d_latch_13 (.E(E), .D(D12), .Q(Q12));  // open: nQ
  Gated_D_Latch gated_d_latch_14 (.E(E), .D(D13), .Q(Q13));  // open: nQ
  Gated_D_Latch gated_d_latch_15 (.E(E), .D(D14), .Q(Q14));  // open: nQ
  Gated_D_Latch gated_d_latch_16 (.E(E), .D(D15), .Q(Q15));  // open: nQ
endmodule

module Operations_Conditional_8_Bit_Register (
  input  E,
  input  _2_0,
  input  _2_1,
  input  _2_2,
  input  _2_3,
  input  _2_4,
  input  _2_5,
  input  _2_6,
  input  _2_7,
  output out_10,
  output out_11,
  output out_12,
  output out_13,
  output out_14,
  output out_15,
  output out_16,
  output out_17,
  output out_18,
  output out_19,
  output out_20,
  output out_21,
  output out_22,
  output out_23,
  output out_24,
  output out_25,
  output out_26,
  output out_27,
  output out_28,
  output out_29,
  output out_30,
  output out_31,
  output out_32,
  output out_33,
  output out_34,
  output out_35,
  output out_36,
  output out_37,
  output out_38,
  output out_39,
  output out_40,
  output out_41,
  output out_42,
  output out_43,
  output out_44,
  output out_45,
  output out_46,
  output out_47,
  output out_48,
  output out_49,
  output out_50,
  output out_51,
  output out_52,
  output out_53,
  output out_54,
  output out_55,
  output out_56,
  output out_57,
  output out_58,
  output out_59,
  output out_60,
  output out_61,
  output out_62
);

  wire and_1_out, and_2_out, and_3_out, and_4_out, and_5_out, and_6_out, and_7_out, and_8_out, and_9_out,
       and_10_out, and_11_out, and_12_out, and_13_out, and_14_out, and_21_out, and_22_out, and_28_out,
       and_29_out, and_35_out, and_36_out, and_42_out, and_43_out, and_44_out, and_49_out, and_50_out,
       and_51_out, and_56_out, and_57_out, and_58_out, and_63_out, and_64_out, and_69_out, and_70_out,
       and_71_out, and_76_out, and_77_out, and_78_out, and_83_out, and_84_out, and_85_out, and_89_out,
       and_90_out, and_94_out, and_95_out, and_96_out, and_98_out, and_99_out, and_100_out,
       gated_d_latch_1_q, gated_d_latch_2_q, gated_d_latch_3_q, gated_d_latch_4_q, gated_d_latch_5_q,
       gated_d_latch_6_q, gated_d_latch_7_q, gated_d_latch_8_q, nand_1_out, nand_2_out, nand_3_out,
       nand_4_out, nand_5_out, nand_6_out, nand_7_out, nand_8_out, nand_9_out, nand_10_out, nand_11_out,
       nand_12_out, not_1_out, not_2_out, not_3_out, not_4_out, not_5_out, not_6_out, not_7_out, not_8_out,
       not_9_out, not_10_out, not_11_out, not_12_out, not_13_out, not_14_out, not_15_out, not_16_out,
       not_17_out, not_18_out, not_19_out, not_20_out, not_21_out;

  Gated_D_Latch gated_d_latch_1 (.E(E), .D(_2_0), .Q(gated_d_latch_1_q));  // open: nQ
  Gated_D_Latch gated_d_latch_2 (.E(E), .D(_2_1), .Q(gated_d_latch_2_q));  // open: nQ
  Gated_D_Latch gated_d_latch_3 (.E(E), .D(_2_2), .Q(gated_d_latch_3_q));  // open: nQ
  Gated_D_Latch gated_d_latch_4 (.E(E), .D(_2_3), .Q(gated_d_latch_4_q));  // open: nQ
  Gated_D_Latch gated_d_latch_5 (.E(E), .D(_2_4), .Q(gated_d_latch_5_q));  // open: nQ
  Gated_D_Latch gated_d_latch_6 (.E(E), .D(_2_5), .Q(gated_d_latch_6_q));  // open: nQ
  Gated_D_Latch gated_d_latch_7 (.E(E), .D(_2_6), .Q(gated_d_latch_7_q));  // open: nQ
  Gated_D_Latch gated_d_latch_8 (.E(E), .D(_2_7), .Q(gated_d_latch_8_q));  // open: nQ
  not not_1 (not_1_out, gated_d_latch_2_q);
  not not_2 (not_2_out, gated_d_latch_6_q);
  not not_3 (not_3_out, gated_d_latch_5_q);
  not not_4 (not_4_out, gated_d_latch_8_q);
  not not_5 (not_5_out, gated_d_latch_6_q);
  not not_6 (not_6_out, gated_d_latch_8_q);
  and and_1 (and_1_out, gated_d_latch_1_q, not_1_out);
  and and_2 (and_2_out, and_1_out, nand_1_out);
  nand nand_1 (nand_1_out, gated_d_latch_3_q, gated_d_latch_4_q);
  nand nand_2 (nand_2_out, gated_d_latch_5_q, gated_d_latch_6_q);
  and and_3 (and_3_out, nand_2_out, nand_3_out);
  nand nand_3 (nand_3_out, gated_d_latch_7_q, gated_d_latch_8_q);
  and and_4 (and_4_out, gated_d_latch_5_q, not_2_out);
  and and_5 (and_5_out, and_4_out, nand_4_out);
  nand nand_4 (nand_4_out, gated_d_latch_7_q, gated_d_latch_8_q);
  and and_6 (and_6_out, not_3_out, gated_d_latch_6_q);
  and and_7 (and_7_out, and_6_out, nand_5_out);
  nand nand_5 (nand_5_out, gated_d_latch_7_q, gated_d_latch_8_q);
  and and_8 (and_8_out, gated_d_latch_5_q, gated_d_latch_6_q);
  and and_9 (and_9_out, and_8_out, nand_6_out);
  nand nand_6 (nand_6_out, gated_d_latch_7_q, gated_d_latch_8_q);
  nand nand_7 (nand_7_out, gated_d_latch_5_q, gated_d_latch_6_q);
  and and_10 (and_10_out, nand_7_out, and_11_out);
  and and_11 (and_11_out, gated_d_latch_7_q, not_4_out);
  and and_12 (and_12_out, gated_d_latch_5_q, not_5_out);
  and and_13 (and_13_out, and_12_out, and_14_out);
  and and_14 (and_14_out, gated_d_latch_7_q, not_6_out);
  and and_15 (out_10, and_3_out, and_2_out);
  and and_16 (out_20, and_5_out, and_2_out);
  and and_17 (out_34, and_7_out, and_2_out);
  and and_18 (out_35, and_9_out, and_2_out);
  and and_19 (out_39, and_10_out, and_2_out);
  and and_20 (out_51, and_13_out, and_2_out);
  not not_7 (not_7_out, gated_d_latch_1_q);
  and and_21 (and_21_out, not_7_out, gated_d_latch_2_q);
  nand nand_8 (nand_8_out, gated_d_latch_3_q, gated_d_latch_4_q);
  and and_22 (and_22_out, and_21_out, nand_8_out);
  and and_23 (out_11, and_3_out, and_22_out);
  and and_24 (out_21, and_5_out, and_22_out);
  and and_25 (out_36, and_9_out, and_22_out);
  and and_26 (out_40, and_10_out, and_22_out);
  and and_27 (out_52, and_13_out, and_22_out);
  and and_28 (and_28_out, gated_d_latch_1_q, gated_d_latch_2_q);
  nand nand_9 (nand_9_out, gated_d_latch_3_q, gated_d_latch_4_q);
  and and_29 (and_29_out, and_28_out, nand_9_out);
  and and_30 (out_12, and_3_out, and_29_out);
  and and_31 (out_22, and_5_out, and_29_out);
  and and_32 (out_37, and_9_out, and_29_out);
  and and_33 (out_41, and_10_out, and_29_out);
  and and_34 (out_53, and_13_out, and_29_out);
  not not_8 (not_8_out, gated_d_latch_4_q);
  nand nand_10 (nand_10_out, gated_d_latch_1_q, gated_d_latch_2_q);
  and and_35 (and_35_out, gated_d_latch_3_q, not_8_out);
  and and_36 (and_36_out, nand_10_out, and_35_out);
  and and_37 (out_13, and_3_out, and_36_out);
  and and_38 (out_23, and_5_out, and_36_out);
  and and_39 (out_38, and_9_out, and_36_out);
  and and_40 (out_42, and_10_out, and_36_out);
  and and_41 (out_54, and_13_out, and_36_out);
  not not_9 (not_9_out, gated_d_latch_2_q);
  not not_10 (not_10_out, gated_d_latch_4_q);
  and and_42 (and_42_out, gated_d_latch_1_q, not_9_out);
  and and_43 (and_43_out, gated_d_latch_3_q, not_10_out);
  and and_44 (and_44_out, and_42_out, and_43_out);
  and and_45 (out_14, and_3_out, and_44_out);
  and and_46 (out_24, and_5_out, and_44_out);
  and and_47 (out_43, and_10_out, and_44_out);
  and and_48 (out_55, and_13_out, and_44_out);
  not not_11 (not_11_out, gated_d_latch_1_q);
  and and_49 (and_49_out, not_11_out, gated_d_latch_2_q);
  and and_50 (and_50_out, gated_d_latch_3_q, not_12_out);
  not not_12 (not_12_out, gated_d_latch_4_q);
  and and_51 (and_51_out, and_49_out, and_50_out);
  and and_52 (out_15, and_3_out, and_51_out);
  and and_53 (out_25, and_5_out, and_51_out);
  and and_54 (out_44, and_10_out, and_51_out);
  and and_55 (out_56, and_13_out, and_51_out);
  and and_56 (and_56_out, gated_d_latch_1_q, gated_d_latch_2_q);
  and and_57 (and_57_out, gated_d_latch_3_q, not_13_out);
  not not_13 (not_13_out, gated_d_latch_4_q);
  and and_58 (and_58_out, and_56_out, and_57_out);
  and and_59 (out_16, and_3_out, and_58_out);
  and and_60 (out_26, and_5_out, and_58_out);
  and and_61 (out_45, and_10_out, and_58_out);
  and and_62 (out_57, and_13_out, and_58_out);
  not not_14 (not_14_out, gated_d_latch_3_q);
  and and_63 (and_63_out, not_14_out, gated_d_latch_4_q);
  nand nand_11 (nand_11_out, gated_d_latch_1_q, gated_d_latch_2_q);
  and and_64 (and_64_out, nand_11_out, and_63_out);
  and and_65 (out_17, and_3_out, and_64_out);
  and and_66 (out_27, and_5_out, and_64_out);
  and and_67 (out_46, and_10_out, and_64_out);
  and and_68 (out_58, and_13_out, and_64_out);
  and and_69 (and_69_out, gated_d_latch_1_q, not_15_out);
  not not_15 (not_15_out, gated_d_latch_2_q);
  not not_16 (not_16_out, gated_d_latch_3_q);
  and and_70 (and_70_out, not_16_out, gated_d_latch_4_q);
  and and_71 (and_71_out, and_69_out, and_70_out);
  and and_72 (out_18, and_3_out, and_71_out);
  and and_73 (out_28, and_5_out, and_71_out);
  and and_74 (out_47, and_10_out, and_71_out);
  and and_75 (out_59, and_13_out, and_71_out);
  not not_17 (not_17_out, gated_d_latch_1_q);
  and and_76 (and_76_out, not_17_out, gated_d_latch_2_q);
  not not_18 (not_18_out, gated_d_latch_3_q);
  and and_77 (and_77_out, not_18_out, gated_d_latch_4_q);
  and and_78 (and_78_out, and_76_out, and_77_out);
  and and_79 (out_19, and_3_out, and_78_out);
  and and_80 (out_29, and_5_out, and_78_out);
  and and_81 (out_48, and_10_out, and_78_out);
  and and_82 (out_60, and_13_out, and_78_out);
  and and_83 (and_83_out, gated_d_latch_1_q, gated_d_latch_2_q);
  not not_19 (not_19_out, gated_d_latch_3_q);
  and and_84 (and_84_out, not_19_out, gated_d_latch_4_q);
  and and_85 (and_85_out, and_83_out, and_84_out);
  and and_86 (out_30, and_5_out, and_85_out);
  and and_87 (out_49, and_10_out, and_85_out);
  and and_88 (out_61, and_13_out, and_85_out);
  and and_89 (and_89_out, gated_d_latch_3_q, gated_d_latch_4_q);
  nand nand_12 (nand_12_out, gated_d_latch_1_q, gated_d_latch_2_q);
  and and_90 (and_90_out, nand_12_out, and_89_out);
  and and_91 (out_31, and_5_out, and_90_out);
  and and_92 (out_50, and_10_out, and_90_out);
  and and_93 (out_62, and_13_out, and_90_out);
  and and_94 (and_94_out, gated_d_latch_1_q, not_20_out);
  not not_20 (not_20_out, gated_d_latch_2_q);
  and and_95 (and_95_out, gated_d_latch_3_q, gated_d_latch_4_q);
  and and_96 (and_96_out, and_94_out, and_95_out);
  and and_97 (out_32, and_5_out, and_96_out);
  not not_21 (not_21_out, gated_d_latch_1_q);
  and and_98 (and_98_out, not_21_out, gated_d_latch_2_q);
  and and_99 (and_99_out, gated_d_latch_3_q, gated_d_latch_4_q);
  and and_100 (and_100_out, and_98_out, and_99_out);
  and and_101 (out_33, and_5_out, and_100_out);

  // Notes on the sheet:
  //   add
  //   and
  //   lui
  //   slt
  //   beq
  //   lb
  //   Arithmatic
  //   Logical
  //   Constant
  //   Manipulation
  //   Comparitors
  //   Branch/Jump
  //   Load/Store
  //   add
  //   and
  //   lui
  //   slt
  //   beq
  //   lb
  //   slti
  //   lbu
  //   addi
  //   andi
  //   bgez
  //   addi
  //   andi
  //   slti
  //   bgez
  //   lbu
  //   addu
  //   nand
  //   sltu
  //   bgezal
  //   lh
  //   addu
  //   nand
  //   sltu
  //   bgezal
  //   lh
  //   addiu
  //   nandi
  //   sltiu
  //   bgtz
  //   lhu
  //   addiu
  //   nandi
  //   sltiu
  //   bgtz
  //   lhu
  //   div
  //   or
  //   blez
  //   lw
  //   div
  //   or
  //   blez
  //   lw
  //   divu
  //   ori
  //   bltzal
  //   lwl
  //   divu
  //   ori
  //   bltzal
  //   lwl
  //   mult
  //   nor
  //   bltz
  //   lwr
  //   mult
  //   nor
  //   bltz
  //   lwr
  //   multu
  //   nori
  //   bne
  //   sb
  //   multu
  //   nori
  //   bne
  //   sb
  //   sub
  //   xor
  //   j
  //   sh
  //   sub
  //   xor
  //   j
  //   sh
  //   subu
  //   xori
  //   jal
  //   sw
  //   subu
  //   xori
  //   jal
  //   sw
  //   xnor
  //   jalr
  //   swl
  //   xnor
  //   jalr
  //   swl
  //   xnori
  //   jr
  //   swr
  //   xnori
  //   jr
  //   swr
  //   sll
  //   sll
  //   slr
  //   slr
endmodule

module Register_Array (
  input  RDest,
  input  RSrc1,
  input  RSrc2,
  input  Imm,
  input  Hi,
  input  Lo,
  input  D0,
  input  D1,
  input  D2,
  input  D3,
  input  D4,
  input  D5,
  input  D6,
  input  D7,
  input  D8,
  input  D9,
  input  D10,
  input  D11,
  input  D12,
  input  D13,
  input  D14,
  input  D15,
  input  D16,
  input  D17,
  input  D18,
  input  D19,
  input  D20,
  input  D21,
  input  D22,
  input  D23,
  input  D24,
  input  D25,
  input  D26,
  input  D27,
  input  D28,
  input  D29,
  input  D30,
  input  D31,
  input  RDest_2,
  input  RSrc1_2,
  input  RSrc2_2,
  input  Imm_2,
  input  Hi_2,
  input  Lo_2,
  output Q0,
  output Q1,
  output Q2,
  output Q3,
  output Q4,
  output Q5,
  output Q6,
  output Q7,
  output Q8,
  output Q9,
  output Q10,
  output Q11,
  output Q12,
  output Q13,
  output Q14,
  output Q15,
  output Q16,
  output Q17,
  output Q18,
  output Q19,
  output Q20,
  output Q21,
  output Q22,
  output Q23,
  output Q24,
  output Q25,
  output Q26,
  output Q27,
  output Q28,
  output Q29,
  output Q30,
  output Q31
);

  wire and_1_out, and_2_out, and_3_out, and_4_out, and_5_out, and_6_out, and_7_out, and_8_out, and_9_out,
       and_10_out, and_11_out, and_12_out, and_13_out, and_14_out, and_15_out, and_16_out, and_17_out,
       and_18_out, and_19_out, and_20_out, and_21_out, and_22_out, and_23_out, and_24_out, and_25_out,
       and_26_out, and_27_out, and_28_out, and_29_out, and_30_out, and_31_out, and_32_out, and_33_out,
       and_34_out, and_35_out, and_36_out, and_37_out, and_38_out, and_39_out, and_40_out, and_41_out,
       and_42_out, and_43_out, and_44_out, and_45_out, and_46_out, and_47_out, and_48_out, and_49_out,
       and_50_out, and_51_out, and_52_out, and_53_out, and_54_out, and_55_out, and_56_out, and_57_out,
       and_58_out, and_59_out, and_60_out, and_61_out, and_62_out, and_63_out, and_64_out, and_65_out,
       and_66_out, and_67_out, and_68_out, and_69_out, and_70_out, and_71_out, and_72_out, and_73_out,
       and_74_out, and_75_out, and_76_out, and_77_out, and_78_out, and_79_out, and_80_out, and_81_out,
       and_82_out, and_83_out, and_84_out, and_85_out, and_86_out, and_87_out, and_88_out, and_89_out,
       and_90_out, and_91_out, and_92_out, and_93_out, and_94_out, and_95_out, and_96_out, and_97_out,
       and_98_out, and_99_out, and_100_out, and_101_out, and_102_out, and_103_out, and_104_out, and_105_out,
       and_106_out, and_107_out, and_108_out, and_109_out, and_110_out, and_111_out, and_112_out,
       and_113_out, and_114_out, and_115_out, and_116_out, and_117_out, and_118_out, and_119_out,
       and_120_out, and_121_out, and_122_out, and_123_out, and_124_out, and_125_out, and_126_out,
       and_127_out, and_128_out, and_129_out, and_130_out, and_131_out, and_132_out, and_133_out,
       and_134_out, and_135_out, and_136_out, and_137_out, and_138_out, and_139_out, and_140_out,
       and_141_out, and_142_out, and_143_out, and_144_out, and_145_out, and_146_out, and_147_out,
       and_148_out, and_149_out, and_150_out, and_151_out, and_152_out, and_153_out, and_154_out,
       and_155_out, and_156_out, and_157_out, and_158_out, and_159_out, and_160_out, and_161_out,
       and_162_out, and_163_out, and_164_out, and_165_out, and_166_out, and_167_out, and_168_out,
       and_169_out, and_170_out, and_171_out, and_172_out, and_173_out, and_174_out, and_175_out,
       and_176_out, Hi_d19_2, Hi_d20_2, Hi_d21_2, Hi_d22_2, Hi_d23_2, Hi_d24_2, Hi_d25_2, Hi_d26_2, Hi_d27_2,
       Hi_d28_2, Hi_d29_2, Hi_d30_2, Hi_d31_2, Hi_q0, Hi_q1, Hi_q2, Hi_q3, Hi_q4, Hi_q5, Hi_q6, Hi_q7, Hi_q8,
       Hi_q9, Hi_q10, Hi_q11, Hi_q12, Hi_q13, Hi_q14, Hi_q15, Hi_q16, Hi_q17, Hi_q18, Imm_q0, Imm_q1, Imm_q2,
       Imm_q3, Imm_q4, Imm_q5, Imm_q6, Imm_q7, Imm_q8, Imm_q9, Imm_q10, Imm_q11, Imm_q12, Imm_q13, Imm_q14,
       Imm_q15, Lo_d19_2, Lo_d20_2, Lo_d21_2, Lo_d22_2, Lo_d23_2, Lo_d24_2, Lo_d25_2, Lo_d26_2, Lo_d27_2,
       Lo_d28_2, Lo_d29_2, Lo_d30_2, Lo_d31_2, Lo_q0, Lo_q1, Lo_q2, Lo_q3, Lo_q4, Lo_q5, Lo_q6, Lo_q7, Lo_q8,
       Lo_q9, Lo_q10, Lo_q11, Lo_q12, Lo_q13, Lo_q14, Lo_q15, Lo_q16, Lo_q17, Lo_q18, or_1_out, or_2_out,
       or_3_out, or_4_out, or_5_out, or_6_out, or_7_out, or_8_out, or_9_out, or_10_out, or_11_out, or_12_out,
       or_13_out, or_14_out, or_15_out, or_16_out, or_17_out, or_18_out, or_19_out, or_20_out, or_21_out,
       or_22_out, or_23_out, or_24_out, or_25_out, or_26_out, or_27_out, or_28_out, or_29_out, or_30_out,
       or_31_out, or_32_out, or_33_out, or_34_out, or_35_out, or_36_out, or_37_out, or_38_out, or_39_out,
       or_40_out, or_41_out, or_42_out, or_43_out, or_44_out, or_45_out, or_46_out, or_47_out, or_48_out,
       or_49_out, or_50_out, or_51_out, or_52_out, or_53_out, or_54_out, or_55_out, or_56_out, or_57_out,
       or_58_out, or_59_out, or_60_out, or_61_out, or_62_out, or_63_out, or_64_out, or_65_out, or_66_out,
       or_67_out, or_68_out, or_69_out, or_70_out, or_71_out, or_72_out, or_73_out, or_74_out, or_75_out,
       or_76_out, or_77_out, or_78_out, or_79_out, or_80_out, or_81_out, or_82_out, or_83_out, or_84_out,
       or_85_out, or_86_out, or_87_out, or_88_out, or_89_out, or_90_out, or_91_out, or_92_out, or_93_out,
       or_94_out, or_95_out, or_96_out, or_97_out, or_98_out, or_99_out, or_100_out, or_101_out, or_102_out,
       or_103_out, or_104_out, or_105_out, or_106_out, or_107_out, or_108_out, or_109_out, or_110_out,
       or_111_out, or_112_out, RDest_d19_2, RDest_d20_2, RDest_d21_2, RDest_d22_2, RDest_d23_2, RDest_d24_2,
       RDest_d25_2, RDest_d26_2, RDest_d27_2, RDest_d28_2, RDest_d29_2, RDest_d30_2, RDest_d31_2, RDest_q0,
       RDest_q1, RDest_q2, RDest_q3, RDest_q4, RDest_q5, RDest_q6, RDest_q7, RDest_q8, RDest_q9, RDest_q10,
       RDest_q11, RDest_q12, RDest_q13, RDest_q14, RDest_q15, RDest_q16, RDest_q17, RDest_q18, RSrc1_d19_2,
       RSrc1_d20_2, RSrc1_d21_2, RSrc1_d22_2, RSrc1_d23_2, RSrc1_d24_2, RSrc1_d25_2, RSrc1_d26_2,
       RSrc1_d27_2, RSrc1_d28_2, RSrc1_d29_2, RSrc1_d30_2, RSrc1_d31_2, RSrc1_q0, RSrc1_q1, RSrc1_q2,
       RSrc1_q3, RSrc1_q4, RSrc1_q5, RSrc1_q6, RSrc1_q7, RSrc1_q8, RSrc1_q9, RSrc1_q10, RSrc1_q11, RSrc1_q12,
       RSrc1_q13, RSrc1_q14, RSrc1_q15, RSrc1_q16, RSrc1_q17, RSrc1_q18, RSrc2_d19_2, RSrc2_d20_2,
       RSrc2_d21_2, RSrc2_d22_2, RSrc2_d23_2, RSrc2_d24_2, RSrc2_d25_2, RSrc2_d26_2, RSrc2_d27_2,
       RSrc2_d28_2, RSrc2_d29_2, RSrc2_d30_2, RSrc2_d31_2, RSrc2_q0, RSrc2_q1, RSrc2_q2, RSrc2_q3, RSrc2_q4,
       RSrc2_q5, RSrc2_q6, RSrc2_q7, RSrc2_q8, RSrc2_q9, RSrc2_q10, RSrc2_q11, RSrc2_q12, RSrc2_q13,
       RSrc2_q14, RSrc2_q15, RSrc2_q16, RSrc2_q17, RSrc2_q18;

  _32_Bit_General_Register u_RDest (
    .E(RDest), .D0(D0), .Q0(RDest_q0), .D1(D1), .Q1(RDest_q1), .D2(D2), .Q2(RDest_q2), .D3(D3),
    .Q3(RDest_q3), .D4(D4), .Q4(RDest_q4), .D5(D5), .Q5(RDest_q5), .D6(D6), .Q6(RDest_q6), .D7(D7),
    .Q7(RDest_q7), .D8(D8), .Q8(RDest_q8), .D9(D9), .Q9(RDest_q9), .D10(D10), .Q10(RDest_q10), .D11(D11),
    .Q11(RDest_q11), .D12(D12), .Q12(RDest_q12), .D13(D13), .Q13(RDest_q13), .D14(D14), .Q14(RDest_q14),
    .D15(D15), .Q15(RDest_q15), .D16(D16), .Q16(RDest_q16), .D17(D17), .Q17(RDest_q17), .D18(D18),
    .Q18(RDest_q18), .D19(D19), .D19_2(RDest_d19_2), .D20(D20), .D20_2(RDest_d20_2), .D21(D21),
    .D21_2(RDest_d21_2), .D22(D22), .D22_2(RDest_d22_2), .D23(D23), .D23_2(RDest_d23_2), .D24(D24),
    .D24_2(RDest_d24_2), .D25(D25), .D25_2(RDest_d25_2), .D26(D26), .D26_2(RDest_d26_2), .D27(D27),
    .D27_2(RDest_d27_2), .D28(D28), .D28_2(RDest_d28_2), .D29(D29), .D29_2(RDest_d29_2), .D30(D30),
    .D30_2(RDest_d30_2), .D31(D31), .D31_2(RDest_d31_2));
  _32_Bit_General_Register u_RSrc1 (
    .E(RSrc1), .D0(D0), .Q0(RSrc1_q0), .D1(D1), .Q1(RSrc1_q1), .D2(D2), .Q2(RSrc1_q2), .D3(D3),
    .Q3(RSrc1_q3), .D4(D4), .Q4(RSrc1_q4), .D5(D5), .Q5(RSrc1_q5), .D6(D6), .Q6(RSrc1_q6), .D7(D7),
    .Q7(RSrc1_q7), .D8(D8), .Q8(RSrc1_q8), .D9(D9), .Q9(RSrc1_q9), .D10(D10), .Q10(RSrc1_q10), .D11(D11),
    .Q11(RSrc1_q11), .D12(D12), .Q12(RSrc1_q12), .D13(D13), .Q13(RSrc1_q13), .D14(D14), .Q14(RSrc1_q14),
    .D15(D15), .Q15(RSrc1_q15), .D16(D16), .Q16(RSrc1_q16), .D17(D17), .Q17(RSrc1_q17), .D18(D18),
    .Q18(RSrc1_q18), .D19(D19), .D19_2(RSrc1_d19_2), .D20(D20), .D20_2(RSrc1_d20_2), .D21(D21),
    .D21_2(RSrc1_d21_2), .D22(D22), .D22_2(RSrc1_d22_2), .D23(D23), .D23_2(RSrc1_d23_2), .D24(D24),
    .D24_2(RSrc1_d24_2), .D25(D25), .D25_2(RSrc1_d25_2), .D26(D26), .D26_2(RSrc1_d26_2), .D27(D27),
    .D27_2(RSrc1_d27_2), .D28(D28), .D28_2(RSrc1_d28_2), .D29(D29), .D29_2(RSrc1_d29_2), .D30(D30),
    .D30_2(RSrc1_d30_2), .D31(D31), .D31_2(RSrc1_d31_2));
  _32_Bit_General_Register u_RSrc2 (
    .E(RSrc2), .D0(D0), .Q0(RSrc2_q0), .D1(D1), .Q1(RSrc2_q1), .D2(D2), .Q2(RSrc2_q2), .D3(D3),
    .Q3(RSrc2_q3), .D4(D4), .Q4(RSrc2_q4), .D5(D5), .Q5(RSrc2_q5), .D6(D6), .Q6(RSrc2_q6), .D7(D7),
    .Q7(RSrc2_q7), .D8(D8), .Q8(RSrc2_q8), .D9(D9), .Q9(RSrc2_q9), .D10(D10), .Q10(RSrc2_q10), .D11(D11),
    .Q11(RSrc2_q11), .D12(D12), .Q12(RSrc2_q12), .D13(D13), .Q13(RSrc2_q13), .D14(D14), .Q14(RSrc2_q14),
    .D15(D15), .Q15(RSrc2_q15), .D16(D16), .Q16(RSrc2_q16), .D17(D17), .Q17(RSrc2_q17), .D18(D18),
    .Q18(RSrc2_q18), .D19(D19), .D19_2(RSrc2_d19_2), .D20(D20), .D20_2(RSrc2_d20_2), .D21(D21),
    .D21_2(RSrc2_d21_2), .D22(D22), .D22_2(RSrc2_d22_2), .D23(D23), .D23_2(RSrc2_d23_2), .D24(D24),
    .D24_2(RSrc2_d24_2), .D25(D25), .D25_2(RSrc2_d25_2), .D26(D26), .D26_2(RSrc2_d26_2), .D27(D27),
    .D27_2(RSrc2_d27_2), .D28(D28), .D28_2(RSrc2_d28_2), .D29(D29), .D29_2(RSrc2_d29_2), .D30(D30),
    .D30_2(RSrc2_d30_2), .D31(D31), .D31_2(RSrc2_d31_2));
  and and_1 (and_1_out, RDest_q0, RDest_2);
  and and_2 (and_2_out, RDest_q1, RDest_2);
  and and_3 (and_3_out, RDest_q2, RDest_2);
  and and_4 (and_4_out, RDest_q3, RDest_2);
  and and_5 (and_5_out, RDest_q4, RDest_2);
  and and_6 (and_6_out, RDest_q5, RDest_2);
  and and_7 (and_7_out, RDest_q6, RDest_2);
  and and_8 (and_8_out, RDest_q7, RDest_2);
  and and_9 (and_9_out, RDest_q8, RDest_2);
  and and_10 (and_10_out, RDest_q9, RDest_2);
  and and_11 (and_11_out, RDest_q10, RDest_2);
  and and_12 (and_12_out, RDest_q11, RDest_2);
  and and_13 (and_13_out, RDest_q12, RDest_2);
  and and_14 (and_14_out, RDest_q13, RDest_2);
  and and_15 (and_15_out, RDest_q14, RDest_2);
  and and_16 (and_16_out, RDest_q15, RDest_2);
  and and_17 (and_17_out, RDest_q16, RDest_2);
  and and_18 (and_18_out, RDest_q17, RDest_2);
  and and_19 (and_19_out, RDest_q18, RDest_2);
  and and_20 (and_20_out, RDest_d19_2, RDest_2);
  and and_21 (and_21_out, RDest_d20_2, RDest_2);
  and and_22 (and_22_out, RDest_d21_2, RDest_2);
  and and_23 (and_23_out, RDest_d22_2, RDest_2);
  and and_24 (and_24_out, RDest_d23_2, RDest_2);
  and and_25 (and_25_out, RDest_d24_2, RDest_2);
  and and_26 (and_26_out, RDest_d25_2, RDest_2);
  and and_27 (and_27_out, RDest_d26_2, RDest_2);
  and and_28 (and_28_out, RDest_d27_2, RDest_2);
  and and_29 (and_29_out, RDest_d28_2, RDest_2);
  and and_30 (and_30_out, RDest_d29_2, RDest_2);
  and and_31 (and_31_out, RDest_d30_2, RDest_2);
  and and_32 (and_32_out, RDest_d31_2, RDest_2);
  and and_33 (and_33_out, RSrc1_q0, RSrc1_2);
  and and_34 (and_34_out, RSrc1_q1, RSrc1_2);
  and and_35 (and_35_out, RSrc1_q2, RSrc1_2);
  and and_36 (and_36_out, RSrc1_q3, RSrc1_2);
  and and_37 (and_37_out, RSrc1_q4, RSrc1_2);
  and and_38 (and_38_out, RSrc1_q5, RSrc1_2);
  and and_39 (and_39_out, RSrc1_q6, RSrc1_2);
  and and_40 (and_40_out, RSrc1_q7, RSrc1_2);
  and and_41 (and_41_out, RSrc1_q8, RSrc1_2);
  and and_42 (and_42_out, RSrc1_q9, RSrc1_2);
  and and_43 (and_43_out, RSrc1_q10, RSrc1_2);
  and and_44 (and_44_out, RSrc1_q11, RSrc1_2);
  and and_45 (and_45_out, RSrc1_q12, RSrc1_2);
  and and_46 (and_46_out, RSrc1_q13, RSrc1_2);
  and and_47 (and_47_out, RSrc1_q14, RSrc1_2);
  and and_48 (and_48_out, RSrc1_q15, RSrc1_2);
  and and_49 (and_49_out, RSrc1_q16, RSrc1_2);
  and and_50 (and_50_out, RSrc1_q17, RSrc1_2);
  and and_51 (and_51_out, RSrc1_q18, RSrc1_2);
  and and_52 (and_52_out, RSrc1_d19_2, RSrc1_2);
  and and_53 (and_53_out, RSrc1_d20_2, RSrc1_2);
  and and_54 (and_54_out, RSrc1_d21_2, RSrc1_2);
  and and_55 (and_55_out, RSrc1_d22_2, RSrc1_2);
  and and_56 (and_56_out, RSrc1_d23_2, RSrc1_2);
  and and_57 (and_57_out, RSrc1_d24_2, RSrc1_2);
  and and_58 (and_58_out, RSrc1_d25_2, RSrc1_2);
  and and_59 (and_59_out, RSrc1_d26_2, RSrc1_2);
  and and_60 (and_60_out, RSrc1_d27_2, RSrc1_2);
  and and_61 (and_61_out, RSrc1_d28_2, RSrc1_2);
  and and_62 (and_62_out, RSrc1_d29_2, RSrc1_2);
  and and_63 (and_63_out, RSrc1_d30_2, RSrc1_2);
  and and_64 (and_64_out, RSrc1_d31_2, RSrc1_2);
  and and_65 (and_65_out, RSrc2_q0, RSrc2_2);
  and and_66 (and_66_out, RSrc2_q1, RSrc2_2);
  and and_67 (and_67_out, RSrc2_q2, RSrc2_2);
  and and_68 (and_68_out, RSrc2_q3, RSrc2_2);
  and and_69 (and_69_out, RSrc2_q4, RSrc2_2);
  and and_70 (and_70_out, RSrc2_q5, RSrc2_2);
  and and_71 (and_71_out, RSrc2_q6, RSrc2_2);
  and and_72 (and_72_out, RSrc2_q7, RSrc2_2);
  and and_73 (and_73_out, RSrc2_q8, RSrc2_2);
  and and_74 (and_74_out, RSrc2_q9, RSrc2_2);
  and and_75 (and_75_out, RSrc2_q10, RSrc2_2);
  and and_76 (and_76_out, RSrc2_q11, RSrc2_2);
  and and_77 (and_77_out, RSrc2_q12, RSrc2_2);
  and and_78 (and_78_out, RSrc2_q13, RSrc2_2);
  and and_79 (and_79_out, RSrc2_q14, RSrc2_2);
  and and_80 (and_80_out, RSrc2_q15, RSrc2_2);
  and and_81 (and_81_out, RSrc2_q16, RSrc2_2);
  and and_82 (and_82_out, RSrc2_q17, RSrc2_2);
  and and_83 (and_83_out, RSrc2_q18, RSrc2_2);
  and and_84 (and_84_out, RSrc2_d19_2, RSrc2_2);
  and and_85 (and_85_out, RSrc2_d20_2, RSrc2_2);
  and and_86 (and_86_out, RSrc2_d21_2, RSrc2_2);
  and and_87 (and_87_out, RSrc2_d22_2, RSrc2_2);
  and and_88 (and_88_out, RSrc2_d23_2, RSrc2_2);
  and and_89 (and_89_out, RSrc2_d24_2, RSrc2_2);
  and and_90 (and_90_out, RSrc2_d25_2, RSrc2_2);
  and and_91 (and_91_out, RSrc2_d26_2, RSrc2_2);
  and and_92 (and_92_out, RSrc2_d27_2, RSrc2_2);
  and and_93 (and_93_out, RSrc2_d28_2, RSrc2_2);
  and and_94 (and_94_out, RSrc2_d29_2, RSrc2_2);
  and and_95 (and_95_out, RSrc2_d30_2, RSrc2_2);
  and and_96 (and_96_out, RSrc2_d31_2, RSrc2_2);
  or or_1 (or_1_out, and_1_out, and_33_out);
  or or_2 (or_2_out, and_2_out, and_34_out);
  or or_3 (or_3_out, and_3_out, and_35_out);
  or or_4 (or_4_out, and_4_out, and_36_out);
  or or_5 (or_5_out, and_5_out, and_37_out);
  or or_6 (or_6_out, and_6_out, and_38_out);
  or or_7 (or_7_out, and_7_out, and_39_out);
  or or_8 (or_8_out, and_8_out, and_40_out);
  or or_9 (or_9_out, and_9_out, and_41_out);
  or or_10 (or_10_out, and_10_out, and_42_out);
  or or_11 (or_11_out, and_11_out, and_43_out);
  or or_12 (or_12_out, and_12_out, and_44_out);
  or or_13 (or_13_out, and_13_out, and_45_out);
  or or_14 (or_14_out, and_14_out, and_46_out);
  or or_15 (or_15_out, and_15_out, and_47_out);
  or or_16 (or_16_out, and_16_out, and_48_out);
  or or_17 (or_17_out, and_17_out, and_49_out);
  or or_18 (or_18_out, and_18_out, and_50_out);
  or or_19 (or_19_out, and_19_out, and_51_out);
  or or_20 (or_20_out, and_20_out, and_52_out);
  or or_21 (or_21_out, and_21_out, and_53_out);
  or or_22 (or_22_out, and_22_out, and_54_out);
  or or_23 (or_23_out, and_23_out, and_55_out);
  or or_24 (or_24_out, and_24_out, and_56_out);
  or or_25 (or_25_out, and_25_out, and_57_out);
  or or_26 (or_26_out, and_26_out, and_58_out);
  or or_27 (or_27_out, and_27_out, and_59_out);
  or or_28 (or_28_out, and_28_out, and_60_out);
  or or_29 (or_29_out, and_29_out, and_61_out);
  or or_30 (or_30_out, and_30_out, and_62_out);
  or or_31 (or_31_out, and_31_out, and_63_out);
  or or_32 (or_32_out, and_32_out, and_64_out);
  or or_33 (or_33_out, or_1_out, and_65_out);
  or or_34 (or_34_out, or_2_out, and_66_out);
  or or_35 (or_35_out, or_3_out, and_67_out);
  or or_36 (or_36_out, or_4_out, and_68_out);
  or or_37 (or_37_out, or_5_out, and_69_out);
  or or_38 (or_38_out, or_6_out, and_70_out);
  or or_39 (or_39_out, or_7_out, and_71_out);
  or or_40 (or_40_out, or_8_out, and_72_out);
  or or_41 (or_41_out, or_9_out, and_73_out);
  or or_42 (or_42_out, or_10_out, and_74_out);
  or or_43 (or_43_out, or_11_out, and_75_out);
  or or_44 (or_44_out, or_12_out, and_76_out);
  or or_45 (or_45_out, or_13_out, and_77_out);
  or or_46 (or_46_out, or_14_out, and_78_out);
  or or_47 (or_47_out, or_15_out, and_79_out);
  or or_48 (or_48_out, or_16_out, and_80_out);
  or or_49 (or_49_out, or_17_out, and_81_out);
  or or_50 (or_50_out, or_18_out, and_82_out);
  or or_51 (or_51_out, or_19_out, and_83_out);
  or or_52 (or_52_out, or_20_out, and_84_out);
  or or_53 (or_53_out, or_21_out, and_85_out);
  or or_54 (or_54_out, or_22_out, and_86_out);
  or or_55 (or_55_out, or_23_out, and_87_out);
  or or_56 (or_56_out, or_24_out, and_88_out);
  or or_57 (or_57_out, or_25_out, and_89_out);
  or or_58 (or_58_out, or_26_out, and_90_out);
  or or_59 (or_59_out, or_27_out, and_91_out);
  or or_60 (or_60_out, or_28_out, and_92_out);
  or or_61 (or_61_out, or_29_out, and_93_out);
  or or_62 (or_62_out, or_30_out, and_94_out);
  or or_63 (or_63_out, or_31_out, and_95_out);
  or or_64 (or_64_out, or_32_out, and_96_out);
  _16_Bit_General_Register u_Imm (
    .E(Imm), .D0(D0), .Q0(Imm_q0), .D1(D1), .Q1(Imm_q1), .D2(D2), .Q2(Imm_q2), .D3(D3), .Q3(Imm_q3), .D4(D4),
    .Q4(Imm_q4), .D5(D5), .Q5(Imm_q5), .D6(D6), .Q6(Imm_q6), .D7(D7), .Q7(Imm_q7), .D8(D8), .Q8(Imm_q8),
    .D9(D9), .Q9(Imm_q9), .D10(D10), .Q10(Imm_q10), .D11(D11), .Q11(Imm_q11), .D12(D12), .Q12(Imm_q12),
    .D13(D13), .Q13(Imm_q13), .D14(D14), .Q14(Imm_q14), .D15(D15), .Q15(Imm_q15));
  _32_Bit_General_Register u_Hi (
    .E(Hi), .D0(D0), .Q0(Hi_q0), .D1(D1), .Q1(Hi_q1), .D2(D2), .Q2(Hi_q2), .D3(D3), .Q3(Hi_q3), .D4(D4),
    .Q4(Hi_q4), .D5(D5), .Q5(Hi_q5), .D6(D6), .Q6(Hi_q6), .D7(D7), .Q7(Hi_q7), .D8(D8), .Q8(Hi_q8), .D9(D9),
    .Q9(Hi_q9), .D10(D10), .Q10(Hi_q10), .D11(D11), .Q11(Hi_q11), .D12(D12), .Q12(Hi_q12), .D13(D13),
    .Q13(Hi_q13), .D14(D14), .Q14(Hi_q14), .D15(D15), .Q15(Hi_q15), .D16(D16), .Q16(Hi_q16), .D17(D17),
    .Q17(Hi_q17), .D18(D18), .Q18(Hi_q18), .D19(D19), .D19_2(Hi_d19_2), .D20(D20), .D20_2(Hi_d20_2),
    .D21(D21), .D21_2(Hi_d21_2), .D22(D22), .D22_2(Hi_d22_2), .D23(D23), .D23_2(Hi_d23_2), .D24(D24),
    .D24_2(Hi_d24_2), .D25(D25), .D25_2(Hi_d25_2), .D26(D26), .D26_2(Hi_d26_2), .D27(D27), .D27_2(Hi_d27_2),
    .D28(D28), .D28_2(Hi_d28_2), .D29(D29), .D29_2(Hi_d29_2), .D30(D30), .D30_2(Hi_d30_2), .D31(D31),
    .D31_2(Hi_d31_2));
  _32_Bit_General_Register u_Lo (
    .E(Lo), .D0(D0), .Q0(Lo_q0), .D1(D1), .Q1(Lo_q1), .D2(D2), .Q2(Lo_q2), .D3(D3), .Q3(Lo_q3), .D4(D4),
    .Q4(Lo_q4), .D5(D5), .Q5(Lo_q5), .D6(D6), .Q6(Lo_q6), .D7(D7), .Q7(Lo_q7), .D8(D8), .Q8(Lo_q8), .D9(D9),
    .Q9(Lo_q9), .D10(D10), .Q10(Lo_q10), .D11(D11), .Q11(Lo_q11), .D12(D12), .Q12(Lo_q12), .D13(D13),
    .Q13(Lo_q13), .D14(D14), .Q14(Lo_q14), .D15(D15), .Q15(Lo_q15), .D16(D16), .Q16(Lo_q16), .D17(D17),
    .Q17(Lo_q17), .D18(D18), .Q18(Lo_q18), .D19(D19), .D19_2(Lo_d19_2), .D20(D20), .D20_2(Lo_d20_2),
    .D21(D21), .D21_2(Lo_d21_2), .D22(D22), .D22_2(Lo_d22_2), .D23(D23), .D23_2(Lo_d23_2), .D24(D24),
    .D24_2(Lo_d24_2), .D25(D25), .D25_2(Lo_d25_2), .D26(D26), .D26_2(Lo_d26_2), .D27(D27), .D27_2(Lo_d27_2),
    .D28(D28), .D28_2(Lo_d28_2), .D29(D29), .D29_2(Lo_d29_2), .D30(D30), .D30_2(Lo_d30_2), .D31(D31),
    .D31_2(Lo_d31_2));
  and and_97 (and_97_out, Imm_q0, Imm_2);
  and and_98 (and_98_out, Imm_q1, Imm_2);
  and and_99 (and_99_out, Imm_q2, Imm_2);
  and and_100 (and_100_out, Imm_q3, Imm_2);
  and and_101 (and_101_out, Imm_q4, Imm_2);
  and and_102 (and_102_out, Imm_q5, Imm_2);
  and and_103 (and_103_out, Imm_q6, Imm_2);
  and and_104 (and_104_out, Imm_q7, Imm_2);
  and and_105 (and_105_out, Imm_q8, Imm_2);
  and and_106 (and_106_out, Imm_q9, Imm_2);
  and and_107 (and_107_out, Imm_q10, Imm_2);
  and and_108 (and_108_out, Imm_q11, Imm_2);
  and and_109 (and_109_out, Imm_q12, Imm_2);
  and and_110 (and_110_out, Imm_q13, Imm_2);
  and and_111 (and_111_out, Imm_q14, Imm_2);
  and and_112 (and_112_out, Imm_q15, Imm_2);
  and and_113 (and_113_out, Hi_q0, Hi_2);
  and and_114 (and_114_out, Hi_q1, Hi_2);
  and and_115 (and_115_out, Hi_q2, Hi_2);
  and and_116 (and_116_out, Hi_q3, Hi_2);
  and and_117 (and_117_out, Hi_q4, Hi_2);
  and and_118 (and_118_out, Hi_q5, Hi_2);
  and and_119 (and_119_out, Hi_q6, Hi_2);
  and and_120 (and_120_out, Hi_q7, Hi_2);
  and and_121 (and_121_out, Hi_q8, Hi_2);
  and and_122 (and_122_out, Hi_q9, Hi_2);
  and and_123 (and_123_out, Hi_q10, Hi_2);
  and and_124 (and_124_out, Hi_q11, Hi_2);
  and and_125 (and_125_out, Hi_q12, Hi_2);
  and and_126 (and_126_out, Hi_q13, Hi_2);
  and and_127 (and_127_out, Hi_q14, Hi_2);
  and and_128 (and_128_out, Hi_q15, Hi_2);
  and and_129 (and_129_out, Hi_q16, Hi_2);
  and and_130 (and_130_out, Hi_q17, Hi_2);
  and and_131 (and_131_out, Hi_q18, Hi_2);
  and and_132 (and_132_out, Hi_d19_2, Hi_2);
  and and_133 (and_133_out, Hi_d20_2, Hi_2);
  and and_134 (and_134_out, Hi_d21_2, Hi_2);
  and and_135 (and_135_out, Hi_d22_2, Hi_2);
  and and_136 (and_136_out, Hi_d23_2, Hi_2);
  and and_137 (and_137_out, Hi_d24_2, Hi_2);
  and and_138 (and_138_out, Hi_d25_2, Hi_2);
  and and_139 (and_139_out, Hi_d26_2, Hi_2);
  and and_140 (and_140_out, Hi_d27_2, Hi_2);
  and and_141 (and_141_out, Hi_d28_2, Hi_2);
  and and_142 (and_142_out, Hi_d29_2, Hi_2);
  and and_143 (and_143_out, Hi_d30_2, Hi_2);
  and and_144 (and_144_out, Hi_d31_2, Hi_2);
  and and_145 (and_145_out, Lo_q0, Lo_2);
  and and_146 (and_146_out, Lo_q1, Lo_2);
  and and_147 (and_147_out, Lo_q2, Lo_2);
  and and_148 (and_148_out, Lo_q3, Lo_2);
  and and_149 (and_149_out, Lo_q4, Lo_2);
  and and_150 (and_150_out, Lo_q5, Lo_2);
  and and_151 (and_151_out, Lo_q6, Lo_2);
  and and_152 (and_152_out, Lo_q7, Lo_2);
  and and_153 (and_153_out, Lo_q8, Lo_2);
  and and_154 (and_154_out, Lo_q9, Lo_2);
  and and_155 (and_155_out, Lo_q10, Lo_2);
  and and_156 (and_156_out, Lo_q11, Lo_2);
  and and_157 (and_157_out, Lo_q12, Lo_2);
  and and_158 (and_158_out, Lo_q13, Lo_2);
  and and_159 (and_159_out, Lo_q14, Lo_2);
  and and_160 (and_160_out, Lo_q15, Lo_2);
  and and_161 (and_161_out, Lo_q16, Lo_2);
  and and_162 (and_162_out, Lo_q17, Lo_2);
  and and_163 (and_163_out, Lo_q18, Lo_2);
  and and_164 (and_164_out, Lo_d19_2, Lo_2);
  and and_165 (and_165_out, Lo_d20_2, Lo_2);
  and and_166 (and_166_out, Lo_d21_2, Lo_2);
  and and_167 (and_167_out, Lo_d22_2, Lo_2);
  and and_168 (and_168_out, Lo_d23_2, Lo_2);
  and and_169 (and_169_out, Lo_d24_2, Lo_2);
  and and_170 (and_170_out, Lo_d25_2, Lo_2);
  and and_171 (and_171_out, Lo_d26_2, Lo_2);
  and and_172 (and_172_out, Lo_d27_2, Lo_2);
  and and_173 (and_173_out, Lo_d28_2, Lo_2);
  and and_174 (and_174_out, Lo_d29_2, Lo_2);
  and and_175 (and_175_out, Lo_d30_2, Lo_2);
  and and_176 (and_176_out, Lo_d31_2, Lo_2);
  or or_65 (or_65_out, and_97_out, and_113_out);
  or or_66 (or_66_out, and_98_out, and_114_out);
  or or_67 (or_67_out, and_99_out, and_115_out);
  or or_68 (or_68_out, and_100_out, and_116_out);
  or or_69 (or_69_out, and_101_out, and_117_out);
  or or_70 (or_70_out, and_102_out, and_118_out);
  or or_71 (or_71_out, and_103_out, and_119_out);
  or or_72 (or_72_out, and_104_out, and_120_out);
  or or_73 (or_73_out, and_105_out, and_121_out);
  or or_74 (or_74_out, and_106_out, and_122_out);
  or or_75 (or_75_out, and_107_out, and_123_out);
  or or_76 (or_76_out, and_108_out, and_124_out);
  or or_77 (or_77_out, and_109_out, and_125_out);
  or or_78 (or_78_out, and_110_out, and_126_out);
  or or_79 (or_79_out, and_111_out, and_127_out);
  or or_80 (or_80_out, and_112_out, and_128_out);
  or or_81 (or_81_out, or_65_out, and_145_out);
  or or_82 (or_82_out, or_66_out, and_146_out);
  or or_83 (or_83_out, or_67_out, and_147_out);
  or or_84 (or_84_out, or_68_out, and_148_out);
  or or_85 (or_85_out, or_69_out, and_149_out);
  or or_86 (or_86_out, or_70_out, and_150_out);
  or or_87 (or_87_out, or_71_out, and_151_out);
  or or_88 (or_88_out, or_72_out, and_152_out);
  or or_89 (or_89_out, or_73_out, and_153_out);
  or or_90 (or_90_out, or_74_out, and_154_out);
  or or_91 (or_91_out, or_75_out, and_155_out);
  or or_92 (or_92_out, or_76_out, and_156_out);
  or or_93 (or_93_out, or_77_out, and_157_out);
  or or_94 (or_94_out, or_78_out, and_158_out);
  or or_95 (or_95_out, or_79_out, and_159_out);
  or or_96 (or_96_out, or_80_out, and_160_out);
  or or_97 (or_97_out, and_129_out, and_161_out);
  or or_98 (or_98_out, and_130_out, and_162_out);
  or or_99 (or_99_out, and_131_out, and_163_out);
  or or_100 (or_100_out, and_132_out, and_164_out);
  or or_101 (or_101_out, and_133_out, and_165_out);
  or or_102 (or_102_out, and_134_out, and_166_out);
  or or_103 (or_103_out, and_135_out, and_167_out);
  or or_104 (or_104_out, and_136_out, and_168_out);
  or or_105 (or_105_out, and_137_out, and_169_out);
  or or_106 (or_106_out, and_138_out, and_170_out);
  or or_107 (or_107_out, and_139_out, and_171_out);
  or or_108 (or_108_out, and_140_out, and_172_out);
  or or_109 (or_109_out, and_141_out, and_173_out);
  or or_110 (or_110_out, and_142_out, and_174_out);
  or or_111 (or_111_out, and_143_out, and_175_out);
  or or_112 (or_112_out, and_144_out, and_176_out);
  or or_113 (Q0, or_33_out, or_81_out);
  or or_114 (Q1, or_34_out, or_82_out);
  or or_115 (Q2, or_35_out, or_83_out);
  or or_116 (Q3, or_36_out, or_84_out);
  or or_117 (Q4, or_37_out, or_85_out);
  or or_118 (Q5, or_38_out, or_86_out);
  or or_119 (Q6, or_39_out, or_87_out);
  or or_120 (Q7, or_40_out, or_88_out);
  or or_121 (Q8, or_41_out, or_89_out);
  or or_122 (Q9, or_42_out, or_90_out);
  or or_123 (Q10, or_43_out, or_91_out);
  or or_124 (Q11, or_44_out, or_92_out);
  or or_125 (Q12, or_45_out, or_93_out);
  or or_126 (Q13, or_46_out, or_94_out);
  or or_127 (Q14, or_47_out, or_95_out);
  or or_128 (Q15, or_48_out, or_96_out);
  or or_129 (Q16, or_49_out, or_97_out);
  or or_130 (Q17, or_50_out, or_98_out);
  or or_131 (Q18, or_51_out, or_99_out);
  or or_132 (Q19, or_52_out, or_100_out);
  or or_133 (Q20, or_53_out, or_101_out);
  or or_134 (Q21, or_54_out, or_102_out);
  or or_135 (Q22, or_55_out, or_103_out);
  or or_136 (Q23, or_56_out, or_104_out);
  or or_137 (Q24, or_57_out, or_105_out);
  or or_138 (Q25, or_58_out, or_106_out);
  or or_139 (Q26, or_59_out, or_107_out);
  or or_140 (Q27, or_60_out, or_108_out);
  or or_141 (Q28, or_61_out, or_109_out);
  or or_142 (Q29, or_62_out, or_110_out);
  or or_143 (Q30, or_63_out, or_111_out);
  or or_144 (Q31, or_64_out, or_112_out);

  // Notes on the sheet:
  //   Input
  //   Write to Input Register
  //   Read from Output Register
  //   Output
endmodule

module Half_Adder (
  input  A,
  input  B,
  output Sum,
  output Carry
);

  xor xor_1 (Sum, A, B);
  and and_1 (Carry, B, A);
endmodule

module Full_Adder (
  input  A,
  input  B,
  input  C_in,
  output Sum,
  output C_out
);

  wire and_1_out, half_adder_1_carry, xor_1_out;

  Half_Adder half_adder_1 (.A(xor_1_out), .B(C_in), .Sum(Sum), .Carry(half_adder_1_carry));
  xor xor_1 (xor_1_out, A, B);
  and and_1 (and_1_out, A, B);
  or or_1 (C_out, half_adder_1_carry, and_1_out);
endmodule

module add (
  input  A0,
  input  B0,
  input  A1,
  input  B1,
  input  A2,
  input  B2,
  input  A3,
  input  B3,
  input  A4,
  input  B4,
  input  A5,
  input  B5,
  input  A6,
  input  B6,
  input  A7,
  input  B7,
  input  A8,
  input  B8,
  input  A9,
  input  B9,
  input  A10,
  input  B10,
  input  A11,
  input  B11,
  input  A12,
  input  B12,
  input  A13,
  input  B13,
  input  A14,
  input  B14,
  input  A15,
  input  B15,
  input  A16,
  input  B16,
  input  A17,
  input  B17,
  input  A18,
  input  B18,
  input  A19,
  input  B19,
  input  A20,
  input  B20,
  input  A21,
  input  B21,
  input  A22,
  input  B22,
  input  A23,
  input  B23,
  input  A24,
  input  B24,
  input  A25,
  input  B25,
  input  A26,
  input  B26,
  input  A27,
  input  B27,
  input  A28,
  input  B28,
  input  A29,
  input  B29,
  input  A30,
  input  B30,
  input  A31,
  input  B31,
  output _0,
  output _1,
  output _2,
  output _3,
  output _4,
  output _5,
  output _6,
  output _7,
  output _8,
  output _9,
  output _10,
  output _11,
  output _12,
  output _13,
  output _14,
  output _15,
  output _16,
  output _17,
  output _18,
  output _19,
  output _20,
  output _21,
  output _22,
  output _23,
  output _24,
  output _25,
  output _26,
  output _27,
  output _28,
  output _29,
  output _30,
  output _31,
  output Carry,
  output Overflow
);

  wire full_adder_1_c_out, full_adder_2_c_out, full_adder_3_c_out, full_adder_4_c_out, full_adder_5_c_out,
       full_adder_6_c_out, full_adder_7_c_out, full_adder_8_c_out, full_adder_9_c_out, full_adder_10_c_out,
       full_adder_11_c_out, full_adder_12_c_out, full_adder_13_c_out, full_adder_14_c_out,
       full_adder_15_c_out, full_adder_16_c_out, full_adder_17_c_out, full_adder_18_c_out,
       full_adder_19_c_out, full_adder_20_c_out, full_adder_21_c_out, full_adder_22_c_out,
       full_adder_23_c_out, full_adder_24_c_out, full_adder_25_c_out, full_adder_26_c_out,
       full_adder_27_c_out, full_adder_28_c_out, full_adder_29_c_out, full_adder_30_c_out, half_adder_1_carry;

  Half_Adder half_adder_1 (.A(A0), .B(B0), .Sum(_0), .Carry(half_adder_1_carry));
  Full_Adder full_adder_1 (.A(A1), .B(B1), .C_in(half_adder_1_carry), .Sum(_1), .C_out(full_adder_1_c_out));
  Full_Adder full_adder_2 (.A(A2), .B(B2), .C_in(full_adder_1_c_out), .Sum(_2), .C_out(full_adder_2_c_out));
  Full_Adder full_adder_3 (.A(A3), .B(B3), .C_in(full_adder_2_c_out), .Sum(_3), .C_out(full_adder_3_c_out));
  Full_Adder full_adder_4 (.A(A4), .B(B4), .C_in(full_adder_3_c_out), .Sum(_4), .C_out(full_adder_4_c_out));
  Full_Adder full_adder_5 (.A(A5), .B(B5), .C_in(full_adder_4_c_out), .Sum(_5), .C_out(full_adder_5_c_out));
  Full_Adder full_adder_6 (.A(A6), .B(B6), .C_in(full_adder_5_c_out), .Sum(_6), .C_out(full_adder_6_c_out));
  Full_Adder full_adder_7 (.A(A7), .B(B7), .C_in(full_adder_6_c_out), .Sum(_7), .C_out(full_adder_7_c_out));
  Full_Adder full_adder_8 (.A(A8), .B(B8), .C_in(full_adder_7_c_out), .Sum(_8), .C_out(full_adder_8_c_out));
  Full_Adder full_adder_9 (.A(A9), .B(B9), .C_in(full_adder_8_c_out), .Sum(_9), .C_out(full_adder_9_c_out));
  Full_Adder full_adder_10 (.A(A10), .B(B10), .C_in(full_adder_9_c_out), .Sum(_10), .C_out(full_adder_10_c_out));
  Full_Adder full_adder_11 (.A(A11), .B(B11), .C_in(full_adder_10_c_out), .Sum(_11), .C_out(full_adder_11_c_out));
  Full_Adder full_adder_12 (.A(A12), .B(B12), .C_in(full_adder_11_c_out), .Sum(_12), .C_out(full_adder_12_c_out));
  Full_Adder full_adder_13 (.A(A13), .B(B13), .C_in(full_adder_12_c_out), .Sum(_13), .C_out(full_adder_13_c_out));
  Full_Adder full_adder_14 (.A(A14), .B(B14), .C_in(full_adder_13_c_out), .Sum(_14), .C_out(full_adder_14_c_out));
  Full_Adder full_adder_15 (.A(A15), .B(B15), .C_in(full_adder_14_c_out), .Sum(_15), .C_out(full_adder_15_c_out));
  Full_Adder full_adder_16 (.A(A16), .B(B16), .C_in(full_adder_15_c_out), .Sum(_16), .C_out(full_adder_16_c_out));
  Full_Adder full_adder_17 (.A(A17), .B(B17), .C_in(full_adder_16_c_out), .Sum(_17), .C_out(full_adder_17_c_out));
  Full_Adder full_adder_18 (.A(A18), .B(B18), .C_in(full_adder_17_c_out), .Sum(_18), .C_out(full_adder_18_c_out));
  Full_Adder full_adder_19 (.A(A19), .B(B19), .C_in(full_adder_18_c_out), .Sum(_19), .C_out(full_adder_19_c_out));
  Full_Adder full_adder_20 (.A(A20), .B(B20), .C_in(full_adder_19_c_out), .Sum(_20), .C_out(full_adder_20_c_out));
  Full_Adder full_adder_21 (.A(A21), .B(B21), .C_in(full_adder_20_c_out), .Sum(_21), .C_out(full_adder_21_c_out));
  Full_Adder full_adder_22 (.A(A22), .B(B22), .C_in(full_adder_21_c_out), .Sum(_22), .C_out(full_adder_22_c_out));
  Full_Adder full_adder_23 (.A(A23), .B(B23), .C_in(full_adder_22_c_out), .Sum(_23), .C_out(full_adder_23_c_out));
  Full_Adder full_adder_24 (.A(A24), .B(B24), .C_in(full_adder_23_c_out), .Sum(_24), .C_out(full_adder_24_c_out));
  Full_Adder full_adder_25 (.A(A25), .B(B25), .C_in(full_adder_24_c_out), .Sum(_25), .C_out(full_adder_25_c_out));
  Full_Adder full_adder_26 (.A(A26), .B(B26), .C_in(full_adder_25_c_out), .Sum(_26), .C_out(full_adder_26_c_out));
  Full_Adder full_adder_27 (.A(A27), .B(B27), .C_in(full_adder_26_c_out), .Sum(_27), .C_out(full_adder_27_c_out));
  Full_Adder full_adder_28 (.A(A28), .B(B28), .C_in(full_adder_27_c_out), .Sum(_28), .C_out(full_adder_28_c_out));
  Full_Adder full_adder_29 (.A(A29), .B(B29), .C_in(full_adder_28_c_out), .Sum(_29), .C_out(full_adder_29_c_out));
  Full_Adder full_adder_30 (.A(A30), .B(B30), .C_in(full_adder_29_c_out), .Sum(_30), .C_out(full_adder_30_c_out));
  Full_Adder full_adder_31 (.A(A31), .B(B31), .C_in(full_adder_30_c_out), .Sum(_31), .C_out(Carry));
  xor xor_1 (Overflow, Carry, full_adder_30_c_out);
endmodule

module addi (
  input  A0,
  input  B0,
  input  A1,
  input  B1,
  input  A2,
  input  B2,
  input  A3,
  input  B3,
  input  A4,
  input  B4,
  input  A5,
  input  B5,
  input  A6,
  input  B6,
  input  A7,
  input  B7,
  input  A8,
  input  B8,
  input  A9,
  input  B9,
  input  A10,
  input  B10,
  input  A11,
  input  B11,
  input  A12,
  input  B12,
  input  A13,
  input  B13,
  input  A14,
  input  B14,
  input  A15,
  input  B15,
  input  A16,
  input  A17,
  input  A18,
  input  A19,
  input  A20,
  input  A21,
  input  A22,
  input  A23,
  input  A24,
  input  A25,
  input  A26,
  input  A27,
  input  A28,
  input  A29,
  input  A30,
  input  A31,
  output _0,
  output _1,
  output _2,
  output _3,
  output _4,
  output _5,
  output _6,
  output _7,
  output _8,
  output _9,
  output _10,
  output _11,
  output _12,
  output _13,
  output _14,
  output _15,
  output _16,
  output _17,
  output _18,
  output _19,
  output _20,
  output _21,
  output _22,
  output _23,
  output _24,
  output _25,
  output _26,
  output _27,
  output _28,
  output _29,
  output _30,
  output _31,
  output Carry,
  output Overflow
);

  wire full_adder_1_c_out, full_adder_2_c_out, full_adder_3_c_out, full_adder_4_c_out, full_adder_5_c_out,
       full_adder_6_c_out, full_adder_7_c_out, full_adder_8_c_out, full_adder_9_c_out, full_adder_10_c_out,
       full_adder_11_c_out, full_adder_12_c_out, full_adder_13_c_out, full_adder_14_c_out,
       full_adder_15_c_out, full_adder_16_c_out, full_adder_17_c_out, full_adder_18_c_out,
       full_adder_19_c_out, full_adder_20_c_out, full_adder_21_c_out, full_adder_22_c_out,
       full_adder_23_c_out, full_adder_24_c_out, full_adder_25_c_out, full_adder_26_c_out,
       full_adder_27_c_out, full_adder_28_c_out, full_adder_29_c_out, full_adder_30_c_out, half_adder_1_carry;

  Half_Adder half_adder_1 (.A(A0), .B(B0), .Sum(_0), .Carry(half_adder_1_carry));
  Full_Adder full_adder_1 (.A(A1), .B(B1), .C_in(half_adder_1_carry), .Sum(_1), .C_out(full_adder_1_c_out));
  Full_Adder full_adder_2 (.A(A2), .B(B2), .C_in(full_adder_1_c_out), .Sum(_2), .C_out(full_adder_2_c_out));
  Full_Adder full_adder_3 (.A(A3), .B(B3), .C_in(full_adder_2_c_out), .Sum(_3), .C_out(full_adder_3_c_out));
  Full_Adder full_adder_4 (.A(A4), .B(B4), .C_in(full_adder_3_c_out), .Sum(_4), .C_out(full_adder_4_c_out));
  Full_Adder full_adder_5 (.A(A5), .B(B5), .C_in(full_adder_4_c_out), .Sum(_5), .C_out(full_adder_5_c_out));
  Full_Adder full_adder_6 (.A(A6), .B(B6), .C_in(full_adder_5_c_out), .Sum(_6), .C_out(full_adder_6_c_out));
  Full_Adder full_adder_7 (.A(A7), .B(B7), .C_in(full_adder_6_c_out), .Sum(_7), .C_out(full_adder_7_c_out));
  Full_Adder full_adder_8 (.A(A8), .B(B8), .C_in(full_adder_7_c_out), .Sum(_8), .C_out(full_adder_8_c_out));
  Full_Adder full_adder_9 (.A(A9), .B(B9), .C_in(full_adder_8_c_out), .Sum(_9), .C_out(full_adder_9_c_out));
  Full_Adder full_adder_10 (.A(A10), .B(B10), .C_in(full_adder_9_c_out), .Sum(_10), .C_out(full_adder_10_c_out));
  Full_Adder full_adder_11 (.A(A11), .B(B11), .C_in(full_adder_10_c_out), .Sum(_11), .C_out(full_adder_11_c_out));
  Full_Adder full_adder_12 (.A(A12), .B(B12), .C_in(full_adder_11_c_out), .Sum(_12), .C_out(full_adder_12_c_out));
  Full_Adder full_adder_13 (.A(A13), .B(B13), .C_in(full_adder_12_c_out), .Sum(_13), .C_out(full_adder_13_c_out));
  Full_Adder full_adder_14 (.A(A14), .B(B14), .C_in(full_adder_13_c_out), .Sum(_14), .C_out(full_adder_14_c_out));
  Full_Adder full_adder_15 (.A(A15), .B(B15), .C_in(full_adder_14_c_out), .Sum(_15), .C_out(full_adder_15_c_out));
  Full_Adder full_adder_16 (.A(A16), .B(1'b0), .C_in(full_adder_15_c_out), .Sum(_16), .C_out(full_adder_16_c_out));
  Full_Adder full_adder_17 (.A(A17), .B(1'b0), .C_in(full_adder_16_c_out), .Sum(_17), .C_out(full_adder_17_c_out));
  Full_Adder full_adder_18 (.A(A18), .B(1'b0), .C_in(full_adder_17_c_out), .Sum(_18), .C_out(full_adder_18_c_out));
  Full_Adder full_adder_19 (.A(A19), .B(1'b0), .C_in(full_adder_18_c_out), .Sum(_19), .C_out(full_adder_19_c_out));
  Full_Adder full_adder_20 (.A(A20), .B(1'b0), .C_in(full_adder_19_c_out), .Sum(_20), .C_out(full_adder_20_c_out));
  Full_Adder full_adder_21 (.A(A21), .B(1'b0), .C_in(full_adder_20_c_out), .Sum(_21), .C_out(full_adder_21_c_out));
  Full_Adder full_adder_22 (.A(A22), .B(1'b0), .C_in(full_adder_21_c_out), .Sum(_22), .C_out(full_adder_22_c_out));
  Full_Adder full_adder_23 (.A(A23), .B(1'b0), .C_in(full_adder_22_c_out), .Sum(_23), .C_out(full_adder_23_c_out));
  Full_Adder full_adder_24 (.A(A24), .B(1'b0), .C_in(full_adder_23_c_out), .Sum(_24), .C_out(full_adder_24_c_out));
  Full_Adder full_adder_25 (.A(A25), .B(1'b0), .C_in(full_adder_24_c_out), .Sum(_25), .C_out(full_adder_25_c_out));
  Full_Adder full_adder_26 (.A(A26), .B(1'b0), .C_in(full_adder_25_c_out), .Sum(_26), .C_out(full_adder_26_c_out));
  Full_Adder full_adder_27 (.A(A27), .B(1'b0), .C_in(full_adder_26_c_out), .Sum(_27), .C_out(full_adder_27_c_out));
  Full_Adder full_adder_28 (.A(A28), .B(1'b0), .C_in(full_adder_27_c_out), .Sum(_28), .C_out(full_adder_28_c_out));
  Full_Adder full_adder_29 (.A(A29), .B(1'b0), .C_in(full_adder_28_c_out), .Sum(_29), .C_out(full_adder_29_c_out));
  Full_Adder full_adder_30 (.A(A30), .B(1'b0), .C_in(full_adder_29_c_out), .Sum(_30), .C_out(full_adder_30_c_out));
  Full_Adder full_adder_31 (.A(A31), .B(1'b0), .C_in(full_adder_30_c_out), .Sum(_31), .C_out(Carry));
  xor xor_1 (Overflow, Carry, full_adder_30_c_out);
endmodule

module addu (
  input  A0,
  input  B0,
  input  A1,
  input  B1,
  input  A2,
  input  B2,
  input  A3,
  input  B3,
  input  A4,
  input  B4,
  input  A5,
  input  B5,
  input  A6,
  input  B6,
  input  A7,
  input  B7,
  input  A8,
  input  B8,
  input  A9,
  input  B9,
  input  A10,
  input  B10,
  input  A11,
  input  B11,
  input  A12,
  input  B12,
  input  A13,
  input  B13,
  input  A14,
  input  B14,
  input  A15,
  input  B15,
  input  A16,
  input  B16,
  input  A17,
  input  B17,
  input  A18,
  input  B18,
  input  A19,
  input  B19,
  input  A20,
  input  B20,
  input  A21,
  input  B21,
  input  A22,
  input  B22,
  input  A23,
  input  B23,
  input  A24,
  input  B24,
  input  A25,
  input  B25,
  input  A26,
  input  B26,
  input  A27,
  input  B27,
  input  A28,
  input  B28,
  input  A29,
  input  B29,
  input  A30,
  input  B30,
  input  A31,
  input  B31,
  output _0,
  output _1,
  output _2,
  output _3,
  output _4,
  output _5,
  output _6,
  output _7,
  output _8,
  output _9,
  output _10,
  output _11,
  output _12,
  output _13,
  output _14,
  output _15,
  output _16,
  output _17,
  output _18,
  output _19,
  output _20,
  output _21,
  output _22,
  output _23,
  output _24,
  output _25,
  output _26,
  output _27,
  output _28,
  output _29,
  output _30,
  output _31,
  output Carry
);

  wire full_adder_1_c_out, full_adder_2_c_out, full_adder_3_c_out, full_adder_4_c_out, full_adder_5_c_out,
       full_adder_6_c_out, full_adder_7_c_out, full_adder_8_c_out, full_adder_9_c_out, full_adder_10_c_out,
       full_adder_11_c_out, full_adder_12_c_out, full_adder_13_c_out, full_adder_14_c_out,
       full_adder_15_c_out, full_adder_16_c_out, full_adder_17_c_out, full_adder_18_c_out,
       full_adder_19_c_out, full_adder_20_c_out, full_adder_21_c_out, full_adder_22_c_out,
       full_adder_23_c_out, full_adder_24_c_out, full_adder_25_c_out, full_adder_26_c_out,
       full_adder_27_c_out, full_adder_28_c_out, full_adder_29_c_out, full_adder_30_c_out, half_adder_1_carry;

  Half_Adder half_adder_1 (.A(A0), .B(B0), .Sum(_0), .Carry(half_adder_1_carry));
  Full_Adder full_adder_1 (.A(A1), .B(B1), .C_in(half_adder_1_carry), .Sum(_1), .C_out(full_adder_1_c_out));
  Full_Adder full_adder_2 (.A(A2), .B(B2), .C_in(full_adder_1_c_out), .Sum(_2), .C_out(full_adder_2_c_out));
  Full_Adder full_adder_3 (.A(A3), .B(B3), .C_in(full_adder_2_c_out), .Sum(_3), .C_out(full_adder_3_c_out));
  Full_Adder full_adder_4 (.A(A4), .B(B4), .C_in(full_adder_3_c_out), .Sum(_4), .C_out(full_adder_4_c_out));
  Full_Adder full_adder_5 (.A(A5), .B(B5), .C_in(full_adder_4_c_out), .Sum(_5), .C_out(full_adder_5_c_out));
  Full_Adder full_adder_6 (.A(A6), .B(B6), .C_in(full_adder_5_c_out), .Sum(_6), .C_out(full_adder_6_c_out));
  Full_Adder full_adder_7 (.A(A7), .B(B7), .C_in(full_adder_6_c_out), .Sum(_7), .C_out(full_adder_7_c_out));
  Full_Adder full_adder_8 (.A(A8), .B(B8), .C_in(full_adder_7_c_out), .Sum(_8), .C_out(full_adder_8_c_out));
  Full_Adder full_adder_9 (.A(A9), .B(B9), .C_in(full_adder_8_c_out), .Sum(_9), .C_out(full_adder_9_c_out));
  Full_Adder full_adder_10 (.A(A10), .B(B10), .C_in(full_adder_9_c_out), .Sum(_10), .C_out(full_adder_10_c_out));
  Full_Adder full_adder_11 (.A(A11), .B(B11), .C_in(full_adder_10_c_out), .Sum(_11), .C_out(full_adder_11_c_out));
  Full_Adder full_adder_12 (.A(A12), .B(B12), .C_in(full_adder_11_c_out), .Sum(_12), .C_out(full_adder_12_c_out));
  Full_Adder full_adder_13 (.A(A13), .B(B13), .C_in(full_adder_12_c_out), .Sum(_13), .C_out(full_adder_13_c_out));
  Full_Adder full_adder_14 (.A(A14), .B(B14), .C_in(full_adder_13_c_out), .Sum(_14), .C_out(full_adder_14_c_out));
  Full_Adder full_adder_15 (.A(A15), .B(B15), .C_in(full_adder_14_c_out), .Sum(_15), .C_out(full_adder_15_c_out));
  Full_Adder full_adder_16 (.A(A16), .B(B16), .C_in(full_adder_15_c_out), .Sum(_16), .C_out(full_adder_16_c_out));
  Full_Adder full_adder_17 (.A(A17), .B(B17), .C_in(full_adder_16_c_out), .Sum(_17), .C_out(full_adder_17_c_out));
  Full_Adder full_adder_18 (.A(A18), .B(B18), .C_in(full_adder_17_c_out), .Sum(_18), .C_out(full_adder_18_c_out));
  Full_Adder full_adder_19 (.A(A19), .B(B19), .C_in(full_adder_18_c_out), .Sum(_19), .C_out(full_adder_19_c_out));
  Full_Adder full_adder_20 (.A(A20), .B(B20), .C_in(full_adder_19_c_out), .Sum(_20), .C_out(full_adder_20_c_out));
  Full_Adder full_adder_21 (.A(A21), .B(B21), .C_in(full_adder_20_c_out), .Sum(_21), .C_out(full_adder_21_c_out));
  Full_Adder full_adder_22 (.A(A22), .B(B22), .C_in(full_adder_21_c_out), .Sum(_22), .C_out(full_adder_22_c_out));
  Full_Adder full_adder_23 (.A(A23), .B(B23), .C_in(full_adder_22_c_out), .Sum(_23), .C_out(full_adder_23_c_out));
  Full_Adder full_adder_24 (.A(A24), .B(B24), .C_in(full_adder_23_c_out), .Sum(_24), .C_out(full_adder_24_c_out));
  Full_Adder full_adder_25 (.A(A25), .B(B25), .C_in(full_adder_24_c_out), .Sum(_25), .C_out(full_adder_25_c_out));
  Full_Adder full_adder_26 (.A(A26), .B(B26), .C_in(full_adder_25_c_out), .Sum(_26), .C_out(full_adder_26_c_out));
  Full_Adder full_adder_27 (.A(A27), .B(B27), .C_in(full_adder_26_c_out), .Sum(_27), .C_out(full_adder_27_c_out));
  Full_Adder full_adder_28 (.A(A28), .B(B28), .C_in(full_adder_27_c_out), .Sum(_28), .C_out(full_adder_28_c_out));
  Full_Adder full_adder_29 (.A(A29), .B(B29), .C_in(full_adder_28_c_out), .Sum(_29), .C_out(full_adder_29_c_out));
  Full_Adder full_adder_30 (.A(A30), .B(B30), .C_in(full_adder_29_c_out), .Sum(_30), .C_out(full_adder_30_c_out));
  Full_Adder full_adder_31 (.A(A31), .B(B31), .C_in(full_adder_30_c_out), .Sum(_31), .C_out(Carry));
endmodule

module addiu (
  input  A0,
  input  B0,
  input  A1,
  input  B1,
  input  A2,
  input  B2,
  input  A3,
  input  B3,
  input  A4,
  input  B4,
  input  A5,
  input  B5,
  input  A6,
  input  B6,
  input  A7,
  input  B7,
  input  A8,
  input  B8,
  input  A9,
  input  B9,
  input  A10,
  input  B10,
  input  A11,
  input  B11,
  input  A12,
  input  B12,
  input  A13,
  input  B13,
  input  A14,
  input  B14,
  input  A15,
  input  B15,
  input  A16,
  input  A17,
  input  A18,
  input  A19,
  input  A20,
  input  A21,
  input  A22,
  input  A23,
  input  A24,
  input  A25,
  input  A26,
  input  A27,
  input  A28,
  input  A29,
  input  A30,
  input  A31,
  output _0,
  output _1,
  output _2,
  output _3,
  output _4,
  output _5,
  output _6,
  output _7,
  output _8,
  output _9,
  output _10,
  output _11,
  output _12,
  output _13,
  output _14,
  output _15,
  output _16,
  output _17,
  output _18,
  output _19,
  output _20,
  output _21,
  output _22,
  output _23,
  output _24,
  output _25,
  output _26,
  output _27,
  output _28,
  output _29,
  output _30,
  output _31,
  output Carry
);

  wire full_adder_1_c_out, full_adder_2_c_out, full_adder_3_c_out, full_adder_4_c_out, full_adder_5_c_out,
       full_adder_6_c_out, full_adder_7_c_out, full_adder_8_c_out, full_adder_9_c_out, full_adder_10_c_out,
       full_adder_11_c_out, full_adder_12_c_out, full_adder_13_c_out, full_adder_14_c_out,
       full_adder_15_c_out, full_adder_16_c_out, full_adder_17_c_out, full_adder_18_c_out,
       full_adder_19_c_out, full_adder_20_c_out, full_adder_21_c_out, full_adder_22_c_out,
       full_adder_23_c_out, full_adder_24_c_out, full_adder_25_c_out, full_adder_26_c_out,
       full_adder_27_c_out, full_adder_28_c_out, full_adder_29_c_out, full_adder_30_c_out, half_adder_1_carry;

  Half_Adder half_adder_1 (.A(A0), .B(B0), .Sum(_0), .Carry(half_adder_1_carry));
  Full_Adder full_adder_1 (.A(A1), .B(B1), .C_in(half_adder_1_carry), .Sum(_1), .C_out(full_adder_1_c_out));
  Full_Adder full_adder_2 (.A(A2), .B(B2), .C_in(full_adder_1_c_out), .Sum(_2), .C_out(full_adder_2_c_out));
  Full_Adder full_adder_3 (.A(A3), .B(B3), .C_in(full_adder_2_c_out), .Sum(_3), .C_out(full_adder_3_c_out));
  Full_Adder full_adder_4 (.A(A4), .B(B4), .C_in(full_adder_3_c_out), .Sum(_4), .C_out(full_adder_4_c_out));
  Full_Adder full_adder_5 (.A(A5), .B(B5), .C_in(full_adder_4_c_out), .Sum(_5), .C_out(full_adder_5_c_out));
  Full_Adder full_adder_6 (.A(A6), .B(B6), .C_in(full_adder_5_c_out), .Sum(_6), .C_out(full_adder_6_c_out));
  Full_Adder full_adder_7 (.A(A7), .B(B7), .C_in(full_adder_6_c_out), .Sum(_7), .C_out(full_adder_7_c_out));
  Full_Adder full_adder_8 (.A(A8), .B(B8), .C_in(full_adder_7_c_out), .Sum(_8), .C_out(full_adder_8_c_out));
  Full_Adder full_adder_9 (.A(A9), .B(B9), .C_in(full_adder_8_c_out), .Sum(_9), .C_out(full_adder_9_c_out));
  Full_Adder full_adder_10 (.A(A10), .B(B10), .C_in(full_adder_9_c_out), .Sum(_10), .C_out(full_adder_10_c_out));
  Full_Adder full_adder_11 (.A(A11), .B(B11), .C_in(full_adder_10_c_out), .Sum(_11), .C_out(full_adder_11_c_out));
  Full_Adder full_adder_12 (.A(A12), .B(B12), .C_in(full_adder_11_c_out), .Sum(_12), .C_out(full_adder_12_c_out));
  Full_Adder full_adder_13 (.A(A13), .B(B13), .C_in(full_adder_12_c_out), .Sum(_13), .C_out(full_adder_13_c_out));
  Full_Adder full_adder_14 (.A(A14), .B(B14), .C_in(full_adder_13_c_out), .Sum(_14), .C_out(full_adder_14_c_out));
  Full_Adder full_adder_15 (.A(A15), .B(B15), .C_in(full_adder_14_c_out), .Sum(_15), .C_out(full_adder_15_c_out));
  Full_Adder full_adder_16 (.A(A16), .B(1'b0), .C_in(full_adder_15_c_out), .Sum(_16), .C_out(full_adder_16_c_out));
  Full_Adder full_adder_17 (.A(A17), .B(1'b0), .C_in(full_adder_16_c_out), .Sum(_17), .C_out(full_adder_17_c_out));
  Full_Adder full_adder_18 (.A(A18), .B(1'b0), .C_in(full_adder_17_c_out), .Sum(_18), .C_out(full_adder_18_c_out));
  Full_Adder full_adder_19 (.A(A19), .B(1'b0), .C_in(full_adder_18_c_out), .Sum(_19), .C_out(full_adder_19_c_out));
  Full_Adder full_adder_20 (.A(A20), .B(1'b0), .C_in(full_adder_19_c_out), .Sum(_20), .C_out(full_adder_20_c_out));
  Full_Adder full_adder_21 (.A(A21), .B(1'b0), .C_in(full_adder_20_c_out), .Sum(_21), .C_out(full_adder_21_c_out));
  Full_Adder full_adder_22 (.A(A22), .B(1'b0), .C_in(full_adder_21_c_out), .Sum(_22), .C_out(full_adder_22_c_out));
  Full_Adder full_adder_23 (.A(A23), .B(1'b0), .C_in(full_adder_22_c_out), .Sum(_23), .C_out(full_adder_23_c_out));
  Full_Adder full_adder_24 (.A(A24), .B(1'b0), .C_in(full_adder_23_c_out), .Sum(_24), .C_out(full_adder_24_c_out));
  Full_Adder full_adder_25 (.A(A25), .B(1'b0), .C_in(full_adder_24_c_out), .Sum(_25), .C_out(full_adder_25_c_out));
  Full_Adder full_adder_26 (.A(A26), .B(1'b0), .C_in(full_adder_25_c_out), .Sum(_26), .C_out(full_adder_26_c_out));
  Full_Adder full_adder_27 (.A(A27), .B(1'b0), .C_in(full_adder_26_c_out), .Sum(_27), .C_out(full_adder_27_c_out));
  Full_Adder full_adder_28 (.A(A28), .B(1'b0), .C_in(full_adder_27_c_out), .Sum(_28), .C_out(full_adder_28_c_out));
  Full_Adder full_adder_29 (.A(A29), .B(1'b0), .C_in(full_adder_28_c_out), .Sum(_29), .C_out(full_adder_29_c_out));
  Full_Adder full_adder_30 (.A(A30), .B(1'b0), .C_in(full_adder_29_c_out), .Sum(_30), .C_out(full_adder_30_c_out));
  Full_Adder full_adder_31 (.A(A31), .B(1'b0), .C_in(full_adder_30_c_out), .Sum(_31), .C_out(Carry));
endmodule

module sub (
  input  A0,
  input  B0,
  input  A1,
  input  B1,
  input  A2,
  input  B2,
  input  A3,
  input  B3,
  input  A4,
  input  B4,
  input  A5,
  input  B5,
  input  A6,
  input  B6,
  input  A7,
  input  B7,
  input  A8,
  input  B8,
  input  A9,
  input  B9,
  input  A10,
  input  B10,
  input  A11,
  input  B11,
  input  A12,
  input  B12,
  input  A13,
  input  B13,
  input  A14,
  input  B14,
  input  A15,
  input  B15,
  input  A16,
  input  B16,
  input  A17,
  input  B17,
  input  A18,
  input  B18,
  input  A19,
  input  B19,
  input  A20,
  input  B20,
  input  A21,
  input  B21,
  input  A22,
  input  B22,
  input  A23,
  input  B23,
  input  A24,
  input  B24,
  input  A25,
  input  B25,
  input  A26,
  input  B26,
  input  A27,
  input  B27,
  input  A28,
  input  B28,
  input  A29,
  input  B29,
  input  A30,
  input  B30,
  input  A31,
  input  B31,
  output _0,
  output _1,
  output _2,
  output _3,
  output _4,
  output _5,
  output _6,
  output _7,
  output _8,
  output _9,
  output _10,
  output _11,
  output _12,
  output _13,
  output _14,
  output _15,
  output _16,
  output _17,
  output _18,
  output _19,
  output _20,
  output _21,
  output _22,
  output _23,
  output _24,
  output _25,
  output _26,
  output _27,
  output _28,
  output _29,
  output _30,
  output _31,
  output Overflow
);

  wire full_adder_1_c_out, full_adder_2_c_out, full_adder_3_c_out, full_adder_4_c_out, full_adder_5_c_out,
       full_adder_6_c_out, full_adder_7_c_out, full_adder_8_c_out, full_adder_9_c_out, full_adder_10_c_out,
       full_adder_11_c_out, full_adder_12_c_out, full_adder_13_c_out, full_adder_14_c_out,
       full_adder_15_c_out, full_adder_16_c_out, full_adder_17_c_out, full_adder_18_c_out,
       full_adder_19_c_out, full_adder_20_c_out, full_adder_21_c_out, full_adder_22_c_out,
       full_adder_23_c_out, full_adder_24_c_out, full_adder_25_c_out, full_adder_26_c_out,
       full_adder_27_c_out, full_adder_28_c_out, full_adder_29_c_out, full_adder_30_c_out,
       full_adder_31_c_out, full_adder_32_c_out, not_1_out, not_2_out, not_3_out, not_4_out, not_5_out,
       not_6_out, not_7_out, not_8_out, not_9_out, not_10_out, not_11_out, not_12_out, not_13_out,
       not_14_out, not_15_out, not_16_out, not_17_out, not_18_out, not_19_out, not_20_out, not_21_out,
       not_22_out, not_23_out, not_24_out, not_25_out, not_26_out, not_27_out, not_28_out, not_29_out,
       not_30_out, not_31_out, not_32_out;

  Full_Adder full_adder_1 (.A(A0), .B(not_1_out), .C_in(1'b1), .Sum(_0), .C_out(full_adder_1_c_out));
  not not_1 (not_1_out, B0);
  not not_2 (not_2_out, B1);
  Full_Adder full_adder_2 (.A(A1), .B(not_2_out), .C_in(full_adder_1_c_out), .Sum(_1), .C_out(full_adder_2_c_out));
  Full_Adder full_adder_3 (.A(A2), .B(not_3_out), .C_in(full_adder_2_c_out), .Sum(_2), .C_out(full_adder_3_c_out));
  not not_3 (not_3_out, B2);
  Full_Adder full_adder_4 (.A(A3), .B(not_4_out), .C_in(full_adder_3_c_out), .Sum(_3), .C_out(full_adder_4_c_out));
  not not_4 (not_4_out, B3);
  Full_Adder full_adder_5 (.A(A4), .B(not_5_out), .C_in(full_adder_4_c_out), .Sum(_4), .C_out(full_adder_5_c_out));
  not not_5 (not_5_out, B4);
  Full_Adder full_adder_6 (.A(A5), .B(not_6_out), .C_in(full_adder_5_c_out), .Sum(_5), .C_out(full_adder_6_c_out));
  not not_6 (not_6_out, B5);
  Full_Adder full_adder_7 (.A(A6), .B(not_7_out), .C_in(full_adder_6_c_out), .Sum(_6), .C_out(full_adder_7_c_out));
  not not_7 (not_7_out, B6);
  Full_Adder full_adder_8 (.A(A7), .B(not_8_out), .C_in(full_adder_7_c_out), .Sum(_7), .C_out(full_adder_8_c_out));
  not not_8 (not_8_out, B7);
  Full_Adder full_adder_9 (.A(A8), .B(not_9_out), .C_in(full_adder_8_c_out), .Sum(_8), .C_out(full_adder_9_c_out));
  not not_9 (not_9_out, B8);
  not not_10 (not_10_out, B9);
  Full_Adder full_adder_10 (.A(A9), .B(not_10_out), .C_in(full_adder_9_c_out), .Sum(_9), .C_out(full_adder_10_c_out));
  Full_Adder full_adder_11 (
    .A(A10), .B(not_11_out), .C_in(full_adder_10_c_out), .Sum(_10), .C_out(full_adder_11_c_out));
  not not_11 (not_11_out, B10);
  Full_Adder full_adder_12 (
    .A(A11), .B(not_12_out), .C_in(full_adder_11_c_out), .Sum(_11), .C_out(full_adder_12_c_out));
  not not_12 (not_12_out, B11);
  Full_Adder full_adder_13 (
    .A(A12), .B(not_13_out), .C_in(full_adder_12_c_out), .Sum(_12), .C_out(full_adder_13_c_out));
  not not_13 (not_13_out, B12);
  Full_Adder full_adder_14 (
    .A(A13), .B(not_14_out), .C_in(full_adder_13_c_out), .Sum(_13), .C_out(full_adder_14_c_out));
  not not_14 (not_14_out, B13);
  Full_Adder full_adder_15 (
    .A(A14), .B(not_15_out), .C_in(full_adder_14_c_out), .Sum(_14), .C_out(full_adder_15_c_out));
  not not_15 (not_15_out, B14);
  Full_Adder full_adder_16 (
    .A(A15), .B(not_16_out), .C_in(full_adder_15_c_out), .Sum(_15), .C_out(full_adder_16_c_out));
  not not_16 (not_16_out, B15);
  Full_Adder full_adder_17 (
    .A(A16), .B(not_17_out), .C_in(full_adder_16_c_out), .Sum(_16), .C_out(full_adder_17_c_out));
  not not_17 (not_17_out, B16);
  not not_18 (not_18_out, B17);
  Full_Adder full_adder_18 (
    .A(A17), .B(not_18_out), .C_in(full_adder_17_c_out), .Sum(_17), .C_out(full_adder_18_c_out));
  Full_Adder full_adder_19 (
    .A(A18), .B(not_19_out), .C_in(full_adder_18_c_out), .Sum(_18), .C_out(full_adder_19_c_out));
  not not_19 (not_19_out, B18);
  Full_Adder full_adder_20 (
    .A(A19), .B(not_20_out), .C_in(full_adder_19_c_out), .Sum(_19), .C_out(full_adder_20_c_out));
  not not_20 (not_20_out, B19);
  Full_Adder full_adder_21 (
    .A(A20), .B(not_21_out), .C_in(full_adder_20_c_out), .Sum(_20), .C_out(full_adder_21_c_out));
  not not_21 (not_21_out, B20);
  Full_Adder full_adder_22 (
    .A(A21), .B(not_22_out), .C_in(full_adder_21_c_out), .Sum(_21), .C_out(full_adder_22_c_out));
  not not_22 (not_22_out, B21);
  Full_Adder full_adder_23 (
    .A(A22), .B(not_23_out), .C_in(full_adder_22_c_out), .Sum(_22), .C_out(full_adder_23_c_out));
  not not_23 (not_23_out, B22);
  Full_Adder full_adder_24 (
    .A(A23), .B(not_24_out), .C_in(full_adder_23_c_out), .Sum(_23), .C_out(full_adder_24_c_out));
  not not_24 (not_24_out, B23);
  Full_Adder full_adder_25 (
    .A(A24), .B(not_25_out), .C_in(full_adder_24_c_out), .Sum(_24), .C_out(full_adder_25_c_out));
  not not_25 (not_25_out, B24);
  not not_26 (not_26_out, B25);
  Full_Adder full_adder_26 (
    .A(A25), .B(not_26_out), .C_in(full_adder_25_c_out), .Sum(_25), .C_out(full_adder_26_c_out));
  Full_Adder full_adder_27 (
    .A(A26), .B(not_27_out), .C_in(full_adder_26_c_out), .Sum(_26), .C_out(full_adder_27_c_out));
  not not_27 (not_27_out, B26);
  Full_Adder full_adder_28 (
    .A(A27), .B(not_28_out), .C_in(full_adder_27_c_out), .Sum(_27), .C_out(full_adder_28_c_out));
  not not_28 (not_28_out, B27);
  Full_Adder full_adder_29 (
    .A(A28), .B(not_29_out), .C_in(full_adder_28_c_out), .Sum(_28), .C_out(full_adder_29_c_out));
  not not_29 (not_29_out, B28);
  Full_Adder full_adder_30 (
    .A(A29), .B(not_30_out), .C_in(full_adder_29_c_out), .Sum(_29), .C_out(full_adder_30_c_out));
  not not_30 (not_30_out, B29);
  Full_Adder full_adder_31 (
    .A(A30), .B(not_31_out), .C_in(full_adder_30_c_out), .Sum(_30), .C_out(full_adder_31_c_out));
  not not_31 (not_31_out, B30);
  Full_Adder full_adder_32 (
    .A(A31), .B(not_32_out), .C_in(full_adder_31_c_out), .Sum(_31), .C_out(full_adder_32_c_out));
  not not_32 (not_32_out, B31);
  xor xor_1 (Overflow, full_adder_32_c_out, full_adder_31_c_out);
endmodule

module subu (
  input  A0,
  input  B0,
  input  A1,
  input  B1,
  input  A2,
  input  B2,
  input  A3,
  input  B3,
  input  A4,
  input  B4,
  input  A5,
  input  B5,
  input  A6,
  input  B6,
  input  A7,
  input  B7,
  input  A8,
  input  B8,
  input  A9,
  input  B9,
  input  A10,
  input  B10,
  input  A11,
  input  B11,
  input  A12,
  input  B12,
  input  A13,
  input  B13,
  input  A14,
  input  B14,
  input  A15,
  input  B15,
  input  A16,
  input  B16,
  input  A17,
  input  B17,
  input  A18,
  input  B18,
  input  A19,
  input  B19,
  input  A20,
  input  B20,
  input  A21,
  input  B21,
  input  A22,
  input  B22,
  input  A23,
  input  B23,
  input  A24,
  input  B24,
  input  A25,
  input  B25,
  input  A26,
  input  B26,
  input  A27,
  input  B27,
  input  A28,
  input  B28,
  input  A29,
  input  B29,
  input  A30,
  input  B30,
  input  A31,
  input  B31,
  output _0,
  output _1,
  output _2,
  output _3,
  output _4,
  output _5,
  output _6,
  output _7,
  output _8,
  output _9,
  output _10,
  output _11,
  output _12,
  output _13,
  output _14,
  output _15,
  output _16,
  output _17,
  output _18,
  output _19,
  output _20,
  output _21,
  output _22,
  output _23,
  output _24,
  output _25,
  output _26,
  output _27,
  output _28,
  output _29,
  output _30,
  output _31
);

  wire full_adder_1_c_out, full_adder_2_c_out, full_adder_3_c_out, full_adder_4_c_out, full_adder_5_c_out,
       full_adder_6_c_out, full_adder_7_c_out, full_adder_8_c_out, full_adder_9_c_out, full_adder_10_c_out,
       full_adder_11_c_out, full_adder_12_c_out, full_adder_13_c_out, full_adder_14_c_out,
       full_adder_15_c_out, full_adder_16_c_out, full_adder_17_c_out, full_adder_18_c_out,
       full_adder_19_c_out, full_adder_20_c_out, full_adder_21_c_out, full_adder_22_c_out,
       full_adder_23_c_out, full_adder_24_c_out, full_adder_25_c_out, full_adder_26_c_out,
       full_adder_27_c_out, full_adder_28_c_out, full_adder_29_c_out, full_adder_30_c_out,
       full_adder_31_c_out, not_1_out, not_2_out, not_3_out, not_4_out, not_5_out, not_6_out, not_7_out,
       not_8_out, not_9_out, not_10_out, not_11_out, not_12_out, not_13_out, not_14_out, not_15_out,
       not_16_out, not_17_out, not_18_out, not_19_out, not_20_out, not_21_out, not_22_out, not_23_out,
       not_24_out, not_25_out, not_26_out, not_27_out, not_28_out, not_29_out, not_30_out, not_31_out,
       not_32_out;

  Full_Adder full_adder_1 (.A(A0), .B(not_1_out), .C_in(1'b1), .Sum(_0), .C_out(full_adder_1_c_out));
  not not_1 (not_1_out, B0);
  not not_2 (not_2_out, B1);
  Full_Adder full_adder_2 (.A(A1), .B(not_2_out), .C_in(full_adder_1_c_out), .Sum(_1), .C_out(full_adder_2_c_out));
  Full_Adder full_adder_3 (.A(A2), .B(not_3_out), .C_in(full_adder_2_c_out), .Sum(_2), .C_out(full_adder_3_c_out));
  not not_3 (not_3_out, B2);
  Full_Adder full_adder_4 (.A(A3), .B(not_4_out), .C_in(full_adder_3_c_out), .Sum(_3), .C_out(full_adder_4_c_out));
  not not_4 (not_4_out, B3);
  Full_Adder full_adder_5 (.A(A4), .B(not_5_out), .C_in(full_adder_4_c_out), .Sum(_4), .C_out(full_adder_5_c_out));
  not not_5 (not_5_out, B4);
  Full_Adder full_adder_6 (.A(A5), .B(not_6_out), .C_in(full_adder_5_c_out), .Sum(_5), .C_out(full_adder_6_c_out));
  not not_6 (not_6_out, B5);
  Full_Adder full_adder_7 (.A(A6), .B(not_7_out), .C_in(full_adder_6_c_out), .Sum(_6), .C_out(full_adder_7_c_out));
  not not_7 (not_7_out, B6);
  Full_Adder full_adder_8 (.A(A7), .B(not_8_out), .C_in(full_adder_7_c_out), .Sum(_7), .C_out(full_adder_8_c_out));
  not not_8 (not_8_out, B7);
  Full_Adder full_adder_9 (.A(A8), .B(not_9_out), .C_in(full_adder_8_c_out), .Sum(_8), .C_out(full_adder_9_c_out));
  not not_9 (not_9_out, B8);
  not not_10 (not_10_out, B9);
  Full_Adder full_adder_10 (.A(A9), .B(not_10_out), .C_in(full_adder_9_c_out), .Sum(_9), .C_out(full_adder_10_c_out));
  Full_Adder full_adder_11 (
    .A(A10), .B(not_11_out), .C_in(full_adder_10_c_out), .Sum(_10), .C_out(full_adder_11_c_out));
  not not_11 (not_11_out, B10);
  Full_Adder full_adder_12 (
    .A(A11), .B(not_12_out), .C_in(full_adder_11_c_out), .Sum(_11), .C_out(full_adder_12_c_out));
  not not_12 (not_12_out, B11);
  Full_Adder full_adder_13 (
    .A(A12), .B(not_13_out), .C_in(full_adder_12_c_out), .Sum(_12), .C_out(full_adder_13_c_out));
  not not_13 (not_13_out, B12);
  Full_Adder full_adder_14 (
    .A(A13), .B(not_14_out), .C_in(full_adder_13_c_out), .Sum(_13), .C_out(full_adder_14_c_out));
  not not_14 (not_14_out, B13);
  Full_Adder full_adder_15 (
    .A(A14), .B(not_15_out), .C_in(full_adder_14_c_out), .Sum(_14), .C_out(full_adder_15_c_out));
  not not_15 (not_15_out, B14);
  Full_Adder full_adder_16 (
    .A(A15), .B(not_16_out), .C_in(full_adder_15_c_out), .Sum(_15), .C_out(full_adder_16_c_out));
  not not_16 (not_16_out, B15);
  Full_Adder full_adder_17 (
    .A(A16), .B(not_17_out), .C_in(full_adder_16_c_out), .Sum(_16), .C_out(full_adder_17_c_out));
  not not_17 (not_17_out, B16);
  not not_18 (not_18_out, B17);
  Full_Adder full_adder_18 (
    .A(A17), .B(not_18_out), .C_in(full_adder_17_c_out), .Sum(_17), .C_out(full_adder_18_c_out));
  Full_Adder full_adder_19 (
    .A(A18), .B(not_19_out), .C_in(full_adder_18_c_out), .Sum(_18), .C_out(full_adder_19_c_out));
  not not_19 (not_19_out, B18);
  Full_Adder full_adder_20 (
    .A(A19), .B(not_20_out), .C_in(full_adder_19_c_out), .Sum(_19), .C_out(full_adder_20_c_out));
  not not_20 (not_20_out, B19);
  Full_Adder full_adder_21 (
    .A(A20), .B(not_21_out), .C_in(full_adder_20_c_out), .Sum(_20), .C_out(full_adder_21_c_out));
  not not_21 (not_21_out, B20);
  Full_Adder full_adder_22 (
    .A(A21), .B(not_22_out), .C_in(full_adder_21_c_out), .Sum(_21), .C_out(full_adder_22_c_out));
  not not_22 (not_22_out, B21);
  Full_Adder full_adder_23 (
    .A(A22), .B(not_23_out), .C_in(full_adder_22_c_out), .Sum(_22), .C_out(full_adder_23_c_out));
  not not_23 (not_23_out, B22);
  Full_Adder full_adder_24 (
    .A(A23), .B(not_24_out), .C_in(full_adder_23_c_out), .Sum(_23), .C_out(full_adder_24_c_out));
  not not_24 (not_24_out, B23);
  Full_Adder full_adder_25 (
    .A(A24), .B(not_25_out), .C_in(full_adder_24_c_out), .Sum(_24), .C_out(full_adder_25_c_out));
  not not_25 (not_25_out, B24);
  not not_26 (not_26_out, B25);
  Full_Adder full_adder_26 (
    .A(A25), .B(not_26_out), .C_in(full_adder_25_c_out), .Sum(_25), .C_out(full_adder_26_c_out));
  Full_Adder full_adder_27 (
    .A(A26), .B(not_27_out), .C_in(full_adder_26_c_out), .Sum(_26), .C_out(full_adder_27_c_out));
  not not_27 (not_27_out, B26);
  Full_Adder full_adder_28 (
    .A(A27), .B(not_28_out), .C_in(full_adder_27_c_out), .Sum(_27), .C_out(full_adder_28_c_out));
  not not_28 (not_28_out, B27);
  Full_Adder full_adder_29 (
    .A(A28), .B(not_29_out), .C_in(full_adder_28_c_out), .Sum(_28), .C_out(full_adder_29_c_out));
  not not_29 (not_29_out, B28);
  Full_Adder full_adder_30 (
    .A(A29), .B(not_30_out), .C_in(full_adder_29_c_out), .Sum(_29), .C_out(full_adder_30_c_out));
  not not_30 (not_30_out, B29);
  Full_Adder full_adder_31 (
    .A(A30), .B(not_31_out), .C_in(full_adder_30_c_out), .Sum(_30), .C_out(full_adder_31_c_out));
  not not_31 (not_31_out, B30);
  Full_Adder full_adder_32 (.A(A31), .B(not_32_out), .C_in(full_adder_31_c_out), .Sum(_31));  // open: C_out
  not not_32 (not_32_out, B31);
endmodule

module \and  (
  input  A0,
  input  B0,
  input  A1,
  input  B1,
  input  A2,
  input  B2,
  input  A3,
  input  B3,
  input  A4,
  input  B4,
  input  A5,
  input  B5,
  input  A6,
  input  B6,
  input  A7,
  input  B7,
  input  A8,
  input  B8,
  input  A9,
  input  B9,
  input  A10,
  input  B10,
  input  A11,
  input  B11,
  input  A12,
  input  B12,
  input  A13,
  input  B13,
  input  A14,
  input  B14,
  input  A15,
  input  B15,
  input  A16,
  input  B16,
  input  A17,
  input  B17,
  input  A18,
  input  B18,
  input  A19,
  input  B19,
  input  A20,
  input  B20,
  input  A21,
  input  B21,
  input  A22,
  input  B22,
  input  A23,
  input  B23,
  input  A24,
  input  B24,
  input  A25,
  input  B25,
  input  A26,
  input  B26,
  input  A27,
  input  B27,
  input  A28,
  input  B28,
  input  A29,
  input  B29,
  input  A30,
  input  B30,
  input  A31,
  input  B31,
  output _0,
  output _1,
  output _2,
  output _3,
  output _4,
  output _5,
  output _6,
  output _7,
  output _8,
  output _9,
  output _10,
  output _11,
  output _12,
  output _13,
  output _14,
  output _15,
  output _16,
  output _17,
  output _18,
  output _19,
  output _20,
  output _21,
  output _22,
  output _23,
  output _24,
  output _25,
  output _26,
  output _27,
  output _28,
  output _29,
  output _30,
  output _31
);

  and and_1 (_0, A0, B0);
  and and_2 (_1, A1, B1);
  and and_3 (_2, A2, B2);
  and and_4 (_3, A3, B3);
  and and_5 (_4, A4, B4);
  and and_6 (_5, A5, B5);
  and and_7 (_6, A6, B6);
  and and_8 (_7, A7, B7);
  and and_9 (_8, A8, B8);
  and and_10 (_9, A9, B9);
  and and_11 (_10, A10, B10);
  and and_12 (_11, A11, B11);
  and and_13 (_12, A12, B12);
  and and_14 (_13, A13, B13);
  and and_15 (_14, A14, B14);
  and and_16 (_15, A15, B15);
  and and_17 (_16, A16, B16);
  and and_18 (_17, A17, B17);
  and and_19 (_18, A18, B18);
  and and_20 (_19, A19, B19);
  and and_21 (_20, A20, B20);
  and and_22 (_21, A21, B21);
  and and_23 (_22, A22, B22);
  and and_24 (_23, A23, B23);
  and and_25 (_24, A24, B24);
  and and_26 (_25, A25, B25);
  and and_27 (_26, A26, B26);
  and and_28 (_27, A27, B27);
  and and_29 (_28, A28, B28);
  and and_30 (_29, A29, B29);
  and and_31 (_30, A30, B30);
  and and_32 (_31, A31, B31);
endmodule

module andi (
  input  A0,
  input  B0,
  input  A1,
  input  B1,
  input  A2,
  input  B2,
  input  A3,
  input  B3,
  input  A4,
  input  B4,
  input  A5,
  input  B5,
  input  A6,
  input  B6,
  input  A7,
  input  B7,
  input  A8,
  input  B8,
  input  A9,
  input  B9,
  input  A10,
  input  B10,
  input  A11,
  input  B11,
  input  A12,
  input  B12,
  input  A13,
  input  B13,
  input  A14,
  input  B14,
  input  A15,
  input  B15,
  output _0,
  output _1,
  output _2,
  output _3,
  output _4,
  output _5,
  output _6,
  output _7,
  output _8,
  output _9,
  output _10,
  output _11,
  output _12,
  output _13,
  output _14,
  output _15
);

  and and_1 (_0, A0, B0);
  and and_2 (_1, A1, B1);
  and and_3 (_2, A2, B2);
  and and_4 (_3, A3, B3);
  and and_5 (_4, A4, B4);
  and and_6 (_5, A5, B5);
  and and_7 (_6, A6, B6);
  and and_8 (_7, A7, B7);
  and and_9 (_8, A8, B8);
  and and_10 (_9, A9, B9);
  and and_11 (_10, A10, B10);
  and and_12 (_11, A11, B11);
  and and_13 (_12, A12, B12);
  and and_14 (_13, A13, B13);
  and and_15 (_14, A14, B14);
  and and_16 (_15, A15, B15);
endmodule

module \nand  (
  input  A0,
  input  B0,
  input  A1,
  input  B1,
  input  A2,
  input  B2,
  input  A3,
  input  B3,
  input  A4,
  input  B4,
  input  A5,
  input  B5,
  input  A6,
  input  B6,
  input  A7,
  input  B7,
  input  A8,
  input  B8,
  input  A9,
  input  B9,
  input  A10,
  input  B10,
  input  A11,
  input  B11,
  input  A12,
  input  B12,
  input  A13,
  input  B13,
  input  A14,
  input  B14,
  input  A15,
  input  B15,
  input  A16,
  input  B16,
  input  A17,
  input  B17,
  input  A18,
  input  B18,
  input  A19,
  input  B19,
  input  A20,
  input  B20,
  input  A21,
  input  B21,
  input  A22,
  input  B22,
  input  A23,
  input  B23,
  input  A24,
  input  B24,
  input  A25,
  input  B25,
  input  A26,
  input  B26,
  input  A27,
  input  B27,
  input  A28,
  input  B28,
  input  A29,
  input  B29,
  input  A30,
  input  B30,
  input  A31,
  input  B31,
  output _0,
  output _1,
  output _2,
  output _3,
  output _4,
  output _5,
  output _6,
  output _7,
  output _8,
  output _9,
  output _10,
  output _11,
  output _12,
  output _13,
  output _14,
  output _15,
  output _16,
  output _17,
  output _18,
  output _19,
  output _20,
  output _21,
  output _22,
  output _23,
  output _24,
  output _25,
  output _26,
  output _27,
  output _28,
  output _29,
  output _30,
  output _31
);

  nand nand_1 (_0, A0, B0);
  nand nand_2 (_1, A1, B1);
  nand nand_3 (_2, A2, B2);
  nand nand_4 (_3, A3, B3);
  nand nand_5 (_4, A4, B4);
  nand nand_6 (_5, A5, B5);
  nand nand_7 (_6, A6, B6);
  nand nand_8 (_7, A7, B7);
  nand nand_9 (_8, A8, B8);
  nand nand_10 (_9, A9, B9);
  nand nand_11 (_10, A10, B10);
  nand nand_12 (_11, A11, B11);
  nand nand_13 (_12, A12, B12);
  nand nand_14 (_13, A13, B13);
  nand nand_15 (_14, A14, B14);
  nand nand_16 (_15, A15, B15);
  nand nand_17 (_16, A16, B16);
  nand nand_18 (_17, A17, B17);
  nand nand_19 (_18, A18, B18);
  nand nand_20 (_19, A19, B19);
  nand nand_21 (_20, A20, B20);
  nand nand_22 (_21, A21, B21);
  nand nand_23 (_22, A22, B22);
  nand nand_24 (_23, A23, B23);
  nand nand_25 (_24, A24, B24);
  nand nand_26 (_25, A25, B25);
  nand nand_27 (_26, A26, B26);
  nand nand_28 (_27, A27, B27);
  nand nand_29 (_28, A28, B28);
  nand nand_30 (_29, A29, B29);
  nand nand_31 (_30, A30, B30);
  nand nand_32 (_31, A31, B31);
endmodule

module nandi (
  input  A0,
  input  B0,
  input  A1,
  input  B1,
  input  A2,
  input  B2,
  input  A3,
  input  B3,
  input  A4,
  input  B4,
  input  A5,
  input  B5,
  input  A6,
  input  B6,
  input  A7,
  input  B7,
  input  A8,
  input  B8,
  input  A9,
  input  B9,
  input  A10,
  input  B10,
  input  A11,
  input  B11,
  input  A12,
  input  B12,
  input  A13,
  input  B13,
  input  A14,
  input  B14,
  input  A15,
  input  B15,
  output _0,
  output _1,
  output _2,
  output _3,
  output _4,
  output _5,
  output _6,
  output _7,
  output _8,
  output _9,
  output _10,
  output _11,
  output _12,
  output _13,
  output _14,
  output _15,
  output _16,
  output _17,
  output _18,
  output _19,
  output _20,
  output _21,
  output _22,
  output _23,
  output _24,
  output _25,
  output _26,
  output _27,
  output _28,
  output _29,
  output _30,
  output _31
);

  nand nand_1 (_0, A0, B0);
  nand nand_2 (_1, A1, B1);
  nand nand_3 (_2, A2, B2);
  nand nand_4 (_3, A3, B3);
  nand nand_5 (_4, A4, B4);
  nand nand_6 (_5, A5, B5);
  nand nand_7 (_6, A6, B6);
  nand nand_8 (_7, A7, B7);
  nand nand_9 (_8, A8, B8);
  nand nand_10 (_9, A9, B9);
  nand nand_11 (_10, A10, B10);
  nand nand_12 (_11, A11, B11);
  nand nand_13 (_12, A12, B12);
  nand nand_14 (_13, A13, B13);
  nand nand_15 (_14, A14, B14);
  nand nand_16 (_15, A15, B15);

  assign _16 = 1'b1;
  assign _17 = 1'b1;
  assign _18 = 1'b1;
  assign _19 = 1'b1;
  assign _20 = 1'b1;
  assign _21 = 1'b1;
  assign _22 = 1'b1;
  assign _23 = 1'b1;
  assign _24 = 1'b1;
  assign _25 = 1'b1;
  assign _26 = 1'b1;
  assign _27 = 1'b1;
  assign _28 = 1'b1;
  assign _29 = 1'b1;
  assign _30 = 1'b1;
  assign _31 = 1'b1;
endmodule

module \or  (
  input  A0,
  input  B0,
  input  A1,
  input  B1,
  input  A2,
  input  B2,
  input  A3,
  input  B3,
  input  A4,
  input  B4,
  input  A5,
  input  B5,
  input  A6,
  input  B6,
  input  A7,
  input  B7,
  input  A8,
  input  B8,
  input  A9,
  input  B9,
  input  A10,
  input  B10,
  input  A11,
  input  B11,
  input  A12,
  input  B12,
  input  A13,
  input  B13,
  input  A14,
  input  B14,
  input  A15,
  input  B15,
  input  A16,
  input  B16,
  input  A17,
  input  B17,
  input  A18,
  input  B18,
  input  A19,
  input  B19,
  input  A20,
  input  B20,
  input  A21,
  input  B21,
  input  A22,
  input  B22,
  input  A23,
  input  B23,
  input  A24,
  input  B24,
  input  A25,
  input  B25,
  input  A26,
  input  B26,
  input  A27,
  input  B27,
  input  A28,
  input  B28,
  input  A29,
  input  B29,
  input  A30,
  input  B30,
  input  A31,
  input  B31,
  output _0,
  output _1,
  output _2,
  output _3,
  output _4,
  output _5,
  output _6,
  output _7,
  output _8,
  output _9,
  output _10,
  output _11,
  output _12,
  output _13,
  output _14,
  output _15,
  output _16,
  output _17,
  output _18,
  output _19,
  output _20,
  output _21,
  output _22,
  output _23,
  output _24,
  output _25,
  output _26,
  output _27,
  output _28,
  output _29,
  output _30,
  output _31
);

  or or_1 (_0, A0, B0);
  or or_2 (_1, A1, B1);
  or or_3 (_2, A2, B2);
  or or_4 (_3, A3, B3);
  or or_5 (_4, A4, B4);
  or or_6 (_5, A5, B5);
  or or_7 (_6, A6, B6);
  or or_8 (_7, A7, B7);
  or or_9 (_8, A8, B8);
  or or_10 (_9, A9, B9);
  or or_11 (_10, A10, B10);
  or or_12 (_11, A11, B11);
  or or_13 (_12, A12, B12);
  or or_14 (_13, A13, B13);
  or or_15 (_14, A14, B14);
  or or_16 (_15, A15, B15);
  or or_17 (_16, A16, B16);
  or or_18 (_17, A17, B17);
  or or_19 (_18, A18, B18);
  or or_20 (_19, A19, B19);
  or or_21 (_20, A20, B20);
  or or_22 (_21, A21, B21);
  or or_23 (_22, A22, B22);
  or or_24 (_23, A23, B23);
  or or_25 (_24, A24, B24);
  or or_26 (_25, A25, B25);
  or or_27 (_26, A26, B26);
  or or_28 (_27, A27, B27);
  or or_29 (_28, A28, B28);
  or or_30 (_29, A29, B29);
  or or_31 (_30, A30, B30);
  or or_32 (_31, A31, B31);
endmodule

module ori (
  input  A0,
  input  B0,
  input  A1,
  input  B1,
  input  A2,
  input  B2,
  input  A3,
  input  B3,
  input  A4,
  input  B4,
  input  A5,
  input  B5,
  input  A6,
  input  B6,
  input  A7,
  input  B7,
  input  A8,
  input  B8,
  input  A9,
  input  B9,
  input  A10,
  input  B10,
  input  A11,
  input  B11,
  input  A12,
  input  B12,
  input  A13,
  input  B13,
  input  A14,
  input  B14,
  input  A15,
  input  B15,
  input  A16,
  input  A17,
  input  A18,
  input  A19,
  input  A20,
  input  A21,
  input  A22,
  input  A23,
  input  A24,
  input  A25,
  input  A26,
  input  A27,
  input  A28,
  input  A29,
  input  A30,
  input  A31,
  output _0,
  output _1,
  output _2,
  output _3,
  output _4,
  output _5,
  output _6,
  output _7,
  output _8,
  output _9,
  output _10,
  output _11,
  output _12,
  output _13,
  output _14,
  output _15,
  output _16,
  output _17,
  output _18,
  output _19,
  output _20,
  output _21,
  output _22,
  output _23,
  output _24,
  output _25,
  output _26,
  output _27,
  output _28,
  output _29,
  output _30,
  output _31
);

  or or_1 (_0, A0, B0);
  or or_2 (_1, A1, B1);
  or or_3 (_2, A2, B2);
  or or_4 (_3, A3, B3);
  or or_5 (_4, A4, B4);
  or or_6 (_5, A5, B5);
  or or_7 (_6, A6, B6);
  or or_8 (_7, A7, B7);
  or or_9 (_8, A8, B8);
  or or_10 (_9, A9, B9);
  or or_11 (_10, A10, B10);
  or or_12 (_11, A11, B11);
  or or_13 (_12, A12, B12);
  or or_14 (_13, A13, B13);
  or or_15 (_14, A14, B14);
  or or_16 (_15, A15, B15);

  assign _16 = A16;
  assign _17 = A17;
  assign _18 = A18;
  assign _19 = A19;
  assign _20 = A20;
  assign _21 = A21;
  assign _22 = A22;
  assign _23 = A23;
  assign _24 = A24;
  assign _25 = A25;
  assign _26 = A26;
  assign _27 = A27;
  assign _28 = A28;
  assign _29 = A29;
  assign _30 = A30;
  assign _31 = A31;
endmodule

module \nor  (
  input  A0,
  input  B0,
  input  A1,
  input  B1,
  input  A2,
  input  B2,
  input  A3,
  input  B3,
  input  A4,
  input  B4,
  input  A5,
  input  B5,
  input  A6,
  input  B6,
  input  A7,
  input  B7,
  input  A8,
  input  B8,
  input  A9,
  input  B9,
  input  A10,
  input  B10,
  input  A11,
  input  B11,
  input  A12,
  input  B12,
  input  A13,
  input  B13,
  input  A14,
  input  B14,
  input  A15,
  input  B15,
  input  A16,
  input  B16,
  input  A17,
  input  B17,
  input  A18,
  input  B18,
  input  A19,
  input  B19,
  input  A20,
  input  B20,
  input  A21,
  input  B21,
  input  A22,
  input  B22,
  input  A23,
  input  B23,
  input  A24,
  input  B24,
  input  A25,
  input  B25,
  input  A26,
  input  B26,
  input  A27,
  input  B27,
  input  A28,
  input  B28,
  input  A29,
  input  B29,
  input  A30,
  input  B30,
  input  A31,
  input  B31,
  output _0,
  output _1,
  output _2,
  output _3,
  output _4,
  output _5,
  output _6,
  output _7,
  output _8,
  output _9,
  output _10,
  output _11,
  output _12,
  output _13,
  output _14,
  output _15,
  output _16,
  output _17,
  output _18,
  output _19,
  output _20,
  output _21,
  output _22,
  output _23,
  output _24,
  output _25,
  output _26,
  output _27,
  output _28,
  output _29,
  output _30,
  output _31
);

  nor nor_1 (_0, A0, B0);
  nor nor_2 (_1, A1, B1);
  nor nor_3 (_2, A2, B2);
  nor nor_4 (_3, A3, B3);
  nor nor_5 (_4, A4, B4);
  nor nor_6 (_5, A5, B5);
  nor nor_7 (_6, A6, B6);
  nor nor_8 (_7, A7, B7);
  nor nor_9 (_8, A8, B8);
  nor nor_10 (_9, A9, B9);
  nor nor_11 (_10, A10, B10);
  nor nor_12 (_11, A11, B11);
  nor nor_13 (_12, A12, B12);
  nor nor_14 (_13, A13, B13);
  nor nor_15 (_14, A14, B14);
  nor nor_16 (_15, A15, B15);
  nor nor_17 (_16, A16, B16);
  nor nor_18 (_17, A17, B17);
  nor nor_19 (_18, A18, B18);
  nor nor_20 (_19, A19, B19);
  nor nor_21 (_20, A20, B20);
  nor nor_22 (_21, A21, B21);
  nor nor_23 (_22, A22, B22);
  nor nor_24 (_23, A23, B23);
  nor nor_25 (_24, A24, B24);
  nor nor_26 (_25, A25, B25);
  nor nor_27 (_26, A26, B26);
  nor nor_28 (_27, A27, B27);
  nor nor_29 (_28, A28, B28);
  nor nor_30 (_29, A29, B29);
  nor nor_31 (_30, A30, B30);
  nor nor_32 (_31, A31, B31);
endmodule

module nori (
  input  A0,
  input  B0,
  input  A1,
  input  B1,
  input  A2,
  input  B2,
  input  A3,
  input  B3,
  input  A4,
  input  B4,
  input  A5,
  input  B5,
  input  A6,
  input  B6,
  input  A7,
  input  B7,
  input  A8,
  input  B8,
  input  A9,
  input  B9,
  input  A10,
  input  B10,
  input  A11,
  input  B11,
  input  A12,
  input  B12,
  input  A13,
  input  B13,
  input  A14,
  input  B14,
  input  A15,
  input  B15,
  input  A16,
  input  A17,
  input  A18,
  input  A19,
  input  A20,
  input  A21,
  input  A22,
  input  A23,
  input  A24,
  input  A25,
  input  A26,
  input  A27,
  input  A28,
  input  A29,
  input  A30,
  input  A31,
  output _0,
  output _1,
  output _2,
  output _3,
  output _4,
  output _5,
  output _6,
  output _7,
  output _8,
  output _9,
  output _10,
  output _11,
  output _12,
  output _13,
  output _14,
  output _15,
  output _16,
  output _17,
  output _18,
  output _19,
  output _20,
  output _21,
  output _22,
  output _23,
  output _24,
  output _25,
  output _26,
  output _27,
  output _28,
  output _29,
  output _30,
  output _31
);

  nor nor_1 (_0, A0, B0);
  nor nor_2 (_1, A1, B1);
  nor nor_3 (_2, A2, B2);
  nor nor_4 (_3, A3, B3);
  nor nor_5 (_4, A4, B4);
  nor nor_6 (_5, A5, B5);
  nor nor_7 (_6, A6, B6);
  nor nor_8 (_7, A7, B7);
  nor nor_9 (_8, A8, B8);
  nor nor_10 (_9, A9, B9);
  nor nor_11 (_10, A10, B10);
  nor nor_12 (_11, A11, B11);
  nor nor_13 (_12, A12, B12);
  nor nor_14 (_13, A13, B13);
  nor nor_15 (_14, A14, B14);
  nor nor_16 (_15, A15, B15);

  assign _16 = A16;
  assign _17 = A17;
  assign _18 = A18;
  assign _19 = A19;
  assign _20 = A20;
  assign _21 = A21;
  assign _22 = A22;
  assign _23 = A23;
  assign _24 = A24;
  assign _25 = A25;
  assign _26 = A26;
  assign _27 = A27;
  assign _28 = A28;
  assign _29 = A29;
  assign _30 = A30;
  assign _31 = A31;
endmodule

module \xor  (
  input  A0,
  input  B0,
  input  A1,
  input  B1,
  input  A2,
  input  B2,
  input  A3,
  input  B3,
  input  A4,
  input  B4,
  input  A5,
  input  B5,
  input  A6,
  input  B6,
  input  A7,
  input  B7,
  input  A8,
  input  B8,
  input  A9,
  input  B9,
  input  A10,
  input  B10,
  input  A11,
  input  B11,
  input  A12,
  input  B12,
  input  A13,
  input  B13,
  input  A14,
  input  B14,
  input  A15,
  input  B15,
  input  A16,
  input  B16,
  input  A17,
  input  B17,
  input  A18,
  input  B18,
  input  A19,
  input  B19,
  input  A20,
  input  B20,
  input  A21,
  input  B21,
  input  A22,
  input  B22,
  input  A23,
  input  B23,
  input  A24,
  input  B24,
  input  A25,
  input  B25,
  input  A26,
  input  B26,
  input  A27,
  input  B27,
  input  A28,
  input  B28,
  input  A29,
  input  B29,
  input  A30,
  input  B30,
  input  A31,
  input  B31,
  output _0,
  output _1,
  output _2,
  output _3,
  output _4,
  output _5,
  output _6,
  output _7,
  output _8,
  output _9,
  output _10,
  output _11,
  output _12,
  output _13,
  output _14,
  output _15,
  output _16,
  output _17,
  output _18,
  output _19,
  output _20,
  output _21,
  output _22,
  output _23,
  output _24,
  output _25,
  output _26,
  output _27,
  output _28,
  output _29,
  output _30,
  output _31
);

  xor xor_1 (_0, A0, B0);
  xor xor_2 (_1, A1, B1);
  xor xor_3 (_2, A2, B2);
  xor xor_4 (_3, A3, B3);
  xor xor_5 (_4, A4, B4);
  xor xor_6 (_5, A5, B5);
  xor xor_7 (_6, A6, B6);
  xor xor_8 (_7, A7, B7);
  xor xor_9 (_8, A8, B8);
  xor xor_10 (_9, A9, B9);
  xor xor_11 (_10, A10, B10);
  xor xor_12 (_11, A11, B11);
  xor xor_13 (_12, A12, B12);
  xor xor_14 (_13, A13, B13);
  xor xor_15 (_14, A14, B14);
  xor xor_16 (_15, A15, B15);
  xor xor_17 (_16, A16, B16);
  xor xor_18 (_17, A17, B17);
  xor xor_19 (_18, A18, B18);
  xor xor_20 (_19, A19, B19);
  xor xor_21 (_20, A20, B20);
  xor xor_22 (_21, A21, B21);
  xor xor_23 (_22, A22, B22);
  xor xor_24 (_23, A23, B23);
  xor xor_25 (_24, A24, B24);
  xor xor_26 (_25, A25, B25);
  xor xor_27 (_26, A26, B26);
  xor xor_28 (_27, A27, B27);
  xor xor_29 (_28, A28, B28);
  xor xor_30 (_29, A29, B29);
  xor xor_31 (_30, A30, B30);
  xor xor_32 (_31, A31, B31);
endmodule
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module slti (
  input  B0,
  input  B1,
  input  B2,
  input  B3,
  input  B4,
  input  B5,
  input  B6,
  input  B7,
  input  B8,
  input  B9,
  input  B10,
  input  B11,
  input  B12,
  input  B13,
  input  B14,
  input  B15,
  input  A0,
  input  A1,
  input  A2,
  input  A3,
  input  A4,
  input  A5,
  input  A6,
  input  A7,
  input  A8,
  input  A9,
  input  A10,
  input  A11,
  input  A12,
  input  A13,
  input  A14,
  input  A15,
  input  A16,
  input  A17,
  input  A18,
  input  A19,
  input  A20,
  input  A21,
  input  A22,
  input  A23,
  input  A24,
  input  A25,
  input  A26,
  input  A27,
  input  A28,
  input  A29,
  input  A30,
  input  A31,
  output _0,
  output _1,
  output _2,
  output _3,
  output _4,
  output _5,
  output _6,
  output _7,
  output _8,
  output _9,
  output _10,
  output _11,
  output _12,
  output _13,
  output _14,
  output _15,
  output _16,
  output _17,
  output _18,
  output _19,
  output _20,
  output _21,
  output _22,
  output _23,
  output _24,
  output _25,
  output _26,
  output _27,
  output _28,
  output _29,
  output _30,
  output _31
);

  wire add_1__0, add_1__1, add_1__2, add_1__3, add_1__4, add_1__5, add_1__6, add_1__7, add_1__8, add_1__9,
       add_1__10, add_1__11, add_1__12, add_1__13, add_1__14, add_1__15, add_2__0, add_2__1, add_2__2,
       add_2__3, add_2__4, add_2__5, add_2__6, add_2__7, add_2__8, add_2__9, add_2__10, add_2__11, add_2__12,
       add_2__13, add_2__14, add_2__15, add_2__16, add_2__17, add_2__18, add_2__19, add_2__20, add_2__21,
       add_2__22, add_2__23, add_2__24, add_2__25, add_2__26, add_2__27, add_2__28, add_2__29, add_2__30,
       add_2__31, and_1_out, and_2_out, and_3_out, and_4_out, and_5_out, and_6_out, and_7_out, and_8_out,
       and_9_out, and_10_out, and_11_out, and_12_out, and_13_out, and_14_out, and_15_out, and_16_out,
       and_17_out, and_18_out, and_19_out, and_20_out, and_21_out, and_22_out, and_23_out, and_24_out,
       and_25_out, and_26_out, and_27_out, and_28_out, and_29_out, and_30_out, and_31_out, and_32_out,
       and_33_out, and_34_out, and_35_out, and_36_out, and_37_out, and_38_out, and_39_out, and_40_out,
       and_41_out, and_42_out, and_43_out, and_44_out, and_45_out, and_46_out, and_47_out, and_48_out,
       and_49_out, and_50_out, and_51_out, nand_1_out, nand_2_out, nand_3_out, nand_4_out, nand_5_out,
       nand_6_out, nand_7_out, nand_8_out, nand_9_out, nand_10_out, nand_11_out, nand_12_out, nand_13_out,
       nand_14_out, nand_15_out, nand_16_out, nand_17_out, nand_18_out, nand_19_out, nand_20_out,
       nand_21_out, nand_22_out, nand_23_out, nand_24_out, nand_25_out, nand_26_out, nand_27_out,
       nand_28_out, nand_29_out, nand_30_out, nand_31_out, nand_32_out, nand_33_out, nand_34_out,
       nand_35_out, nand_36_out, nand_37_out, nand_38_out, nand_39_out, nand_40_out, nand_41_out,
       nand_42_out, nand_43_out, nand_44_out, nand_45_out, nand_46_out, nand_47_out, nand_48_out, not_1_out,
       not_2_out, not_3_out, or_2_out, or_4_out, or_6_out, or_8_out, or_10_out, or_12_out, or_14_out,
       or_16_out, or_18_out, or_20_out, or_22_out, or_24_out, or_26_out, or_28_out, or_30_out, or_32_out,
       or_34_out, or_36_out, or_38_out, or_40_out, or_42_out, or_44_out, or_46_out, or_48_out, or_50_out,
       or_52_out, or_54_out, or_56_out, or_58_out, or_60_out, or_62_out, or_64_out, sltu_1__0, sltu_1__1,
       sltu_1__2, sltu_1__3, sltu_1__4, sltu_1__5, sltu_1__6, sltu_1__7, sltu_1__8, sltu_1__9, sltu_1__10,
       sltu_1__11, sltu_1__12, sltu_1__13, sltu_1__14, sltu_1__15, sltu_1__16, sltu_1__17, sltu_1__18,
       sltu_1__19, sltu_1__20, sltu_1__21, sltu_1__22, sltu_1__23, sltu_1__24, sltu_1__25, sltu_1__26,
       sltu_1__27, sltu_1__28, sltu_1__29, sltu_1__30, sltu_1__31, sltu_2__0, sltu_2__1, sltu_2__2,
       sltu_2__3, sltu_2__4, sltu_2__5, sltu_2__6, sltu_2__7, sltu_2__8, sltu_2__9, sltu_2__10, sltu_2__11,
       sltu_2__12, sltu_2__13, sltu_2__14, sltu_2__15, sltu_2__16, sltu_2__17, sltu_2__18, sltu_2__19,
       sltu_2__20, sltu_2__21, sltu_2__22, sltu_2__23, sltu_2__24, sltu_2__25, sltu_2__26, sltu_2__27,
       sltu_2__28, sltu_2__29, sltu_2__30, sltu_2__31;

  not not_1 (not_1_out, B15);
  not not_2 (not_2_out, A31);
  and and_1 (and_1_out, and_49_out, B0);
  and and_2 (and_2_out, and_49_out, B1);
  and and_3 (and_3_out, and_49_out, B2);
  and and_4 (and_4_out, and_49_out, B3);
  and and_5 (and_5_out, and_49_out, B4);
  and and_6 (and_6_out, and_49_out, B5);
  and and_7 (and_7_out, and_49_out, B6);
  and and_8 (and_8_out, and_49_out, B7);
  and and_9 (and_9_out, and_49_out, B8);
  and and_10 (and_10_out, and_49_out, B9);
  and and_11 (and_11_out, and_49_out, B10);
  and and_12 (and_12_out, and_49_out, B11);
  and and_13 (and_13_out, and_49_out, B12);
  and and_14 (and_14_out, and_49_out, B13);
  and and_15 (and_15_out, and_49_out, B14);
  and and_16 (and_16_out, and_49_out, B15);
  and and_17 (and_17_out, and_49_out, A0);
  and and_18 (and_18_out, and_49_out, A1);
  and and_19 (and_19_out, and_49_out, A2);
  and and_20 (and_20_out, and_49_out, A3);
  and and_21 (and_21_out, and_49_out, A4);
  and and_22 (and_22_out, and_49_out, A5);
  and and_23 (and_23_out, and_49_out, A6);
  and and_24 (and_24_out, and_49_out, A7);
  and and_25 (and_25_out, and_49_out, A8);
  and and_26 (and_26_out, and_49_out, A9);
  and and_27 (and_27_out, and_49_out, A10);
  and and_28 (and_28_out, and_49_out, A11);
  and and_29 (and_29_out, and_49_out, A12);
  and and_30 (and_30_out, and_49_out, A13);
  and and_31 (and_31_out, and_49_out, A14);
  and and_32 (and_32_out, and_49_out, A15);
  and and_33 (and_33_out, and_49_out, A16);
  and and_34 (and_34_out, and_49_out, A17);
  and and_35 (and_35_out, and_49_out, A18);
  and and_36 (and_36_out, and_49_out, A19);
  and and_37 (and_37_out, and_49_out, A20);
  and and_38 (and_38_out, and_49_out, A21);
  and and_39 (and_39_out, and_49_out, A22);
  and and_40 (and_40_out, and_49_out, A23);
  and and_41 (and_41_out, and_49_out, A24);
  and and_42 (and_42_out, and_49_out, A25);
  and and_43 (and_43_out, and_49_out, A26);
  and and_44 (and_44_out, and_49_out, A27);
  and and_45 (and_45_out, and_49_out, A28);
  and and_46 (and_46_out, and_49_out, A29);
  and and_47 (and_47_out, and_49_out, A30);
  and and_48 (and_48_out, and_49_out, A31);
  and and_49 (and_49_out, not_1_out, not_2_out);
  not not_3 (not_3_out, B15);
  and and_50 (and_50_out, not_3_out, A31);
  and and_51 (and_51_out, B15, A31);
  sltu sltu_1 (
    .A0(and_17_out), .A1(and_18_out), .A2(and_19_out), .A3(and_20_out), .A4(and_21_out), .A5(and_22_out),
    .A6(and_23_out), .A7(and_24_out), .A8(and_25_out), .A9(and_26_out), .A10(and_27_out), .A11(and_28_out),
    .A12(and_29_out), .A13(and_30_out), .A14(and_31_out), .A15(and_32_out), .A16(and_33_out),
    .A17(and_34_out), .A18(and_35_out), .A19(and_36_out), .A20(and_37_out), .A21(and_38_out),
    .A22(and_39_out), .A23(and_40_out), .A24(and_41_out), .A25(and_42_out), .A26(and_43_out),
    .A27(and_44_out), .A28(and_45_out), .A29(and_46_out), .A30(and_47_out), .A31(and_48_out), ._0(sltu_1__0),
    ._1(sltu_1__1), ._2(sltu_1__2), ._3(sltu_1__3), ._4(sltu_1__4), ._5(sltu_1__5), ._6(sltu_1__6),
    ._7(sltu_1__7), ._8(sltu_1__8), ._9(sltu_1__9), ._10(sltu_1__10), ._11(sltu_1__11), ._12(sltu_1__12),
    ._13(sltu_1__13), ._14(sltu_1__14), ._15(sltu_1__15), ._16(sltu_1__16), ._17(sltu_1__17),
    ._18(sltu_1__18), ._19(sltu_1__19), ._20(sltu_1__20), ._21(sltu_1__21), ._22(sltu_1__22),
    ._23(sltu_1__23), ._24(sltu_1__24), ._25(sltu_1__25), ._26(sltu_1__26), ._27(sltu_1__27),
    ._28(sltu_1__28), ._29(sltu_1__29), ._30(sltu_1__30), ._31(sltu_1__31), .B0(and_1_out), .B1(and_2_out),
    .B2(and_3_out), .B3(and_4_out), .B4(and_5_out), .B5(and_6_out), .B6(and_7_out), .B7(and_8_out),
    .B8(and_9_out), .B9(and_10_out), .B10(and_11_out), .B11(and_12_out), .B12(and_13_out), .B13(and_14_out),
    .B14(and_15_out), .B15(and_16_out), .B16(1'b0), .B17(1'b0), .B18(1'b0), .B19(1'b0), .B20(1'b0),
    .B21(1'b0), .B22(1'b0), .B23(1'b0), .B24(1'b0), .B25(1'b0), .B26(1'b0), .B27(1'b0), .B28(1'b0),
    .B29(1'b0), .B30(1'b0), .B31(1'b0));
  nand nand_1 (nand_1_out, and_51_out, B0);
  nand nand_2 (nand_2_out, and_51_out, B1);
  nand nand_3 (nand_3_out, and_51_out, B2);
  nand nand_4 (nand_4_out, and_51_out, B3);
  nand nand_5 (nand_5_out, and_51_out, B4);
  nand nand_6 (nand_6_out, and_51_out, B5);
  nand nand_7 (nand_7_out, and_51_out, B6);
  nand nand_8 (nand_8_out, and_51_out, B7);
  nand nand_9 (nand_9_out, and_51_out, B8);
  nand nand_10 (nand_10_out, and_51_out, B9);
  nand nand_11 (nand_11_out, and_51_out, B10);
  nand nand_12 (nand_12_out, and_51_out, B11);
  nand nand_13 (nand_13_out, and_51_out, B12);
  nand nand_14 (nand_14_out, and_51_out, B13);
  nand nand_15 (nand_15_out, and_51_out, B14);
  nand nand_16 (nand_16_out, and_51_out, B15);
  nand nand_17 (nand_17_out, and_51_out, A0);
  nand nand_18 (nand_18_out, and_51_out, A1);
  nand nand_19 (nand_19_out, and_51_out, A2);
  nand nand_20 (nand_20_out, and_51_out, A3);
  nand nand_21 (nand_21_out, and_51_out, A4);
  nand nand_22 (nand_22_out, and_51_out, A5);
  nand nand_23 (nand_23_out, and_51_out, A6);
  nand nand_24 (nand_24_out, and_51_out, A7);
  nand nand_25 (nand_25_out, and_51_out, A8);
  nand nand_26 (nand_26_out, and_51_out, A9);
  nand nand_27 (nand_27_out, and_51_out, A10);
  nand nand_28 (nand_28_out, and_51_out, A11);
  nand nand_29 (nand_29_out, and_51_out, A12);
  nand nand_30 (nand_30_out, and_51_out, A13);
  nand nand_31 (nand_31_out, and_51_out, A14);
  nand nand_32 (nand_32_out, and_51_out, A15);
  nand nand_33 (nand_33_out, and_51_out, A16);
  nand nand_34 (nand_34_out, and_51_out, A17);
  nand nand_35 (nand_35_out, and_51_out, A18);
  nand nand_36 (nand_36_out, and_51_out, A19);
  nand nand_37 (nand_37_out, and_51_out, A20);
  nand nand_38 (nand_38_out, and_51_out, A21);
  nand nand_39 (nand_39_out, and_51_out, A22);
  nand nand_40 (nand_40_out, and_51_out, A23);
  nand nand_41 (nand_41_out, and_51_out, A24);
  nand nand_42 (nand_42_out, and_51_out, A25);
  nand nand_43 (nand_43_out, and_51_out, A26);
  nand nand_44 (nand_44_out, and_51_out, A27);
  nand nand_45 (nand_45_out, and_51_out, A28);
  nand nand_46 (nand_46_out, and_51_out, A29);
  nand nand_47 (nand_47_out, and_51_out, A30);
  nand nand_48 (nand_48_out, and_51_out, A31);
  add add_1 (
    .A0(nand_1_out), .B0(1'b1), .A1(nand_2_out), .B1(1'b0), .A2(nand_3_out), .B2(1'b0), .A3(nand_4_out),
    .B3(1'b0), .A4(nand_5_out), .B4(1'b0), .A5(nand_6_out), .B5(1'b0), .A6(nand_7_out), .B6(1'b0),
    .A7(nand_8_out), .B7(1'b0), .A8(nand_9_out), .B8(1'b0), .A9(nand_10_out), .B9(1'b0), .A10(nand_11_out),
    .B10(1'b0), .A11(nand_12_out), .B11(1'b0), .A12(nand_13_out), .B12(1'b0), .A13(nand_14_out), .B13(1'b0),
    .A14(nand_15_out), .B14(1'b0), .A15(nand_16_out), .B15(1'b0), .A16(1'b0), .B16(1'b0), .A17(1'b0),
    .B17(1'b0), .A18(1'b0), .B18(1'b0), .A19(1'b0), .B19(1'b0), .A20(1'b0), .B20(1'b0), .A21(1'b0),
    .B21(1'b0), .A22(1'b0), .B22(1'b0), .A23(1'b0), .B23(1'b0), .A24(1'b0), .B24(1'b0), .A25(1'b0),
    .B25(1'b0), .A26(1'b0), .B26(1'b0), .A27(1'b0), .B27(1'b0), .A28(1'b0), .B28(1'b0), .A29(1'b0),
    .B29(1'b0), .A30(1'b0), .B30(1'b0), .A31(1'b0), ._0(add_1__0), ._1(add_1__1), ._2(add_1__2),
    ._3(add_1__3), ._4(add_1__4), ._5(add_1__5), ._6(add_1__6), ._7(add_1__7), ._8(add_1__8), ._9(add_1__9),
    ._10(add_1__10), ._11(add_1__11), ._12(add_1__12), ._13(add_1__13), ._14(add_1__14), ._15(add_1__15),
    .B31(1'b0));  // open: _16, _17, _18, _19, _20, _21, _22, _23, _24, _25, _26, _27, _28, _29, _30, _31, Carry, Overflow
  add add_2 (
    .A0(nand_17_out), .B0(1'b1), .A1(nand_18_out), .B1(1'b0), .A2(nand_19_out), .B2(1'b0), .A3(nand_20_out),
    .B3(1'b0), .A4(nand_21_out), .B4(1'b0), .A5(nand_22_out), .B5(1'b0), .A6(nand_23_out), .B6(1'b0),
    .A7(nand_24_out), .B7(1'b0), .A8(nand_25_out), .B8(1'b0), .A9(nand_26_out), .B9(1'b0), .A10(nand_27_out),
    .B10(1'b0), .A11(nand_28_out), .B11(1'b0), .A12(nand_29_out), .B12(1'b0), .A13(nand_30_out), .B13(1'b0),
    .A14(nand_31_out), .B14(1'b0), .A15(nand_32_out), .B15(1'b0), .A16(nand_33_out), .B16(1'b0),
    .A17(nand_34_out), .B17(1'b0), .A18(nand_35_out), .B18(1'b0), .A19(nand_36_out), .B19(1'b0),
    .A20(nand_37_out), .B20(1'b0), .A21(nand_38_out), .B21(1'b0), .A22(nand_39_out), .B22(1'b0),
    .A23(nand_40_out), .B23(1'b0), .A24(nand_41_out), .B24(1'b0), .A25(nand_42_out), .B25(1'b0),
    .A26(nand_43_out), .B26(1'b0), .A27(nand_44_out), .B27(1'b0), .A28(nand_45_out), .B28(1'b0),
    .A29(nand_46_out), .B29(1'b0), .A30(nand_47_out), .B30(1'b0), .A31(nand_48_out), ._0(add_2__0),
    ._1(add_2__1), ._2(add_2__2), ._3(add_2__3), ._4(add_2__4), ._5(add_2__5), ._6(add_2__6), ._7(add_2__7),
    ._8(add_2__8), ._9(add_2__9), ._10(add_2__10), ._11(add_2__11), ._12(add_2__12), ._13(add_2__13),
    ._14(add_2__14), ._15(add_2__15), ._16(add_2__16), ._17(add_2__17), ._18(add_2__18), ._19(add_2__19),
    ._20(add_2__20), ._21(add_2__21), ._22(add_2__22), ._23(add_2__23), ._24(add_2__24), ._25(add_2__25),
    ._26(add_2__26), ._27(add_2__27), ._28(add_2__28), ._29(add_2__29), ._30(add_2__30), ._31(add_2__31),
    .B31(1'b0));  // open: Carry, Overflow
  sltu sltu_2 (
    .A0(add_1__0), .A1(add_1__1), .A2(add_1__2), .A3(add_1__3), .A4(add_1__4), .A5(add_1__5), .A6(add_1__6),
    .A7(add_1__7), .A8(add_1__8), .A9(add_1__9), .A10(add_1__10), .A11(add_1__11), .A12(add_1__12),
    .A13(add_1__13), .A14(add_1__14), .A15(add_1__15), .A16(1'b0), .A17(1'b0), .A18(1'b0), .A19(1'b0),
    .A20(1'b0), .A21(1'b0), .A22(1'b0), .A23(1'b0), .A24(1'b0), .A25(1'b0), .A26(1'b0), .A27(1'b0),
    .A28(1'b0), .A29(1'b0), .A30(1'b0), .A31(1'b0), ._0(sltu_2__0), ._1(sltu_2__1), ._2(sltu_2__2),
    ._3(sltu_2__3), ._4(sltu_2__4), ._5(sltu_2__5), ._6(sltu_2__6), ._7(sltu_2__7), ._8(sltu_2__8),
    ._9(sltu_2__9), ._10(sltu_2__10), ._11(sltu_2__11), ._12(sltu_2__12), ._13(sltu_2__13), ._14(sltu_2__14),
    ._15(sltu_2__15), ._16(sltu_2__16), ._17(sltu_2__17), ._18(sltu_2__18), ._19(sltu_2__19),
    ._20(sltu_2__20), ._21(sltu_2__21), ._22(sltu_2__22), ._23(sltu_2__23), ._24(sltu_2__24),
    ._25(sltu_2__25), ._26(sltu_2__26), ._27(sltu_2__27), ._28(sltu_2__28), ._29(sltu_2__29),
    ._30(sltu_2__30), ._31(sltu_2__31), .B0(add_2__0), .B1(add_2__1), .B2(add_2__2), .B3(add_2__3),
    .B4(add_2__4), .B5(add_2__5), .B6(add_2__6), .B7(add_2__7), .B8(add_2__8), .B9(add_2__9),
    .B10(add_2__10), .B11(add_2__11), .B12(add_2__12), .B13(add_2__13), .B14(add_2__14), .B15(add_2__15),
    .B16(add_2__16), .B17(add_2__17), .B18(add_2__18), .B19(add_2__19), .B20(add_2__20), .B21(add_2__21),
    .B22(add_2__22), .B23(add_2__23), .B24(add_2__24), .B25(add_2__25), .B26(add_2__26), .B27(add_2__27),
    .B28(add_2__28), .B29(add_2__29), .B30(add_2__30), .B31(add_2__31));
  or or_1 (_0, and_50_out, or_2_out);
  or or_2 (or_2_out, sltu_2__0, sltu_1__0);
  or or_3 (_1, and_50_out, or_4_out);
  or or_4 (or_4_out, sltu_2__1, sltu_1__1);
  or or_5 (_2, and_50_out, or_6_out);
  or or_6 (or_6_out, sltu_2__2, sltu_1__2);
  or or_7 (_3, and_50_out, or_8_out);
  or or_8 (or_8_out, sltu_2__3, sltu_1__3);
  or or_9 (_4, and_50_out, or_10_out);
  or or_10 (or_10_out, sltu_2__4, sltu_1__4);
  or or_11 (_5, and_50_out, or_12_out);
  or or_12 (or_12_out, sltu_2__5, sltu_1__5);
  or or_13 (_6, and_50_out, or_14_out);
  or or_14 (or_14_out, sltu_2__6, sltu_1__6);
  or or_15 (_7, and_50_out, or_16_out);
  or or_16 (or_16_out, sltu_2__7, sltu_1__7);
  or or_17 (_8, and_50_out, or_18_out);
  or or_18 (or_18_out, sltu_2__8, sltu_1__8);
  or or_19 (_9, and_50_out, or_20_out);
  or or_20 (or_20_out, sltu_2__9, sltu_1__9);
  or or_21 (_10, and_50_out, or_22_out);
  or or_22 (or_22_out, sltu_2__10, sltu_1__10);
  or or_23 (_11, and_50_out, or_24_out);
  or or_24 (or_24_out, sltu_2__11, sltu_1__11);
  or or_25 (_12, and_50_out, or_26_out);
  or or_26 (or_26_out, sltu_2__12, sltu_1__12);
  or or_27 (_13, and_50_out, or_28_out);
  or or_28 (or_28_out, sltu_2__13, sltu_1__13);
  or or_29 (_14, and_50_out, or_30_out);
  or or_30 (or_30_out, sltu_2__14, sltu_1__14);
  or or_31 (_15, and_50_out, or_32_out);
  or or_32 (or_32_out, sltu_2__15, sltu_1__15);
  or or_33 (_16, and_50_out, or_34_out);
  or or_34 (or_34_out, sltu_2__16, sltu_1__16);
  or or_35 (_17, and_50_out, or_36_out);
  or or_36 (or_36_out, sltu_2__17, sltu_1__17);
  or or_37 (_18, and_50_out, or_38_out);
  or or_38 (or_38_out, sltu_2__18, sltu_1__18);
  or or_39 (_19, and_50_out, or_40_out);
  or or_40 (or_40_out, sltu_2__19, sltu_1__19);
  or or_41 (_20, and_50_out, or_42_out);
  or or_42 (or_42_out, sltu_2__20, sltu_1__20);
  or or_43 (_21, and_50_out, or_44_out);
  or or_44 (or_44_out, sltu_2__21, sltu_1__21);
  or or_45 (_22, and_50_out, or_46_out);
  or or_46 (or_46_out, sltu_2__22, sltu_1__22);
  or or_47 (_23, and_50_out, or_48_out);
  or or_48 (or_48_out, sltu_2__23, sltu_1__23);
  or or_49 (_24, and_50_out, or_50_out);
  or or_50 (or_50_out, sltu_2__24, sltu_1__24);
  or or_51 (_25, and_50_out, or_52_out);
  or or_52 (or_52_out, sltu_2__25, sltu_1__25);
  or or_53 (_26, and_50_out, or_54_out);
  or or_54 (or_54_out, sltu_2__26, sltu_1__26);
  or or_55 (_27, and_50_out, or_56_out);
  or or_56 (or_56_out, sltu_2__27, sltu_1__27);
  or or_57 (_28, and_50_out, or_58_out);
  or or_58 (or_58_out, sltu_2__28, sltu_1__28);
  or or_59 (_29, and_50_out, or_60_out);
  or or_60 (or_60_out, sltu_2__29, sltu_1__29);
  or or_61 (_30, and_50_out, or_62_out);
  or or_62 (or_62_out, sltu_2__30, sltu_1__30);
  or or_63 (_31, and_50_out, or_64_out);
  or or_64 (or_64_out, sltu_2__31, sltu_1__31);

  // Notes on the sheet:
  //   A
  //   B
endmodule

module sltu (
  input  B0,
  input  B1,
  input  B2,
  input  B3,
  input  B4,
  input  B5,
  input  B6,
  input  B7,
  input  B8,
  input  B9,
  input  B10,
  input  B11,
  input  B12,
  input  B13,
  input  B14,
  input  B15,
  input  B16,
  input  B17,
  input  B18,
  input  B19,
  input  B20,
  input  B21,
  input  B22,
  input  B23,
  input  B24,
  input  B25,
  input  B26,
  input  B27,
  input  B28,
  input  B29,
  input  B30,
  input  B31,
  input  A0,
  input  A1,
  input  A2,
  input  A3,
  input  A4,
  input  A5,
  input  A6,
  input  A7,
  input  A8,
  input  A9,
  input  A10,
  input  A11,
  input  A12,
  input  A13,
  input  A14,
  input  A15,
  input  A16,
  input  A17,
  input  A18,
  input  A19,
  input  A20,
  input  A21,
  input  A22,
  input  A23,
  input  A24,
  input  A25,
  input  A26,
  input  A27,
  input  A28,
  input  A29,
  input  A30,
  input  A31,
  output _0,
  output _1,
  output _2,
  output _3,
  output _4,
  output _5,
  output _6,
  output _7,
  output _8,
  output _9,
  output _10,
  output _11,
  output _12,
  output _13,
  output _14,
  output _15,
  output _16,
  output _17,
  output _18,
  output _19,
  output _20,
  output _21,
  output _22,
  output _23,
  output _24,
  output _25,
  output _26,
  output _27,
  output _28,
  output _29,
  output _30,
  output _31
);

  wire and_1_out, and_2_out, and_3_out, and_4_out, and_5_out, and_6_out, and_7_out, and_8_out, and_9_out,
       and_10_out, and_11_out, and_12_out, and_13_out, and_14_out, and_15_out, and_16_out, and_17_out,
       and_18_out, and_19_out, and_20_out, and_21_out, and_22_out, and_23_out, and_24_out, and_25_out,
       and_26_out, and_27_out, and_28_out, and_29_out, and_30_out, and_31_out, and_32_out, and_33_out,
       and_34_out, and_35_out, and_36_out, and_37_out, and_38_out, and_39_out, and_40_out, and_41_out,
       and_42_out, and_43_out, and_44_out, and_45_out, and_46_out, and_47_out, and_48_out, and_49_out,
       and_50_out, and_51_out, and_52_out, and_53_out, and_54_out, and_55_out, and_56_out, and_57_out,
       and_58_out, and_59_out, and_60_out, and_61_out, and_62_out, and_63_out, and_64_out, and_65_out,
       and_66_out, and_67_out, and_68_out, and_69_out, and_70_out, and_71_out, and_72_out, and_73_out,
       and_74_out, and_75_out, and_76_out, and_77_out, and_78_out, and_79_out, and_80_out, and_81_out,
       and_82_out, and_83_out, and_84_out, and_85_out, and_86_out, and_87_out, and_88_out, and_89_out,
       and_90_out, and_91_out, and_92_out, and_93_out, not_1_out, not_2_out, not_3_out, not_4_out, not_5_out,
       not_6_out, not_7_out, not_8_out, not_9_out, not_10_out, not_11_out, not_12_out, not_13_out,
       not_14_out, not_15_out, not_16_out, not_17_out, not_18_out, not_19_out, not_20_out, not_21_out,
       not_22_out, not_23_out, not_24_out, not_25_out, not_26_out, not_27_out, not_28_out, not_29_out,
       not_30_out, not_31_out, not_32_out, not_33_out, not_34_out, not_35_out, not_36_out, not_37_out,
       not_38_out, not_39_out, not_40_out, not_41_out, not_42_out, not_43_out, not_44_out, not_45_out,
       not_46_out, not_47_out, not_48_out, not_49_out, not_50_out, not_51_out, not_52_out, not_53_out,
       not_54_out, not_55_out, not_56_out, not_57_out, not_58_out, not_59_out, not_60_out, not_61_out,
       not_62_out, not_63_out, not_64_out, not_65_out, not_66_out, not_67_out, not_68_out, not_69_out,
       not_70_out, not_71_out, not_72_out, not_73_out, not_74_out, not_75_out, not_76_out, not_77_out,
       not_78_out, not_79_out, not_80_out, not_81_out, not_82_out, not_83_out, not_84_out, not_85_out,
       not_86_out, not_87_out, not_88_out, not_89_out, not_90_out, not_91_out, not_92_out, not_93_out,
       not_94_out, or_1_out, or_2_out, or_3_out, or_4_out, or_5_out, or_6_out, or_7_out, or_8_out, or_9_out,
       or_10_out, or_11_out, or_12_out, or_13_out, or_14_out, or_15_out, or_16_out, or_17_out, or_18_out,
       or_19_out, or_20_out, or_21_out, or_22_out, or_23_out, or_24_out, or_25_out, or_26_out, or_27_out,
       or_28_out, or_29_out, or_30_out;

  not not_1 (not_1_out, B31);
  not not_2 (not_2_out, A31);
  not not_3 (not_3_out, A31);
  not not_4 (not_4_out, B30);
  not not_5 (not_5_out, A30);
  not not_6 (not_6_out, A30);
  and and_1 (and_1_out, not_1_out, not_2_out);
  and and_2 (and_2_out, B31, not_3_out);
  or or_1 (or_1_out, and_2_out, and_5_out);
  or or_2 (or_2_out, or_1_out, and_8_out);
  or or_3 (or_3_out, or_2_out, and_10_out);
  or or_4 (or_4_out, or_3_out, and_13_out);
  or or_5 (or_5_out, or_4_out, and_16_out);
  or or_6 (or_6_out, or_5_out, and_19_out);
  and and_3 (and_3_out, not_4_out, not_5_out);
  and and_4 (and_4_out, and_3_out, and_1_out);
  and and_5 (and_5_out, B30, not_6_out, and_1_out);
  or or_7 (or_7_out, or_6_out, and_22_out);
  or or_8 (or_8_out, or_7_out, and_25_out);
  or or_9 (or_9_out, or_8_out, and_29_out);
  or or_10 (or_10_out, or_9_out, and_32_out);
  or or_11 (or_11_out, or_10_out, and_34_out);
  or or_12 (or_12_out, or_11_out, and_37_out);
  or or_13 (or_13_out, or_12_out, and_40_out);
  or or_14 (or_14_out, or_13_out, and_43_out);
  not not_7 (not_7_out, B29);
  not not_8 (not_8_out, A29);
  not not_9 (not_9_out, A29);
  or or_15 (or_15_out, or_14_out, and_46_out);
  or or_16 (or_16_out, or_15_out, and_49_out);
  or or_17 (or_17_out, or_16_out, and_53_out);
  or or_18 (or_18_out, or_17_out, and_56_out);
  or or_19 (or_19_out, or_18_out, and_58_out);
  or or_20 (or_20_out, or_19_out, and_61_out);
  or or_21 (or_21_out, or_20_out, and_64_out);
  or or_22 (or_22_out, or_21_out, and_67_out);
  and and_6 (and_6_out, not_7_out, not_8_out);
  and and_7 (and_7_out, and_6_out, and_4_out);
  and and_8 (and_8_out, B29, not_9_out, and_4_out);
  or or_23 (or_23_out, or_22_out, and_70_out);
  or or_24 (or_24_out, or_23_out, and_73_out);
  or or_25 (or_25_out, or_24_out, and_77_out);
  or or_26 (or_26_out, or_25_out, and_80_out);
  or or_27 (or_27_out, or_26_out, and_82_out);
  or or_28 (or_28_out, or_27_out, and_85_out);
  or or_29 (or_29_out, or_28_out, and_88_out);
  or or_30 (or_30_out, or_29_out, and_91_out);
  not not_10 (not_10_out, B28);
  and and_9 (and_9_out, not_10_out, not_11_out);
  not not_11 (not_11_out, A28);
  and and_10 (and_10_out, B28, not_12_out, and_7_out);
  not not_12 (not_12_out, A28);
  or or_31 (_0, or_30_out, and_93_out);
  and and_11 (and_11_out, and_9_out, and_7_out);
  not not_13 (not_13_out, B27);
  and and_12 (and_12_out, not_13_out, not_14_out);
  not not_14 (not_14_out, A27);
  and and_13 (and_13_out, B27, not_15_out, and_11_out);
  not not_15 (not_15_out, A27);
  and and_14 (and_14_out, and_12_out, and_11_out);
  not not_16 (not_16_out, B26);
  and and_15 (and_15_out, not_16_out, not_17_out);
  not not_17 (not_17_out, A26);
  not not_18 (not_18_out, A26);
  and and_16 (and_16_out, B26, not_18_out, and_14_out);
  not not_19 (not_19_out, A25);
  and and_17 (and_17_out, and_15_out, and_14_out);
  not not_20 (not_20_out, B25);
  and and_18 (and_18_out, not_20_out, not_21_out);
  not not_21 (not_21_out, A25);
  and and_19 (and_19_out, B25, not_19_out, and_17_out);
  not not_22 (not_22_out, A24);
  and and_20 (and_20_out, and_18_out, and_17_out);
  not not_23 (not_23_out, B24);
  and and_21 (and_21_out, not_23_out, not_24_out);
  not not_24 (not_24_out, A24);
  and and_22 (and_22_out, B24, not_22_out, and_20_out);
  not not_25 (not_25_out, B23);
  not not_26 (not_26_out, A23);
  not not_27 (not_27_out, A23);
  and and_23 (and_23_out, and_21_out, and_20_out);
  and and_24 (and_24_out, not_25_out, not_26_out);
  and and_25 (and_25_out, B23, not_27_out, and_23_out);
  not not_28 (not_28_out, B22);
  not not_29 (not_29_out, A22);
  not not_30 (not_30_out, A22);
  and and_26 (and_26_out, and_24_out, and_23_out);
  and and_27 (and_27_out, not_28_out, not_29_out);
  and and_28 (and_28_out, and_27_out, and_26_out);
  and and_29 (and_29_out, B22, not_30_out, and_26_out);
  not not_31 (not_31_out, B21);
  not not_32 (not_32_out, A21);
  not not_33 (not_33_out, A21);
  and and_30 (and_30_out, not_31_out, not_32_out);
  and and_31 (and_31_out, and_30_out, and_28_out);
  and and_32 (and_32_out, B21, not_33_out, and_28_out);
  not not_34 (not_34_out, B20);
  and and_33 (and_33_out, not_34_out, not_35_out);
  not not_35 (not_35_out, A20);
  not not_36 (not_36_out, A20);
  and and_34 (and_34_out, B20, not_36_out, and_31_out);
  and and_35 (and_35_out, and_33_out, and_31_out);
  not not_37 (not_37_out, B19);
  and and_36 (and_36_out, not_37_out, not_38_out);
  not not_38 (not_38_out, A19);
  not not_39 (not_39_out, A19);
  and and_37 (and_37_out, B19, not_39_out, and_35_out);
  and and_38 (and_38_out, and_36_out, and_35_out);
  not not_40 (not_40_out, B18);
  and and_39 (and_39_out, not_40_out, not_41_out);
  not not_41 (not_41_out, A18);
  not not_42 (not_42_out, A18);
  and and_40 (and_40_out, B18, not_42_out, and_38_out);
  not not_43 (not_43_out, A17);
  and and_41 (and_41_out, and_39_out, and_38_out);
  not not_44 (not_44_out, B17);
  and and_42 (and_42_out, not_44_out, not_45_out);
  not not_45 (not_45_out, A17);
  and and_43 (and_43_out, B17, not_43_out, and_41_out);
  not not_46 (not_46_out, A16);
  and and_44 (and_44_out, and_42_out, and_41_out);
  not not_47 (not_47_out, B16);
  and and_45 (and_45_out, not_47_out, not_48_out);
  not not_48 (not_48_out, A16);
  and and_46 (and_46_out, B16, not_46_out, and_44_out);
  not not_49 (not_49_out, B15);
  not not_50 (not_50_out, A15);
  not not_51 (not_51_out, A15);
  and and_47 (and_47_out, and_45_out, and_44_out);
  and and_48 (and_48_out, not_49_out, not_50_out);
  and and_49 (and_49_out, B15, not_51_out, and_47_out);
  not not_52 (not_52_out, B14);
  not not_53 (not_53_out, A14);
  not not_54 (not_54_out, A14);
  and and_50 (and_50_out, and_48_out, and_47_out);
  and and_51 (and_51_out, not_52_out, not_53_out);
  and and_52 (and_52_out, and_51_out, and_50_out);
  and and_53 (and_53_out, B14, not_54_out, and_50_out);
  not not_55 (not_55_out, B13);
  not not_56 (not_56_out, A13);
  not not_57 (not_57_out, A13);
  and and_54 (and_54_out, not_55_out, not_56_out);
  and and_55 (and_55_out, and_54_out, and_52_out);
  and and_56 (and_56_out, B13, not_57_out, and_52_out);
  not not_58 (not_58_out, B12);
  and and_57 (and_57_out, not_58_out, not_59_out);
  not not_59 (not_59_out, A12);
  not not_60 (not_60_out, A12);
  and and_58 (and_58_out, B12, not_60_out, and_55_out);
  and and_59 (and_59_out, and_57_out, and_55_out);
  not not_61 (not_61_out, B11);
  and and_60 (and_60_out, not_61_out, not_62_out);
  not not_62 (not_62_out, A11);
  and and_61 (and_61_out, B11, not_63_out, and_59_out);
  not not_63 (not_63_out, A11);
  and and_62 (and_62_out, and_60_out, and_59_out);
  not not_64 (not_64_out, B10);
  and and_63 (and_63_out, not_64_out, not_65_out);
  not not_65 (not_65_out, A10);
  and and_64 (and_64_out, B10, not_66_out, and_62_out);
  not not_66 (not_66_out, A10);
  not not_67 (not_67_out, A9);
  and and_65 (and_65_out, and_63_out, and_62_out);
  not not_68 (not_68_out, B9);
  and and_66 (and_66_out, not_68_out, not_69_out);
  not not_69 (not_69_out, A9);
  and and_67 (and_67_out, B9, not_67_out, and_65_out);
  not not_70 (not_70_out, A8);
  and and_68 (and_68_out, and_66_out, and_65_out);
  not not_71 (not_71_out, B8);
  and and_69 (and_69_out, not_71_out, not_72_out);
  not not_72 (not_72_out, A8);
  and and_70 (and_70_out, B8, not_70_out, and_68_out);
  not not_73 (not_73_out, B7);
  not not_74 (not_74_out, A7);
  not not_75 (not_75_out, A7);
  and and_71 (and_71_out, and_69_out, and_68_out);
  and and_72 (and_72_out, not_73_out, not_74_out);
  and and_73 (and_73_out, B7, not_75_out, and_71_out);
  not not_76 (not_76_out, B6);
  not not_77 (not_77_out, A6);
  not not_78 (not_78_out, A6);
  and and_74 (and_74_out, and_72_out, and_71_out);
  and and_75 (and_75_out, not_76_out, not_77_out);
  and and_76 (and_76_out, and_75_out, and_74_out);
  and and_77 (and_77_out, B6, not_78_out, and_74_out);
  not not_79 (not_79_out, B5);
  not not_80 (not_80_out, A5);
  not not_81 (not_81_out, A5);
  and and_78 (and_78_out, not_79_out, not_80_out);
  and and_79 (and_79_out, and_78_out, and_76_out);
  and and_80 (and_80_out, B5, not_81_out, and_76_out);
  not not_82 (not_82_out, B4);
  and and_81 (and_81_out, not_82_out, not_83_out);
  not not_83 (not_83_out, A4);
  not not_84 (not_84_out, A4);
  and and_82 (and_82_out, B4, not_84_out, and_79_out);
  and and_83 (and_83_out, and_81_out, and_79_out);
  not not_85 (not_85_out, B3);
  and and_84 (and_84_out, not_85_out, not_86_out);
  not not_86 (not_86_out, A3);
  not not_87 (not_87_out, A3);
  and and_85 (and_85_out, B3, not_87_out, and_83_out);
  and and_86 (and_86_out, and_84_out, and_83_out);
  not not_88 (not_88_out, B2);
  and and_87 (and_87_out, not_88_out, not_89_out);
  not not_89 (not_89_out, A2);
  not not_90 (not_90_out, A2);
  and and_88 (and_88_out, B2, not_90_out, and_86_out);
  not not_91 (not_91_out, A1);
  and and_89 (and_89_out, and_87_out, and_86_out);
  not not_92 (not_92_out, B1);
  and and_90 (and_90_out, not_92_out, not_93_out);
  not not_93 (not_93_out, A1);
  and and_91 (and_91_out, B1, not_91_out, and_89_out);
  not not_94 (not_94_out, A0);
  and and_92 (and_92_out, and_90_out, and_89_out);
  and and_93 (and_93_out, B0, not_94_out, and_92_out);

  assign _1 = _0;
  assign _2 = _0;
  assign _3 = _0;
  assign _4 = _0;
  assign _5 = _0;
  assign _6 = _0;
  assign _7 = _0;
  assign _8 = _0;
  assign _9 = _0;
  assign _10 = _0;
  assign _11 = _0;
  assign _12 = _0;
  assign _13 = _0;
  assign _14 = _0;
  assign _15 = _0;
  assign _16 = _0;
  assign _17 = _0;
  assign _18 = _0;
  assign _19 = _0;
  assign _20 = _0;
  assign _21 = _0;
  assign _22 = _0;
  assign _23 = _0;
  assign _24 = _0;
  assign _25 = _0;
  assign _26 = _0;
  assign _27 = _0;
  assign _28 = _0;
  assign _29 = _0;
  assign _30 = _0;
  assign _31 = _0;

  // Notes on the sheet:
  //   b
  //   a
  //   b
  //   a
  //   b
  //   a
  //   b
  //   a
  //   b
  //   a
  //   b
  //   a
  //   b
  //   a
  //   b
  //   a
  //   b
  //   a
  //   b
  //   a
  //   b
  //   a
  //   b
  //   a
  //   b
  //   a
  //   b
  //   a
  //   b
  //   a
  //   b
  //   a
  //   b
  //   a
  //   b
  //   a
  //   b
  //   a
  //   b
  //   a
  //   b
  //   a
  //   b
  //   a
  //   b
  //   a
  //   b
  //   a
  //   b
  //   a
  //   b
  //   a
  //   b
  //   a
  //   b
  //   a
  //   b
  //   a
  //   b
  //   a
endmodule

module sltui (
  input  B0,
  input  B1,
  input  B2,
  input  B3,
  input  B4,
  input  B5,
  input  B6,
  input  B7,
  input  B8,
  input  B9,
  input  B10,
  input  B11,
  input  B12,
  input  B13,
  input  B14,
  input  B15,
  input  A0,
  input  A1,
  input  A2,
  input  A3,
  input  A4,
  input  A5,
  input  A6,
  input  A7,
  input  A8,
  input  A9,
  input  A10,
  input  A11,
  input  A12,
  input  A13,
  input  A14,
  input  A15,
  input  A16,
  input  A17,
  input  A18,
  input  A19,
  input  A20,
  input  A21,
  input  A22,
  input  A23,
  input  A24,
  input  A25,
  input  A26,
  input  A27,
  input  A28,
  input  A29,
  input  A30,
  input  A31,
  output _0,
  output _1,
  output _2,
  output _3,
  output _4,
  output _5,
  output _6,
  output _7,
  output _8,
  output _9,
  output _10,
  output _11,
  output _12,
  output _13,
  output _14,
  output _15,
  output _16,
  output _17,
  output _18,
  output _19,
  output _20,
  output _21,
  output _22,
  output _23,
  output _24,
  output _25,
  output _26,
  output _27,
  output _28,
  output _29,
  output _30,
  output _31
);

  wire and_1_out, and_2_out, and_3_out, and_4_out, and_5_out, and_6_out, and_7_out, and_8_out, and_9_out,
       and_10_out, and_11_out, and_12_out, and_13_out, and_14_out, and_15_out, and_16_out, and_17_out,
       and_18_out, and_19_out, and_20_out, and_21_out, and_22_out, and_23_out, and_24_out, and_25_out,
       and_26_out, and_27_out, and_28_out, and_29_out, and_30_out, and_31_out, and_32_out, and_33_out,
       and_34_out, and_35_out, and_36_out, and_37_out, and_38_out, and_39_out, and_40_out, and_41_out,
       and_42_out, and_43_out, and_44_out, and_45_out, and_46_out, and_47_out, and_48_out, and_49_out,
       and_50_out, and_51_out, and_52_out, and_53_out, and_54_out, and_55_out, and_56_out, and_57_out,
       and_58_out, and_59_out, and_60_out, and_61_out, and_62_out, and_63_out, and_64_out, and_65_out,
       and_66_out, and_67_out, and_68_out, and_69_out, and_70_out, and_71_out, and_72_out, and_73_out,
       and_74_out, and_75_out, and_76_out, and_77_out, and_78_out, and_79_out, and_80_out, and_81_out,
       and_82_out, and_83_out, and_84_out, and_85_out, and_86_out, and_87_out, and_88_out, and_89_out,
       and_90_out, and_91_out, and_92_out, and_93_out, not_1_out, not_2_out, not_3_out, not_4_out, not_5_out,
       not_6_out, not_7_out, not_8_out, not_9_out, not_10_out, not_11_out, not_12_out, not_13_out,
       not_14_out, not_15_out, not_16_out, not_17_out, not_18_out, not_19_out, not_20_out, not_21_out,
       not_22_out, not_23_out, not_24_out, not_25_out, not_26_out, not_27_out, not_28_out, not_29_out,
       not_30_out, not_31_out, not_32_out, not_33_out, not_34_out, not_35_out, not_36_out, not_37_out,
       not_38_out, not_39_out, not_40_out, not_41_out, not_42_out, not_43_out, not_44_out, not_45_out,
       not_46_out, not_47_out, not_48_out, not_49_out, not_50_out, not_51_out, not_52_out, not_53_out,
       not_54_out, not_55_out, not_56_out, not_57_out, not_58_out, not_59_out, not_60_out, not_61_out,
       not_62_out, not_63_out, not_64_out, not_65_out, not_66_out, not_67_out, not_68_out, not_69_out,
       not_70_out, not_71_out, not_72_out, not_73_out, not_74_out, not_75_out, not_76_out, not_77_out,
       not_78_out, not_79_out, not_80_out, not_81_out, not_82_out, not_83_out, not_84_out, not_85_out,
       not_86_out, not_87_out, not_88_out, not_89_out, not_90_out, not_91_out, not_92_out, not_93_out,
       not_94_out, or_1_out, or_2_out, or_3_out, or_4_out, or_5_out, or_6_out, or_7_out, or_8_out, or_9_out,
       or_10_out, or_11_out, or_12_out, or_13_out, or_14_out, or_15_out, or_16_out, or_17_out, or_18_out,
       or_19_out, or_20_out, or_21_out, or_22_out, or_23_out, or_24_out, or_25_out, or_26_out, or_27_out,
       or_28_out, or_29_out, or_30_out;

  not not_1 (not_1_out, 1'b0);
  not not_2 (not_2_out, A31);
  not not_3 (not_3_out, A31);
  not not_4 (not_4_out, 1'b0);
  not not_5 (not_5_out, A30);
  not not_6 (not_6_out, A30);
  and and_1 (and_1_out, not_1_out, not_2_out);
  and and_2 (and_2_out, 1'b0, not_3_out);
  or or_1 (or_1_out, and_2_out, and_5_out);
  or or_2 (or_2_out, or_1_out, and_8_out);
  or or_3 (or_3_out, or_2_out, and_10_out);
  or or_4 (or_4_out, or_3_out, and_13_out);
  or or_5 (or_5_out, or_4_out, and_16_out);
  or or_6 (or_6_out, or_5_out, and_19_out);
  and and_3 (and_3_out, not_4_out, not_5_out);
  and and_4 (and_4_out, and_3_out, and_1_out);
  and and_5 (and_5_out, 1'b0, not_6_out, and_1_out);
  or or_7 (or_7_out, or_6_out, and_22_out);
  or or_8 (or_8_out, or_7_out, and_25_out);
  or or_9 (or_9_out, or_8_out, and_29_out);
  or or_10 (or_10_out, or_9_out, and_32_out);
  or or_11 (or_11_out, or_10_out, and_34_out);
  or or_12 (or_12_out, or_11_out, and_37_out);
  or or_13 (or_13_out, or_12_out, and_40_out);
  or or_14 (or_14_out, or_13_out, and_43_out);
  not not_7 (not_7_out, 1'b0);
  not not_8 (not_8_out, A29);
  not not_9 (not_9_out, A29);
  or or_15 (or_15_out, or_14_out, and_46_out);
  or or_16 (or_16_out, or_15_out, and_49_out);
  or or_17 (or_17_out, or_16_out, and_53_out);
  or or_18 (or_18_out, or_17_out, and_56_out);
  or or_19 (or_19_out, or_18_out, and_58_out);
  or or_20 (or_20_out, or_19_out, and_61_out);
  or or_21 (or_21_out, or_20_out, and_64_out);
  or or_22 (or_22_out, or_21_out, and_67_out);
  and and_6 (and_6_out, not_7_out, not_8_out);
  and and_7 (and_7_out, and_6_out, and_4_out);
  and and_8 (and_8_out, 1'b0, not_9_out, and_4_out);
  or or_23 (or_23_out, or_22_out, and_70_out);
  or or_24 (or_24_out, or_23_out, and_73_out);
  or or_25 (or_25_out, or_24_out, and_77_out);
  or or_26 (or_26_out, or_25_out, and_80_out);
  or or_27 (or_27_out, or_26_out, and_82_out);
  or or_28 (or_28_out, or_27_out, and_85_out);
  or or_29 (or_29_out, or_28_out, and_88_out);
  or or_30 (or_30_out, or_29_out, and_91_out);
  not not_10 (not_10_out, 1'b0);
  and and_9 (and_9_out, not_10_out, not_11_out);
  not not_11 (not_11_out, A28);
  not not_12 (not_12_out, A28);
  and and_10 (and_10_out, 1'b0, not_12_out, and_7_out);
  or or_31 (_0, or_30_out, and_93_out);
  and and_11 (and_11_out, and_9_out, and_7_out);
  not not_13 (not_13_out, 1'b0);
  and and_12 (and_12_out, not_13_out, not_14_out);
  not not_14 (not_14_out, A27);
  not not_15 (not_15_out, A27);
  and and_13 (and_13_out, 1'b0, not_15_out, and_11_out);
  and and_14 (and_14_out, and_12_out, and_11_out);
  not not_16 (not_16_out, 1'b0);
  and and_15 (and_15_out, not_16_out, not_17_out);
  not not_17 (not_17_out, A26);
  not not_18 (not_18_out, A26);
  and and_16 (and_16_out, 1'b0, not_18_out, and_14_out);
  not not_19 (not_19_out, A25);
  and and_17 (and_17_out, and_15_out, and_14_out);
  not not_20 (not_20_out, 1'b0);
  and and_18 (and_18_out, not_20_out, not_21_out);
  not not_21 (not_21_out, A25);
  and and_19 (and_19_out, 1'b0, not_19_out, and_17_out);
  not not_22 (not_22_out, A24);
  and and_20 (and_20_out, and_18_out, and_17_out);
  not not_23 (not_23_out, 1'b0);
  and and_21 (and_21_out, not_23_out, not_24_out);
  not not_24 (not_24_out, A24);
  and and_22 (and_22_out, 1'b0, not_22_out, and_20_out);
  not not_25 (not_25_out, 1'b0);
  not not_26 (not_26_out, A23);
  not not_27 (not_27_out, A23);
  and and_23 (and_23_out, and_21_out, and_20_out);
  and and_24 (and_24_out, not_25_out, not_26_out);
  and and_25 (and_25_out, 1'b0, not_27_out, and_23_out);
  not not_28 (not_28_out, 1'b0);
  not not_29 (not_29_out, A22);
  not not_30 (not_30_out, A22);
  and and_26 (and_26_out, and_24_out, and_23_out);
  and and_27 (and_27_out, not_28_out, not_29_out);
  and and_28 (and_28_out, and_27_out, and_26_out);
  and and_29 (and_29_out, 1'b0, not_30_out, and_26_out);
  not not_31 (not_31_out, 1'b0);
  not not_32 (not_32_out, A21);
  not not_33 (not_33_out, A21);
  and and_30 (and_30_out, not_31_out, not_32_out);
  and and_31 (and_31_out, and_30_out, and_28_out);
  and and_32 (and_32_out, 1'b0, not_33_out, and_28_out);
  not not_34 (not_34_out, 1'b0);
  and and_33 (and_33_out, not_34_out, not_35_out);
  not not_35 (not_35_out, A20);
  and and_34 (and_34_out, 1'b0, not_36_out, and_31_out);
  not not_36 (not_36_out, A20);
  and and_35 (and_35_out, and_33_out, and_31_out);
  not not_37 (not_37_out, 1'b0);
  and and_36 (and_36_out, not_37_out, not_38_out);
  not not_38 (not_38_out, A19);
  not not_39 (not_39_out, A19);
  and and_37 (and_37_out, 1'b0, not_39_out, and_35_out);
  and and_38 (and_38_out, and_36_out, and_35_out);
  not not_40 (not_40_out, 1'b0);
  and and_39 (and_39_out, not_40_out, not_41_out);
  not not_41 (not_41_out, A18);
  not not_42 (not_42_out, A18);
  and and_40 (and_40_out, 1'b0, not_42_out, and_38_out);
  not not_43 (not_43_out, A17);
  and and_41 (and_41_out, and_39_out, and_38_out);
  not not_44 (not_44_out, 1'b0);
  and and_42 (and_42_out, not_44_out, not_45_out);
  not not_45 (not_45_out, A17);
  and and_43 (and_43_out, 1'b0, not_43_out, and_41_out);
  not not_46 (not_46_out, A16);
  and and_44 (and_44_out, and_42_out, and_41_out);
  not not_47 (not_47_out, 1'b0);
  and and_45 (and_45_out, not_47_out, not_48_out);
  not not_48 (not_48_out, A16);
  and and_46 (and_46_out, 1'b0, not_46_out, and_44_out);
  not not_49 (not_49_out, B15);
  not not_50 (not_50_out, A15);
  not not_51 (not_51_out, A15);
  and and_47 (and_47_out, and_45_out, and_44_out);
  and and_48 (and_48_out, not_49_out, not_50_out);
  and and_49 (and_49_out, B15, not_51_out, and_47_out);
  not not_52 (not_52_out, B14);
  not not_53 (not_53_out, A14);
  not not_54 (not_54_out, A14);
  and and_50 (and_50_out, and_48_out, and_47_out);
  and and_51 (and_51_out, not_52_out, not_53_out);
  and and_52 (and_52_out, and_51_out, and_50_out);
  and and_53 (and_53_out, B14, not_54_out, and_50_out);
  not not_55 (not_55_out, B13);
  not not_56 (not_56_out, A13);
  not not_57 (not_57_out, A13);
  and and_54 (and_54_out, not_55_out, not_56_out);
  and and_55 (and_55_out, and_54_out, and_52_out);
  and and_56 (and_56_out, B13, not_57_out, and_52_out);
  not not_58 (not_58_out, B12);
  and and_57 (and_57_out, not_58_out, not_59_out);
  not not_59 (not_59_out, A12);
  and and_58 (and_58_out, B12, not_60_out, and_55_out);
  not not_60 (not_60_out, A12);
  and and_59 (and_59_out, and_57_out, and_55_out);
  not not_61 (not_61_out, B11);
  and and_60 (and_60_out, not_61_out, not_62_out);
  not not_62 (not_62_out, A11);
  and and_61 (and_61_out, B11, not_63_out, and_59_out);
  not not_63 (not_63_out, A11);
  and and_62 (and_62_out, and_60_out, and_59_out);
  not not_64 (not_64_out, B10);
  and and_63 (and_63_out, not_64_out, not_65_out);
  not not_65 (not_65_out, A10);
  and and_64 (and_64_out, B10, not_66_out, and_62_out);
  not not_66 (not_66_out, A10);
  not not_67 (not_67_out, A9);
  and and_65 (and_65_out, and_63_out, and_62_out);
  not not_68 (not_68_out, B9);
  and and_66 (and_66_out, not_68_out, not_69_out);
  not not_69 (not_69_out, A9);
  and and_67 (and_67_out, B9, not_67_out, and_65_out);
  not not_70 (not_70_out, A8);
  and and_68 (and_68_out, and_66_out, and_65_out);
  not not_71 (not_71_out, B8);
  and and_69 (and_69_out, not_71_out, not_72_out);
  not not_72 (not_72_out, A8);
  and and_70 (and_70_out, B8, not_70_out, and_68_out);
  not not_73 (not_73_out, B7);
  not not_74 (not_74_out, A7);
  not not_75 (not_75_out, A7);
  and and_71 (and_71_out, and_69_out, and_68_out);
  and and_72 (and_72_out, not_73_out, not_74_out);
  and and_73 (and_73_out, B7, not_75_out, and_71_out);
  not not_76 (not_76_out, B6);
  not not_77 (not_77_out, A6);
  not not_78 (not_78_out, A6);
  and and_74 (and_74_out, and_72_out, and_71_out);
  and and_75 (and_75_out, not_76_out, not_77_out);
  and and_76 (and_76_out, and_75_out, and_74_out);
  and and_77 (and_77_out, B6, not_78_out, and_74_out);
  not not_79 (not_79_out, B5);
  not not_80 (not_80_out, A5);
  not not_81 (not_81_out, A5);
  and and_78 (and_78_out, not_79_out, not_80_out);
  and and_79 (and_79_out, and_78_out, and_76_out);
  and and_80 (and_80_out, B5, not_81_out, and_76_out);
  not not_82 (not_82_out, B4);
  and and_81 (and_81_out, not_82_out, not_83_out);
  not not_83 (not_83_out, A4);
  and and_82 (and_82_out, B4, not_84_out, and_79_out);
  not not_84 (not_84_out, A4);
  and and_83 (and_83_out, and_81_out, and_79_out);
  not not_85 (not_85_out, B3);
  and and_84 (and_84_out, not_85_out, not_86_out);
  not not_86 (not_86_out, A3);
  and and_85 (and_85_out, B3, not_87_out, and_83_out);
  not not_87 (not_87_out, A3);
  and and_86 (and_86_out, and_84_out, and_83_out);
  not not_88 (not_88_out, B2);
  and and_87 (and_87_out, not_88_out, not_89_out);
  not not_89 (not_89_out, A2);
  not not_90 (not_90_out, A2);
  and and_88 (and_88_out, B2, not_90_out, and_86_out);
  not not_91 (not_91_out, A1);
  and and_89 (and_89_out, and_87_out, and_86_out);
  not not_92 (not_92_out, B1);
  and and_90 (and_90_out, not_92_out, not_93_out);
  not not_93 (not_93_out, A1);
  and and_91 (and_91_out, B1, not_91_out, and_89_out);
  not not_94 (not_94_out, A0);
  and and_92 (and_92_out, and_90_out, and_89_out);
  and and_93 (and_93_out, B0, not_94_out, and_92_out);

  assign _1 = _0;
  assign _2 = _0;
  assign _3 = _0;
  assign _4 = _0;
  assign _5 = _0;
  assign _6 = _0;
  assign _7 = _0;
  assign _8 = _0;
  assign _9 = _0;
  assign _10 = _0;
  assign _11 = _0;
  assign _12 = _0;
  assign _13 = _0;
  assign _14 = _0;
  assign _15 = _0;
  assign _16 = _0;
  assign _17 = _0;
  assign _18 = _0;
  assign _19 = _0;
  assign _20 = _0;
  assign _21 = _0;
  assign _22 = _0;
  assign _23 = _0;
  assign _24 = _0;
  assign _25 = _0;
  assign _26 = _0;
  assign _27 = _0;
  assign _28 = _0;
  assign _29 = _0;
  assign _30 = _0;
  assign _31 = _0;

  // Notes on the sheet:
  //   b
  //   a
  //   b
  //   a
  //   b
  //   a
  //   b
  //   a
  //   b
  //   a
  //   b
  //   a
  //   b
  //   a
  //   b
  //   a
  //   b
  //   a
  //   b
  //   a
  //   b
  //   a
  //   b
  //   a
  //   b
  //   a
  //   b
  //   a
  //   b
  //   a
  //   b
  //   a
  //   b
  //   a
  //   b
  //   a
  //   b
  //   a
  //   b
  //   a
  //   b
  //   a
  //   b
  //   a
  //   b
  //   a
  //   b
  //   a
  //   b
  //   a
  //   b
  //   a
  //   b
  //   a
  //   b
  //   a
  //   b
  //   a
  //   b
  //   a
endmodule
