// Logisim project ALU.circ as structural Verilog: 1 circuit, main circuit ALU
module ALU (
  input  in_1,
  input  in_2,
  input  in_3,
  input  in_4,
  input  in_5,
  input  in_6,
  input  in_7,
  input  in_8,
  input  in_9,
  input  in_10,
  input  [31:0] in_11,
  input  [31:0] in_12,
  input  [15:0] in_13,
  output [31:0] out_14,
  output [31:0] out_15,
  output [31:0] out_16,
  output out_17,
  output out_18
);

  wire or_1_out, or_3_out;
  wire [31:0] alu_1_out_124, alu_1_out_125, not_1_out;
  wire [31:31] or_2_out;

  ALU_ALU alu_1 (
    ._2_0(in_11[0]), .in_12(in_11[1]), .in_13(in_11[2]), .in_14(in_11[3]), .in_15(in_11[4]),
    .in_16(in_11[5]), .in_17(in_11[6]), .in_18(in_11[7]), .in_19(in_11[8]), .in_20(in_11[9]),
    .in_21(in_11[10]), .in_22(in_11[11]), .in_23(in_11[12]), .in_24(in_11[13]), .in_25(in_11[14]),
    .in_26(in_11[15]), .in_27(in_11[16]), .in_28(in_11[17]), .in_29(in_11[18]), .in_30(in_11[19]),
    .in_31(in_11[20]), .in_32(in_11[21]), .in_33(in_11[22]), .in_34(in_11[23]), .in_35(in_11[24]),
    .in_36(in_11[25]), .in_37(in_11[26]), .in_38(in_11[27]), .in_39(in_11[28]), .in_40(in_11[29]),
    .in_41(in_11[30]), .in_42(in_11[31]), ._2_0_2(in_12[0]), .in_44(in_12[1]), .in_45(in_12[2]),
    .in_46(in_12[3]), .in_47(in_12[4]), .in_48(in_12[5]), .in_49(in_12[6]), .in_50(in_12[7]),
    .in_51(in_12[8]), .in_52(in_12[9]), .in_53(in_12[10]), .in_54(in_12[11]), .in_55(in_12[12]),
    .in_56(in_12[13]), .in_57(in_12[14]), .in_58(in_12[15]), .in_59(in_12[16]), .in_60(in_12[17]),
    .in_61(in_12[18]), .in_62(in_12[19]), .in_63(in_12[20]), .in_64(in_12[21]), .in_65(in_12[22]),
    .in_66(in_12[23]), .in_67(in_12[24]), .in_68(in_12[25]), .in_69(in_12[26]), .in_70(in_12[27]),
    .in_71(in_12[28]), .in_72(in_12[29]), .in_73(in_12[30]), .in_74(in_12[31]), ._2_0_3(in_13[0]),
    .in_76(in_13[1]), .in_77(in_13[2]), .in_78(in_13[3]), .in_79(in_13[4]), .in_80(in_13[5]),
    .in_81(in_13[6]), .in_82(in_13[7]), .in_83(in_13[8]), .in_84(in_13[9]), .in_85(in_13[10]),
    .in_86(in_13[11]), .in_87(in_13[12]), .in_88(in_13[13]), .in_89(in_13[14]), .in_90(in_13[15]),
    .add(in_1), .addi(in_2), .addu(in_3), .addiu(in_4), .sub(in_5), .subu(in_6), .mult(in_7), .multu(in_8),
    .div(in_9), .divu(in_10), .out_93(alu_1_out_124[31]), .out_94(alu_1_out_124[30]),
    .out_95(alu_1_out_124[29]), .out_96(alu_1_out_124[28]), .out_97(alu_1_out_124[27]),
    .out_98(alu_1_out_124[26]), .out_99(alu_1_out_124[25]), .out_100(alu_1_out_124[24]),
    .out_101(alu_1_out_124[23]), .out_102(alu_1_out_124[22]), .out_103(alu_1_out_124[21]),
    .out_104(alu_1_out_124[20]), .out_105(alu_1_out_124[19]), .out_106(alu_1_out_124[18]),
    .out_107(alu_1_out_124[17]), .out_108(alu_1_out_124[16]), .out_109(alu_1_out_124[15]),
    .out_110(alu_1_out_124[14]), .out_111(alu_1_out_124[13]), .out_112(alu_1_out_124[12]),
    .out_113(alu_1_out_124[11]), .out_114(alu_1_out_124[10]), .out_115(alu_1_out_124[9]),
    .out_116(alu_1_out_124[8]), .out_117(alu_1_out_124[7]), .out_118(alu_1_out_124[6]),
    .out_119(alu_1_out_124[5]), .out_120(alu_1_out_124[4]), .out_121(alu_1_out_124[3]),
    .out_122(alu_1_out_124[2]), .out_123(alu_1_out_124[1]), .out_124(alu_1_out_124[0]),
    .out_125(alu_1_out_125[0]), .out_126(alu_1_out_125[1]), .out_127(alu_1_out_125[2]),
    .out_128(alu_1_out_125[3]), .out_129(alu_1_out_125[4]), .out_130(alu_1_out_125[5]),
    .out_131(alu_1_out_125[6]), .out_132(alu_1_out_125[7]), .out_133(alu_1_out_125[8]),
    .out_134(alu_1_out_125[9]), .out_135(alu_1_out_125[10]), .out_136(alu_1_out_125[11]),
    .out_137(alu_1_out_125[12]), .out_138(alu_1_out_125[13]), .out_139(alu_1_out_125[14]),
    .out_140(alu_1_out_125[15]), .out_141(alu_1_out_125[16]), .out_142(alu_1_out_125[17]),
    .out_143(alu_1_out_125[18]), .out_144(alu_1_out_125[19]), .out_145(alu_1_out_125[20]),
    .out_146(alu_1_out_125[21]), .out_147(alu_1_out_125[22]), .out_148(alu_1_out_125[23]),
    .out_149(alu_1_out_125[24]), .out_150(alu_1_out_125[25]), .out_151(alu_1_out_125[26]),
    .out_152(alu_1_out_125[27]), .out_153(alu_1_out_125[28]), .out_154(alu_1_out_125[29]),
    .out_155(alu_1_out_125[30]), .out_156(alu_1_out_125[31]), .Carry(out_17), .Overflow(out_18));
  or or_1 (or_1_out, in_10, in_9);
  or or_2 (or_2_out[31], or_1_out, or_3_out);
  or or_3 (or_3_out, in_8, in_7);
  assign out_16 = {32{or_2_out[31]}} & alu_1_out_124;  // AND_Gate and_1, 32 bits wide
  assign not_1_out = ~{32{or_2_out[31]}};  // NOT_Gate not_1, 32 bits wide
  assign out_14 = not_1_out & alu_1_out_124;  // AND_Gate and_2, 32 bits wide
  assign out_15 = {32{or_2_out[31]}} & alu_1_out_125;  // AND_Gate and_3, 32 bits wide

  // Notes on the sheet:
  //   $s
  //   $t
  //   imm
  //   $d
  //   hi
  //   lo
endmodule
