// Logisim project Bitwise Logic Unit.circ as structural Verilog: 1 circuit, main circuit BLU
module BLU (
  input  in_1,
  input  in_2,
  input  in_3,
  input  in_4,
  input  in_5,
  input  in_6,
  input  in_7,
  input  in_8,
  input  in_9,
  input  in_10,
  input  in_11,
  input  in_12,
  input  in_13,
  input  in_14,
  input  in_15,
  input  in_16,
  input  in_17,
  input  in_18,
  input  in_19,
  input  in_20,
  input  in_21,
  input  in_22,
  input  in_23,
  input  in_24,
  input  [31:0] in_25,
  input  [31:0] in_26,
  input  [15:0] in_27,
  input  [4:0] in_28,
  output [31:0] out_29
);

  wire or_1_out, or_2_out, or_3_out, or_4_out, or_5_out, or_6_out, or_7_out, or_8_out, or_9_out, or_10_out,
       or_12_out, or_13_out, or_14_out, or_15_out, or_18_out, or_19_out, or_20_out, or_21_out;
  wire [4:0] and_8_out;
  wire [15:0] and_3_out, and_7_out, and_12_out;
  wire [15:15] or_11_out;
  wire [31:0] and_1_out, and_2_out, and_4_out, and_5_out, and_6_out, and_9_out, and_10_out, and_11_out,
       and_13_out, bitwise_logic_main_1__0, branch_unit_1__0, logical_unit_1__0, or_17_out;
  wire [31:31] or_16_out, or_22_out;

  or or_1 (or_1_out, in_1, in_2);
  or or_2 (or_2_out, in_5, in_6);
  or or_3 (or_3_out, in_3, in_4);
  or or_4 (or_4_out, or_1_out, or_3_out);
  or or_5 (or_5_out, or_2_out, or_7_out);
  or or_6 (or_6_out, or_4_out, or_5_out);
  or or_7 (or_7_out, in_7, in_8);
  or or_8 (or_8_out, in_9, in_10);
  or or_9 (or_9_out, in_11, in_12);
  or or_10 (or_10_out, or_8_out, or_9_out);
  or or_11 (or_11_out[15], or_6_out, or_10_out);
  assign and_1_out = in_25 & {32{or_11_out[15]}};  // AND_Gate and_1, 32 bits wide
  assign and_2_out = in_26 & {32{or_11_out[15]}};  // AND_Gate and_2, 32 bits wide
  Bitwise_Logic__Main bitwise_logic_main_1 (
    ._2_0(and_3_out[0]), .in_2(and_3_out[1]), .in_3(and_3_out[2]), .in_4(and_3_out[3]), .in_5(and_3_out[4]),
    .in_6(and_3_out[5]), .in_7(and_3_out[6]), .in_8(and_3_out[7]), .in_9(and_3_out[8]), .in_10(and_3_out[9]),
    .in_11(and_3_out[10]), .in_12(and_3_out[11]), .in_13(and_3_out[12]), .in_14(and_3_out[13]),
    .in_15(and_3_out[14]), .in_16(and_3_out[15]), ._2_0_2(and_1_out[0]), .in_18(and_1_out[1]),
    .in_19(and_1_out[2]), .in_20(and_1_out[3]), .in_21(and_1_out[4]), .in_22(and_1_out[5]),
    .in_23(and_1_out[6]), .in_24(and_1_out[7]), .in_25(and_1_out[8]), .in_26(and_1_out[9]),
    .in_27(and_1_out[10]), .in_28(and_1_out[11]), .in_29(and_1_out[12]), .in_30(and_1_out[13]),
    .in_31(and_1_out[14]), .in_32(and_1_out[15]), .in_33(and_1_out[16]), .in_34(and_1_out[17]),
    .in_35(and_1_out[18]), .in_36(and_1_out[19]), .in_37(and_1_out[20]), .in_38(and_1_out[21]),
    .in_39(and_1_out[22]), .in_40(and_1_out[23]), .in_41(and_1_out[24]), .in_42(and_1_out[25]),
    .in_43(and_1_out[26]), .in_44(and_1_out[27]), .in_45(and_1_out[28]), .in_46(and_1_out[29]),
    .in_47(and_1_out[30]), .t(and_1_out[31]), ._2_0_3(and_2_out[0]), .in_50(and_2_out[1]),
    .in_51(and_2_out[2]), .in_52(and_2_out[3]), .in_53(and_2_out[4]), .in_54(and_2_out[5]),
    .in_55(and_2_out[6]), .in_56(and_2_out[7]), .in_57(and_2_out[8]), .in_58(and_2_out[9]),
    .in_59(and_2_out[10]), .in_60(and_2_out[11]), .in_61(and_2_out[12]), .in_62(and_2_out[13]),
    .in_63(and_2_out[14]), .in_64(and_2_out[15]), .in_65(and_2_out[16]), .in_66(and_2_out[17]),
    .in_67(and_2_out[18]), .in_68(and_2_out[19]), .in_69(and_2_out[20]), .in_70(and_2_out[21]),
    .in_71(and_2_out[22]), .in_72(and_2_out[23]), .in_73(and_2_out[24]), .in_74(and_2_out[25]),
    .in_75(and_2_out[26]), .in_76(and_2_out[27]), .in_77(and_2_out[28]), .in_78(and_2_out[29]),
    .in_79(and_2_out[30]), .in_80(and_2_out[31]), ._0(bitwise_logic_main_1__0[0]),
    .out_94(bitwise_logic_main_1__0[1]), .out_95(bitwise_logic_main_1__0[2]),
    .out_96(bitwise_logic_main_1__0[3]), .out_97(bitwise_logic_main_1__0[4]),
    .out_98(bitwise_logic_main_1__0[5]), .out_99(bitwise_logic_main_1__0[6]),
    .out_100(bitwise_logic_main_1__0[7]), .out_101(bitwise_logic_main_1__0[8]),
    .out_102(bitwise_logic_main_1__0[9]), .out_103(bitwise_logic_main_1__0[10]),
    .out_104(bitwise_logic_main_1__0[11]), .out_105(bitwise_logic_main_1__0[12]),
    .out_106(bitwise_logic_main_1__0[13]), .out_107(bitwise_logic_main_1__0[14]),
    .out_108(bitwise_logic_main_1__0[15]), .out_109(bitwise_logic_main_1__0[16]),
    .out_110(bitwise_logic_main_1__0[17]), .out_111(bitwise_logic_main_1__0[18]),
    .out_112(bitwise_logic_main_1__0[19]), .out_113(bitwise_logic_main_1__0[20]),
    .out_114(bitwise_logic_main_1__0[21]), .out_115(bitwise_logic_main_1__0[22]),
    .out_116(bitwise_logic_main_1__0[23]), .out_117(bitwise_logic_main_1__0[24]),
    .out_118(bitwise_logic_main_1__0[25]), .out_119(bitwise_logic_main_1__0[26]),
    .out_120(bitwise_logic_main_1__0[27]), .out_121(bitwise_logic_main_1__0[28]),
    .out_122(bitwise_logic_main_1__0[29]), .out_123(bitwise_logic_main_1__0[30]),
    .out_124(bitwise_logic_main_1__0[31]), .\and (in_1), .andi(in_2), .\nand (in_3), .nandi(in_4),
    .\or (in_5), .ori(in_6), .\nor (in_7), .nori(in_8), .\xor (in_9), .xori(in_10), .\xnor (in_11),
    .xnori(in_12));
  assign and_3_out = {16{or_11_out[15]}} & in_27;  // AND_Gate and_3, 16 bits wide
  assign and_4_out = bitwise_logic_main_1__0 & {32{or_11_out[15]}};  // AND_Gate and_4, 32 bits wide
  assign and_5_out = in_26 & {32{or_16_out[31]}};  // AND_Gate and_5, 32 bits wide
  assign and_6_out = in_25 & {32{or_16_out[31]}};  // AND_Gate and_6, 32 bits wide
  assign and_7_out = {16{or_16_out[31]}} & in_27;  // AND_Gate and_7, 16 bits wide
  Logical_Unit logical_unit_1 (
    ._2_0(and_7_out[0]), .in_13(and_7_out[1]), .in_14(and_7_out[2]), .in_15(and_7_out[3]),
    .in_16(and_7_out[4]), .in_17(and_7_out[5]), .in_18(and_7_out[6]), .in_19(and_7_out[7]),
    .in_20(and_7_out[8]), .in_21(and_7_out[9]), .in_22(and_7_out[10]), .in_23(and_7_out[11]),
    .in_24(and_7_out[12]), .in_25(and_7_out[13]), .in_26(and_7_out[14]), .in_27(and_7_out[15]),
    ._2_0_2(and_5_out[0]), .in_29(and_5_out[1]), .in_30(and_5_out[2]), .in_31(and_5_out[3]),
    .in_32(and_5_out[4]), .in_33(and_5_out[5]), .in_34(and_5_out[6]), .in_35(and_5_out[7]),
    .in_36(and_5_out[8]), .in_37(and_5_out[9]), .in_38(and_5_out[10]), .in_39(and_5_out[11]),
    .in_40(and_5_out[12]), .in_41(and_5_out[13]), .in_42(and_5_out[14]), .in_43(and_5_out[15]),
    .in_44(and_5_out[16]), .in_45(and_5_out[17]), .in_46(and_5_out[18]), .in_47(and_5_out[19]),
    .in_48(and_5_out[20]), .in_49(and_5_out[21]), .in_50(and_5_out[22]), .in_51(and_5_out[23]),
    .in_52(and_5_out[24]), .in_53(and_5_out[25]), .in_54(and_5_out[26]), .in_55(and_5_out[27]),
    .in_56(and_5_out[28]), .in_57(and_5_out[29]), .in_58(and_5_out[30]), .in_59(and_5_out[31]),
    ._2_0_3(and_6_out[0]), .in_61(and_6_out[1]), .in_62(and_6_out[2]), .in_63(and_6_out[3]),
    .in_64(and_6_out[4]), .in_65(and_6_out[5]), .in_66(and_6_out[6]), .in_67(and_6_out[7]),
    .in_68(and_6_out[8]), .in_69(and_6_out[9]), .in_70(and_6_out[10]), .in_71(and_6_out[11]),
    .in_72(and_6_out[12]), .in_73(and_6_out[13]), .in_74(and_6_out[14]), .in_75(and_6_out[15]),
    .in_76(and_6_out[16]), .in_77(and_6_out[17]), .in_78(and_6_out[18]), .in_79(and_6_out[19]),
    .in_80(and_6_out[20]), .in_81(and_6_out[21]), .in_82(and_6_out[22]), .in_83(and_6_out[23]),
    .in_84(and_6_out[24]), .in_85(and_6_out[25]), .in_86(and_6_out[26]), .in_87(and_6_out[27]),
    .in_88(and_6_out[28]), .in_89(and_6_out[29]), .in_90(and_6_out[30]), .in_91(and_6_out[31]),
    ._0(logical_unit_1__0[0]), .out_93(logical_unit_1__0[1]), .out_94(logical_unit_1__0[2]),
    .out_95(logical_unit_1__0[3]), .out_96(logical_unit_1__0[4]), .out_97(logical_unit_1__0[5]),
    .out_98(logical_unit_1__0[6]), .out_99(logical_unit_1__0[7]), .out_100(logical_unit_1__0[8]),
    .out_101(logical_unit_1__0[9]), .out_102(logical_unit_1__0[10]), .out_103(logical_unit_1__0[11]),
    .out_104(logical_unit_1__0[12]), .out_105(logical_unit_1__0[13]), .out_106(logical_unit_1__0[14]),
    .out_107(logical_unit_1__0[15]), .out_108(logical_unit_1__0[16]), .out_109(logical_unit_1__0[17]),
    .out_110(logical_unit_1__0[18]), .out_111(logical_unit_1__0[19]), .out_112(logical_unit_1__0[20]),
    .out_113(logical_unit_1__0[21]), .out_114(logical_unit_1__0[22]), .out_115(logical_unit_1__0[23]),
    .out_116(logical_unit_1__0[24]), .out_117(logical_unit_1__0[25]), .out_118(logical_unit_1__0[26]),
    .out_119(logical_unit_1__0[27]), .out_120(logical_unit_1__0[28]), .out_121(logical_unit_1__0[29]),
    .out_122(logical_unit_1__0[30]), .out_123(logical_unit_1__0[31]), .in_1(in_13), .in_2(in_14),
    .in_3(in_15), .in_4(in_16), .in_5(in_17), .in_6(in_18), .H0(and_8_out[0]), .in_8(and_8_out[1]),
    .in_9(and_8_out[2]), .in_10(and_8_out[3]), .in_11(and_8_out[4]));
  or or_12 (or_12_out, in_15, in_16);
  or or_13 (or_13_out, in_13, in_14);
  or or_14 (or_14_out, or_13_out, or_12_out);
  or or_15 (or_15_out, in_17, in_18);
  or or_16 (or_16_out[31], or_14_out, or_15_out);
  assign and_8_out = in_28 & {5{or_16_out[31]}};  // AND_Gate and_8, 5 bits wide
  assign and_9_out = logical_unit_1__0 & {32{or_16_out[31]}};  // AND_Gate and_9, 32 bits wide
  assign and_10_out = in_25 & {32{or_22_out[31]}};  // AND_Gate and_10, 32 bits wide
  assign and_11_out = in_26 & {32{or_22_out[31]}};  // AND_Gate and_11, 32 bits wide
  Branch_Unit branch_unit_1 (
    ._2_0(and_11_out[0]), .in_8(and_11_out[1]), .in_9(and_11_out[2]), .in_10(and_11_out[3]),
    .in_11(and_11_out[4]), .in_12(and_11_out[5]), .in_13(and_11_out[6]), .in_14(and_11_out[7]),
    .in_15(and_11_out[8]), .in_16(and_11_out[9]), .in_17(and_11_out[10]), .in_18(and_11_out[11]),
    .in_19(and_11_out[12]), .in_20(and_11_out[13]), .in_21(and_11_out[14]), .in_22(and_11_out[15]),
    .in_23(and_11_out[16]), .in_24(and_11_out[17]), .in_25(and_11_out[18]), .in_26(and_11_out[19]),
    .in_27(and_11_out[20]), .in_28(and_11_out[21]), .in_29(and_11_out[22]), .in_30(and_11_out[23]),
    .in_31(and_11_out[24]), .in_32(and_11_out[25]), .in_33(and_11_out[26]), .in_34(and_11_out[27]),
    .in_35(and_11_out[28]), .in_36(and_11_out[29]), .in_37(and_11_out[30]), .in_38(and_11_out[31]),
    ._2_0_2(and_10_out[0]), .in_40(and_10_out[1]), .in_41(and_10_out[2]), .in_42(and_10_out[3]),
    .in_43(and_10_out[4]), .in_44(and_10_out[5]), .in_45(and_10_out[6]), .in_46(and_10_out[7]),
    .in_47(and_10_out[8]), .in_48(and_10_out[9]), .in_49(and_10_out[10]), .in_50(and_10_out[11]),
    .in_51(and_10_out[12]), .in_52(and_10_out[13]), .in_53(and_10_out[14]), .in_54(and_10_out[15]),
    .in_55(and_10_out[16]), .in_56(and_10_out[17]), .in_57(and_10_out[18]), .in_58(and_10_out[19]),
    .in_59(and_10_out[20]), .in_60(and_10_out[21]), .in_61(and_10_out[22]), .in_62(and_10_out[23]),
    .in_63(and_10_out[24]), .in_64(and_10_out[25]), .in_65(and_10_out[26]), .in_66(and_10_out[27]),
    .in_67(and_10_out[28]), .in_68(and_10_out[29]), .in_69(and_10_out[30]), .in_70(and_10_out[31]),
    ._2_0_3(and_12_out[0]), .in_72(and_12_out[1]), .in_73(and_12_out[2]), .in_74(and_12_out[3]),
    .in_75(and_12_out[4]), .in_76(and_12_out[5]), .in_77(and_12_out[6]), .in_78(and_12_out[7]),
    .in_79(and_12_out[8]), .in_80(and_12_out[9]), .in_81(and_12_out[10]), .in_82(and_12_out[11]),
    .in_83(and_12_out[12]), .in_84(and_12_out[13]), .in_85(and_12_out[14]), .in_86(and_12_out[15]),
    ._0(branch_unit_1__0[0]), .out_88(branch_unit_1__0[1]), .out_89(branch_unit_1__0[2]),
    .out_90(branch_unit_1__0[3]), .out_91(branch_unit_1__0[4]), .out_92(branch_unit_1__0[5]),
    .out_93(branch_unit_1__0[6]), .out_94(branch_unit_1__0[7]), .out_95(branch_unit_1__0[8]),
    .out_96(branch_unit_1__0[9]), .out_97(branch_unit_1__0[10]), .out_98(branch_unit_1__0[11]),
    .out_99(branch_unit_1__0[12]), .out_100(branch_unit_1__0[13]), .out_101(branch_unit_1__0[14]),
    .out_102(branch_unit_1__0[15]), .out_103(branch_unit_1__0[16]), .out_104(branch_unit_1__0[17]),
    .out_105(branch_unit_1__0[18]), .out_106(branch_unit_1__0[19]), .out_107(branch_unit_1__0[20]),
    .out_108(branch_unit_1__0[21]), .out_109(branch_unit_1__0[22]), .out_110(branch_unit_1__0[23]),
    .out_111(branch_unit_1__0[24]), .out_112(branch_unit_1__0[25]), .out_113(branch_unit_1__0[26]),
    .out_114(branch_unit_1__0[27]), .out_115(branch_unit_1__0[28]), .out_116(branch_unit_1__0[29]),
    .out_117(branch_unit_1__0[30]), .out_118(branch_unit_1__0[31]), .in_1(in_19), .in_2(in_20), .in_3(in_21),
    .in_4(in_22), .in_5(in_23), .in_6(in_24));
  assign or_17_out = and_4_out | and_9_out;  // OR_Gate or_17, 32 bits wide
  assign and_12_out = {16{or_22_out[31]}} & in_27;  // AND_Gate and_12, 16 bits wide
  or or_18 (or_18_out, in_19, in_20);
  or or_19 (or_19_out, in_21, in_22);
  or or_20 (or_20_out, or_18_out, or_19_out);
  or or_21 (or_21_out, in_23, in_24);
  or or_22 (or_22_out[31], or_20_out, or_21_out);
  assign and_13_out = branch_unit_1__0 & {32{or_22_out[31]}};  // AND_Gate and_13, 32 bits wide
  assign out_29 = or_17_out | and_13_out;  // OR_Gate or_23, 32 bits wide

  // Notes on the sheet:
  //   $s
  //   $t
  //   imm
  //   H
endmodule
