// Logisim project MIPS.circ as structural Verilog: 6 circuits, main circuit Init Check
module Init_Check (
  input  A0,
  input  A1,
  input  A2,
  input  A3,
  input  A4,
  input  A5,
  input  A6,
  input  A7,
  input  A8,
  input  A9,
  input  A10,
  input  A11,
  input  A12,
  input  A13,
  input  A14,
  input  A15,
  input  A16,
  input  A17,
  input  A18,
  input  A19,
  input  A20,
  input  A21,
  input  A22,
  input  A23,
  input  A24,
  input  A25,
  input  A26,
  input  A27,
  input  A28,
  input  A29,
  input  A30,
  input  A31,
  output out_33
);

  wire and_1_out, and_2_out, and_3_out, and_4_out, and_5_out, and_6_out, and_7_out, and_8_out, and_9_out,
       and_10_out, and_11_out, and_12_out, and_13_out, and_14_out, and_15_out, and_16_out, and_17_out,
       and_18_out, and_19_out, and_20_out, and_21_out, and_22_out, and_23_out, and_24_out, and_25_out,
       and_26_out, and_27_out, and_28_out, and_29_out, and_30_out;

  and and_1 (and_1_out, A0, A1);
  and and_2 (and_2_out, A2, A3);
  and and_3 (and_3_out, A4, A5);
  and and_4 (and_4_out, A6, A7);
  and and_5 (and_5_out, A8, A9);
  and and_6 (and_6_out, A10, A11);
  and and_7 (and_7_out, A12, A13);
  and and_8 (and_8_out, A14, A15);
  and and_9 (and_9_out, A16, A17);
  and and_10 (and_10_out, A18, A19);
  and and_11 (and_11_out, A20, A21);
  and and_12 (and_12_out, A22, A23);
  and and_13 (and_13_out, A24, A25);
  and and_14 (and_14_out, A26, A27);
  and and_15 (and_15_out, A28, A29);
  and and_16 (and_16_out, A30, A31);
  and and_17 (and_17_out, and_1_out, and_2_out);
  and and_18 (and_18_out, and_3_out, and_4_out);
  and and_19 (and_19_out, and_5_out, and_6_out);
  and and_20 (and_20_out, and_7_out, and_8_out);
  and and_21 (and_21_out, and_9_out, and_10_out);
  and and_22 (and_22_out, and_11_out, and_12_out);
  and and_23 (and_23_out, and_13_out, and_14_out);
  and and_24 (and_24_out, and_15_out, and_16_out);
  and and_25 (and_25_out, and_17_out, and_18_out);
  and and_26 (and_26_out, and_25_out, and_27_out);
  and and_27 (and_27_out, and_19_out, and_20_out);
  and and_28 (and_28_out, and_21_out, and_22_out);
  and and_29 (and_29_out, and_28_out, and_30_out);
  and and_30 (and_30_out, and_23_out, and_24_out);
  and and_31 (out_33, and_26_out, and_29_out);
endmodule

module syscall_noop (
  input  A0,
  input  A1,
  input  A2,
  input  A3,
  input  A4,
  input  A5,
  input  A6,
  input  A7,
  input  A8,
  input  A9,
  input  A10,
  input  A11,
  input  A12,
  input  A13,
  input  A14,
  input  A15,
  input  A16,
  input  A17,
  input  A18,
  input  A19,
  input  A20,
  input  A21,
  input  A22,
  input  A23,
  input  A24,
  input  A25,
  input  A26,
  input  A27,
  input  A28,
  input  A29,
  input  A30,
  input  A31,
  output out_33
);

  wire and_1_out, and_2_out, and_3_out, and_4_out, and_5_out, and_6_out, and_7_out, and_8_out, and_9_out,
       and_10_out, and_11_out, and_12_out, and_13_out, and_14_out, and_15_out, and_16_out, and_17_out,
       and_18_out, and_19_out, and_20_out, and_21_out, and_22_out, and_23_out, and_24_out, and_25_out,
       and_26_out, and_27_out, and_28_out, and_29_out, and_30_out, not_1_out, not_2_out, not_3_out,
       not_4_out, not_5_out, not_6_out, not_7_out, not_8_out, not_9_out, not_10_out, not_11_out, not_12_out,
       not_13_out, not_14_out, not_15_out, not_16_out, not_17_out, not_18_out, not_19_out, not_20_out,
       not_21_out, not_22_out, not_23_out, not_24_out, not_25_out, not_26_out, not_27_out, not_28_out,
       not_29_out, not_30_out, not_31_out, not_32_out;

  not not_1 (not_1_out, A0);
  not not_2 (not_2_out, A1);
  not not_3 (not_3_out, A2);
  not not_4 (not_4_out, A3);
  not not_5 (not_5_out, A4);
  not not_6 (not_6_out, A5);
  not not_7 (not_7_out, A6);
  not not_8 (not_8_out, A7);
  not not_9 (not_9_out, A8);
  not not_10 (not_10_out, A9);
  not not_11 (not_11_out, A10);
  not not_12 (not_12_out, A11);
  not not_13 (not_13_out, A12);
  not not_14 (not_14_out, A13);
  not not_15 (not_15_out, A14);
  not not_16 (not_16_out, A15);
  not not_17 (not_17_out, A16);
  not not_18 (not_18_out, A17);
  not not_19 (not_19_out, A18);
  not not_20 (not_20_out, A19);
  not not_21 (not_21_out, A20);
  not not_22 (not_22_out, A21);
  not not_23 (not_23_out, A22);
  not not_24 (not_24_out, A23);
  not not_25 (not_25_out, A24);
  not not_26 (not_26_out, A25);
  not not_27 (not_27_out, A26);
  not not_28 (not_28_out, A27);
  not not_29 (not_29_out, A28);
  not not_30 (not_30_out, A29);
  not not_31 (not_31_out, A30);
  not not_32 (not_32_out, A31);
  and and_1 (and_1_out, not_1_out, not_2_out);
  and and_2 (and_2_out, not_3_out, not_4_out);
  and and_3 (and_3_out, and_2_out, and_4_out);
  and and_4 (and_4_out, not_5_out, not_6_out);
  and and_5 (and_5_out, not_7_out, not_8_out);
  and and_6 (and_6_out, and_5_out, and_7_out);
  and and_7 (and_7_out, not_9_out, not_10_out);
  and and_8 (and_8_out, not_11_out, not_12_out);
  and and_9 (and_9_out, and_8_out, and_10_out);
  and and_10 (and_10_out, not_13_out, not_14_out);
  and and_11 (and_11_out, not_15_out, not_16_out);
  and and_12 (and_12_out, and_11_out, and_13_out);
  and and_13 (and_13_out, not_17_out, not_18_out);
  and and_14 (and_14_out, not_19_out, not_20_out);
  and and_15 (and_15_out, and_14_out, and_16_out);
  and and_16 (and_16_out, not_21_out, not_22_out);
  and and_17 (and_17_out, not_23_out, not_24_out);
  and and_18 (and_18_out, and_17_out, and_19_out);
  and and_19 (and_19_out, not_25_out, not_26_out);
  and and_20 (and_20_out, not_27_out, not_28_out);
  and and_21 (and_21_out, and_20_out, and_22_out);
  and and_22 (and_22_out, not_29_out, not_30_out);
  and and_23 (and_23_out, not_31_out, not_32_out);
  and and_24 (and_24_out, and_1_out, and_3_out);
  and and_25 (and_25_out, and_9_out, and_12_out);
  and and_26 (and_26_out, and_15_out, and_18_out);
  and and_27 (and_27_out, and_21_out, and_23_out);
  and and_28 (and_28_out, and_6_out, and_25_out);
  and and_29 (and_29_out, and_28_out, and_30_out);
  and and_30 (and_30_out, and_26_out, and_27_out);
  or or_1 (out_33, and_24_out, and_29_out);
endmodule

module Program_Counter (
  input  On_reset,
  input  offset____2,
  input  target___2,
  input  s,
  input  _0,
  input  in_6,
  input  in_7,
  input  in_8,
  input  in_9,
  input  in_10,
  input  in_11,
  input  in_12,
  input  in_13,
  input  in_14,
  input  in_15,
  input  in_16,
  input  in_17,
  input  in_18,
  input  in_19,
  input  in_20,
  input  in_21,
  input  in_22,
  input  in_23,
  input  in_24,
  input  in_25,
  input  in_26,
  input  in_27,
  input  in_28,
  input  in_29,
  input  in_30,
  input  in_31,
  input  in_32,
  input  in_33,
  input  in_34,
  input  in_35,
  input  in_36,
  output _0_2,
  output out_38,
  output out_39,
  output out_40,
  output out_41,
  output out_42,
  output out_43,
  output out_44,
  output out_45,
  output out_46,
  output out_47,
  output out_48,
  output out_49,
  output out_50,
  output out_51,
  output out_52,
  output out_53,
  output out_54,
  output out_55,
  output out_56,
  output out_57,
  output out_58,
  output out_59,
  output out_60,
  output out_61,
  output out_62,
  output out_63,
  output out_64,
  output out_65,
  output out_66,
  output out_67,
  output out_68
);

  wire add_1__0, add_1__1, add_1__2, add_1__3, add_1__4, add_1__5, add_1__6, add_1__7, add_1__8, add_1__9,
       add_1__10, add_1__11, add_1__12, add_1__13, add_1__14, add_1__15, add_1__16, add_1__17, add_1__18,
       add_1__19, add_1__20, add_1__21, add_1__22, add_1__23, add_1__24, add_1__25, add_1__26, add_1__27,
       add_1__28, add_1__29, add_1__30, add_1__31, and_1_out, and_2_out, and_3_out, and_4_out, and_5_out,
       and_6_out, and_7_out, and_8_out, and_9_out, and_10_out, and_11_out, and_12_out, and_13_out,
       and_14_out, and_15_out, and_16_out, and_17_out, and_18_out, and_19_out, and_20_out, and_21_out,
       and_22_out, and_23_out, and_24_out, and_25_out, and_26_out, and_27_out, and_28_out, and_29_out,
       and_30_out, and_31_out, and_32_out, and_33_out, and_34_out, and_35_out, and_36_out, and_37_out,
       and_38_out, and_39_out, and_40_out, and_41_out, and_42_out, and_43_out, and_44_out, and_45_out,
       and_46_out, and_47_out, and_48_out, and_49_out, and_50_out, and_51_out, and_52_out, and_53_out,
       and_54_out, and_55_out, and_56_out, and_57_out, and_58_out, and_59_out, and_60_out, and_61_out,
       and_62_out, and_63_out, and_64_out, and_65_out, and_66_out, and_67_out, and_68_out, and_69_out,
       and_70_out, and_71_out, and_72_out, and_73_out, and_74_out, and_75_out, and_76_out, and_77_out,
       and_78_out, and_79_out, and_80_out, and_81_out, and_82_out, and_83_out, and_84_out, and_85_out,
       and_86_out, and_87_out, and_88_out, and_89_out, and_90_out, and_91_out, and_92_out, and_93_out,
       and_94_out, and_95_out, and_96_out, and_97_out, and_98_out, and_99_out, and_100_out, and_101_out,
       and_102_out, and_103_out, and_104_out, and_105_out, and_106_out, and_107_out, and_108_out,
       and_109_out, and_110_out, and_111_out, and_112_out, and_113_out, and_114_out, and_115_out,
       and_116_out, and_117_out, and_118_out, and_119_out, and_120_out, and_121_out, and_122_out,
       and_123_out, and_124_out, and_125_out, and_126_out, and_127_out, and_128_out, and_129_out,
       and_130_out, and_131_out, and_132_out, and_133_out, and_134_out, and_135_out, and_136_out,
       and_137_out, and_138_out, and_139_out, and_140_out, and_141_out, and_142_out, and_143_out,
       and_144_out, and_145_out, and_146_out, and_147_out, and_148_out, and_149_out, and_150_out,
       and_151_out, and_152_out, and_153_out, and_154_out, and_155_out, and_156_out, and_157_out,
       and_158_out, and_159_out, and_160_out, and_161_out, and_162_out, and_163_out, and_164_out,
       and_165_out, and_166_out, and_167_out, and_168_out, and_169_out, and_170_out, and_171_out,
       and_172_out, and_173_out, and_174_out, and_175_out, and_176_out, and_177_out, and_178_out,
       and_179_out, and_180_out, and_181_out, and_182_out, and_183_out, and_184_out, and_185_out,
       and_186_out, and_187_out, and_188_out, and_189_out, and_190_out, and_191_out, and_192_out,
       and_193_out, and_194_out, and_195_out, and_196_out, and_197_out, and_198_out, and_199_out,
       and_200_out, and_201_out, and_202_out, and_203_out, and_204_out, and_205_out, and_206_out,
       and_207_out, and_208_out, and_209_out, and_210_out, and_211_out, and_212_out, and_213_out,
       and_214_out, and_215_out, and_216_out, and_217_out, and_218_out, and_219_out, and_220_out,
       and_221_out, and_222_out, and_223_out, and_224_out, and_225_out, and_226_out, and_227__0, and_227__1,
       and_227__2, and_227__3, and_227__4, and_227__5, and_227__6, and_227__7, and_227__8, and_227__9,
       and_227__10, and_227__11, and_227__12, and_227__13, and_227__14, and_227__15, and_227__16,
       and_227__17, and_227__18, and_227__19, and_227__20, and_227__21, and_227__22, and_227__23,
       and_227__24, and_227__25, and_227__26, and_227__27, and_227__28, and_227__29, and_227__30,
       and_227__31, clock_1_out, n32_bit_general_register_2_d19_2, n32_bit_general_register_2_d20_2,
       n32_bit_general_register_2_d21_2, n32_bit_general_register_2_d22_2, n32_bit_general_register_2_d23_2,
       n32_bit_general_register_2_d24_2, n32_bit_general_register_2_d25_2, n32_bit_general_register_2_d26_2,
       n32_bit_general_register_2_d27_2, n32_bit_general_register_2_d28_2, n32_bit_general_register_2_d29_2,
       n32_bit_general_register_2_d30_2, n32_bit_general_register_2_d31_2, n32_bit_general_register_2_q0,
       n32_bit_general_register_2_q1, n32_bit_general_register_2_q2, n32_bit_general_register_2_q3,
       n32_bit_general_register_2_q4, n32_bit_general_register_2_q5, n32_bit_general_register_2_q6,
       n32_bit_general_register_2_q7, n32_bit_general_register_2_q8, n32_bit_general_register_2_q9,
       n32_bit_general_register_2_q10, n32_bit_general_register_2_q11, n32_bit_general_register_2_q12,
       n32_bit_general_register_2_q13, n32_bit_general_register_2_q14, n32_bit_general_register_2_q15,
       n32_bit_general_register_2_q16, n32_bit_general_register_2_q17, n32_bit_general_register_2_q18,
       not_1_out, not_2_out, not_3_out, not_4_out, not_5_out, or_1_out, or_2_out, or_3_out, or_4_out,
       or_5_out, or_6_out, or_7_out, or_8_out, or_9_out, or_10_out, or_11_out, or_12_out, or_13_out,
       or_14_out, or_15_out, or_16_out, or_17_out, or_18_out, or_19_out, or_20_out, or_21_out, or_22_out,
       or_23_out, or_24_out, or_25_out, or_26_out, or_27_out, or_28_out, or_29_out, or_30_out, or_31_out,
       or_32_out, or_33_out, or_34_out, or_35__0, or_35__1, or_35__2, or_35__3, or_35__4, or_35__5, or_35__6,
       or_35__7, or_35__8, or_35__9, or_35__10, or_35__11, or_35__12, or_35__13, or_35__14, or_35__15,
       or_35__16, or_35__17, or_35__18, or_35__19, or_35__20, or_35__21, or_35__22, or_35__23, or_35__24,
       or_35__25, or_35__26, or_35__27, or_35__28, or_35__29, or_35__30, or_35__31, or_36_out, or_37_out,
       or_38_out, or_39_out, or_40_out, or_41_out, or_42_out, or_43_out, or_44_out, or_45_out, or_46_out,
       or_47_out, or_48_out, or_49_out, or_50_out, or_51_out, or_52_out, or_53_out, or_54_out, or_55_out,
       or_56_out, or_57_out, or_58_out, or_59_out, or_60_out, or_61_out, or_62_out, or_63_out, or_64_out,
       or_65_out, or_66_out, or_67_out, or_68_out, sll_1__0, sll_1__1, sll_1__2, sll_1__3, sll_1__4,
       sll_1__5, sll_1__6, sll_1__7, sll_1__8, sll_1__9, sll_1__10, sll_1__11, sll_1__12, sll_1__13,
       sll_1__14, sll_1__15, sll_1__16, sll_1__17, sll_1__18, sll_1__19, sll_1__20, sll_1__21, sll_1__22,
       sll_1__23, sll_1__24, sll_1__25, sll_1__26, sll_1__27, sll_1__28, sll_1__29, sll_1__30, sll_1__31;

  Clock clock_1 (.out(clock_1_out));
  not not_1 (not_1_out, On_reset);
  _32_Bit_General_Register u_32_bit_general_register_1 (
    .E(or_1_out), .D0(and_1_out), .Q0(_0_2), .D1(and_2_out), .Q1(out_38), .D2(and_3_out), .Q2(out_39),
    .D3(and_4_out), .Q3(out_40), .D4(and_5_out), .Q4(out_41), .D5(and_6_out), .Q5(out_42), .D6(and_7_out),
    .Q6(out_43), .D7(and_8_out), .Q7(out_44), .D8(and_9_out), .Q8(out_45), .D9(and_10_out), .Q9(out_46),
    .D10(and_11_out), .Q10(out_47), .D11(and_12_out), .Q11(out_48), .D12(and_13_out), .Q12(out_49),
    .D13(and_14_out), .Q13(out_50), .D14(and_15_out), .Q14(out_51), .D15(and_16_out), .Q15(out_52),
    .D16(and_17_out), .Q16(out_53), .D17(and_18_out), .Q17(out_54), .D18(and_19_out), .Q18(out_55),
    .D19(and_20_out), .D19_2(out_56), .D20(and_21_out), .D20_2(out_57), .D21(and_22_out), .D21_2(out_58),
    .D22(and_23_out), .D22_2(out_59), .D23(and_24_out), .D23_2(out_60), .D24(and_25_out), .D24_2(out_61),
    .D25(and_26_out), .D25_2(out_62), .D26(and_27_out), .D26_2(out_63), .D27(and_28_out), .D27_2(out_64),
    .D28(and_29_out), .D28_2(out_65), .D29(and_30_out), .D29_2(out_66), .D30(and_31_out), .D30_2(out_67),
    .D31(and_32_out), .D31_2(out_68));
  and and_1 (and_1_out, not_1_out, n32_bit_general_register_2_q0);
  and and_2 (and_2_out, not_1_out, n32_bit_general_register_2_q1);
  and and_3 (and_3_out, not_1_out, n32_bit_general_register_2_q2);
  and and_4 (and_4_out, not_1_out, n32_bit_general_register_2_q3);
  and and_5 (and_5_out, not_1_out, n32_bit_general_register_2_q4);
  and and_6 (and_6_out, not_1_out, n32_bit_general_register_2_q5);
  and and_7 (and_7_out, not_1_out, n32_bit_general_register_2_q6);
  and and_8 (and_8_out, not_1_out, n32_bit_general_register_2_q7);
  and and_9 (and_9_out, not_1_out, n32_bit_general_register_2_q8);
  and and_10 (and_10_out, not_1_out, n32_bit_general_register_2_q9);
  and and_11 (and_11_out, not_1_out, n32_bit_general_register_2_q10);
  and and_12 (and_12_out, not_1_out, n32_bit_general_register_2_q11);
  and and_13 (and_13_out, not_1_out, n32_bit_general_register_2_q12);
  and and_14 (and_14_out, not_1_out, n32_bit_general_register_2_q13);
  and and_15 (and_15_out, not_1_out, n32_bit_general_register_2_q14);
  and and_16 (and_16_out, not_1_out, n32_bit_general_register_2_q15);
  and and_17 (and_17_out, not_1_out, n32_bit_general_register_2_q16);
  and and_18 (and_18_out, not_1_out, n32_bit_general_register_2_q17);
  and and_19 (and_19_out, not_1_out, n32_bit_general_register_2_q18);
  and and_20 (and_20_out, not_1_out, n32_bit_general_register_2_d19_2);
  and and_21 (and_21_out, not_1_out, n32_bit_general_register_2_d20_2);
  and and_22 (and_22_out, not_1_out, n32_bit_general_register_2_d21_2);
  and and_23 (and_23_out, not_1_out, n32_bit_general_register_2_d22_2);
  and and_24 (and_24_out, not_1_out, n32_bit_general_register_2_d23_2);
  and and_25 (and_25_out, not_1_out, n32_bit_general_register_2_d24_2);
  and and_26 (and_26_out, not_1_out, n32_bit_general_register_2_d25_2);
  and and_27 (and_27_out, not_1_out, n32_bit_general_register_2_d26_2);
  and and_28 (and_28_out, not_1_out, n32_bit_general_register_2_d27_2);
  and and_29 (and_29_out, not_1_out, n32_bit_general_register_2_d28_2);
  and and_30 (and_30_out, not_1_out, n32_bit_general_register_2_d29_2);
  and and_31 (and_31_out, not_1_out, n32_bit_general_register_2_d30_2);
  and and_32 (and_32_out, not_1_out, n32_bit_general_register_2_d31_2);
  or or_1 (or_1_out, On_reset, clock_1_out);
  not not_2 (not_2_out, clock_1_out);
  _32_Bit_General_Register u_32_bit_general_register_2 (
    .E(not_2_out), .D0(or_2_out), .Q0(n32_bit_general_register_2_q0), .D1(or_5_out),
    .Q1(n32_bit_general_register_2_q1), .D2(or_3_out), .Q2(n32_bit_general_register_2_q2), .D3(or_4_out),
    .Q3(n32_bit_general_register_2_q3), .D4(or_6_out), .Q4(n32_bit_general_register_2_q4), .D5(or_8_out),
    .Q5(n32_bit_general_register_2_q5), .D6(or_7_out), .Q6(n32_bit_general_register_2_q6), .D7(or_10_out),
    .Q7(n32_bit_general_register_2_q7), .D8(or_9_out), .Q8(n32_bit_general_register_2_q8), .D9(or_12_out),
    .Q9(n32_bit_general_register_2_q9), .D10(or_13_out), .Q10(n32_bit_general_register_2_q10),
    .D11(or_14_out), .Q11(n32_bit_general_register_2_q11), .D12(or_17_out),
    .Q12(n32_bit_general_register_2_q12), .D13(or_15_out), .Q13(n32_bit_general_register_2_q13),
    .D14(or_16_out), .Q14(n32_bit_general_register_2_q14), .D15(or_18_out),
    .Q15(n32_bit_general_register_2_q15), .D16(or_19_out), .Q16(n32_bit_general_register_2_q16),
    .D17(or_20_out), .Q17(n32_bit_general_register_2_q17), .D18(or_21_out),
    .Q18(n32_bit_general_register_2_q18), .D19(or_22_out), .D19_2(n32_bit_general_register_2_d19_2),
    .D20(or_24_out), .D20_2(n32_bit_general_register_2_d20_2), .D21(or_23_out),
    .D21_2(n32_bit_general_register_2_d21_2), .D22(or_25_out), .D22_2(n32_bit_general_register_2_d22_2),
    .D23(or_27_out), .D23_2(n32_bit_general_register_2_d23_2), .D24(or_26_out),
    .D24_2(n32_bit_general_register_2_d24_2), .D25(or_29_out), .D25_2(n32_bit_general_register_2_d25_2),
    .D26(or_28_out), .D26_2(n32_bit_general_register_2_d26_2), .D27(or_30_out),
    .D27_2(n32_bit_general_register_2_d27_2), .D28(or_31_out), .D28_2(n32_bit_general_register_2_d28_2),
    .D29(or_32_out), .D29_2(n32_bit_general_register_2_d29_2), .D30(or_33_out),
    .D30_2(n32_bit_general_register_2_d30_2), .D31(or_34_out), .D31_2(n32_bit_general_register_2_d31_2));
  or or_2 (or_2_out, and_33_out, or_37_out);
  and and_33 (and_33_out, s, _0);
  and and_34 (and_34_out, s, in_6);
  and and_35 (and_35_out, s, in_7);
  and and_36 (and_36_out, s, in_8);
  and and_37 (and_37_out, s, in_9);
  and and_38 (and_38_out, s, in_10);
  and and_39 (and_39_out, s, in_11);
  and and_40 (and_40_out, s, in_12);
  and and_41 (and_41_out, s, in_13);
  and and_42 (and_42_out, s, in_14);
  and and_43 (and_43_out, s, in_15);
  and and_44 (and_44_out, s, in_16);
  and and_45 (and_45_out, s, in_17);
  and and_46 (and_46_out, s, in_18);
  and and_47 (and_47_out, s, in_19);
  and and_48 (and_48_out, s, in_20);
  and and_49 (and_49_out, s, in_21);
  and and_50 (and_50_out, s, in_22);
  and and_51 (and_51_out, s, in_23);
  and and_52 (and_52_out, s, in_24);
  and and_53 (and_53_out, s, in_25);
  and and_54 (and_54_out, s, in_26);
  and and_55 (and_55_out, s, in_27);
  and and_56 (and_56_out, s, in_28);
  and and_57 (and_57_out, s, in_29);
  and and_58 (and_58_out, s, in_30);
  and and_59 (and_59_out, s, in_31);
  and and_60 (and_60_out, s, in_32);
  and and_61 (and_61_out, s, in_33);
  and and_62 (and_62_out, s, in_34);
  and and_63 (and_63_out, s, in_35);
  and and_64 (and_64_out, s, in_36);
  and and_65 (and_65_out, offset____2, _0);
  and and_66 (and_66_out, offset____2, in_6);
  and and_67 (and_67_out, offset____2, in_7);
  and and_68 (and_68_out, offset____2, in_8);
  and and_69 (and_69_out, offset____2, in_9);
  and and_70 (and_70_out, offset____2, in_10);
  and and_71 (and_71_out, offset____2, in_11);
  and and_72 (and_72_out, offset____2, in_12);
  and and_73 (and_73_out, offset____2, in_13);
  and and_74 (and_74_out, offset____2, in_14);
  and and_75 (and_75_out, offset____2, in_15);
  and and_76 (and_76_out, offset____2, in_16);
  and and_77 (and_77_out, offset____2, in_17);
  and and_78 (and_78_out, offset____2, in_18);
  and and_79 (and_79_out, offset____2, in_19);
  and and_80 (and_80_out, offset____2, in_20);
  and and_81 (and_81_out, offset____2, in_21);
  and and_82 (and_82_out, offset____2, in_22);
  and and_83 (and_83_out, offset____2, in_23);
  and and_84 (and_84_out, offset____2, in_24);
  and and_85 (and_85_out, offset____2, in_25);
  and and_86 (and_86_out, offset____2, in_26);
  and and_87 (and_87_out, offset____2, in_27);
  and and_88 (and_88_out, offset____2, in_28);
  and and_89 (and_89_out, offset____2, in_29);
  and and_90 (and_90_out, offset____2, in_30);
  and and_91 (and_91_out, offset____2, in_31);
  and and_92 (and_92_out, offset____2, in_32);
  and and_93 (and_93_out, offset____2, in_33);
  and and_94 (and_94_out, offset____2, in_34);
  and and_95 (and_95_out, offset____2, in_35);
  and and_96 (and_96_out, offset____2, in_36);
  and and_97 (and_97_out, target___2, _0);
  and and_98 (and_98_out, target___2, in_6);
  and and_99 (and_99_out, target___2, in_7);
  and and_100 (and_100_out, target___2, in_8);
  and and_101 (and_101_out, target___2, in_9);
  and and_102 (and_102_out, target___2, in_10);
  and and_103 (and_103_out, target___2, in_11);
  and and_104 (and_104_out, target___2, in_12);
  and and_105 (and_105_out, target___2, in_13);
  and and_106 (and_106_out, target___2, in_14);
  and and_107 (and_107_out, target___2, in_15);
  and and_108 (and_108_out, target___2, in_16);
  and and_109 (and_109_out, target___2, in_17);
  and and_110 (and_110_out, target___2, in_18);
  and and_111 (and_111_out, target___2, in_19);
  and and_112 (and_112_out, target___2, in_20);
  and and_113 (and_113_out, target___2, in_21);
  and and_114 (and_114_out, target___2, in_22);
  and and_115 (and_115_out, target___2, in_23);
  and and_116 (and_116_out, target___2, in_24);
  and and_117 (and_117_out, target___2, in_25);
  and and_118 (and_118_out, target___2, in_26);
  and and_119 (and_119_out, target___2, in_27);
  and and_120 (and_120_out, target___2, in_28);
  and and_121 (and_121_out, target___2, in_29);
  and and_122 (and_122_out, target___2, in_30);
  and and_123 (and_123_out, target___2, in_31);
  and and_124 (and_124_out, target___2, in_32);
  and and_125 (and_125_out, target___2, in_33);
  and and_126 (and_126_out, target___2, in_34);
  and and_127 (and_127_out, target___2, in_35);
  and and_128 (and_128_out, target___2, in_36);
  or or_3 (or_3_out, and_35_out, or_39_out);
  or or_4 (or_4_out, and_36_out, or_40_out);
  or or_5 (or_5_out, and_34_out, or_38_out);
  or or_6 (or_6_out, and_37_out, or_41_out);
  or or_7 (or_7_out, and_39_out, or_43_out);
  or or_8 (or_8_out, and_38_out, or_42_out);
  not not_3 (not_3_out, offset____2);
  not not_4 (not_4_out, target___2);
  and and_129 (and_129_out, not_3_out, not_4_out);
  and and_130 (and_130_out, and_129_out, not_5_out);
  or or_9 (or_9_out, and_41_out, or_45_out);
  or or_10 (or_10_out, and_40_out, or_44_out);
  not not_5 (not_5_out, s);
  or or_11 (or_11_out, and_130_out, and_67_out);
  add add_1 (
    .A0(_0_2), .B0(and_65_out), .A1(out_38), .B1(and_66_out), .A2(out_39), .B2(or_11_out), .A3(out_40),
    .B3(and_68_out), .A4(out_41), .B4(and_69_out), .A5(out_42), .B5(and_70_out), .A6(out_43),
    .B6(and_71_out), .A7(out_44), .B7(and_72_out), .A8(out_45), .B8(and_73_out), .A9(out_46),
    .B9(and_74_out), .A10(out_47), .B10(and_75_out), .A11(out_48), .B11(and_76_out), .A12(out_49),
    .B12(and_77_out), .A13(out_50), .B13(and_78_out), .A14(out_51), .B14(and_79_out), .A15(out_52),
    .B15(and_80_out), .A16(out_53), .B16(and_81_out), .A17(out_54), .B17(and_82_out), .A18(out_55),
    .B18(and_83_out), .A19(out_56), .B19(and_84_out), .A20(out_57), .B20(and_85_out), .A21(out_58),
    .B21(and_86_out), .A22(out_59), .B22(and_87_out), .A23(out_60), .B23(and_88_out), .A24(out_61),
    .B24(and_89_out), .A25(out_62), .B25(and_90_out), .A26(out_63), .B26(and_91_out), .A27(out_64),
    .B27(and_92_out), .A28(out_65), .B28(and_93_out), .A29(out_66), .B29(and_94_out), .A30(out_67),
    .B30(and_95_out), .A31(out_68), ._0(add_1__0), ._1(add_1__1), ._2(add_1__2), ._3(add_1__3),
    ._4(add_1__4), ._5(add_1__5), ._6(add_1__6), ._7(add_1__7), ._8(add_1__8), ._9(add_1__9),
    ._10(add_1__10), ._11(add_1__11), ._12(add_1__12), ._13(add_1__13), ._14(add_1__14), ._15(add_1__15),
    ._16(add_1__16), ._17(add_1__17), ._18(add_1__18), ._19(add_1__19), ._20(add_1__20), ._21(add_1__21),
    ._22(add_1__22), ._23(add_1__23), ._24(add_1__24), ._25(add_1__25), ._26(add_1__26), ._27(add_1__27),
    ._28(add_1__28), ._29(add_1__29), ._30(add_1__30), ._31(add_1__31), .B31(and_96_out));  // open: Carry, Overflow
  or or_12 (or_12_out, and_42_out, or_46_out);
  or or_13 (or_13_out, and_43_out, or_47_out);
  or or_14 (or_14_out, and_44_out, or_48_out);
  sll sll_1 (
    .B0(1'b0), .B1(target___2), .B2(1'b0), .B3(1'b0), .B4(1'b0), .A0(and_97_out), .A1(and_98_out),
    .A2(and_99_out), .A3(and_100_out), .A4(and_101_out), .A5(and_102_out), .A6(and_103_out),
    .A7(and_104_out), .A8(and_105_out), .A9(and_106_out), .A10(and_107_out), .A11(and_108_out),
    .A12(and_109_out), .A13(and_110_out), .A14(and_111_out), .A15(and_112_out), .A16(and_113_out),
    .A17(and_114_out), .A18(and_115_out), .A19(and_116_out), .A20(and_117_out), .A21(and_118_out),
    .A22(and_119_out), .A23(and_120_out), .A24(and_121_out), .A25(and_122_out), .A26(and_123_out),
    .A27(and_124_out), .A28(and_125_out), .A29(and_126_out), .A30(and_127_out), .A31(and_128_out),
    ._0(sll_1__0), ._1(sll_1__1), ._2(sll_1__2), ._3(sll_1__3), ._4(sll_1__4), ._5(sll_1__5), ._6(sll_1__6),
    ._7(sll_1__7), ._8(sll_1__8), ._9(sll_1__9), ._10(sll_1__10), ._11(sll_1__11), ._12(sll_1__12),
    ._13(sll_1__13), ._14(sll_1__14), ._15(sll_1__15), ._16(sll_1__16), ._17(sll_1__17), ._18(sll_1__18),
    ._19(sll_1__19), ._20(sll_1__20), ._21(sll_1__21), ._22(sll_1__22), ._23(sll_1__23), ._24(sll_1__24),
    ._25(sll_1__25), ._26(sll_1__26), ._27(sll_1__27), ._28(sll_1__28), ._29(sll_1__29), ._30(sll_1__30),
    ._31(sll_1__31));
  or or_15 (or_15_out, and_46_out, or_50_out);
  or or_16 (or_16_out, and_47_out, or_51_out);
  or or_17 (or_17_out, and_45_out, or_49_out);
  or or_18 (or_18_out, and_48_out, or_52_out);
  or or_19 (or_19_out, and_49_out, or_53_out);
  or or_20 (or_20_out, and_50_out, or_54_out);
  or or_21 (or_21_out, and_51_out, or_55_out);
  or or_22 (or_22_out, and_52_out, or_56_out);
  or or_23 (or_23_out, and_54_out, or_58_out);
  or or_24 (or_24_out, and_53_out, or_57_out);
  or or_25 (or_25_out, and_55_out, or_59_out);
  or or_26 (or_26_out, and_57_out, or_61_out);
  or or_27 (or_27_out, and_56_out, or_60_out);
  or or_28 (or_28_out, and_59_out, or_63_out);
  or or_29 (or_29_out, and_58_out, or_62_out);
  or or_30 (or_30_out, and_60_out, or_64_out);
  or or_31 (or_31_out, and_61_out, or_65_out);
  or or_32 (or_32_out, and_62_out, or_66_out);
  or or_33 (or_33_out, and_63_out, or_67_out);
  or or_34 (or_34_out, and_64_out, or_68_out);
  \or  or_35 (
    .A0(sll_1__0), .B0(and_227__0), .A1(sll_1__1), .B1(and_227__1), .A2(sll_1__2), .B2(and_227__2),
    .A3(sll_1__3), .B3(and_227__3), .A4(sll_1__4), .B4(and_227__4), .A5(sll_1__5), .B5(and_227__5),
    .A6(sll_1__6), .B6(and_227__6), .A7(sll_1__7), .B7(and_227__7), .A8(sll_1__8), .B8(and_227__8),
    .A9(sll_1__9), .B9(and_227__9), .A10(sll_1__10), .B10(and_227__10), .A11(sll_1__11), .B11(and_227__11),
    .A12(sll_1__12), .B12(and_227__12), .A13(sll_1__13), .B13(and_227__13), .A14(sll_1__14),
    .B14(and_227__14), .A15(sll_1__15), .B15(and_227__15), .A16(sll_1__16), .B16(and_227__16),
    .A17(sll_1__17), .B17(and_227__17), .A18(sll_1__18), .B18(and_227__18), .A19(sll_1__19),
    .B19(and_227__19), .A20(sll_1__20), .B20(and_227__20), .A21(sll_1__21), .B21(and_227__21),
    .A22(sll_1__22), .B22(and_227__22), .A23(sll_1__23), .B23(and_227__23), .A24(sll_1__24),
    .B24(and_227__24), .A25(sll_1__25), .B25(and_227__25), .A26(sll_1__26), .B26(and_227__26),
    .A27(sll_1__27), .B27(and_227__27), .A28(sll_1__28), .B28(and_227__28), .A29(sll_1__29),
    .B29(and_227__29), .A30(sll_1__30), .B30(and_227__30), .A31(sll_1__31), .B31(and_227__31), ._0(or_35__0),
    ._1(or_35__1), ._2(or_35__2), ._3(or_35__3), ._4(or_35__4), ._5(or_35__5), ._6(or_35__6), ._7(or_35__7),
    ._8(or_35__8), ._9(or_35__9), ._10(or_35__10), ._11(or_35__11), ._12(or_35__12), ._13(or_35__13),
    ._14(or_35__14), ._15(or_35__15), ._16(or_35__16), ._17(or_35__17), ._18(or_35__18), ._19(or_35__19),
    ._20(or_35__20), ._21(or_35__21), ._22(or_35__22), ._23(or_35__23), ._24(or_35__24), ._25(or_35__25),
    ._26(or_35__26), ._27(or_35__27), ._28(or_35__28), ._29(or_35__29), ._30(or_35__30), ._31(or_35__31));
  or or_36 (or_36_out, offset____2, and_130_out);
  and and_131 (and_131_out, or_36_out, add_1__0);
  and and_132 (and_132_out, or_36_out, add_1__1);
  and and_133 (and_133_out, or_36_out, add_1__2);
  and and_134 (and_134_out, or_36_out, add_1__3);
  and and_135 (and_135_out, or_36_out, add_1__4);
  and and_136 (and_136_out, or_36_out, add_1__5);
  and and_137 (and_137_out, or_36_out, add_1__6);
  and and_138 (and_138_out, or_36_out, add_1__7);
  and and_139 (and_139_out, or_36_out, add_1__8);
  and and_140 (and_140_out, or_36_out, add_1__9);
  and and_141 (and_141_out, or_36_out, add_1__10);
  and and_142 (and_142_out, or_36_out, add_1__11);
  and and_143 (and_143_out, or_36_out, add_1__12);
  and and_144 (and_144_out, or_36_out, add_1__13);
  and and_145 (and_145_out, or_36_out, add_1__14);
  and and_146 (and_146_out, or_36_out, add_1__15);
  and and_147 (and_147_out, or_36_out, add_1__16);
  and and_148 (and_148_out, or_36_out, add_1__17);
  and and_149 (and_149_out, or_36_out, add_1__18);
  and and_150 (and_150_out, or_36_out, add_1__19);
  and and_151 (and_151_out, or_36_out, add_1__20);
  and and_152 (and_152_out, or_36_out, add_1__21);
  and and_153 (and_153_out, or_36_out, add_1__22);
  and and_154 (and_154_out, or_36_out, add_1__23);
  and and_155 (and_155_out, or_36_out, add_1__24);
  and and_156 (and_156_out, or_36_out, add_1__25);
  and and_157 (and_157_out, or_36_out, add_1__26);
  and and_158 (and_158_out, or_36_out, add_1__27);
  and and_159 (and_159_out, or_36_out, add_1__28);
  and and_160 (and_160_out, or_36_out, add_1__29);
  and and_161 (and_161_out, or_36_out, add_1__30);
  and and_162 (and_162_out, or_36_out, add_1__31);
  and and_163 (and_163_out, target___2, add_1__0);
  and and_164 (and_164_out, target___2, add_1__1);
  and and_165 (and_165_out, target___2, add_1__2);
  and and_166 (and_166_out, target___2, add_1__3);
  and and_167 (and_167_out, target___2, add_1__4);
  and and_168 (and_168_out, target___2, add_1__5);
  and and_169 (and_169_out, target___2, add_1__6);
  and and_170 (and_170_out, target___2, add_1__7);
  and and_171 (and_171_out, target___2, add_1__8);
  and and_172 (and_172_out, target___2, add_1__9);
  and and_173 (and_173_out, target___2, add_1__10);
  and and_174 (and_174_out, target___2, add_1__11);
  and and_175 (and_175_out, target___2, add_1__12);
  and and_176 (and_176_out, target___2, add_1__13);
  and and_177 (and_177_out, target___2, add_1__14);
  and and_178 (and_178_out, target___2, add_1__15);
  and and_179 (and_179_out, target___2, add_1__16);
  and and_180 (and_180_out, target___2, add_1__17);
  and and_181 (and_181_out, target___2, add_1__18);
  and and_182 (and_182_out, target___2, add_1__19);
  and and_183 (and_183_out, target___2, add_1__20);
  and and_184 (and_184_out, target___2, add_1__21);
  and and_185 (and_185_out, target___2, add_1__22);
  and and_186 (and_186_out, target___2, add_1__23);
  and and_187 (and_187_out, target___2, add_1__24);
  and and_188 (and_188_out, target___2, add_1__25);
  and and_189 (and_189_out, target___2, add_1__26);
  and and_190 (and_190_out, target___2, add_1__27);
  and and_191 (and_191_out, target___2, add_1__28);
  and and_192 (and_192_out, target___2, add_1__29);
  and and_193 (and_193_out, target___2, add_1__30);
  and and_194 (and_194_out, target___2, add_1__31);
  or or_37 (or_37_out, and_195_out, and_131_out);
  or or_38 (or_38_out, and_196_out, and_132_out);
  or or_39 (or_39_out, and_197_out, and_133_out);
  or or_40 (or_40_out, and_198_out, and_134_out);
  or or_41 (or_41_out, and_199_out, and_135_out);
  or or_42 (or_42_out, and_200_out, and_136_out);
  or or_43 (or_43_out, and_201_out, and_137_out);
  or or_44 (or_44_out, and_202_out, and_138_out);
  or or_45 (or_45_out, and_203_out, and_139_out);
  or or_46 (or_46_out, and_204_out, and_140_out);
  or or_47 (or_47_out, and_205_out, and_141_out);
  or or_48 (or_48_out, and_206_out, and_142_out);
  or or_49 (or_49_out, and_207_out, and_143_out);
  or or_50 (or_50_out, and_208_out, and_144_out);
  or or_51 (or_51_out, and_209_out, and_145_out);
  or or_52 (or_52_out, and_210_out, and_146_out);
  or or_53 (or_53_out, and_211_out, and_147_out);
  or or_54 (or_54_out, and_212_out, and_148_out);
  or or_55 (or_55_out, and_213_out, and_149_out);
  or or_56 (or_56_out, and_214_out, and_150_out);
  or or_57 (or_57_out, and_215_out, and_151_out);
  or or_58 (or_58_out, and_216_out, and_152_out);
  or or_59 (or_59_out, and_217_out, and_153_out);
  or or_60 (or_60_out, and_218_out, and_154_out);
  or or_61 (or_61_out, and_219_out, and_155_out);
  or or_62 (or_62_out, and_220_out, and_156_out);
  or or_63 (or_63_out, and_221_out, and_157_out);
  or or_64 (or_64_out, and_222_out, and_158_out);
  or or_65 (or_65_out, and_223_out, and_159_out);
  or or_66 (or_66_out, and_224_out, and_160_out);
  or or_67 (or_67_out, and_225_out, and_161_out);
  or or_68 (or_68_out, and_226_out, and_162_out);
  and and_195 (and_195_out, target___2, or_35__0);
  and and_196 (and_196_out, target___2, or_35__1);
  and and_197 (and_197_out, target___2, or_35__2);
  and and_198 (and_198_out, target___2, or_35__3);
  and and_199 (and_199_out, target___2, or_35__4);
  and and_200 (and_200_out, target___2, or_35__5);
  and and_201 (and_201_out, target___2, or_35__6);
  and and_202 (and_202_out, target___2, or_35__7);
  and and_203 (and_203_out, target___2, or_35__8);
  and and_204 (and_204_out, target___2, or_35__9);
  and and_205 (and_205_out, target___2, or_35__10);
  and and_206 (and_206_out, target___2, or_35__11);
  and and_207 (and_207_out, target___2, or_35__12);
  and and_208 (and_208_out, target___2, or_35__13);
  and and_209 (and_209_out, target___2, or_35__14);
  and and_210 (and_210_out, target___2, or_35__15);
  and and_211 (and_211_out, target___2, or_35__16);
  and and_212 (and_212_out, target___2, or_35__17);
  and and_213 (and_213_out, target___2, or_35__18);
  and and_214 (and_214_out, target___2, or_35__19);
  and and_215 (and_215_out, target___2, or_35__20);
  and and_216 (and_216_out, target___2, or_35__21);
  and and_217 (and_217_out, target___2, or_35__22);
  and and_218 (and_218_out, target___2, or_35__23);
  and and_219 (and_219_out, target___2, or_35__24);
  and and_220 (and_220_out, target___2, or_35__25);
  and and_221 (and_221_out, target___2, or_35__26);
  and and_222 (and_222_out, target___2, or_35__27);
  and and_223 (and_223_out, target___2, or_35__28);
  and and_224 (and_224_out, target___2, or_35__29);
  and and_225 (and_225_out, target___2, or_35__30);
  and and_226 (and_226_out, target___2, or_35__31);
  \and  and_227 (
    .A0(and_163_out), .B0(1'b0), .A1(and_164_out), .B1(1'b0), .A2(and_165_out), .B2(1'b0), .A3(and_166_out),
    .B3(1'b0), .A4(and_167_out), .B4(1'b0), .A5(and_168_out), .B5(1'b0), .A6(and_169_out), .B6(1'b0),
    .A7(and_170_out), .B7(1'b0), .A8(and_171_out), .B8(1'b0), .A9(and_172_out), .B9(1'b0), .A10(and_173_out),
    .B10(1'b0), .A11(and_174_out), .B11(1'b0), .A12(and_175_out), .B12(1'b0), .A13(and_176_out), .B13(1'b0),
    .A14(and_177_out), .B14(1'b0), .A15(and_178_out), .B15(1'b0), .A16(and_179_out), .B16(1'b0),
    .A17(and_180_out), .B17(1'b0), .A18(and_181_out), .B18(1'b0), .A19(and_182_out), .B19(1'b0),
    .A20(and_183_out), .B20(1'b0), .A21(and_184_out), .B21(1'b0), .A22(and_185_out), .B22(1'b0),
    .A23(and_186_out), .B23(1'b0), .A24(and_187_out), .B24(1'b0), .A25(and_188_out), .B25(1'b0),
    .A26(and_189_out), .B26(1'b0), .A27(and_190_out), .B27(1'b0), .A28(and_191_out), .B28(1'b1),
    .A29(and_192_out), .B29(1'b1), .A30(and_193_out), .B30(1'b1), .A31(and_194_out), .B31(1'b1),
    ._0(and_227__0), ._1(and_227__1), ._2(and_227__2), ._3(and_227__3), ._4(and_227__4), ._5(and_227__5),
    ._6(and_227__6), ._7(and_227__7), ._8(and_227__8), ._9(and_227__9), ._10(and_227__10), ._11(and_227__11),
    ._12(and_227__12), ._13(and_227__13), ._14(and_227__14), ._15(and_227__15), ._16(and_227__16),
    ._17(and_227__17), ._18(and_227__18), ._19(and_227__19), ._20(and_227__20), ._21(and_227__21),
    ._22(and_227__22), ._23(and_227__23), ._24(and_227__24), ._25(and_227__25), ._26(and_227__26),
    ._27(and_227__27), ._28(and_227__28), ._29(and_227__29), ._30(and_227__30), ._31(and_227__31));

  // Notes on the sheet:
  //   CLK
  //   $s
  //   offset
  //   target
  //   PC
  //   nPC
  //   ADV_PC(4)
  //   target
endmodule
module Main (
  input  On_Off,
  input  Load_from_ROM
);

  wire add_1__0, add_1__1, add_1__2, add_1__3, add_1__4, add_1__5, add_1__6, add_1__7, add_1__8, add_1__9,
       add_1__10, add_1__11, add_1__12, add_1__13, add_1__14, add_1__15, add_1__16, add_1__17, add_1__18,
       add_1__19, add_1__20, add_1__21, add_1__22, add_1__23, add_1__24, add_1__25, add_1__26, add_1__27,
       add_1__28, add_1__29, add_1__30, add_1__31, alu_1_out_93, alu_1_out_94, alu_1_out_95, alu_1_out_96,
       alu_1_out_97, alu_1_out_98, alu_1_out_99, alu_1_out_100, alu_1_out_101, alu_1_out_102, alu_1_out_103,
       alu_1_out_104, alu_1_out_105, alu_1_out_106, alu_1_out_107, alu_1_out_108, alu_1_out_109,
       alu_1_out_110, alu_1_out_111, alu_1_out_112, alu_1_out_113, alu_1_out_114, alu_1_out_115,
       alu_1_out_116, alu_1_out_117, alu_1_out_118, alu_1_out_119, alu_1_out_120, alu_1_out_121,
       alu_1_out_122, alu_1_out_123, alu_1_out_124, alu_1_out_125, alu_1_out_126, alu_1_out_127,
       alu_1_out_128, alu_1_out_129, alu_1_out_130, alu_1_out_131, alu_1_out_132, alu_1_out_133,
       alu_1_out_134, alu_1_out_135, alu_1_out_136, alu_1_out_137, alu_1_out_138, alu_1_out_139,
       alu_1_out_140, alu_1_out_141, alu_1_out_142, alu_1_out_143, alu_1_out_144, alu_1_out_145,
       alu_1_out_146, alu_1_out_147, alu_1_out_148, alu_1_out_149, alu_1_out_150, alu_1_out_151,
       alu_1_out_152, alu_1_out_153, alu_1_out_154, alu_1_out_155, alu_1_out_156, and_1_out, and_2_out,
       and_3_out, and_4_out, and_5_out, and_6_out, and_7_out, and_8_out, and_9_out, and_10_out, and_11_out,
       and_12_out, and_13_out, and_14_out, and_15_out, and_16_out, and_17_out, and_18_out, and_19_out,
       and_20_out, and_21_out, and_22_out, and_23_out, and_24_out, and_25_out, and_26_out, and_27_out,
       and_28_out, and_29_out, and_30_out, and_31_out, and_32_out, and_33_out, and_34_out, and_35_out,
       and_36_out, and_37_out, and_38_out, and_39_out, and_40_out, and_41_out, and_42_out, and_43_out,
       and_44_out, and_45_out, and_46_out, and_47_out, and_48_out, and_49_out, and_50_out, and_51_out,
       and_52_out, and_53_out, and_54_out, and_55_out, and_56_out, and_57_out, and_58_out, and_59_out,
       and_60_out, and_61_out, and_62_out, and_63_out, and_64_out, and_65_out, and_66_out, and_67_out,
       and_68_out, and_69_out, and_70_out, and_71_out, and_72_out, and_73_out, and_74_out, and_75_out,
       and_76_out, and_77_out, and_78_out, and_79_out, and_80_out, and_81_out, and_82_out, and_83_out,
       and_84_out, and_85_out, and_86_out, and_87_out, and_88_out, and_89_out, and_90_out, and_91_out,
       and_92_out, and_93_out, and_94_out, and_95_out, and_96_out, and_97_out, and_98_out, and_99_out,
       and_100_out, and_101_out, and_102_out, and_103_out, and_104_out, and_105_out, and_106_out,
       and_107_out, and_108_out, and_109_out, and_110_out, and_111_out, and_112_out, and_113_out,
       and_114_out, and_115_out, and_116_out, and_117_out, and_118_out, and_119_out, and_120_out,
       and_121_out, and_122_out, and_123_out, and_124_out, and_125_out, and_126_out, and_127_out,
       and_128_out, and_129_out, and_130_out, and_131_out, and_132_out, and_133_out, and_134_out,
       and_135_out, and_136_out, and_137_out, and_138_out, and_139_out, and_140_out, and_141_out,
       and_142_out, and_143_out, and_144_out, and_145_out, and_146_out, and_147_out, and_148_out,
       and_149_out, and_150_out, and_151_out, and_152_out, and_153_out, and_154_out, and_155_out,
       and_156_out, and_157_out, and_158_out, and_159_out, and_160_out, and_161_out, and_162_out,
       and_163_out, and_164_out, and_165_out, and_166_out, and_167_out, and_168_out, and_169_out,
       and_170_out, and_171_out, and_172_out, and_173_out, and_174_out, and_175_out, and_176_out,
       and_177_out, and_178_out, and_179_out, and_180_out, and_181_out, and_182_out, and_183_out,
       and_184_out, and_185_out, and_186_out, and_187_out, and_188_out, and_189_out, and_190_out,
       and_191_out, and_192_out, and_193_out, and_194_out, and_195_out, and_196_out, and_197_out,
       and_198_out, and_199_out, and_200_out, and_201_out, and_202_out, and_203_out, and_204_out,
       and_205_out, and_206_out, and_207_out, and_208_out, and_209_out, and_210_out, and_211_out,
       and_212_out, and_213_out, and_214_out, and_215_out, and_216_out, and_217_out, and_218_out,
       and_219_out, and_220_out, and_221_out, and_222_out, and_223_out, and_224_out, and_225_out,
       and_226_out, and_227_out, and_228_out, and_229_out, and_230_out, and_231_out, and_232_out,
       and_233_out, and_234_out, and_235_out, and_236_out, and_237_out, and_238_out, and_239_out,
       and_240_out, and_241_out, and_242_out, and_243_out, and_244_out, and_245_out, and_246_out,
       and_247_out, and_248_out, and_249_out, and_250_out, and_251_out, and_252_out, and_253_out,
       and_254_out, and_255_out, and_256_out, and_257_out, and_258_out, and_259_out, and_260_out,
       and_261_out, and_262_out, and_263_out, and_264_out, and_265_out, bitwise_logic_main_1__0,
       bitwise_logic_main_1_out_94, bitwise_logic_main_1_out_95, bitwise_logic_main_1_out_96,
       bitwise_logic_main_1_out_97, bitwise_logic_main_1_out_98, bitwise_logic_main_1_out_99,
       bitwise_logic_main_1_out_100, bitwise_logic_main_1_out_101, bitwise_logic_main_1_out_102,
       bitwise_logic_main_1_out_103, bitwise_logic_main_1_out_104, bitwise_logic_main_1_out_105,
       bitwise_logic_main_1_out_106, bitwise_logic_main_1_out_107, bitwise_logic_main_1_out_108,
       bitwise_logic_main_1_out_109, bitwise_logic_main_1_out_110, bitwise_logic_main_1_out_111,
       bitwise_logic_main_1_out_112, bitwise_logic_main_1_out_113, bitwise_logic_main_1_out_114,
       bitwise_logic_main_1_out_115, bitwise_logic_main_1_out_116, bitwise_logic_main_1_out_117,
       bitwise_logic_main_1_out_118, bitwise_logic_main_1_out_119, bitwise_logic_main_1_out_120,
       bitwise_logic_main_1_out_121, bitwise_logic_main_1_out_122, bitwise_logic_main_1_out_123,
       bitwise_logic_main_1_out_124, branch_unit_1__0, branch_unit_1_out_88, branch_unit_1_out_89,
       branch_unit_1_out_90, branch_unit_1_out_91, branch_unit_1_out_92, branch_unit_1_out_93,
       branch_unit_1_out_94, branch_unit_1_out_95, branch_unit_1_out_96, branch_unit_1_out_97,
       branch_unit_1_out_98, branch_unit_1_out_99, branch_unit_1_out_100, branch_unit_1_out_101,
       branch_unit_1_out_102, branch_unit_1_out_103, branch_unit_1_out_104, branch_unit_1_out_105,
       branch_unit_1_out_106, branch_unit_1_out_107, branch_unit_1_out_108, branch_unit_1_out_109,
       branch_unit_1_out_110, branch_unit_1_out_111, branch_unit_1_out_112, branch_unit_1_out_113,
       branch_unit_1_out_114, branch_unit_1_out_115, branch_unit_1_out_116, branch_unit_1_out_117,
       branch_unit_1_out_118, clock_1_out, gated_d_latch_1_nq, gated_d_latch_1_q, logical_unit_1__0,
       logical_unit_1_out_93, logical_unit_1_out_94, logical_unit_1_out_95, logical_unit_1_out_96,
       logical_unit_1_out_97, logical_unit_1_out_98, logical_unit_1_out_99, logical_unit_1_out_100,
       logical_unit_1_out_101, logical_unit_1_out_102, logical_unit_1_out_103, logical_unit_1_out_104,
       logical_unit_1_out_105, logical_unit_1_out_106, logical_unit_1_out_107, logical_unit_1_out_108,
       logical_unit_1_out_109, logical_unit_1_out_110, logical_unit_1_out_111, logical_unit_1_out_112,
       logical_unit_1_out_113, logical_unit_1_out_114, logical_unit_1_out_115, logical_unit_1_out_116,
       logical_unit_1_out_117, logical_unit_1_out_118, logical_unit_1_out_119, logical_unit_1_out_120,
       logical_unit_1_out_121, logical_unit_1_out_122, logical_unit_1_out_123,
       n32_bit_general_register_1_d19_2, n32_bit_general_register_1_d20_2, n32_bit_general_register_1_d21_2,
       n32_bit_general_register_1_d22_2, n32_bit_general_register_1_d23_2, n32_bit_general_register_1_d24_2,
       n32_bit_general_register_1_d25_2, n32_bit_general_register_1_d26_2, n32_bit_general_register_1_d27_2,
       n32_bit_general_register_1_d28_2, n32_bit_general_register_1_d29_2, n32_bit_general_register_1_d30_2,
       n32_bit_general_register_1_d31_2, n32_bit_general_register_1_q0, n32_bit_general_register_1_q1,
       n32_bit_general_register_1_q2, n32_bit_general_register_1_q3, n32_bit_general_register_1_q4,
       n32_bit_general_register_1_q5, n32_bit_general_register_1_q6, n32_bit_general_register_1_q7,
       n32_bit_general_register_1_q8, n32_bit_general_register_1_q9, n32_bit_general_register_1_q10,
       n32_bit_general_register_1_q11, n32_bit_general_register_1_q12, n32_bit_general_register_1_q13,
       n32_bit_general_register_1_q14, n32_bit_general_register_1_q15, n32_bit_general_register_1_q16,
       n32_bit_general_register_1_q17, n32_bit_general_register_1_q18, n32_bit_general_register_2_d19_2,
       n32_bit_general_register_2_d20_2, n32_bit_general_register_2_d21_2, n32_bit_general_register_2_d22_2,
       n32_bit_general_register_2_d23_2, n32_bit_general_register_2_d24_2, n32_bit_general_register_2_d25_2,
       n32_bit_general_register_2_d26_2, n32_bit_general_register_2_d27_2, n32_bit_general_register_2_d28_2,
       n32_bit_general_register_2_d29_2, n32_bit_general_register_2_d30_2, n32_bit_general_register_2_d31_2,
       n32_bit_general_register_2_q0, n32_bit_general_register_2_q1, n32_bit_general_register_2_q2,
       n32_bit_general_register_2_q3, n32_bit_general_register_2_q4, n32_bit_general_register_2_q5,
       n32_bit_general_register_2_q6, n32_bit_general_register_2_q7, n32_bit_general_register_2_q8,
       n32_bit_general_register_2_q9, n32_bit_general_register_2_q10, n32_bit_general_register_2_q11,
       n32_bit_general_register_2_q12, n32_bit_general_register_2_q13, n32_bit_general_register_2_q14,
       n32_bit_general_register_2_q15, n32_bit_general_register_2_q16, n32_bit_general_register_2_q17,
       n32_bit_general_register_2_q18, nor_1_out, nor_2_out, not_1_out, not_2_out, not_3_out,
       operations_conditional_6_bit_register_1_out_8, operations_conditional_6_bit_register_1_out_9,
       operations_conditional_6_bit_register_1_out_10, operations_conditional_6_bit_register_1_out_11,
       operations_conditional_6_bit_register_1_out_12, operations_conditional_6_bit_register_1_out_13,
       operations_conditional_6_bit_register_1_out_14, operations_conditional_6_bit_register_1_out_15,
       operations_conditional_6_bit_register_1_out_16, operations_conditional_6_bit_register_1_out_17,
       operations_conditional_6_bit_register_1_out_18, operations_conditional_6_bit_register_1_out_19,
       operations_conditional_6_bit_register_1_out_20, operations_conditional_6_bit_register_1_out_21,
       operations_conditional_6_bit_register_1_out_22, operations_conditional_6_bit_register_1_out_23,
       operations_conditional_6_bit_register_1_out_24, operations_conditional_6_bit_register_1_out_25,
       operations_conditional_6_bit_register_1_out_26, operations_conditional_6_bit_register_1_out_27,
       operations_conditional_6_bit_register_1_out_28, operations_conditional_6_bit_register_1_out_29,
       operations_conditional_6_bit_register_1_out_30, operations_conditional_6_bit_register_1_out_31,
       operations_conditional_6_bit_register_1_out_32, operations_conditional_6_bit_register_1_out_33,
       operations_conditional_6_bit_register_1_out_34, operations_conditional_6_bit_register_1_out_35,
       operations_conditional_6_bit_register_1_out_36, operations_conditional_6_bit_register_1_out_37,
       operations_conditional_6_bit_register_1_out_38, operations_conditional_6_bit_register_1_out_39,
       operations_conditional_6_bit_register_1_out_40, operations_conditional_6_bit_register_1_out_41,
       operations_conditional_6_bit_register_1_out_42, operations_conditional_6_bit_register_1_out_43,
       operations_conditional_6_bit_register_1_out_44, operations_conditional_6_bit_register_1_out_45,
       operations_conditional_6_bit_register_1_out_46, operations_conditional_6_bit_register_1_out_47,
       operations_conditional_6_bit_register_1_out_54, operations_conditional_6_bit_register_1_out_55,
       operations_conditional_6_bit_register_1_out_56, operations_conditional_6_bit_register_1_out_57,
       or_30_out, or_31_out, or_32_out, or_33_out, or_34_out, or_35_out, or_36_out, or_37_out, or_38_out,
       or_39_out, or_40_out, or_41_out, or_42_out, or_43_out, or_44_out, or_45_out, or_46_out, or_47_out,
       or_48_out, or_49_out, or_50_out, or_51_out, or_52_out, or_53_out, or_54_out, or_55_out, or_59_out,
       or_60_out, or_61_out, or_62_out, or_63_out, or_64_out, or_65_out, or_66_out, or_67_out, or_68_out,
       or_69_out, or_70_out, or_71_out, or_72_out, or_73_out, or_74_out, or_75_out, or_76_out, or_77_out,
       or_78_out, or_79_out, or_80_out, or_81_out, or_82_out, or_83_out, or_84_out, or_85_out, or_86_out,
       or_87_out, or_88_out, or_89_out, or_90_out, or_91_out, or_92_out, or_93_out, or_94_out, or_95_out,
       or_96_out, or_97_out, or_98_out, or_99_out, or_100_out, or_101_out, or_102_out, or_103_out,
       or_104_out, or_105_out, or_106_out, or_107_out, or_108_out, or_109_out, or_110_out, or_111_out,
       or_112_out, or_113_out, or_114_out, or_115_out, or_116_out, or_117_out, or_118_out, or_119_out,
       or_120_out, or_121_out, or_122_out, or_123_out, or_124_out, or_125_out, or_126_out, or_127_out,
       or_128_out, or_129_out, or_130_out, or_131_out, or_132_out, or_133_out, or_134_out, or_135_out,
       or_136_out, or_137_out, or_138_out, or_139_out, or_140_out, or_141_out, or_142_out, or_143_out,
       or_144_out, or_145_out, or_146_out, or_147_out, or_148_out, or_149_out, or_150_out, or_151_out,
       or_152_out, or_153_out, or_154_out, or_155_out, or_156_out, or_157_out, or_158_out, or_159_out,
       or_160_out, or_161_out, or_162_out, or_163_out, or_164_out, or_165_out, or_166_out, or_167_out,
       or_168_out, or_169_out, or_170_out, or_171_out, or_172_out, or_173_out, or_174_out, or_175_out,
       or_176_out, or_177_out, or_178_out, or_179_out, or_180_out, or_181_out, or_182_out, or_183_out,
       or_184_out, or_185_out, or_186_out, or_187_out, or_188_out, or_189_out, or_190_out, or_191_out,
       or_192_out, or_193_out, or_194_out, or_195_out, or_196_out, or_197_out, or_198_out, or_199_out,
       or_200_out, or_201_out, or_202_out, or_203_out, or_204_out, or_205_out, or_206_out, or_207_out,
       or_208_out, or_209_out, or_210_out, or_211_out, or_212_out, or_213_out, or_214_out, or_215_out,
       or_216_out, or_217_out, or_218_out, or_219_out, or_220_out, or_221_out, or_222_out, or_223_out,
       or_224_out, or_225_out, or_226_out, or_227_out, or_228_out, or_229_out, or_230_out, or_231_out,
       or_232_out, or_233_out, or_234_out, or_235_out, or_236_out, or_237_out, or_238_out, or_239_out,
       or_240_out, or_241_out, or_242_out, or_243_out, or_244_out, or_245_out, or_246_out, or_247_out,
       or_248_out, or_249_out, or_250_out, or_251_out, or_252_out, or_253_out, or_254_out, or_255_out,
       or_256_out, or_257_out, or_258_out, or_259_out, or_260_out, or_261_out, or_262_out, or_263_out,
       or_264_out, or_265_out, or_266_out, or_267_out, or_268_out, or_269_out, or_270_out, or_271_out,
       or_272_out, or_273_out, or_274_out, or_275_out, or_276_out, or_277_out, or_278_out, or_279_out,
       or_280_out, or_281_out, or_282_out, or_283_out, or_284_out, or_285_out, or_286_out, or_287_out,
       or_288_out, or_289_out, or_290_out, or_291_out, or_292_out, or_293_out, or_294_out, or_295_out,
       or_296_out, or_297_out, or_298_out, or_299_out, or_300_out, or_301_out, or_302_out, or_303_out,
       or_304_out, or_305_out, or_306_out, or_307_out, or_308_out, or_309_out, or_310_out, or_311_out,
       or_312_out, or_313_out, or_314_out, or_315_out, or_316_out, or_317_out, or_318_out, or_319_out,
       or_320_out, or_321_out, or_322_out, or_323_out, or_324_out, or_325_out, or_326_out, or_327_out,
       or_328_out, or_329_out, or_330_out, or_331_out, or_332_out, or_333_out, or_334_out, or_335_out,
       or_336_out, or_337_out, or_338_out, or_339_out, or_340_out, or_341_out, program_counter_1__0_2,
       program_counter_1_out_38, program_counter_1_out_39, program_counter_1_out_40,
       program_counter_1_out_41, program_counter_1_out_42, program_counter_1_out_43,
       program_counter_1_out_44, program_counter_1_out_45, program_counter_1_out_46,
       program_counter_1_out_47, program_counter_1_out_48, program_counter_1_out_49,
       program_counter_1_out_50, program_counter_1_out_51, program_counter_1_out_52,
       program_counter_1_out_53, program_counter_1_out_54, program_counter_1_out_55,
       program_counter_1_out_56, program_counter_1_out_57, program_counter_1_out_58,
       program_counter_1_out_59, program_counter_1_out_60, program_counter_1_out_61,
       program_counter_1_out_62, program_counter_1_out_63, program_counter_1_out_64,
       program_counter_1_out_65, program_counter_1_out_66, program_counter_1_out_67,
       program_counter_1_out_68, register_arrays_and_decoder_1__0, register_arrays_and_decoder_1__0_2,
       register_arrays_and_decoder_1_out_50, register_arrays_and_decoder_1_out_51,
       register_arrays_and_decoder_1_out_52, register_arrays_and_decoder_1_out_53,
       register_arrays_and_decoder_1_out_54, register_arrays_and_decoder_1_out_55,
       register_arrays_and_decoder_1_out_56, register_arrays_and_decoder_1_out_57,
       register_arrays_and_decoder_1_out_58, register_arrays_and_decoder_1_out_59,
       register_arrays_and_decoder_1_out_60, register_arrays_and_decoder_1_out_61,
       register_arrays_and_decoder_1_out_62, register_arrays_and_decoder_1_out_63,
       register_arrays_and_decoder_1_out_64, register_arrays_and_decoder_1_out_65,
       register_arrays_and_decoder_1_out_66, register_arrays_and_decoder_1_out_67,
       register_arrays_and_decoder_1_out_68, register_arrays_and_decoder_1_out_69,
       register_arrays_and_decoder_1_out_70, register_arrays_and_decoder_1_out_71,
       register_arrays_and_decoder_1_out_72, register_arrays_and_decoder_1_out_73,
       register_arrays_and_decoder_1_out_74, register_arrays_and_decoder_1_out_75,
       register_arrays_and_decoder_1_out_76, register_arrays_and_decoder_1_out_77,
       register_arrays_and_decoder_1_out_78, register_arrays_and_decoder_1_out_79,
       register_arrays_and_decoder_1_out_80, register_arrays_and_decoder_1_out_82,
       register_arrays_and_decoder_1_out_83, register_arrays_and_decoder_1_out_84,
       register_arrays_and_decoder_1_out_85, register_arrays_and_decoder_1_out_86,
       register_arrays_and_decoder_1_out_87, register_arrays_and_decoder_1_out_88,
       register_arrays_and_decoder_1_out_89, register_arrays_and_decoder_1_out_90,
       register_arrays_and_decoder_1_out_91, register_arrays_and_decoder_1_out_92,
       register_arrays_and_decoder_1_out_93, register_arrays_and_decoder_1_out_94,
       register_arrays_and_decoder_1_out_95, register_arrays_and_decoder_1_out_96,
       register_arrays_and_decoder_1_out_97, register_arrays_and_decoder_1_out_98,
       register_arrays_and_decoder_1_out_99, register_arrays_and_decoder_1_out_100,
       register_arrays_and_decoder_1_out_101, register_arrays_and_decoder_1_out_102,
       register_arrays_and_decoder_1_out_103, register_arrays_and_decoder_1_out_104,
       register_arrays_and_decoder_1_out_105, register_arrays_and_decoder_1_out_106,
       register_arrays_and_decoder_1_out_107, register_arrays_and_decoder_1_out_108,
       register_arrays_and_decoder_1_out_109, register_arrays_and_decoder_1_out_110,
       register_arrays_and_decoder_1_out_111, register_arrays_and_decoder_1_out_112, rom_1__0_2, rom_1_data,
       rom_1_out_32, rom_1_out_33, rom_1_out_34, rom_1_out_35, rom_1_out_36, rom_1_out_37, rom_1_out_38,
       rom_1_out_39, rom_1_out_40, rom_1_out_41, rom_1_out_42, rom_1_out_43, rom_1_out_44, rom_1_out_45,
       rom_1_out_46, rom_1_out_47, rom_1_out_48, rom_1_out_49, rom_1_out_50, rom_1_out_51, rom_1_out_52,
       rom_1_out_53, rom_1_out_54, rom_1_out_55, rom_1_out_56, rom_1_out_57, rom_1_out_58, rom_1_out_59,
       rom_1_out_60, rom_1_out_61, undriven;
  wire [31:0] undriven_2;

  not not_1 (not_1_out, 1'b0);
  add add_1 (
    .A0(1'b0), .B0(program_counter_1__0_2), .A1(1'b0), .B1(program_counter_1_out_38), .A2(1'b0),
    .B2(program_counter_1_out_39), .A3(not_1_out), .B3(program_counter_1_out_40), .A4(1'b0),
    .B4(program_counter_1_out_41), .A5(1'b0), .B5(program_counter_1_out_42), .A6(1'b0),
    .B6(program_counter_1_out_43), .A7(1'b0), .B7(program_counter_1_out_44), .A8(1'b0),
    .B8(program_counter_1_out_45), .A9(1'b0), .B9(program_counter_1_out_46), .A10(1'b0),
    .B10(program_counter_1_out_47), .A11(1'b0), .B11(program_counter_1_out_48), .A12(1'b0),
    .B12(program_counter_1_out_49), .A13(1'b0), .B13(program_counter_1_out_50), .A14(1'b0),
    .B14(program_counter_1_out_51), .A15(1'b0), .B15(program_counter_1_out_52), .A16(1'b0),
    .B16(program_counter_1_out_53), .A17(1'b0), .B17(program_counter_1_out_54), .A18(1'b0),
    .B18(program_counter_1_out_55), .A19(1'b0), .B19(program_counter_1_out_56), .A20(1'b0),
    .B20(program_counter_1_out_57), .A21(1'b0), .B21(program_counter_1_out_58), .A22(1'b0),
    .B22(program_counter_1_out_59), .A23(1'b0), .B23(program_counter_1_out_60), .A24(1'b0),
    .B24(program_counter_1_out_61), .A25(1'b0), .B25(program_counter_1_out_62), .A26(1'b0),
    .B26(program_counter_1_out_63), .A27(1'b0), .B27(program_counter_1_out_64), .A28(1'b0),
    .B28(program_counter_1_out_65), .A29(1'b0), .B29(program_counter_1_out_66), .A30(1'b0),
    .B30(program_counter_1_out_67), .A31(1'b0), ._0(add_1__0), ._1(add_1__1), ._2(add_1__2), ._3(add_1__3),
    ._4(add_1__4), ._5(add_1__5), ._6(add_1__6), ._7(add_1__7), ._8(add_1__8), ._9(add_1__9),
    ._10(add_1__10), ._11(add_1__11), ._12(add_1__12), ._13(add_1__13), ._14(add_1__14), ._15(add_1__15),
    ._16(add_1__16), ._17(add_1__17), ._18(add_1__18), ._19(add_1__19), ._20(add_1__20), ._21(add_1__21),
    ._22(add_1__22), ._23(add_1__23), ._24(add_1__24), ._25(add_1__25), ._26(add_1__26), ._27(add_1__27),
    ._28(add_1__28), ._29(add_1__29), ._30(add_1__30), ._31(add_1__31), .B31(program_counter_1_out_68));  // open: Carry, Overflow
  // OR_Gate or_1 has open pins: in0=or_154_out, in1=or_91_out, out=open
  // OR_Gate or_2 has open pins: in0=or_153_out, in1=or_92_out, out=open
  and and_1 (and_1_out, add_1__0, operations_conditional_6_bit_register_1_out_47);
  and and_2 (and_2_out, add_1__1, operations_conditional_6_bit_register_1_out_47);
  and and_3 (and_3_out, add_1__2, operations_conditional_6_bit_register_1_out_47);
  and and_4 (and_4_out, add_1__3, operations_conditional_6_bit_register_1_out_47);
  and and_5 (and_5_out, add_1__4, operations_conditional_6_bit_register_1_out_47);
  and and_6 (and_6_out, add_1__5, operations_conditional_6_bit_register_1_out_47);
  and and_7 (and_7_out, add_1__6, operations_conditional_6_bit_register_1_out_47);
  and and_8 (and_8_out, add_1__7, operations_conditional_6_bit_register_1_out_47);
  and and_9 (and_9_out, add_1__8, operations_conditional_6_bit_register_1_out_47);
  and and_10 (and_10_out, add_1__9, operations_conditional_6_bit_register_1_out_47);
  and and_11 (and_11_out, add_1__10, operations_conditional_6_bit_register_1_out_47);
  and and_12 (and_12_out, add_1__11, operations_conditional_6_bit_register_1_out_47);
  and and_13 (and_13_out, add_1__12, operations_conditional_6_bit_register_1_out_47);
  and and_14 (and_14_out, add_1__13, operations_conditional_6_bit_register_1_out_47);
  and and_15 (and_15_out, add_1__14, operations_conditional_6_bit_register_1_out_47);
  and and_16 (and_16_out, add_1__15, operations_conditional_6_bit_register_1_out_47);
  and and_17 (and_17_out, add_1__16, operations_conditional_6_bit_register_1_out_47);
  and and_18 (and_18_out, add_1__17, operations_conditional_6_bit_register_1_out_47);
  and and_19 (and_19_out, add_1__18, operations_conditional_6_bit_register_1_out_47);
  and and_20 (and_20_out, add_1__19, operations_conditional_6_bit_register_1_out_47);
  and and_21 (and_21_out, add_1__20, operations_conditional_6_bit_register_1_out_47);
  and and_22 (and_22_out, add_1__21, operations_conditional_6_bit_register_1_out_47);
  and and_23 (and_23_out, add_1__22, operations_conditional_6_bit_register_1_out_47);
  and and_24 (and_24_out, add_1__23, operations_conditional_6_bit_register_1_out_47);
  and and_25 (and_25_out, add_1__24, operations_conditional_6_bit_register_1_out_47);
  and and_26 (and_26_out, add_1__25, operations_conditional_6_bit_register_1_out_47);
  and and_27 (and_27_out, add_1__26, operations_conditional_6_bit_register_1_out_47);
  and and_28 (and_28_out, add_1__27, operations_conditional_6_bit_register_1_out_47);
  and and_29 (and_29_out, add_1__28, operations_conditional_6_bit_register_1_out_47);
  and and_30 (and_30_out, add_1__29, operations_conditional_6_bit_register_1_out_47);
  and and_31 (and_31_out, add_1__30, operations_conditional_6_bit_register_1_out_47);
  and and_32 (and_32_out, add_1__31, operations_conditional_6_bit_register_1_out_47);
  // OR_Gate or_3 has open pins: in0=or_152_out, in1=or_93_out, out=open
  // OR_Gate or_4 has open pins: in0=or_151_out, in1=or_94_out, out=open
  // OR_Gate or_5 has open pins: in0=or_150_out, in1=or_95_out, out=open
  // OR_Gate or_6 has open pins: in0=or_149_out, in1=or_96_out, out=open
  // OR_Gate or_7 has open pins: in0=or_147_out, in1=or_98_out, out=open
  // OR_Gate or_8 has open pins: in0=or_148_out, in1=or_97_out, out=open
  // OR_Gate or_9 has open pins: in0=or_145_out, in1=or_100_out, out=open
  // OR_Gate or_10 has open pins: in0=or_146_out, in1=or_99_out, out=open
  // OR_Gate or_11 has open pins: in0=or_143_out, in1=or_102_out, out=open
  // OR_Gate or_12 has open pins: in0=or_142_out, in1=or_103_out, out=open
  // OR_Gate or_13 has open pins: in0=or_144_out, in1=or_101_out, out=open
  // OR_Gate or_14 has open pins: in0=or_140_out, in1=or_105_out, out=open
  // OR_Gate or_15 has open pins: in0=or_141_out, in1=or_104_out, out=open
  // OR_Gate or_16 has open pins: in0=or_139_out, in1=or_106_out, out=open
  // OR_Gate or_17 has open pins: in0=or_138_out, in1=or_107_out, out=open
  // OR_Gate or_18 has open pins: in0=or_137_out, in1=or_108_out, out=open
  and and_33 (and_33_out, register_arrays_and_decoder_1__0, operations_conditional_6_bit_register_1_out_47);
  and and_34 (and_34_out, register_arrays_and_decoder_1_out_50, operations_conditional_6_bit_register_1_out_47);
  and and_35 (and_35_out, register_arrays_and_decoder_1_out_51, operations_conditional_6_bit_register_1_out_47);
  and and_36 (and_36_out, register_arrays_and_decoder_1_out_52, operations_conditional_6_bit_register_1_out_47);
  and and_37 (and_37_out, register_arrays_and_decoder_1_out_53, operations_conditional_6_bit_register_1_out_47);
  and and_38 (and_38_out, register_arrays_and_decoder_1_out_54, operations_conditional_6_bit_register_1_out_47);
  and and_39 (and_39_out, register_arrays_and_decoder_1_out_55, operations_conditional_6_bit_register_1_out_47);
  and and_40 (and_40_out, register_arrays_and_decoder_1_out_56, operations_conditional_6_bit_register_1_out_47);
  and and_41 (and_41_out, register_arrays_and_decoder_1_out_57, operations_conditional_6_bit_register_1_out_47);
  and and_42 (and_42_out, register_arrays_and_decoder_1_out_58, operations_conditional_6_bit_register_1_out_47);
  and and_43 (and_43_out, register_arrays_and_decoder_1_out_59, operations_conditional_6_bit_register_1_out_47);
  and and_44 (and_44_out, register_arrays_and_decoder_1_out_60, operations_conditional_6_bit_register_1_out_47);
  and and_45 (and_45_out, register_arrays_and_decoder_1_out_61, operations_conditional_6_bit_register_1_out_47);
  and and_46 (and_46_out, register_arrays_and_decoder_1_out_62, operations_conditional_6_bit_register_1_out_47);
  and and_47 (and_47_out, register_arrays_and_decoder_1_out_63, operations_conditional_6_bit_register_1_out_47);
  and and_48 (and_48_out, register_arrays_and_decoder_1_out_64, operations_conditional_6_bit_register_1_out_47);
  and and_49 (and_49_out, register_arrays_and_decoder_1_out_65, operations_conditional_6_bit_register_1_out_47);
  and and_50 (and_50_out, register_arrays_and_decoder_1_out_66, operations_conditional_6_bit_register_1_out_47);
  and and_51 (and_51_out, register_arrays_and_decoder_1_out_67, operations_conditional_6_bit_register_1_out_47);
  and and_52 (and_52_out, register_arrays_and_decoder_1_out_68, operations_conditional_6_bit_register_1_out_47);
  and and_53 (and_53_out, register_arrays_and_decoder_1_out_69, operations_conditional_6_bit_register_1_out_47);
  and and_54 (and_54_out, register_arrays_and_decoder_1_out_70, operations_conditional_6_bit_register_1_out_47);
  and and_55 (and_55_out, register_arrays_and_decoder_1_out_71, operations_conditional_6_bit_register_1_out_47);
  and and_56 (and_56_out, register_arrays_and_decoder_1_out_72, operations_conditional_6_bit_register_1_out_47);
  and and_57 (and_57_out, register_arrays_and_decoder_1_out_73, operations_conditional_6_bit_register_1_out_47);
  and and_58 (and_58_out, register_arrays_and_decoder_1_out_74, operations_conditional_6_bit_register_1_out_47);
  and and_59 (and_59_out, register_arrays_and_decoder_1_out_75, operations_conditional_6_bit_register_1_out_47);
  and and_60 (and_60_out, register_arrays_and_decoder_1_out_76, operations_conditional_6_bit_register_1_out_47);
  and and_61 (and_61_out, register_arrays_and_decoder_1_out_77, operations_conditional_6_bit_register_1_out_47);
  and and_62 (and_62_out, register_arrays_and_decoder_1_out_78, operations_conditional_6_bit_register_1_out_47);
  and and_63 (and_63_out, register_arrays_and_decoder_1_out_79, operations_conditional_6_bit_register_1_out_47);
  and and_64 (and_64_out, register_arrays_and_decoder_1_out_80, operations_conditional_6_bit_register_1_out_47);
  // OR_Gate or_19 has open pins: in0=or_134_out, in1=or_111_out, out=open
  // OR_Gate or_20 has open pins: in0=or_135_out, in1=or_110_out, out=open
  // OR_Gate or_21 has open pins: in0=or_136_out, in1=or_109_out, out=open
  // OR_Gate or_22 has open pins: in0=or_132_out, in1=or_113_out, out=open
  // OR_Gate or_23 has open pins: in0=or_131_out, in1=or_114_out, out=open
  // OR_Gate or_24 has open pins: in0=or_133_out, in1=or_112_out, out=open
  // OR_Gate or_25 has open pins: in0=or_130_out, in1=or_115_out, out=open
  // OR_Gate or_26 has open pins: in0=or_129_out, in1=or_116_out, out=open
  // OR_Gate or_27 has open pins: in0=or_128_out, in1=or_117_out, out=open
  // OR_Gate or_28 has open pins: in0=or_126_out, in1=or_119_out, out=open
  // OR_Gate or_29 has open pins: in0=or_127_out, in1=or_118_out, out=open
  or or_30 (or_30_out, and_240_out, and_33_out);
  or or_31 (or_31_out, and_241_out, and_34_out);
  or or_32 (or_32_out, and_242_out, and_35_out);
  or or_33 (or_33_out, and_243_out, and_36_out);
  or or_34 (or_34_out, and_244_out, and_37_out);
  or or_35 (or_35_out, and_245_out, and_38_out);
  or or_36 (or_36_out, and_246_out, and_39_out);
  or or_37 (or_37_out, and_247_out, and_40_out);
  or or_38 (or_38_out, and_248_out, and_41_out);
  or or_39 (or_39_out, and_249_out, and_42_out);
  or or_40 (or_40_out, and_250_out, and_43_out);
  or or_41 (or_41_out, and_251_out, and_44_out);
  or or_42 (or_42_out, and_252_out, and_45_out);
  or or_43 (or_43_out, and_253_out, and_46_out);
  or or_44 (or_44_out, and_254_out, and_47_out);
  or or_45 (or_45_out, and_255_out, and_48_out);
  or or_46 (or_46_out, and_256_out, and_49_out);
  or or_47 (or_47_out, and_257_out, and_50_out);
  or or_48 (or_48_out, and_258_out, and_51_out);
  or or_49 (or_49_out, and_259_out, and_52_out);
  or or_50 (or_50_out, and_260_out, and_53_out);
  or or_51 (or_51_out, and_261_out, and_54_out);
  or or_52 (or_52_out, and_262_out, and_55_out);
  or or_53 (or_53_out, and_263_out, and_56_out);
  or or_54 (or_54_out, and_264_out, and_57_out);
  or or_55 (or_55_out, and_265_out, and_58_out);
  // OR_Gate or_56 has open pins: in0=or_125_out, in1=or_120_out, out=open
  // OR_Gate or_57 has open pins: in0=or_123_out, in1=or_122_out, out=open
  // OR_Gate or_58 has open pins: in0=or_124_out, in1=or_121_out, out=open
  or or_59 (or_59_out, branch_unit_1__0, or_30_out);
  or or_60 (or_60_out, branch_unit_1_out_88, or_31_out);
  or or_61 (or_61_out, branch_unit_1_out_89, or_32_out);
  or or_62 (or_62_out, branch_unit_1_out_90, or_33_out);
  or or_63 (or_63_out, branch_unit_1_out_91, or_34_out);
  or or_64 (or_64_out, branch_unit_1_out_92, or_35_out);
  or or_65 (or_65_out, branch_unit_1_out_93, or_36_out);
  or or_66 (or_66_out, branch_unit_1_out_94, or_37_out);
  or or_67 (or_67_out, branch_unit_1_out_95, or_38_out);
  or or_68 (or_68_out, branch_unit_1_out_96, or_39_out);
  or or_69 (or_69_out, branch_unit_1_out_97, or_40_out);
  or or_70 (or_70_out, branch_unit_1_out_98, or_41_out);
  or or_71 (or_71_out, branch_unit_1_out_99, or_42_out);
  or or_72 (or_72_out, branch_unit_1_out_100, or_43_out);
  or or_73 (or_73_out, branch_unit_1_out_101, or_44_out);
  or or_74 (or_74_out, branch_unit_1_out_102, or_45_out);
  or or_75 (or_75_out, branch_unit_1_out_103, or_46_out);
  or or_76 (or_76_out, branch_unit_1_out_104, or_47_out);
  or or_77 (or_77_out, branch_unit_1_out_105, or_48_out);
  or or_78 (or_78_out, branch_unit_1_out_106, or_49_out);
  or or_79 (or_79_out, branch_unit_1_out_107, or_50_out);
  or or_80 (or_80_out, branch_unit_1_out_108, or_51_out);
  or or_81 (or_81_out, branch_unit_1_out_109, or_52_out);
  or or_82 (or_82_out, branch_unit_1_out_110, or_53_out);
  or or_83 (or_83_out, branch_unit_1_out_111, or_54_out);
  or or_84 (or_84_out, branch_unit_1_out_112, or_55_out);
  or or_85 (or_85_out, branch_unit_1_out_113, and_59_out);
  or or_86 (or_86_out, branch_unit_1_out_114, and_60_out);
  or or_87 (or_87_out, branch_unit_1_out_115, and_61_out);
  or or_88 (or_88_out, branch_unit_1_out_116, and_62_out);
  or or_89 (or_89_out, branch_unit_1_out_117, and_63_out);
  or or_90 (or_90_out, branch_unit_1_out_118, and_64_out);
  or or_91 (or_91_out, and_66_out, or_278_out);
  or or_92 (or_92_out, and_65_out, or_281_out);
  or or_93 (or_93_out, and_68_out, or_283_out);
  or or_94 (or_94_out, and_69_out, or_282_out);
  or or_95 (or_95_out, and_67_out, or_288_out);
  or or_96 (or_96_out, and_70_out, or_287_out);
  or or_97 (or_97_out, and_71_out, or_292_out);
  or or_98 (or_98_out, and_72_out, or_294_out);
  or or_99 (or_99_out, and_74_out, or_293_out);
  or or_100 (or_100_out, and_73_out, or_299_out);
  or or_101 (or_101_out, and_76_out, or_297_out);
  or or_102 (or_102_out, and_77_out, or_298_out);
  or or_103 (or_103_out, and_78_out, or_303_out);
  or or_104 (or_104_out, and_81_out, or_304_out);
  or or_105 (or_105_out, and_79_out, or_309_out);
  or or_106 (or_106_out, and_80_out, or_310_out);
  or or_107 (or_107_out, and_82_out, or_308_out);
  or or_108 (or_108_out, and_83_out, or_313_out);
  or or_109 (or_109_out, and_86_out, or_315_out);
  or or_110 (or_110_out, and_84_out, or_314_out);
  or or_111 (or_111_out, and_85_out, or_320_out);
  or or_112 (or_112_out, and_87_out, or_319_out);
  or or_113 (or_113_out, and_89_out, or_327_out);
  or or_114 (or_114_out, and_88_out, or_325_out);
  or or_115 (or_115_out, and_91_out, or_326_out);
  or or_116 (or_116_out, and_90_out, or_332_out);
  or or_117 (or_117_out, and_95_out, or_331_out);
  or or_118 (or_118_out, and_93_out, or_333_out);
  or or_119 (or_119_out, and_94_out, or_335_out);
  or or_120 (or_120_out, and_100_out, or_334_out);
  or or_121 (or_121_out, and_99_out, or_337_out);
  or or_122 (or_122_out, and_98_out, or_336_out);
  or or_123 (or_123_out, and_238_out, and_190_out);
  or or_124 (or_124_out, and_237_out, and_191_out);
  or or_125 (or_125_out, and_235_out, and_185_out);
  or or_126 (or_126_out, and_236_out, and_184_out);
  or or_127 (or_127_out, and_234_out, and_177_out);
  or or_128 (or_128_out, and_233_out, and_178_out);
  or or_129 (or_129_out, and_232_out, and_179_out);
  or or_130 (or_130_out, and_231_out, and_169_out);
  or or_131 (or_131_out, and_230_out, and_170_out);
  or or_132 (or_132_out, and_229_out, and_171_out);
  or or_133 (or_133_out, and_228_out, and_163_out);
  or or_134 (or_134_out, and_227_out, and_162_out);
  or or_135 (or_135_out, and_225_out, and_155_out);
  or or_136 (or_136_out, and_226_out, and_156_out);
  or or_137 (or_137_out, and_222_out, and_157_out);
  or or_138 (or_138_out, and_223_out, and_147_out);
  or or_139 (or_139_out, and_224_out, and_149_out);
  or or_140 (or_140_out, and_220_out, and_148_out);
  or or_141 (or_141_out, and_219_out, and_140_out);
  or or_142 (or_142_out, and_221_out, and_139_out);
  or or_143 (or_143_out, and_218_out, and_133_out);
  or or_144 (or_144_out, and_217_out, and_134_out);
  or or_145 (or_145_out, and_214_out, and_135_out);
  or or_146 (or_146_out, and_212_out, and_125_out);
  or or_147 (or_147_out, and_213_out, and_124_out);
  or or_148 (or_148_out, and_203_out, and_126_out);
  or or_149 (or_149_out, and_205_out, and_118_out);
  or or_150 (or_150_out, and_204_out, and_119_out);
  or or_151 (or_151_out, and_200_out, and_110_out);
  or or_152 (or_152_out, and_199_out, and_111_out);
  or or_153 (or_153_out, and_194_out, and_112_out);
  or or_154 (or_154_out, and_195_out, and_104_out);
  and and_65 (and_65_out, not_2_out, alu_1_out_94);
  and and_66 (and_66_out, not_2_out, alu_1_out_93);
  and and_67 (and_67_out, not_2_out, alu_1_out_97);
  and and_68 (and_68_out, not_2_out, alu_1_out_95);
  and and_69 (and_69_out, not_2_out, alu_1_out_96);
  Program_Counter program_counter_1 (
    ._0(or_59_out), .in_6(or_60_out), .in_7(or_61_out), .in_8(or_62_out), .in_9(or_63_out),
    .in_10(or_64_out), .in_11(or_65_out), .in_12(or_66_out), .in_13(or_67_out), .in_14(or_68_out),
    .in_15(or_69_out), .in_16(or_70_out), .in_17(or_71_out), .in_18(or_72_out), .in_19(or_73_out),
    .in_20(or_74_out), .in_21(or_75_out), .in_22(or_76_out), .in_23(or_77_out), .in_24(or_78_out),
    .in_25(or_79_out), .in_26(or_80_out), .in_27(or_81_out), .in_28(or_82_out), .in_29(or_83_out),
    .in_30(or_84_out), .in_31(or_85_out), .in_32(or_86_out), .in_33(or_87_out), .in_34(or_88_out),
    .in_35(or_89_out), .in_36(or_90_out), ._0_2(program_counter_1__0_2), .out_38(program_counter_1_out_38),
    .out_39(program_counter_1_out_39), .out_40(program_counter_1_out_40), .out_41(program_counter_1_out_41),
    .out_42(program_counter_1_out_42), .out_43(program_counter_1_out_43), .out_44(program_counter_1_out_44),
    .out_45(program_counter_1_out_45), .out_46(program_counter_1_out_46), .out_47(program_counter_1_out_47),
    .out_48(program_counter_1_out_48), .out_49(program_counter_1_out_49), .out_50(program_counter_1_out_50),
    .out_51(program_counter_1_out_51), .out_52(program_counter_1_out_52), .out_53(program_counter_1_out_53),
    .out_54(program_counter_1_out_54), .out_55(program_counter_1_out_55), .out_56(program_counter_1_out_56),
    .out_57(program_counter_1_out_57), .out_58(program_counter_1_out_58), .out_59(program_counter_1_out_59),
    .out_60(program_counter_1_out_60), .out_61(program_counter_1_out_61), .out_62(program_counter_1_out_62),
    .out_63(program_counter_1_out_63), .out_64(program_counter_1_out_64), .out_65(program_counter_1_out_65),
    .out_66(program_counter_1_out_66), .out_67(program_counter_1_out_67), .out_68(program_counter_1_out_68),
    .On_reset(or_155_out));  // open: offset____2, target___2, s
  and and_70 (and_70_out, not_2_out, alu_1_out_98);
  and and_71 (and_71_out, not_2_out, alu_1_out_99);
  and and_72 (and_72_out, not_2_out, alu_1_out_100);
  or or_155 (or_155_out, gated_d_latch_1_nq, or_162_out);
  Gated_D_Latch gated_d_latch_1 (.E(clock_1_out), .D(On_Off), .nQ(gated_d_latch_1_nq), .Q(gated_d_latch_1_q));
  Clock clock_1 (.out(clock_1_out));
  and and_73 (and_73_out, not_2_out, alu_1_out_102);
  and and_74 (and_74_out, not_2_out, alu_1_out_101);
  or or_156 (or_156_out, program_counter_1_out_61, program_counter_1_out_62);
  or or_157 (or_157_out, or_156_out, or_160_out);
  and and_75 (and_75_out, gated_d_latch_1_q, clock_1_out);
  and and_76 (and_76_out, not_2_out, alu_1_out_103);
  and and_77 (and_77_out, not_2_out, alu_1_out_104);
  and and_78 (and_78_out, not_2_out, alu_1_out_105);
  or or_158 (or_158_out, program_counter_1_out_65, program_counter_1_out_66);
  or or_159 (or_159_out, program_counter_1_out_67, program_counter_1_out_68);
  or or_160 (or_160_out, program_counter_1_out_63, program_counter_1_out_64);
  or or_161 (or_161_out, or_158_out, or_159_out);
  or or_162 (or_162_out, or_157_out, or_161_out);
  buf or_163 (or_163_out, and_1_out);  // OR_Gate
  buf or_164 (or_164_out, and_2_out);  // OR_Gate
  buf or_165 (or_165_out, and_3_out);  // OR_Gate
  buf or_166 (or_166_out, and_4_out);  // OR_Gate
  buf or_167 (or_167_out, and_5_out);  // OR_Gate
  buf or_168 (or_168_out, and_6_out);  // OR_Gate
  buf or_169 (or_169_out, and_7_out);  // OR_Gate
  buf or_170 (or_170_out, and_8_out);  // OR_Gate
  buf or_171 (or_171_out, and_9_out);  // OR_Gate
  buf or_172 (or_172_out, and_10_out);  // OR_Gate
  buf or_173 (or_173_out, and_11_out);  // OR_Gate
  buf or_174 (or_174_out, and_12_out);  // OR_Gate
  buf or_175 (or_175_out, and_13_out);  // OR_Gate
  buf or_176 (or_176_out, and_14_out);  // OR_Gate
  buf or_177 (or_177_out, and_15_out);  // OR_Gate
  buf or_178 (or_178_out, and_16_out);  // OR_Gate
  buf or_179 (or_179_out, and_17_out);  // OR_Gate
  buf or_180 (or_180_out, and_18_out);  // OR_Gate
  buf or_181 (or_181_out, and_19_out);  // OR_Gate
  buf or_182 (or_182_out, and_20_out);  // OR_Gate
  buf or_183 (or_183_out, and_21_out);  // OR_Gate
  buf or_184 (or_184_out, and_22_out);  // OR_Gate
  buf or_185 (or_185_out, and_23_out);  // OR_Gate
  buf or_186 (or_186_out, and_24_out);  // OR_Gate
  buf or_187 (or_187_out, and_25_out);  // OR_Gate
  buf or_188 (or_188_out, and_26_out);  // OR_Gate
  buf or_189 (or_189_out, and_27_out);  // OR_Gate
  buf or_190 (or_190_out, and_28_out);  // OR_Gate
  buf or_191 (or_191_out, and_29_out);  // OR_Gate
  buf or_192 (or_192_out, and_30_out);  // OR_Gate
  buf or_193 (or_193_out, and_31_out);  // OR_Gate
  buf or_194 (or_194_out, and_32_out);  // OR_Gate
  and and_79 (and_79_out, not_2_out, alu_1_out_107);
  and and_80 (and_80_out, not_2_out, alu_1_out_108);
  and and_81 (and_81_out, not_2_out, alu_1_out_106);
  and and_82 (and_82_out, not_2_out, alu_1_out_109);
  and and_83 (and_83_out, not_2_out, alu_1_out_110);
  and and_84 (and_84_out, not_2_out, alu_1_out_112);
  and and_85 (and_85_out, not_2_out, alu_1_out_113);
  and and_86 (and_86_out, not_2_out, alu_1_out_111);
  Operations_Conditional_6_Bit_Register operations_conditional_6_bit_register_1 (
    ._2_0(rom_1_out_56), ._2_1(rom_1_out_57), ._2_2(rom_1_out_58), ._2_3(rom_1_out_59), ._2_4(rom_1_out_60),
    ._2_5(rom_1_out_61), .out_8(operations_conditional_6_bit_register_1_out_8),
    .out_9(operations_conditional_6_bit_register_1_out_9),
    .out_10(operations_conditional_6_bit_register_1_out_10),
    .out_11(operations_conditional_6_bit_register_1_out_11),
    .out_12(operations_conditional_6_bit_register_1_out_12),
    .out_13(operations_conditional_6_bit_register_1_out_13),
    .out_14(operations_conditional_6_bit_register_1_out_14),
    .out_15(operations_conditional_6_bit_register_1_out_15),
    .out_16(operations_conditional_6_bit_register_1_out_16),
    .out_17(operations_conditional_6_bit_register_1_out_17),
    .out_18(operations_conditional_6_bit_register_1_out_18),
    .out_19(operations_conditional_6_bit_register_1_out_19),
    .out_20(operations_conditional_6_bit_register_1_out_20),
    .out_21(operations_conditional_6_bit_register_1_out_21),
    .out_22(operations_conditional_6_bit_register_1_out_22),
    .out_23(operations_conditional_6_bit_register_1_out_23),
    .out_24(operations_conditional_6_bit_register_1_out_24),
    .out_25(operations_conditional_6_bit_register_1_out_25),
    .out_26(operations_conditional_6_bit_register_1_out_26),
    .out_27(operations_conditional_6_bit_register_1_out_27),
    .out_28(operations_conditional_6_bit_register_1_out_28),
    .out_29(operations_conditional_6_bit_register_1_out_29),
    .out_30(operations_conditional_6_bit_register_1_out_30),
    .out_31(operations_conditional_6_bit_register_1_out_31),
    .out_32(operations_conditional_6_bit_register_1_out_32),
    .out_33(operations_conditional_6_bit_register_1_out_33),
    .out_34(operations_conditional_6_bit_register_1_out_34),
    .out_35(operations_conditional_6_bit_register_1_out_35),
    .out_36(operations_conditional_6_bit_register_1_out_36),
    .out_37(operations_conditional_6_bit_register_1_out_37),
    .out_38(operations_conditional_6_bit_register_1_out_38),
    .out_39(operations_conditional_6_bit_register_1_out_39),
    .out_40(operations_conditional_6_bit_register_1_out_40),
    .out_41(operations_conditional_6_bit_register_1_out_41),
    .out_42(operations_conditional_6_bit_register_1_out_42),
    .out_43(operations_conditional_6_bit_register_1_out_43),
    .out_44(operations_conditional_6_bit_register_1_out_44),
    .out_45(operations_conditional_6_bit_register_1_out_45),
    .out_46(operations_conditional_6_bit_register_1_out_46),
    .out_47(operations_conditional_6_bit_register_1_out_47),
    .out_54(operations_conditional_6_bit_register_1_out_54),
    .out_55(operations_conditional_6_bit_register_1_out_55),
    .out_56(operations_conditional_6_bit_register_1_out_56),
    .out_57(operations_conditional_6_bit_register_1_out_57), .E(and_75_out));  // open: out_48, out_49, out_50, out_51, out_52, out_53
  and and_87 (and_87_out, not_2_out, alu_1_out_114);
  and and_88 (and_88_out, not_2_out, alu_1_out_116);
  and and_89 (and_89_out, not_2_out, alu_1_out_115);
  ROM rom_1 (
    .Start_clear(gated_d_latch_1_nq), .in_12(Load_from_ROM), ._0_2(rom_1__0_2), .Data(rom_1_data),
    .out_32(rom_1_out_32), .out_33(rom_1_out_33), .out_34(rom_1_out_34), .out_35(rom_1_out_35),
    .out_36(rom_1_out_36), .out_37(rom_1_out_37), .out_38(rom_1_out_38), .out_39(rom_1_out_39),
    .out_40(rom_1_out_40), .out_41(rom_1_out_41), .out_42(rom_1_out_42), .out_43(rom_1_out_43),
    .out_44(rom_1_out_44), .out_45(rom_1_out_45), .out_46(rom_1_out_46), .out_47(rom_1_out_47),
    .out_48(rom_1_out_48), .out_49(rom_1_out_49), .out_50(rom_1_out_50), .out_51(rom_1_out_51),
    .out_52(rom_1_out_52), .out_53(rom_1_out_53), .out_54(rom_1_out_54), .out_55(rom_1_out_55),
    .out_56(rom_1_out_56), .out_57(rom_1_out_57), .out_58(rom_1_out_58), .out_59(rom_1_out_59),
    .out_60(rom_1_out_60), .out_61(rom_1_out_61), ._0(program_counter_1__0_2),
    .in_3(program_counter_1_out_38), .in_4(program_counter_1_out_39), .in_5(program_counter_1_out_40),
    .in_6(program_counter_1_out_41), .in_7(program_counter_1_out_42), .in_8(program_counter_1_out_43),
    .in_9(program_counter_1_out_44), .in_13(program_counter_1_out_45), .in_14(program_counter_1_out_46),
    .in_15(program_counter_1_out_47), .in_16(program_counter_1_out_48), .in_17(program_counter_1_out_49),
    .in_18(program_counter_1_out_50), .in_19(program_counter_1_out_51), .in_20(program_counter_1_out_52),
    .in_21(program_counter_1_out_53), .in_22(program_counter_1_out_54), .in_23(program_counter_1_out_55),
    .in_24(program_counter_1_out_56), .in_25(program_counter_1_out_57), .in_26(program_counter_1_out_58),
    .in_27(program_counter_1_out_59), .in_28(program_counter_1_out_60), .CLK(and_75_out),
    .Store_else_Load(undriven), .in_1(undriven_2));
  or or_195 (or_195_out, operations_conditional_6_bit_register_1_out_55, operations_conditional_6_bit_register_1_out_54);
  nor nor_1 (nor_1_out, or_195_out, or_197_out);
  and and_90 (and_90_out, not_2_out, alu_1_out_118);
  and and_91 (and_91_out, not_2_out, alu_1_out_117);
  or or_196 (or_196_out, operations_conditional_6_bit_register_1_out_46, operations_conditional_6_bit_register_1_out_45);
  or or_197 (or_197_out, or_196_out, operations_conditional_6_bit_register_1_out_32);
  and and_92 (and_92_out, rom_1_out_55, nor_1_out);
  Register_Arrays_and_Decoder register_arrays_and_decoder_1 (
    .A0(or_163_out), .A1(or_164_out), .A2(or_165_out), .A3(or_166_out), .A4(or_167_out), .A5(or_168_out),
    .A6(or_169_out), .A7(or_170_out), .A8(or_171_out), .A9(or_172_out), .A10(or_173_out), .A11(or_174_out),
    .A12(or_175_out), .A13(or_176_out), .A14(or_177_out), .A15(or_178_out), .A16(or_179_out),
    .A17(or_180_out), .A18(or_181_out), .A19(or_182_out), .A20(or_183_out), .A21(or_184_out),
    .A22(or_185_out), .A23(or_186_out), .A24(or_187_out), .A25(or_188_out), .A26(or_189_out),
    .A27(or_190_out), .A28(or_191_out), .A29(or_192_out), .A30(or_193_out), .A31(or_194_out),
    ._2_0(gated_d_latch_1_nq), ._2_1(and_101_out), ._2_2(and_102_out), ._2_3(and_96_out), ._2_4(and_97_out),
    ._2_0_2(and_92_out), ._2_1_2(and_172_out), ._2_2_2(and_164_out), ._2_3_2(and_165_out),
    ._2_4_2(and_159_out), ._2_0_3(and_158_out), ._2_1_3(or_206_out), ._2_2_3(or_207_out),
    ._2_3_3(or_214_out), ._2_4_3(or_216_out), .in_16(or_215_out), ._0(register_arrays_and_decoder_1__0),
    .out_50(register_arrays_and_decoder_1_out_50), .out_51(register_arrays_and_decoder_1_out_51),
    .out_52(register_arrays_and_decoder_1_out_52), .out_53(register_arrays_and_decoder_1_out_53),
    .out_54(register_arrays_and_decoder_1_out_54), .out_55(register_arrays_and_decoder_1_out_55),
    .out_56(register_arrays_and_decoder_1_out_56), .out_57(register_arrays_and_decoder_1_out_57),
    .out_58(register_arrays_and_decoder_1_out_58), .out_59(register_arrays_and_decoder_1_out_59),
    .out_60(register_arrays_and_decoder_1_out_60), .out_61(register_arrays_and_decoder_1_out_61),
    .out_62(register_arrays_and_decoder_1_out_62), .out_63(register_arrays_and_decoder_1_out_63),
    .out_64(register_arrays_and_decoder_1_out_64), .out_65(register_arrays_and_decoder_1_out_65),
    .out_66(register_arrays_and_decoder_1_out_66), .out_67(register_arrays_and_decoder_1_out_67),
    .out_68(register_arrays_and_decoder_1_out_68), .out_69(register_arrays_and_decoder_1_out_69),
    .out_70(register_arrays_and_decoder_1_out_70), .out_71(register_arrays_and_decoder_1_out_71),
    .out_72(register_arrays_and_decoder_1_out_72), .out_73(register_arrays_and_decoder_1_out_73),
    .out_74(register_arrays_and_decoder_1_out_74), .out_75(register_arrays_and_decoder_1_out_75),
    .out_76(register_arrays_and_decoder_1_out_76), .out_77(register_arrays_and_decoder_1_out_77),
    .out_78(register_arrays_and_decoder_1_out_78), .out_79(register_arrays_and_decoder_1_out_79),
    .out_80(register_arrays_and_decoder_1_out_80), ._0_2(register_arrays_and_decoder_1__0_2),
    .out_82(register_arrays_and_decoder_1_out_82), .out_83(register_arrays_and_decoder_1_out_83),
    .out_84(register_arrays_and_decoder_1_out_84), .out_85(register_arrays_and_decoder_1_out_85),
    .out_86(register_arrays_and_decoder_1_out_86), .out_87(register_arrays_and_decoder_1_out_87),
    .out_88(register_arrays_and_decoder_1_out_88), .out_89(register_arrays_and_decoder_1_out_89),
    .out_90(register_arrays_and_decoder_1_out_90), .out_91(register_arrays_and_decoder_1_out_91),
    .out_92(register_arrays_and_decoder_1_out_92), .out_93(register_arrays_and_decoder_1_out_93),
    .out_94(register_arrays_and_decoder_1_out_94), .out_95(register_arrays_and_decoder_1_out_95),
    .out_96(register_arrays_and_decoder_1_out_96), .out_97(register_arrays_and_decoder_1_out_97),
    .out_98(register_arrays_and_decoder_1_out_98), .out_99(register_arrays_and_decoder_1_out_99),
    .out_100(register_arrays_and_decoder_1_out_100), .out_101(register_arrays_and_decoder_1_out_101),
    .out_102(register_arrays_and_decoder_1_out_102), .out_103(register_arrays_and_decoder_1_out_103),
    .out_104(register_arrays_and_decoder_1_out_104), .out_105(register_arrays_and_decoder_1_out_105),
    .out_106(register_arrays_and_decoder_1_out_106), .out_107(register_arrays_and_decoder_1_out_107),
    .out_108(register_arrays_and_decoder_1_out_108), .out_109(register_arrays_and_decoder_1_out_109),
    .out_110(register_arrays_and_decoder_1_out_110), .out_111(register_arrays_and_decoder_1_out_111),
    .out_112(register_arrays_and_decoder_1_out_112));
  and and_93 (and_93_out, not_2_out, alu_1_out_120);
  and and_94 (and_94_out, not_2_out, alu_1_out_121);
  and and_95 (and_95_out, not_2_out, alu_1_out_119);
  and and_96 (and_96_out, rom_1_out_53, nor_1_out);
  and and_97 (and_97_out, rom_1_out_54, nor_1_out);
  and and_98 (and_98_out, not_2_out, alu_1_out_124);
  and and_99 (and_99_out, not_2_out, alu_1_out_123);
  and and_100 (and_100_out, not_2_out, alu_1_out_122);
  and and_101 (and_101_out, rom_1_out_51, nor_1_out);
  and and_102 (and_102_out, rom_1_out_52, nor_1_out);
  or or_198 (or_198_out, and_106_out, and_142_out);
  not not_2 (not_2_out, or_340_out);
  and and_103 (and_103_out, or_340_out, alu_1_out_93);
  or or_199 (or_199_out, and_103_out, register_arrays_and_decoder_1_out_80);
  and and_104 (and_104_out, operations_conditional_6_bit_register_1_out_55, n32_bit_general_register_1_d31_2);
  or or_200 (or_200_out, operations_conditional_6_bit_register_1_out_54, operations_conditional_6_bit_register_1_out_32);
  or or_201 (or_201_out, operations_conditional_6_bit_register_1_out_55, or_200_out);
  and and_105 (and_105_out, rom_1_out_54, or_201_out);
  and and_106 (and_106_out, rom_1_out_55, or_201_out);
  or or_202 (or_202_out, and_105_out, and_143_out);
  or or_203 (or_203_out, and_114_out, and_141_out);
  or or_204 (or_204_out, or_202_out, and_192_out);
  or or_205 (or_205_out, or_198_out, and_193_out);
  or or_206 (or_206_out, or_221_out, operations_conditional_6_bit_register_1_out_47);
  or or_207 (or_207_out, or_213_out, operations_conditional_6_bit_register_1_out_47);
  and and_107 (and_107_out, or_340_out, alu_1_out_96);
  and and_108 (and_108_out, or_340_out, alu_1_out_94);
  and and_109 (and_109_out, or_340_out, alu_1_out_95);
  or or_208 (or_208_out, and_108_out, register_arrays_and_decoder_1_out_79);
  or or_209 (or_209_out, and_109_out, register_arrays_and_decoder_1_out_78);
  and and_110 (and_110_out, operations_conditional_6_bit_register_1_out_55, n32_bit_general_register_1_d28_2);
  and and_111 (and_111_out, operations_conditional_6_bit_register_1_out_55, n32_bit_general_register_1_d29_2);
  and and_112 (and_112_out, operations_conditional_6_bit_register_1_out_55, n32_bit_general_register_1_d30_2);
  and and_113 (and_113_out, rom_1_out_51, or_201_out);
  and and_114 (and_114_out, rom_1_out_53, or_201_out);
  and and_115 (and_115_out, rom_1_out_52, or_201_out);
  or or_210 (or_210_out, and_113_out, and_150_out);
  or or_211 (or_211_out, and_115_out, and_151_out);
  or or_212 (or_212_out, or_203_out, and_197_out);
  or or_213 (or_213_out, or_211_out, and_196_out);
  or or_214 (or_214_out, or_212_out, operations_conditional_6_bit_register_1_out_47);
  or or_215 (or_215_out, or_205_out, operations_conditional_6_bit_register_1_out_47);
  or or_216 (or_216_out, or_204_out, operations_conditional_6_bit_register_1_out_47);
  and and_116 (and_116_out, or_340_out, alu_1_out_97);
  and and_117 (and_117_out, or_340_out, alu_1_out_98);
  or or_217 (or_217_out, and_117_out, register_arrays_and_decoder_1_out_75);
  or or_218 (or_218_out, and_116_out, register_arrays_and_decoder_1_out_76);
  or or_219 (or_219_out, and_107_out, register_arrays_and_decoder_1_out_77);
  and and_118 (and_118_out, operations_conditional_6_bit_register_1_out_55, n32_bit_general_register_1_d26_2);
  and and_119 (and_119_out, operations_conditional_6_bit_register_1_out_55, n32_bit_general_register_1_d27_2);
  or or_220 (or_220_out, operations_conditional_6_bit_register_1_out_46, operations_conditional_6_bit_register_1_out_45);
  and and_120 (and_120_out, rom_1_out_55, or_220_out);
  or or_221 (or_221_out, or_210_out, and_198_out);
  and and_121 (and_121_out, or_340_out, alu_1_out_100);
  and and_122 (and_122_out, or_340_out, alu_1_out_101);
  and and_123 (and_123_out, or_340_out, alu_1_out_99);
  or or_222 (or_222_out, and_123_out, register_arrays_and_decoder_1_out_74);
  or or_223 (or_223_out, and_122_out, register_arrays_and_decoder_1_out_72);
  or or_224 (or_224_out, and_121_out, register_arrays_and_decoder_1_out_73);
  and and_124 (and_124_out, operations_conditional_6_bit_register_1_out_55, n32_bit_general_register_1_d24_2);
  and and_125 (and_125_out, operations_conditional_6_bit_register_1_out_55, n32_bit_general_register_1_d23_2);
  and and_126 (and_126_out, operations_conditional_6_bit_register_1_out_55, n32_bit_general_register_1_d25_2);
  or or_225 (or_225_out, operations_conditional_6_bit_register_1_out_9, operations_conditional_6_bit_register_1_out_11);
  or or_226 (or_226_out, operations_conditional_6_bit_register_1_out_23, operations_conditional_6_bit_register_1_out_25);
  or or_227 (or_227_out, operations_conditional_6_bit_register_1_out_19, operations_conditional_6_bit_register_1_out_21);
  or or_228 (or_228_out, or_225_out, or_227_out);
  or or_229 (or_229_out, or_228_out, or_226_out);
  and and_127 (and_127_out, rom_1_out_54, or_220_out);
  and and_128 (and_128_out, rom_1_out_53, or_220_out);
  and and_129 (and_129_out, rom_1_out_52, or_220_out);
  ALU alu_1 (
    ._2_0(register_arrays_and_decoder_1__0), .in_12(register_arrays_and_decoder_1_out_50),
    .in_13(register_arrays_and_decoder_1_out_51), .in_14(register_arrays_and_decoder_1_out_52),
    .in_15(register_arrays_and_decoder_1_out_53), .in_16(register_arrays_and_decoder_1_out_54),
    .in_17(register_arrays_and_decoder_1_out_55), .in_18(register_arrays_and_decoder_1_out_56),
    .in_19(register_arrays_and_decoder_1_out_57), .in_20(register_arrays_and_decoder_1_out_58),
    .in_21(register_arrays_and_decoder_1_out_59), .in_22(register_arrays_and_decoder_1_out_60),
    .in_23(register_arrays_and_decoder_1_out_61), .in_24(register_arrays_and_decoder_1_out_62),
    .in_25(register_arrays_and_decoder_1_out_63), .in_26(register_arrays_and_decoder_1_out_64),
    .in_27(register_arrays_and_decoder_1_out_65), .in_28(register_arrays_and_decoder_1_out_66),
    .in_29(register_arrays_and_decoder_1_out_67), .in_30(register_arrays_and_decoder_1_out_68),
    .in_31(register_arrays_and_decoder_1_out_69), .in_32(register_arrays_and_decoder_1_out_70),
    .in_33(register_arrays_and_decoder_1_out_71), .in_34(register_arrays_and_decoder_1_out_72),
    .in_35(register_arrays_and_decoder_1_out_73), .in_36(register_arrays_and_decoder_1_out_74),
    .in_37(register_arrays_and_decoder_1_out_75), .in_38(register_arrays_and_decoder_1_out_76),
    .in_39(register_arrays_and_decoder_1_out_77), .in_40(register_arrays_and_decoder_1_out_78),
    .in_41(register_arrays_and_decoder_1_out_79), .in_42(register_arrays_and_decoder_1_out_80),
    ._2_0_2(register_arrays_and_decoder_1__0_2), .in_44(register_arrays_and_decoder_1_out_82),
    .in_45(register_arrays_and_decoder_1_out_83), .in_46(register_arrays_and_decoder_1_out_84),
    .in_47(register_arrays_and_decoder_1_out_85), .in_48(register_arrays_and_decoder_1_out_86),
    .in_49(register_arrays_and_decoder_1_out_87), .in_50(register_arrays_and_decoder_1_out_88),
    .in_51(register_arrays_and_decoder_1_out_89), .in_52(register_arrays_and_decoder_1_out_90),
    .in_53(register_arrays_and_decoder_1_out_91), .in_54(register_arrays_and_decoder_1_out_92),
    .in_55(register_arrays_and_decoder_1_out_93), .in_56(register_arrays_and_decoder_1_out_94),
    .in_57(register_arrays_and_decoder_1_out_95), .in_58(register_arrays_and_decoder_1_out_96),
    .in_59(register_arrays_and_decoder_1_out_97), .in_60(register_arrays_and_decoder_1_out_98),
    .in_61(register_arrays_and_decoder_1_out_99), .in_62(register_arrays_and_decoder_1_out_100),
    .in_63(register_arrays_and_decoder_1_out_101), .in_64(register_arrays_and_decoder_1_out_102),
    .in_65(register_arrays_and_decoder_1_out_103), .in_66(register_arrays_and_decoder_1_out_104),
    .in_67(register_arrays_and_decoder_1_out_105), .in_68(register_arrays_and_decoder_1_out_106),
    .in_69(register_arrays_and_decoder_1_out_107), .in_70(register_arrays_and_decoder_1_out_108),
    .in_71(register_arrays_and_decoder_1_out_109), .in_72(register_arrays_and_decoder_1_out_110),
    .in_73(register_arrays_and_decoder_1_out_111), .in_74(register_arrays_and_decoder_1_out_112),
    ._2_0_3(rom_1__0_2), .in_76(rom_1_data), .in_77(rom_1_out_32), .in_78(rom_1_out_33),
    .in_79(rom_1_out_34), .in_80(rom_1_out_35), .in_81(rom_1_out_36), .in_82(rom_1_out_37),
    .in_83(rom_1_out_38), .in_84(rom_1_out_39), .in_85(rom_1_out_40), .in_86(and_216_out),
    .in_87(and_210_out), .in_88(and_209_out), .in_89(and_211_out), .in_90(and_202_out),
    .add(operations_conditional_6_bit_register_1_out_8),
    .addi(operations_conditional_6_bit_register_1_out_9),
    .addu(operations_conditional_6_bit_register_1_out_10),
    .addiu(operations_conditional_6_bit_register_1_out_11),
    .sub(operations_conditional_6_bit_register_1_out_16),
    .subu(operations_conditional_6_bit_register_1_out_17),
    .mult(operations_conditional_6_bit_register_1_out_14),
    .multu(operations_conditional_6_bit_register_1_out_15),
    .div(operations_conditional_6_bit_register_1_out_12),
    .divu(operations_conditional_6_bit_register_1_out_13), .out_93(alu_1_out_93), .out_94(alu_1_out_94),
    .out_95(alu_1_out_95), .out_96(alu_1_out_96), .out_97(alu_1_out_97), .out_98(alu_1_out_98),
    .out_99(alu_1_out_99), .out_100(alu_1_out_100), .out_101(alu_1_out_101), .out_102(alu_1_out_102),
    .out_103(alu_1_out_103), .out_104(alu_1_out_104), .out_105(alu_1_out_105), .out_106(alu_1_out_106),
    .out_107(alu_1_out_107), .out_108(alu_1_out_108), .out_109(alu_1_out_109), .out_110(alu_1_out_110),
    .out_111(alu_1_out_111), .out_112(alu_1_out_112), .out_113(alu_1_out_113), .out_114(alu_1_out_114),
    .out_115(alu_1_out_115), .out_116(alu_1_out_116), .out_117(alu_1_out_117), .out_118(alu_1_out_118),
    .out_119(alu_1_out_119), .out_120(alu_1_out_120), .out_121(alu_1_out_121), .out_122(alu_1_out_122),
    .out_123(alu_1_out_123), .out_124(alu_1_out_124), .out_125(alu_1_out_125), .out_126(alu_1_out_126),
    .out_127(alu_1_out_127), .out_128(alu_1_out_128), .out_129(alu_1_out_129), .out_130(alu_1_out_130),
    .out_131(alu_1_out_131), .out_132(alu_1_out_132), .out_133(alu_1_out_133), .out_134(alu_1_out_134),
    .out_135(alu_1_out_135), .out_136(alu_1_out_136), .out_137(alu_1_out_137), .out_138(alu_1_out_138),
    .out_139(alu_1_out_139), .out_140(alu_1_out_140), .out_141(alu_1_out_141), .out_142(alu_1_out_142),
    .out_143(alu_1_out_143), .out_144(alu_1_out_144), .out_145(alu_1_out_145), .out_146(alu_1_out_146),
    .out_147(alu_1_out_147), .out_148(alu_1_out_148), .out_149(alu_1_out_149), .out_150(alu_1_out_150),
    .out_151(alu_1_out_151), .out_152(alu_1_out_152), .out_153(alu_1_out_153), .out_154(alu_1_out_154),
    .out_155(alu_1_out_155), .out_156(alu_1_out_156));  // open: Carry, Overflow
  and and_130 (and_130_out, or_340_out, alu_1_out_103);
  and and_131 (and_131_out, or_340_out, alu_1_out_102);
  and and_132 (and_132_out, or_340_out, alu_1_out_104);
  or or_230 (or_230_out, and_131_out, register_arrays_and_decoder_1_out_71);
  or or_231 (or_231_out, and_130_out, register_arrays_and_decoder_1_out_70);
  and and_133 (and_133_out, operations_conditional_6_bit_register_1_out_55, n32_bit_general_register_1_d20_2);
  and and_134 (and_134_out, operations_conditional_6_bit_register_1_out_55, n32_bit_general_register_1_d21_2);
  and and_135 (and_135_out, operations_conditional_6_bit_register_1_out_55, n32_bit_general_register_1_d22_2);
  or or_232 (or_232_out, operations_conditional_6_bit_register_1_out_27, operations_conditional_6_bit_register_1_out_29);
  or or_233 (or_233_out, operations_conditional_6_bit_register_1_out_34, operations_conditional_6_bit_register_1_out_36);
  or or_234 (or_234_out, or_232_out, or_233_out);
  or or_235 (or_235_out, or_229_out, or_234_out);
  and and_136 (and_136_out, rom_1_out_51, or_220_out);
  and and_137 (and_137_out, or_340_out, alu_1_out_106);
  and and_138 (and_138_out, or_340_out, alu_1_out_105);
  or or_236 (or_236_out, and_138_out, register_arrays_and_decoder_1_out_68);
  or or_237 (or_237_out, and_132_out, register_arrays_and_decoder_1_out_69);
  or or_238 (or_238_out, and_137_out, register_arrays_and_decoder_1_out_67);
  and and_139 (and_139_out, operations_conditional_6_bit_register_1_out_55, n32_bit_general_register_1_d19_2);
  and and_140 (and_140_out, operations_conditional_6_bit_register_1_out_55, n32_bit_general_register_1_q18);
  and and_141 (and_141_out, rom_1_out_48, or_235_out);
  and and_142 (and_142_out, rom_1_out_50, or_235_out);
  and and_143 (and_143_out, rom_1_out_49, or_235_out);
  and and_144 (and_144_out, or_340_out, alu_1_out_107);
  and and_145 (and_145_out, or_340_out, alu_1_out_108);
  and and_146 (and_146_out, or_340_out, alu_1_out_109);
  or or_239 (or_239_out, and_145_out, register_arrays_and_decoder_1_out_65);
  or or_240 (or_240_out, and_146_out, register_arrays_and_decoder_1_out_64);
  or or_241 (or_241_out, and_144_out, register_arrays_and_decoder_1_out_66);
  and and_147 (and_147_out, operations_conditional_6_bit_register_1_out_55, n32_bit_general_register_1_q15);
  and and_148 (and_148_out, operations_conditional_6_bit_register_1_out_55, n32_bit_general_register_1_q17);
  and and_149 (and_149_out, operations_conditional_6_bit_register_1_out_55, n32_bit_general_register_1_q16);
  and and_150 (and_150_out, rom_1_out_46, or_235_out);
  and and_151 (and_151_out, rom_1_out_47, or_235_out);
  Logical_Unit logical_unit_1 (
    ._2_0(rom_1__0_2), .in_13(rom_1_data), .in_14(rom_1_out_32), .in_15(rom_1_out_33), .in_16(rom_1_out_34),
    .in_17(rom_1_out_35), .in_18(rom_1_out_36), .in_19(rom_1_out_37), .in_20(rom_1_out_38),
    .in_21(rom_1_out_39), .in_22(rom_1_out_40), .in_23(and_216_out), .in_24(and_210_out),
    .in_25(and_209_out), .in_26(and_211_out), .in_27(and_202_out),
    ._2_0_2(register_arrays_and_decoder_1__0_2), .in_29(register_arrays_and_decoder_1_out_82),
    .in_30(register_arrays_and_decoder_1_out_83), .in_31(register_arrays_and_decoder_1_out_84),
    .in_32(register_arrays_and_decoder_1_out_85), .in_33(register_arrays_and_decoder_1_out_86),
    .in_34(register_arrays_and_decoder_1_out_87), .in_35(register_arrays_and_decoder_1_out_88),
    .in_36(register_arrays_and_decoder_1_out_89), .in_37(register_arrays_and_decoder_1_out_90),
    .in_38(register_arrays_and_decoder_1_out_91), .in_39(register_arrays_and_decoder_1_out_92),
    .in_40(register_arrays_and_decoder_1_out_93), .in_41(register_arrays_and_decoder_1_out_94),
    .in_42(register_arrays_and_decoder_1_out_95), .in_43(register_arrays_and_decoder_1_out_96),
    .in_44(register_arrays_and_decoder_1_out_97), .in_45(register_arrays_and_decoder_1_out_98),
    .in_46(register_arrays_and_decoder_1_out_99), .in_47(register_arrays_and_decoder_1_out_100),
    .in_48(register_arrays_and_decoder_1_out_101), .in_49(register_arrays_and_decoder_1_out_102),
    .in_50(register_arrays_and_decoder_1_out_103), .in_51(register_arrays_and_decoder_1_out_104),
    .in_52(register_arrays_and_decoder_1_out_105), .in_53(register_arrays_and_decoder_1_out_106),
    .in_54(register_arrays_and_decoder_1_out_107), .in_55(register_arrays_and_decoder_1_out_108),
    .in_56(register_arrays_and_decoder_1_out_109), .in_57(register_arrays_and_decoder_1_out_110),
    .in_58(register_arrays_and_decoder_1_out_111), .in_59(register_arrays_and_decoder_1_out_112),
    ._2_0_3(register_arrays_and_decoder_1__0), .in_61(register_arrays_and_decoder_1_out_50),
    .in_62(register_arrays_and_decoder_1_out_51), .in_63(register_arrays_and_decoder_1_out_52),
    .in_64(register_arrays_and_decoder_1_out_53), .in_65(register_arrays_and_decoder_1_out_54),
    .in_66(register_arrays_and_decoder_1_out_55), .in_67(register_arrays_and_decoder_1_out_56),
    .in_68(register_arrays_and_decoder_1_out_57), .in_69(register_arrays_and_decoder_1_out_58),
    .in_70(register_arrays_and_decoder_1_out_59), .in_71(register_arrays_and_decoder_1_out_60),
    .in_72(register_arrays_and_decoder_1_out_61), .in_73(register_arrays_and_decoder_1_out_62),
    .in_74(register_arrays_and_decoder_1_out_63), .in_75(register_arrays_and_decoder_1_out_64),
    .in_76(register_arrays_and_decoder_1_out_65), .in_77(register_arrays_and_decoder_1_out_66),
    .in_78(register_arrays_and_decoder_1_out_67), .in_79(register_arrays_and_decoder_1_out_68),
    .in_80(register_arrays_and_decoder_1_out_69), .in_81(register_arrays_and_decoder_1_out_70),
    .in_82(register_arrays_and_decoder_1_out_71), .in_83(register_arrays_and_decoder_1_out_72),
    .in_84(register_arrays_and_decoder_1_out_73), .in_85(register_arrays_and_decoder_1_out_74),
    .in_86(register_arrays_and_decoder_1_out_75), .in_87(register_arrays_and_decoder_1_out_76),
    .in_88(register_arrays_and_decoder_1_out_77), .in_89(register_arrays_and_decoder_1_out_78),
    .in_90(register_arrays_and_decoder_1_out_79), .in_91(register_arrays_and_decoder_1_out_80),
    ._0(logical_unit_1__0), .out_93(logical_unit_1_out_93), .out_94(logical_unit_1_out_94),
    .out_95(logical_unit_1_out_95), .out_96(logical_unit_1_out_96), .out_97(logical_unit_1_out_97),
    .out_98(logical_unit_1_out_98), .out_99(logical_unit_1_out_99), .out_100(logical_unit_1_out_100),
    .out_101(logical_unit_1_out_101), .out_102(logical_unit_1_out_102), .out_103(logical_unit_1_out_103),
    .out_104(logical_unit_1_out_104), .out_105(logical_unit_1_out_105), .out_106(logical_unit_1_out_106),
    .out_107(logical_unit_1_out_107), .out_108(logical_unit_1_out_108), .out_109(logical_unit_1_out_109),
    .out_110(logical_unit_1_out_110), .out_111(logical_unit_1_out_111), .out_112(logical_unit_1_out_112),
    .out_113(logical_unit_1_out_113), .out_114(logical_unit_1_out_114), .out_115(logical_unit_1_out_115),
    .out_116(logical_unit_1_out_116), .out_117(logical_unit_1_out_117), .out_118(logical_unit_1_out_118),
    .out_119(logical_unit_1_out_119), .out_120(logical_unit_1_out_120), .out_121(logical_unit_1_out_121),
    .out_122(logical_unit_1_out_122), .out_123(logical_unit_1_out_123),
    .in_1(operations_conditional_6_bit_register_1_out_30),
    .in_2(operations_conditional_6_bit_register_1_out_31),
    .in_3(operations_conditional_6_bit_register_1_out_33),
    .in_4(operations_conditional_6_bit_register_1_out_34),
    .in_5(operations_conditional_6_bit_register_1_out_35),
    .in_6(operations_conditional_6_bit_register_1_out_36), .H0(and_215_out), .in_8(and_207_out),
    .in_9(and_206_out), .in_10(and_208_out), .in_11(and_201_out));
  Bitwise_Logic__Main bitwise_logic_main_1 (
    ._2_0(rom_1__0_2), .in_2(rom_1_data), .in_3(rom_1_out_32), .in_4(rom_1_out_33), .in_5(rom_1_out_34),
    .in_6(rom_1_out_35), .in_7(rom_1_out_36), .in_8(rom_1_out_37), .in_9(rom_1_out_38), .in_10(rom_1_out_39),
    .in_11(rom_1_out_40), .in_12(and_216_out), .in_13(and_210_out), .in_14(and_209_out), .in_15(and_211_out),
    .in_16(and_202_out), ._2_0_2(register_arrays_and_decoder_1__0),
    .in_18(register_arrays_and_decoder_1_out_50), .in_19(register_arrays_and_decoder_1_out_51),
    .in_20(register_arrays_and_decoder_1_out_52), .in_21(register_arrays_and_decoder_1_out_53),
    .in_22(register_arrays_and_decoder_1_out_54), .in_23(register_arrays_and_decoder_1_out_55),
    .in_24(register_arrays_and_decoder_1_out_56), .in_25(register_arrays_and_decoder_1_out_57),
    .in_26(register_arrays_and_decoder_1_out_58), .in_27(register_arrays_and_decoder_1_out_59),
    .in_28(register_arrays_and_decoder_1_out_60), .in_29(register_arrays_and_decoder_1_out_61),
    .in_30(register_arrays_and_decoder_1_out_62), .in_31(register_arrays_and_decoder_1_out_63),
    .in_32(register_arrays_and_decoder_1_out_64), .in_33(register_arrays_and_decoder_1_out_65),
    .in_34(register_arrays_and_decoder_1_out_66), .in_35(register_arrays_and_decoder_1_out_67),
    .in_36(register_arrays_and_decoder_1_out_68), .in_37(register_arrays_and_decoder_1_out_69),
    .in_38(register_arrays_and_decoder_1_out_70), .in_39(register_arrays_and_decoder_1_out_71),
    .in_40(register_arrays_and_decoder_1_out_72), .in_41(register_arrays_and_decoder_1_out_73),
    .in_42(register_arrays_and_decoder_1_out_74), .in_43(register_arrays_and_decoder_1_out_75),
    .in_44(register_arrays_and_decoder_1_out_76), .in_45(register_arrays_and_decoder_1_out_77),
    .in_46(register_arrays_and_decoder_1_out_78), .in_47(register_arrays_and_decoder_1_out_79),
    .t(register_arrays_and_decoder_1_out_80), ._2_0_3(register_arrays_and_decoder_1__0_2),
    .in_50(register_arrays_and_decoder_1_out_82), .in_51(register_arrays_and_decoder_1_out_83),
    .in_52(register_arrays_and_decoder_1_out_84), .in_53(register_arrays_and_decoder_1_out_85),
    .in_54(register_arrays_and_decoder_1_out_86), .in_55(register_arrays_and_decoder_1_out_87),
    .in_56(register_arrays_and_decoder_1_out_88), .in_57(register_arrays_and_decoder_1_out_89),
    .in_58(register_arrays_and_decoder_1_out_90), .in_59(register_arrays_and_decoder_1_out_91),
    .in_60(register_arrays_and_decoder_1_out_92), .in_61(register_arrays_and_decoder_1_out_93),
    .in_62(register_arrays_and_decoder_1_out_94), .in_63(register_arrays_and_decoder_1_out_95),
    .in_64(register_arrays_and_decoder_1_out_96), .in_65(register_arrays_and_decoder_1_out_97),
    .in_66(register_arrays_and_decoder_1_out_98), .in_67(register_arrays_and_decoder_1_out_99),
    .in_68(register_arrays_and_decoder_1_out_100), .in_69(register_arrays_and_decoder_1_out_101),
    .in_70(register_arrays_and_decoder_1_out_102), .in_71(register_arrays_and_decoder_1_out_103),
    .in_72(register_arrays_and_decoder_1_out_104), .in_73(register_arrays_and_decoder_1_out_105),
    .in_74(register_arrays_and_decoder_1_out_106), .in_75(register_arrays_and_decoder_1_out_107),
    .in_76(register_arrays_and_decoder_1_out_108), .in_77(register_arrays_and_decoder_1_out_109),
    .in_78(register_arrays_and_decoder_1_out_110), .in_79(register_arrays_and_decoder_1_out_111),
    .in_80(register_arrays_and_decoder_1_out_112), ._0(bitwise_logic_main_1__0),
    .out_94(bitwise_logic_main_1_out_94), .out_95(bitwise_logic_main_1_out_95),
    .out_96(bitwise_logic_main_1_out_96), .out_97(bitwise_logic_main_1_out_97),
    .out_98(bitwise_logic_main_1_out_98), .out_99(bitwise_logic_main_1_out_99),
    .out_100(bitwise_logic_main_1_out_100), .out_101(bitwise_logic_main_1_out_101),
    .out_102(bitwise_logic_main_1_out_102), .out_103(bitwise_logic_main_1_out_103),
    .out_104(bitwise_logic_main_1_out_104), .out_105(bitwise_logic_main_1_out_105),
    .out_106(bitwise_logic_main_1_out_106), .out_107(bitwise_logic_main_1_out_107),
    .out_108(bitwise_logic_main_1_out_108), .out_109(bitwise_logic_main_1_out_109),
    .out_110(bitwise_logic_main_1_out_110), .out_111(bitwise_logic_main_1_out_111),
    .out_112(bitwise_logic_main_1_out_112), .out_113(bitwise_logic_main_1_out_113),
    .out_114(bitwise_logic_main_1_out_114), .out_115(bitwise_logic_main_1_out_115),
    .out_116(bitwise_logic_main_1_out_116), .out_117(bitwise_logic_main_1_out_117),
    .out_118(bitwise_logic_main_1_out_118), .out_119(bitwise_logic_main_1_out_119),
    .out_120(bitwise_logic_main_1_out_120), .out_121(bitwise_logic_main_1_out_121),
    .out_122(bitwise_logic_main_1_out_122), .out_123(bitwise_logic_main_1_out_123),
    .out_124(bitwise_logic_main_1_out_124), .\and (operations_conditional_6_bit_register_1_out_18),
    .andi(operations_conditional_6_bit_register_1_out_19),
    .\nand (operations_conditional_6_bit_register_1_out_20),
    .nandi(operations_conditional_6_bit_register_1_out_21),
    .\or (operations_conditional_6_bit_register_1_out_22),
    .ori(operations_conditional_6_bit_register_1_out_23),
    .\nor (operations_conditional_6_bit_register_1_out_24),
    .nori(operations_conditional_6_bit_register_1_out_25),
    .\xor (operations_conditional_6_bit_register_1_out_26),
    .xori(operations_conditional_6_bit_register_1_out_27),
    .\xnor (operations_conditional_6_bit_register_1_out_28),
    .xnori(operations_conditional_6_bit_register_1_out_29));
  Branch_Unit branch_unit_1 (
    ._2_0(register_arrays_and_decoder_1__0_2), .in_8(register_arrays_and_decoder_1_out_82),
    .in_9(register_arrays_and_decoder_1_out_83), .in_10(register_arrays_and_decoder_1_out_84),
    .in_11(register_arrays_and_decoder_1_out_85), .in_12(register_arrays_and_decoder_1_out_86),
    .in_13(register_arrays_and_decoder_1_out_87), .in_14(register_arrays_and_decoder_1_out_88),
    .in_15(register_arrays_and_decoder_1_out_89), .in_16(register_arrays_and_decoder_1_out_90),
    .in_17(register_arrays_and_decoder_1_out_91), .in_18(register_arrays_and_decoder_1_out_92),
    .in_19(register_arrays_and_decoder_1_out_93), .in_20(register_arrays_and_decoder_1_out_94),
    .in_21(register_arrays_and_decoder_1_out_95), .in_22(register_arrays_and_decoder_1_out_96),
    .in_23(register_arrays_and_decoder_1_out_97), .in_24(register_arrays_and_decoder_1_out_98),
    .in_25(register_arrays_and_decoder_1_out_99), .in_26(register_arrays_and_decoder_1_out_100),
    .in_27(register_arrays_and_decoder_1_out_101), .in_28(register_arrays_and_decoder_1_out_102),
    .in_29(register_arrays_and_decoder_1_out_103), .in_30(register_arrays_and_decoder_1_out_104),
    .in_31(register_arrays_and_decoder_1_out_105), .in_32(register_arrays_and_decoder_1_out_106),
    .in_33(register_arrays_and_decoder_1_out_107), .in_34(register_arrays_and_decoder_1_out_108),
    .in_35(register_arrays_and_decoder_1_out_109), .in_36(register_arrays_and_decoder_1_out_110),
    .in_37(register_arrays_and_decoder_1_out_111), .in_38(register_arrays_and_decoder_1_out_112),
    ._2_0_2(register_arrays_and_decoder_1__0), .in_40(register_arrays_and_decoder_1_out_50),
    .in_41(register_arrays_and_decoder_1_out_51), .in_42(register_arrays_and_decoder_1_out_52),
    .in_43(register_arrays_and_decoder_1_out_53), .in_44(register_arrays_and_decoder_1_out_54),
    .in_45(register_arrays_and_decoder_1_out_55), .in_46(register_arrays_and_decoder_1_out_56),
    .in_47(register_arrays_and_decoder_1_out_57), .in_48(register_arrays_and_decoder_1_out_58),
    .in_49(register_arrays_and_decoder_1_out_59), .in_50(register_arrays_and_decoder_1_out_60),
    .in_51(register_arrays_and_decoder_1_out_61), .in_52(register_arrays_and_decoder_1_out_62),
    .in_53(register_arrays_and_decoder_1_out_63), .in_54(register_arrays_and_decoder_1_out_64),
    .in_55(register_arrays_and_decoder_1_out_65), .in_56(register_arrays_and_decoder_1_out_66),
    .in_57(register_arrays_and_decoder_1_out_67), .in_58(register_arrays_and_decoder_1_out_68),
    .in_59(register_arrays_and_decoder_1_out_69), .in_60(register_arrays_and_decoder_1_out_70),
    .in_61(register_arrays_and_decoder_1_out_71), .in_62(register_arrays_and_decoder_1_out_72),
    .in_63(register_arrays_and_decoder_1_out_73), .in_64(register_arrays_and_decoder_1_out_74),
    .in_65(register_arrays_and_decoder_1_out_75), .in_66(register_arrays_and_decoder_1_out_76),
    .in_67(register_arrays_and_decoder_1_out_77), .in_68(register_arrays_and_decoder_1_out_78),
    .in_69(register_arrays_and_decoder_1_out_79), .in_70(register_arrays_and_decoder_1_out_80),
    ._2_0_3(rom_1__0_2), .in_72(rom_1_data), .in_73(rom_1_out_32), .in_74(rom_1_out_33),
    .in_75(rom_1_out_34), .in_76(rom_1_out_35), .in_77(rom_1_out_36), .in_78(rom_1_out_37),
    .in_79(rom_1_out_38), .in_80(rom_1_out_39), .in_81(rom_1_out_40), .in_82(and_216_out),
    .in_83(and_210_out), .in_84(and_209_out), .in_85(and_211_out), .in_86(and_202_out),
    ._0(branch_unit_1__0), .out_88(branch_unit_1_out_88), .out_89(branch_unit_1_out_89),
    .out_90(branch_unit_1_out_90), .out_91(branch_unit_1_out_91), .out_92(branch_unit_1_out_92),
    .out_93(branch_unit_1_out_93), .out_94(branch_unit_1_out_94), .out_95(branch_unit_1_out_95),
    .out_96(branch_unit_1_out_96), .out_97(branch_unit_1_out_97), .out_98(branch_unit_1_out_98),
    .out_99(branch_unit_1_out_99), .out_100(branch_unit_1_out_100), .out_101(branch_unit_1_out_101),
    .out_102(branch_unit_1_out_102), .out_103(branch_unit_1_out_103), .out_104(branch_unit_1_out_104),
    .out_105(branch_unit_1_out_105), .out_106(branch_unit_1_out_106), .out_107(branch_unit_1_out_107),
    .out_108(branch_unit_1_out_108), .out_109(branch_unit_1_out_109), .out_110(branch_unit_1_out_110),
    .out_111(branch_unit_1_out_111), .out_112(branch_unit_1_out_112), .out_113(branch_unit_1_out_113),
    .out_114(branch_unit_1_out_114), .out_115(branch_unit_1_out_115), .out_116(branch_unit_1_out_116),
    .out_117(branch_unit_1_out_117), .out_118(branch_unit_1_out_118),
    .in_1(operations_conditional_6_bit_register_1_out_37), .in_2(or_324_out),
    .in_3(operations_conditional_6_bit_register_1_out_40),
    .in_4(operations_conditional_6_bit_register_1_out_41), .in_5(or_330_out),
    .in_6(operations_conditional_6_bit_register_1_out_44));
  and and_152 (and_152_out, or_340_out, alu_1_out_111);
  and and_153 (and_153_out, or_340_out, alu_1_out_112);
  and and_154 (and_154_out, or_340_out, alu_1_out_110);
  or or_242 (or_242_out, and_154_out, register_arrays_and_decoder_1_out_63);
  or or_243 (or_243_out, and_152_out, register_arrays_and_decoder_1_out_62);
  and and_155 (and_155_out, operations_conditional_6_bit_register_1_out_55, n32_bit_general_register_1_q12);
  and and_156 (and_156_out, operations_conditional_6_bit_register_1_out_55, n32_bit_general_register_1_q13);
  and and_157 (and_157_out, operations_conditional_6_bit_register_1_out_55, n32_bit_general_register_1_q14);
  nor nor_2 (nor_2_out, or_235_out, or_254_out);
  and and_158 (and_158_out, rom_1_out_50, nor_2_out);
  and and_159 (and_159_out, rom_1_out_49, nor_2_out);
  and and_160 (and_160_out, or_340_out, alu_1_out_114);
  and and_161 (and_161_out, or_340_out, alu_1_out_113);
  or or_244 (or_244_out, and_153_out, register_arrays_and_decoder_1_out_61);
  or or_245 (or_245_out, and_160_out, register_arrays_and_decoder_1_out_59);
  or or_246 (or_246_out, and_161_out, register_arrays_and_decoder_1_out_60);
  and and_162 (and_162_out, operations_conditional_6_bit_register_1_out_55, n32_bit_general_register_1_q11);
  and and_163 (and_163_out, operations_conditional_6_bit_register_1_out_55, n32_bit_general_register_1_q10);
  and and_164 (and_164_out, rom_1_out_47, nor_2_out);
  and and_165 (and_165_out, rom_1_out_48, nor_2_out);
  and and_166 (and_166_out, or_340_out, alu_1_out_117);
  and and_167 (and_167_out, or_340_out, alu_1_out_116);
  and and_168 (and_168_out, or_340_out, alu_1_out_115);
  or or_247 (or_247_out, and_166_out, register_arrays_and_decoder_1_out_56);
  or or_248 (or_248_out, and_167_out, register_arrays_and_decoder_1_out_57);
  or or_249 (or_249_out, and_168_out, register_arrays_and_decoder_1_out_58);
  and and_169 (and_169_out, operations_conditional_6_bit_register_1_out_55, n32_bit_general_register_1_q7);
  and and_170 (and_170_out, operations_conditional_6_bit_register_1_out_55, n32_bit_general_register_1_q8);
  and and_171 (and_171_out, operations_conditional_6_bit_register_1_out_55, n32_bit_general_register_1_q9);
  and and_172 (and_172_out, rom_1_out_46, nor_2_out);
  and and_173 (and_173_out, rom_1_out_50, or_254_out);
  and and_174 (and_174_out, or_340_out, alu_1_out_118);
  and and_175 (and_175_out, or_340_out, alu_1_out_119);
  and and_176 (and_176_out, or_340_out, alu_1_out_120);
  or or_250 (or_250_out, and_174_out, register_arrays_and_decoder_1_out_55);
  or or_251 (or_251_out, and_175_out, register_arrays_and_decoder_1_out_54);
  and and_177 (and_177_out, operations_conditional_6_bit_register_1_out_55, n32_bit_general_register_1_q4);
  and and_178 (and_178_out, operations_conditional_6_bit_register_1_out_55, n32_bit_general_register_1_q5);
  and and_179 (and_179_out, operations_conditional_6_bit_register_1_out_55, n32_bit_general_register_1_q6);
  or or_252 (or_252_out, operations_conditional_6_bit_register_1_out_8, operations_conditional_6_bit_register_1_out_10);
  or or_253 (or_253_out, or_252_out, or_258_out);
  or or_254 (or_254_out, operations_conditional_6_bit_register_1_out_46, operations_conditional_6_bit_register_1_out_45);
  and and_180 (and_180_out, rom_1_out_48, or_254_out);
  and and_181 (and_181_out, rom_1_out_49, or_254_out);
  and and_182 (and_182_out, or_340_out, alu_1_out_121);
  and and_183 (and_183_out, or_340_out, alu_1_out_122);
  or or_255 (or_255_out, and_176_out, register_arrays_and_decoder_1_out_53);
  or or_256 (or_256_out, and_183_out, register_arrays_and_decoder_1_out_51);
  or or_257 (or_257_out, and_182_out, register_arrays_and_decoder_1_out_52);
  and and_184 (and_184_out, operations_conditional_6_bit_register_1_out_55, n32_bit_general_register_1_q3);
  and and_185 (and_185_out, operations_conditional_6_bit_register_1_out_55, n32_bit_general_register_1_q2);
  or or_258 (or_258_out, operations_conditional_6_bit_register_1_out_16, operations_conditional_6_bit_register_1_out_17);
  or or_259 (or_259_out, operations_conditional_6_bit_register_1_out_18, operations_conditional_6_bit_register_1_out_20);
  or or_260 (or_260_out, operations_conditional_6_bit_register_1_out_22, operations_conditional_6_bit_register_1_out_24);
  or or_261 (or_261_out, or_259_out, or_260_out);
  or or_262 (or_262_out, or_253_out, or_261_out);
  and and_186 (and_186_out, rom_1_out_47, or_254_out);
  and and_187 (and_187_out, rom_1_out_46, or_254_out);
  and and_188 (and_188_out, or_340_out, alu_1_out_123);
  and and_189 (and_189_out, or_340_out, alu_1_out_124);
  or or_263 (or_263_out, and_189_out, register_arrays_and_decoder_1__0);
  or or_264 (or_264_out, and_188_out, register_arrays_and_decoder_1_out_50);
  _32_Bit_General_Register u_32_bit_general_register_1 (
    .E(or_265_out), .D0(or_263_out), .Q0(n32_bit_general_register_1_q0), .D1(or_264_out),
    .Q1(n32_bit_general_register_1_q1), .D2(or_256_out), .Q2(n32_bit_general_register_1_q2), .D3(or_257_out),
    .Q3(n32_bit_general_register_1_q3), .D4(or_255_out), .Q4(n32_bit_general_register_1_q4), .D5(or_251_out),
    .Q5(n32_bit_general_register_1_q5), .D6(or_250_out), .Q6(n32_bit_general_register_1_q6), .D7(or_247_out),
    .Q7(n32_bit_general_register_1_q7), .D8(or_248_out), .Q8(n32_bit_general_register_1_q8), .D9(or_249_out),
    .Q9(n32_bit_general_register_1_q9), .D10(or_245_out), .Q10(n32_bit_general_register_1_q10),
    .D11(or_246_out), .Q11(n32_bit_general_register_1_q11), .D12(or_244_out),
    .Q12(n32_bit_general_register_1_q12), .D13(or_243_out), .Q13(n32_bit_general_register_1_q13),
    .D14(or_242_out), .Q14(n32_bit_general_register_1_q14), .D15(or_240_out),
    .Q15(n32_bit_general_register_1_q15), .D16(or_239_out), .Q16(n32_bit_general_register_1_q16),
    .D17(or_241_out), .Q17(n32_bit_general_register_1_q17), .D18(or_238_out),
    .Q18(n32_bit_general_register_1_q18), .D19(or_236_out), .D19_2(n32_bit_general_register_1_d19_2),
    .D20(or_237_out), .D20_2(n32_bit_general_register_1_d20_2), .D21(or_231_out),
    .D21_2(n32_bit_general_register_1_d21_2), .D22(or_230_out), .D22_2(n32_bit_general_register_1_d22_2),
    .D23(or_223_out), .D23_2(n32_bit_general_register_1_d23_2), .D24(or_224_out),
    .D24_2(n32_bit_general_register_1_d24_2), .D25(or_222_out), .D25_2(n32_bit_general_register_1_d25_2),
    .D26(or_217_out), .D26_2(n32_bit_general_register_1_d26_2), .D27(or_218_out),
    .D27_2(n32_bit_general_register_1_d27_2), .D28(or_219_out), .D28_2(n32_bit_general_register_1_d28_2),
    .D29(or_209_out), .D29_2(n32_bit_general_register_1_d29_2), .D30(or_208_out),
    .D30_2(n32_bit_general_register_1_d30_2), .D31(or_199_out), .D31_2(n32_bit_general_register_1_d31_2));
  or or_265 (or_265_out, and_239_out, operations_conditional_6_bit_register_1_out_57);
  and and_190 (and_190_out, operations_conditional_6_bit_register_1_out_55, n32_bit_general_register_1_q0);
  and and_191 (and_191_out, operations_conditional_6_bit_register_1_out_55, n32_bit_general_register_1_q1);
  or or_266 (or_266_out, operations_conditional_6_bit_register_1_out_33, operations_conditional_6_bit_register_1_out_35);
  or or_267 (or_267_out, operations_conditional_6_bit_register_1_out_26, operations_conditional_6_bit_register_1_out_28);
  or or_268 (or_268_out, or_267_out, or_266_out);
  or or_269 (or_269_out, or_262_out, or_268_out);
  and and_192 (and_192_out, rom_1_out_44, or_269_out);
  and and_193 (and_193_out, rom_1_out_45, or_269_out);
  or or_270 (or_270_out, alu_1_out_125, register_arrays_and_decoder_1_out_80);
  and and_194 (and_194_out, operations_conditional_6_bit_register_1_out_54, n32_bit_general_register_2_d30_2);
  and and_195 (and_195_out, operations_conditional_6_bit_register_1_out_54, n32_bit_general_register_2_d31_2);
  and and_196 (and_196_out, rom_1_out_42, or_269_out);
  and and_197 (and_197_out, rom_1_out_43, or_269_out);
  and and_198 (and_198_out, rom_1_out_41, or_269_out);
  or or_271 (or_271_out, alu_1_out_126, register_arrays_and_decoder_1_out_79);
  or or_272 (or_272_out, alu_1_out_127, register_arrays_and_decoder_1_out_78);
  or or_273 (or_273_out, alu_1_out_128, register_arrays_and_decoder_1_out_77);
  and and_199 (and_199_out, operations_conditional_6_bit_register_1_out_54, n32_bit_general_register_2_d29_2);
  and and_200 (and_200_out, operations_conditional_6_bit_register_1_out_54, n32_bit_general_register_2_d28_2);
  or or_274 (or_274_out, operations_conditional_6_bit_register_1_out_31, operations_conditional_6_bit_register_1_out_30);
  and and_201 (and_201_out, rom_1_out_45, or_274_out);
  not not_3 (not_3_out, or_269_out);
  and and_202 (and_202_out, rom_1_out_45, not_3_out);
  or or_275 (or_275_out, alu_1_out_131, register_arrays_and_decoder_1_out_74);
  or or_276 (or_276_out, alu_1_out_129, register_arrays_and_decoder_1_out_76);
  or or_277 (or_277_out, alu_1_out_130, register_arrays_and_decoder_1_out_75);
  and and_203 (and_203_out, operations_conditional_6_bit_register_1_out_54, n32_bit_general_register_2_d25_2);
  and and_204 (and_204_out, operations_conditional_6_bit_register_1_out_54, n32_bit_general_register_2_d27_2);
  and and_205 (and_205_out, operations_conditional_6_bit_register_1_out_54, n32_bit_general_register_2_d26_2);
  and and_206 (and_206_out, rom_1_out_43, or_274_out);
  and and_207 (and_207_out, rom_1_out_42, or_274_out);
  and and_208 (and_208_out, rom_1_out_44, or_274_out);
  and and_209 (and_209_out, rom_1_out_43, not_3_out);
  and and_210 (and_210_out, rom_1_out_42, not_3_out);
  and and_211 (and_211_out, rom_1_out_44, not_3_out);
  or or_278 (or_278_out, bitwise_logic_main_1_out_124, logical_unit_1_out_123);
  or or_279 (or_279_out, alu_1_out_133, register_arrays_and_decoder_1_out_72);
  or or_280 (or_280_out, alu_1_out_132, register_arrays_and_decoder_1_out_73);
  and and_212 (and_212_out, operations_conditional_6_bit_register_1_out_54, n32_bit_general_register_2_d23_2);
  and and_213 (and_213_out, operations_conditional_6_bit_register_1_out_54, n32_bit_general_register_2_d24_2);
  and and_214 (and_214_out, operations_conditional_6_bit_register_1_out_54, n32_bit_general_register_2_d22_2);
  and and_215 (and_215_out, rom_1_out_41, or_274_out);
  and and_216 (and_216_out, rom_1_out_41, not_3_out);
  or or_281 (or_281_out, bitwise_logic_main_1_out_123, logical_unit_1_out_122);
  or or_282 (or_282_out, bitwise_logic_main_1_out_121, logical_unit_1_out_120);
  or or_283 (or_283_out, bitwise_logic_main_1_out_122, logical_unit_1_out_121);
  or or_284 (or_284_out, alu_1_out_135, register_arrays_and_decoder_1_out_70);
  or or_285 (or_285_out, alu_1_out_136, register_arrays_and_decoder_1_out_69);
  or or_286 (or_286_out, alu_1_out_134, register_arrays_and_decoder_1_out_71);
  and and_217 (and_217_out, operations_conditional_6_bit_register_1_out_54, n32_bit_general_register_2_d21_2);
  and and_218 (and_218_out, operations_conditional_6_bit_register_1_out_54, n32_bit_general_register_2_d20_2);
  or or_287 (or_287_out, bitwise_logic_main_1_out_119, logical_unit_1_out_118);
  or or_288 (or_288_out, bitwise_logic_main_1_out_120, logical_unit_1_out_119);
  or or_289 (or_289_out, alu_1_out_139, register_arrays_and_decoder_1_out_66);
  or or_290 (or_290_out, alu_1_out_138, register_arrays_and_decoder_1_out_67);
  or or_291 (or_291_out, alu_1_out_137, register_arrays_and_decoder_1_out_68);
  and and_219 (and_219_out, operations_conditional_6_bit_register_1_out_54, n32_bit_general_register_2_q18);
  and and_220 (and_220_out, operations_conditional_6_bit_register_1_out_54, n32_bit_general_register_2_q17);
  and and_221 (and_221_out, operations_conditional_6_bit_register_1_out_54, n32_bit_general_register_2_d19_2);
  or or_292 (or_292_out, bitwise_logic_main_1_out_118, logical_unit_1_out_117);
  or or_293 (or_293_out, bitwise_logic_main_1_out_116, logical_unit_1_out_115);
  or or_294 (or_294_out, bitwise_logic_main_1_out_117, logical_unit_1_out_116);
  or or_295 (or_295_out, alu_1_out_140, register_arrays_and_decoder_1_out_65);
  or or_296 (or_296_out, alu_1_out_141, register_arrays_and_decoder_1_out_64);
  and and_222 (and_222_out, operations_conditional_6_bit_register_1_out_54, n32_bit_general_register_2_q14);
  and and_223 (and_223_out, operations_conditional_6_bit_register_1_out_54, n32_bit_general_register_2_q15);
  and and_224 (and_224_out, operations_conditional_6_bit_register_1_out_54, n32_bit_general_register_2_q16);
  or or_297 (or_297_out, bitwise_logic_main_1_out_114, logical_unit_1_out_113);
  or or_298 (or_298_out, bitwise_logic_main_1_out_113, logical_unit_1_out_112);
  or or_299 (or_299_out, bitwise_logic_main_1_out_115, logical_unit_1_out_114);
  or or_300 (or_300_out, alu_1_out_142, register_arrays_and_decoder_1_out_63);
  or or_301 (or_301_out, alu_1_out_144, register_arrays_and_decoder_1_out_61);
  or or_302 (or_302_out, alu_1_out_143, register_arrays_and_decoder_1_out_62);
  and and_225 (and_225_out, operations_conditional_6_bit_register_1_out_54, n32_bit_general_register_2_q12);
  and and_226 (and_226_out, operations_conditional_6_bit_register_1_out_54, n32_bit_general_register_2_q13);
  or or_303 (or_303_out, bitwise_logic_main_1_out_112, logical_unit_1_out_111);
  or or_304 (or_304_out, bitwise_logic_main_1_out_111, logical_unit_1_out_110);
  or or_305 (or_305_out, alu_1_out_147, register_arrays_and_decoder_1_out_58);
  or or_306 (or_306_out, alu_1_out_146, register_arrays_and_decoder_1_out_59);
  or or_307 (or_307_out, alu_1_out_145, register_arrays_and_decoder_1_out_60);
  and and_227 (and_227_out, operations_conditional_6_bit_register_1_out_54, n32_bit_general_register_2_q11);
  and and_228 (and_228_out, operations_conditional_6_bit_register_1_out_54, n32_bit_general_register_2_q10);
  and and_229 (and_229_out, operations_conditional_6_bit_register_1_out_54, n32_bit_general_register_2_q9);
  or or_308 (or_308_out, bitwise_logic_main_1_out_108, logical_unit_1_out_107);
  or or_309 (or_309_out, bitwise_logic_main_1_out_110, logical_unit_1_out_109);
  or or_310 (or_310_out, bitwise_logic_main_1_out_109, logical_unit_1_out_108);
  or or_311 (or_311_out, alu_1_out_148, register_arrays_and_decoder_1_out_57);
  or or_312 (or_312_out, alu_1_out_149, register_arrays_and_decoder_1_out_56);
  and and_230 (and_230_out, operations_conditional_6_bit_register_1_out_54, n32_bit_general_register_2_q8);
  and and_231 (and_231_out, operations_conditional_6_bit_register_1_out_54, n32_bit_general_register_2_q7);
  and and_232 (and_232_out, operations_conditional_6_bit_register_1_out_54, n32_bit_general_register_2_q6);
  or or_313 (or_313_out, bitwise_logic_main_1_out_107, logical_unit_1_out_106);
  or or_314 (or_314_out, bitwise_logic_main_1_out_105, logical_unit_1_out_104);
  or or_315 (or_315_out, bitwise_logic_main_1_out_106, logical_unit_1_out_105);
  or or_316 (or_316_out, alu_1_out_150, register_arrays_and_decoder_1_out_55);
  or or_317 (or_317_out, alu_1_out_151, register_arrays_and_decoder_1_out_54);
  or or_318 (or_318_out, alu_1_out_152, register_arrays_and_decoder_1_out_53);
  and and_233 (and_233_out, operations_conditional_6_bit_register_1_out_54, n32_bit_general_register_2_q5);
  and and_234 (and_234_out, operations_conditional_6_bit_register_1_out_54, n32_bit_general_register_2_q4);
  or or_319 (or_319_out, bitwise_logic_main_1_out_103, logical_unit_1_out_102);
  or or_320 (or_320_out, bitwise_logic_main_1_out_104, logical_unit_1_out_103);
  or or_321 (or_321_out, alu_1_out_154, register_arrays_and_decoder_1_out_51);
  or or_322 (or_322_out, alu_1_out_155, register_arrays_and_decoder_1_out_50);
  or or_323 (or_323_out, alu_1_out_153, register_arrays_and_decoder_1_out_52);
  and and_235 (and_235_out, operations_conditional_6_bit_register_1_out_54, n32_bit_general_register_2_q2);
  and and_236 (and_236_out, operations_conditional_6_bit_register_1_out_54, n32_bit_general_register_2_q3);
  and and_237 (and_237_out, operations_conditional_6_bit_register_1_out_54, n32_bit_general_register_2_q1);
  or or_324 (or_324_out, operations_conditional_6_bit_register_1_out_39, operations_conditional_6_bit_register_1_out_38);
  or or_325 (or_325_out, bitwise_logic_main_1_out_101, logical_unit_1_out_100);
  or or_326 (or_326_out, bitwise_logic_main_1_out_100, logical_unit_1_out_99);
  or or_327 (or_327_out, bitwise_logic_main_1_out_102, logical_unit_1_out_101);
  or or_328 (or_328_out, alu_1_out_156, register_arrays_and_decoder_1__0);
  _32_Bit_General_Register u_32_bit_general_register_2 (
    .E(or_329_out), .D0(or_328_out), .Q0(n32_bit_general_register_2_q0), .D1(or_322_out),
    .Q1(n32_bit_general_register_2_q1), .D2(or_321_out), .Q2(n32_bit_general_register_2_q2), .D3(or_323_out),
    .Q3(n32_bit_general_register_2_q3), .D4(or_318_out), .Q4(n32_bit_general_register_2_q4), .D5(or_317_out),
    .Q5(n32_bit_general_register_2_q5), .D6(or_316_out), .Q6(n32_bit_general_register_2_q6), .D7(or_312_out),
    .Q7(n32_bit_general_register_2_q7), .D8(or_311_out), .Q8(n32_bit_general_register_2_q8), .D9(or_305_out),
    .Q9(n32_bit_general_register_2_q9), .D10(or_306_out), .Q10(n32_bit_general_register_2_q10),
    .D11(or_307_out), .Q11(n32_bit_general_register_2_q11), .D12(or_301_out),
    .Q12(n32_bit_general_register_2_q12), .D13(or_302_out), .Q13(n32_bit_general_register_2_q13),
    .D14(or_300_out), .Q14(n32_bit_general_register_2_q14), .D15(or_296_out),
    .Q15(n32_bit_general_register_2_q15), .D16(or_295_out), .Q16(n32_bit_general_register_2_q16),
    .D17(or_289_out), .Q17(n32_bit_general_register_2_q17), .D18(or_290_out),
    .Q18(n32_bit_general_register_2_q18), .D19(or_291_out), .D19_2(n32_bit_general_register_2_d19_2),
    .D20(or_285_out), .D20_2(n32_bit_general_register_2_d20_2), .D21(or_284_out),
    .D21_2(n32_bit_general_register_2_d21_2), .D22(or_286_out), .D22_2(n32_bit_general_register_2_d22_2),
    .D23(or_279_out), .D23_2(n32_bit_general_register_2_d23_2), .D24(or_280_out),
    .D24_2(n32_bit_general_register_2_d24_2), .D25(or_275_out), .D25_2(n32_bit_general_register_2_d25_2),
    .D26(or_277_out), .D26_2(n32_bit_general_register_2_d26_2), .D27(or_276_out),
    .D27_2(n32_bit_general_register_2_d27_2), .D28(or_273_out), .D28_2(n32_bit_general_register_2_d28_2),
    .D29(or_272_out), .D29_2(n32_bit_general_register_2_d29_2), .D30(or_271_out),
    .D30_2(n32_bit_general_register_2_d30_2), .D31(or_270_out), .D31_2(n32_bit_general_register_2_d31_2));
  or or_329 (or_329_out, and_239_out, operations_conditional_6_bit_register_1_out_56);
  and and_238 (and_238_out, operations_conditional_6_bit_register_1_out_54, n32_bit_general_register_2_q0);
  or or_330 (or_330_out, operations_conditional_6_bit_register_1_out_42, operations_conditional_6_bit_register_1_out_43);
  or or_331 (or_331_out, bitwise_logic_main_1_out_98, logical_unit_1_out_97);
  or or_332 (or_332_out, bitwise_logic_main_1_out_99, logical_unit_1_out_98);
  or or_333 (or_333_out, bitwise_logic_main_1_out_97, logical_unit_1_out_96);
  or or_334 (or_334_out, bitwise_logic_main_1_out_95, logical_unit_1_out_94);
  or or_335 (or_335_out, bitwise_logic_main_1_out_96, logical_unit_1_out_95);
  or or_336 (or_336_out, bitwise_logic_main_1__0, logical_unit_1__0);
  or or_337 (or_337_out, bitwise_logic_main_1_out_94, logical_unit_1_out_93);
  or or_338 (or_338_out, operations_conditional_6_bit_register_1_out_12, operations_conditional_6_bit_register_1_out_13);
  or or_339 (or_339_out, operations_conditional_6_bit_register_1_out_14, operations_conditional_6_bit_register_1_out_15);
  or or_340 (or_340_out, or_339_out, or_338_out);
  and and_239 (and_239_out, or_340_out, and_75_out);
  or or_341 (or_341_out, operations_conditional_6_bit_register_1_out_46, operations_conditional_6_bit_register_1_out_45);
  and and_240 (and_240_out, rom_1__0_2, or_341_out);
  and and_241 (and_241_out, rom_1_data, or_341_out);
  and and_242 (and_242_out, rom_1_out_32, or_341_out);
  and and_243 (and_243_out, rom_1_out_33, or_341_out);
  and and_244 (and_244_out, rom_1_out_34, or_341_out);
  and and_245 (and_245_out, rom_1_out_35, or_341_out);
  and and_246 (and_246_out, rom_1_out_36, or_341_out);
  and and_247 (and_247_out, rom_1_out_37, or_341_out);
  and and_248 (and_248_out, rom_1_out_38, or_341_out);
  and and_249 (and_249_out, rom_1_out_39, or_341_out);
  and and_250 (and_250_out, rom_1_out_40, or_341_out);
  and and_251 (and_251_out, and_216_out, or_341_out);
  and and_252 (and_252_out, and_210_out, or_341_out);
  and and_253 (and_253_out, and_209_out, or_341_out);
  and and_254 (and_254_out, and_211_out, or_341_out);
  and and_255 (and_255_out, and_202_out, or_341_out);
  and and_256 (and_256_out, and_187_out, or_341_out);
  and and_257 (and_257_out, and_186_out, or_341_out);
  and and_258 (and_258_out, and_180_out, or_341_out);
  and and_259 (and_259_out, and_181_out, or_341_out);
  and and_260 (and_260_out, and_173_out, or_341_out);
  and and_261 (and_261_out, and_136_out, or_341_out);
  and and_262 (and_262_out, and_129_out, or_341_out);
  and and_263 (and_263_out, and_128_out, or_341_out);
  and and_264 (and_264_out, and_127_out, or_341_out);
  and and_265 (and_265_out, and_120_out, or_341_out);

  // Notes on the sheet:
  //   31
  //   0
  //   0
  //   0
  //   to RAM
  //   CLK
  //   Data In
  //   Store
  //   write to $31
  //   $s
  //   25
  //   $s
  //   4
  //   $d
  //   21
  //   25
  //   $d
  //   0
  //   4
  //   imm
  //   21
  //   25
  //   0
  //   $d
  //   20
  //   21
  //   16
  //   $t
  //   20
  //   $t
  //   4
  //   imm
  //   16
  //   20
  //   0
  //   16
  //   mtlo
  //   mflo
  //   $d
  //   15
  //   imm
  //   25
  //   H
  //   15
  //   imm
  //   11
  //   15
  //   0
  //   11
  //   11
  //   mthi
  //   mfhi
  //   0
endmodule

module ROM (
  input  [31:0] in_1,
  input  _0,
  input  in_3,
  input  in_4,
  input  in_5,
  input  in_6,
  input  in_7,
  input  in_8,
  input  in_9,
  input  Start_clear,
  input  CLK,
  input  in_12,
  input  in_13,
  input  in_14,
  input  in_15,
  input  in_16,
  input  in_17,
  input  in_18,
  input  in_19,
  input  in_20,
  input  in_21,
  input  in_22,
  input  in_23,
  input  in_24,
  input  in_25,
  input  in_26,
  input  in_27,
  input  in_28,
  input  Store_else_Load,
  output _0_2,
  output Data,
  output out_32,
  output out_33,
  output out_34,
  output out_35,
  output out_36,
  output out_37,
  output out_38,
  output out_39,
  output out_40,
  output out_41,
  output out_42,
  output out_43,
  output out_44,
  output out_45,
  output out_46,
  output out_47,
  output out_48,
  output out_49,
  output out_50,
  output out_51,
  output out_52,
  output out_53,
  output out_54,
  output out_55,
  output out_56,
  output out_57,
  output out_58,
  output out_59,
  output out_60,
  output out_61
);

  wire add_1__0, add_1__1, add_1__2, add_1__3, add_1__4, add_1__5, add_1__6, add_1__7, add_1__8, add_1__9,
       add_1__10, add_1__11, add_1__12, add_1__13, add_1__14, add_1__15, add_1__16, add_1__17, add_1__18,
       add_1__19, add_1__20, add_1__21, add_1__22, add_1__23, add_1__24, add_1__25, add_1__26, add_1__27,
       add_1__28, add_1__29, add_1__30, add_1__31, and_1_out, and_2_out, and_3_out, and_4_out, and_5_out,
       and_6_out, and_7_out, and_8_out, and_9_out, and_10_out, and_11_out, and_12_out, and_13_out,
       and_14_out, and_15_out, and_16_out, and_17_out, and_18_out, and_19_out, and_20_out, and_21_out,
       and_22_out, and_23_out, and_24_out, and_25_out, and_26_out, and_27_out, and_28_out, and_29_out,
       and_30_out, and_31_out, and_32_out, and_33_out, and_34_out, and_39_out,
       n32_bit_general_register_1_d19_2, n32_bit_general_register_1_d20_2, n32_bit_general_register_1_d21_2,
       n32_bit_general_register_1_d22_2, n32_bit_general_register_1_d23_2, n32_bit_general_register_1_d24_2,
       n32_bit_general_register_1_d25_2, n32_bit_general_register_1_d26_2, n32_bit_general_register_1_d27_2,
       n32_bit_general_register_1_d28_2, n32_bit_general_register_1_d29_2, n32_bit_general_register_1_d30_2,
       n32_bit_general_register_1_d31_2, n32_bit_general_register_1_q0, n32_bit_general_register_1_q1,
       n32_bit_general_register_1_q2, n32_bit_general_register_1_q3, n32_bit_general_register_1_q4,
       n32_bit_general_register_1_q5, n32_bit_general_register_1_q6, n32_bit_general_register_1_q7,
       n32_bit_general_register_1_q8, n32_bit_general_register_1_q9, n32_bit_general_register_1_q10,
       n32_bit_general_register_1_q11, n32_bit_general_register_1_q12, n32_bit_general_register_1_q13,
       n32_bit_general_register_1_q14, n32_bit_general_register_1_q15, n32_bit_general_register_1_q16,
       n32_bit_general_register_1_q17, n32_bit_general_register_1_q18, n32_bit_general_register_2_d24_2,
       n32_bit_general_register_2_d25_2, n32_bit_general_register_2_d26_2, n32_bit_general_register_2_d27_2,
       n32_bit_general_register_2_d28_2, n32_bit_general_register_2_d29_2, n32_bit_general_register_2_d30_2,
       n32_bit_general_register_2_d31_2, not_1_out, not_2_out, not_3_out, not_4_out, not_6_out, or_1_out,
       or_2_out, or_5_out;
  wire [23:0] and_36_out, and_38_out, n32_bit_general_register_2_q0, not_5_out, or_3_out;
  wire [23:23] and_35_out;
  wire [31:0] and_37_out, or_4_out, rom_1_data;

  or or_1 (or_1_out, Start_clear, not_1_out);
  _32_Bit_General_Register u_32_bit_general_register_1 (
    .E(or_1_out), .D0(add_1__0), .Q0(n32_bit_general_register_1_q0), .D1(add_1__1),
    .Q1(n32_bit_general_register_1_q1), .D2(add_1__2), .Q2(n32_bit_general_register_1_q2), .D3(add_1__3),
    .Q3(n32_bit_general_register_1_q3), .D4(add_1__4), .Q4(n32_bit_general_register_1_q4), .D5(add_1__5),
    .Q5(n32_bit_general_register_1_q5), .D6(add_1__6), .Q6(n32_bit_general_register_1_q6), .D7(add_1__7),
    .Q7(n32_bit_general_register_1_q7), .D8(add_1__8), .Q8(n32_bit_general_register_1_q8), .D9(add_1__9),
    .Q9(n32_bit_general_register_1_q9), .D10(add_1__10), .Q10(n32_bit_general_register_1_q10),
    .D11(add_1__11), .Q11(n32_bit_general_register_1_q11), .D12(add_1__12),
    .Q12(n32_bit_general_register_1_q12), .D13(add_1__13), .Q13(n32_bit_general_register_1_q13),
    .D14(add_1__14), .Q14(n32_bit_general_register_1_q14), .D15(add_1__15),
    .Q15(n32_bit_general_register_1_q15), .D16(add_1__16), .Q16(n32_bit_general_register_1_q16),
    .D17(add_1__17), .Q17(n32_bit_general_register_1_q17), .D18(add_1__18),
    .Q18(n32_bit_general_register_1_q18), .D19(add_1__19), .D19_2(n32_bit_general_register_1_d19_2),
    .D20(add_1__20), .D20_2(n32_bit_general_register_1_d20_2), .D21(add_1__21),
    .D21_2(n32_bit_general_register_1_d21_2), .D22(add_1__22), .D22_2(n32_bit_general_register_1_d22_2),
    .D23(add_1__23), .D23_2(n32_bit_general_register_1_d23_2), .D24(add_1__24),
    .D24_2(n32_bit_general_register_1_d24_2), .D25(add_1__25), .D25_2(n32_bit_general_register_1_d25_2),
    .D26(add_1__26), .D26_2(n32_bit_general_register_1_d26_2), .D27(add_1__27),
    .D27_2(n32_bit_general_register_1_d27_2), .D28(add_1__28), .D28_2(n32_bit_general_register_1_d28_2),
    .D29(add_1__29), .D29_2(n32_bit_general_register_1_d29_2), .D30(add_1__30),
    .D30_2(n32_bit_general_register_1_d30_2), .D31(add_1__31), .D31_2(n32_bit_general_register_1_d31_2));
  not not_1 (not_1_out, and_34_out);
  not not_2 (not_2_out, Start_clear);
  _32_Bit_General_Register u_32_bit_general_register_2 (
    .E(or_2_out), .D0(and_1_out), .Q0(n32_bit_general_register_2_q0[0]), .D1(and_2_out),
    .Q1(n32_bit_general_register_2_q0[1]), .D2(and_3_out), .Q2(n32_bit_general_register_2_q0[2]),
    .D3(and_4_out), .Q3(n32_bit_general_register_2_q0[3]), .D4(and_5_out),
    .Q4(n32_bit_general_register_2_q0[4]), .D5(and_6_out), .Q5(n32_bit_general_register_2_q0[5]),
    .D6(and_7_out), .Q6(n32_bit_general_register_2_q0[6]), .D7(and_8_out),
    .Q7(n32_bit_general_register_2_q0[7]), .D8(and_9_out), .Q8(n32_bit_general_register_2_q0[8]),
    .D9(and_10_out), .Q9(n32_bit_general_register_2_q0[9]), .D10(and_11_out),
    .Q10(n32_bit_general_register_2_q0[10]), .D11(and_12_out), .Q11(n32_bit_general_register_2_q0[11]),
    .D12(and_13_out), .Q12(n32_bit_general_register_2_q0[12]), .D13(and_14_out),
    .Q13(n32_bit_general_register_2_q0[13]), .D14(and_15_out), .Q14(n32_bit_general_register_2_q0[14]),
    .D15(and_16_out), .Q15(n32_bit_general_register_2_q0[15]), .D16(and_17_out),
    .Q16(n32_bit_general_register_2_q0[16]), .D17(and_18_out), .Q17(n32_bit_general_register_2_q0[17]),
    .D18(and_19_out), .Q18(n32_bit_general_register_2_q0[18]), .D19(and_20_out),
    .D19_2(n32_bit_general_register_2_q0[19]), .D20(and_21_out), .D20_2(n32_bit_general_register_2_q0[20]),
    .D21(and_22_out), .D21_2(n32_bit_general_register_2_q0[21]), .D22(and_23_out),
    .D22_2(n32_bit_general_register_2_q0[22]), .D23(and_24_out), .D23_2(n32_bit_general_register_2_q0[23]),
    .D24(and_25_out), .D24_2(n32_bit_general_register_2_d24_2), .D25(and_26_out),
    .D25_2(n32_bit_general_register_2_d25_2), .D26(and_27_out), .D26_2(n32_bit_general_register_2_d26_2),
    .D27(and_28_out), .D27_2(n32_bit_general_register_2_d27_2), .D28(and_29_out),
    .D28_2(n32_bit_general_register_2_d28_2), .D29(and_30_out), .D29_2(n32_bit_general_register_2_d29_2),
    .D30(and_31_out), .D30_2(n32_bit_general_register_2_d30_2), .D31(and_32_out),
    .D31_2(n32_bit_general_register_2_d31_2));
  and and_1 (and_1_out, n32_bit_general_register_1_q0, not_2_out);
  and and_2 (and_2_out, n32_bit_general_register_1_q1, not_2_out);
  and and_3 (and_3_out, n32_bit_general_register_1_q2, not_2_out);
  and and_4 (and_4_out, n32_bit_general_register_1_q3, not_2_out);
  and and_5 (and_5_out, n32_bit_general_register_1_q4, not_2_out);
  and and_6 (and_6_out, n32_bit_general_register_1_q5, not_2_out);
  and and_7 (and_7_out, n32_bit_general_register_1_q6, not_2_out);
  and and_8 (and_8_out, n32_bit_general_register_1_q7, not_2_out);
  and and_9 (and_9_out, n32_bit_general_register_1_q8, not_2_out);
  and and_10 (and_10_out, n32_bit_general_register_1_q9, not_2_out);
  and and_11 (and_11_out, n32_bit_general_register_1_q10, not_2_out);
  and and_12 (and_12_out, n32_bit_general_register_1_q11, not_2_out);
  and and_13 (and_13_out, n32_bit_general_register_1_q12, not_2_out);
  and and_14 (and_14_out, n32_bit_general_register_1_q13, not_2_out);
  and and_15 (and_15_out, n32_bit_general_register_1_q14, not_2_out);
  and and_16 (and_16_out, n32_bit_general_register_1_q15, not_2_out);
  and and_17 (and_17_out, n32_bit_general_register_1_q16, not_2_out);
  and and_18 (and_18_out, n32_bit_general_register_1_q17, not_2_out);
  and and_19 (and_19_out, n32_bit_general_register_1_q18, not_2_out);
  and and_20 (and_20_out, n32_bit_general_register_1_d19_2, not_2_out);
  and and_21 (and_21_out, n32_bit_general_register_1_d20_2, not_2_out);
  and and_22 (and_22_out, n32_bit_general_register_1_d21_2, not_2_out);
  and and_23 (and_23_out, n32_bit_general_register_1_d22_2, not_2_out);
  and and_24 (and_24_out, n32_bit_general_register_1_d23_2, not_2_out);
  and and_25 (and_25_out, n32_bit_general_register_1_d24_2, not_2_out);
  and and_26 (and_26_out, n32_bit_general_register_1_d25_2, not_2_out);
  and and_27 (and_27_out, n32_bit_general_register_1_d26_2, not_2_out);
  and and_28 (and_28_out, n32_bit_general_register_1_d27_2, not_2_out);
  and and_29 (and_29_out, n32_bit_general_register_1_d28_2, not_2_out);
  and and_30 (and_30_out, n32_bit_general_register_1_d29_2, not_2_out);
  and and_31 (and_31_out, n32_bit_general_register_1_d30_2, not_2_out);
  and and_32 (and_32_out, n32_bit_general_register_1_d31_2, not_2_out);
  and and_33 (and_33_out, CLK, in_12);
  not not_3 (not_3_out, add_1__24);
  and and_34 (and_34_out, not_3_out, and_33_out);
  or or_2 (or_2_out, Start_clear, and_34_out);
  and and_35 (and_35_out[23], in_12, not_3_out);
  not not_4 (not_4_out, 1'b0);
  add add_1 (
    .A0(n32_bit_general_register_2_q0[0]), .B0(not_4_out), .A1(n32_bit_general_register_2_q0[1]), .B1(1'b0),
    .A2(n32_bit_general_register_2_q0[2]), .B2(1'b0), .A3(n32_bit_general_register_2_q0[3]), .B3(1'b0),
    .A4(n32_bit_general_register_2_q0[4]), .B4(1'b0), .A5(n32_bit_general_register_2_q0[5]), .B5(1'b0),
    .A6(n32_bit_general_register_2_q0[6]), .B6(1'b0), .A7(n32_bit_general_register_2_q0[7]), .B7(1'b0),
    .A8(n32_bit_general_register_2_q0[8]), .B8(1'b0), .A9(n32_bit_general_register_2_q0[9]), .B9(1'b0),
    .A10(n32_bit_general_register_2_q0[10]), .B10(1'b0), .A11(n32_bit_general_register_2_q0[11]), .B11(1'b0),
    .A12(n32_bit_general_register_2_q0[12]), .B12(1'b0), .A13(n32_bit_general_register_2_q0[13]), .B13(1'b0),
    .A14(n32_bit_general_register_2_q0[14]), .B14(1'b0), .A15(n32_bit_general_register_2_q0[15]), .B15(1'b0),
    .A16(n32_bit_general_register_2_q0[16]), .B16(1'b0), .A17(n32_bit_general_register_2_q0[17]), .B17(1'b0),
    .A18(n32_bit_general_register_2_q0[18]), .B18(1'b0), .A19(n32_bit_general_register_2_q0[19]), .B19(1'b0),
    .A20(n32_bit_general_register_2_q0[20]), .B20(1'b0), .A21(n32_bit_general_register_2_q0[21]), .B21(1'b0),
    .A22(n32_bit_general_register_2_q0[22]), .B22(1'b0), .A23(n32_bit_general_register_2_q0[23]), .B23(1'b0),
    .A24(n32_bit_general_register_2_d24_2), .B24(1'b0), .A25(n32_bit_general_register_2_d25_2), .B25(1'b0),
    .A26(n32_bit_general_register_2_d26_2), .B26(1'b0), .A27(n32_bit_general_register_2_d27_2), .B27(1'b0),
    .A28(n32_bit_general_register_2_d28_2), .B28(1'b0), .A29(n32_bit_general_register_2_d29_2), .B29(1'b0),
    .A30(n32_bit_general_register_2_d30_2), .B30(1'b0), .A31(n32_bit_general_register_2_d31_2),
    ._0(add_1__0), ._1(add_1__1), ._2(add_1__2), ._3(add_1__3), ._4(add_1__4), ._5(add_1__5), ._6(add_1__6),
    ._7(add_1__7), ._8(add_1__8), ._9(add_1__9), ._10(add_1__10), ._11(add_1__11), ._12(add_1__12),
    ._13(add_1__13), ._14(add_1__14), ._15(add_1__15), ._16(add_1__16), ._17(add_1__17), ._18(add_1__18),
    ._19(add_1__19), ._20(add_1__20), ._21(add_1__21), ._22(add_1__22), ._23(add_1__23), ._24(add_1__24),
    ._25(add_1__25), ._26(add_1__26), ._27(add_1__27), ._28(add_1__28), ._29(add_1__29), ._30(add_1__30),
    ._31(add_1__31), .B31(1'b0));  // open: Carry, Overflow
  assign and_36_out = {24{and_35_out[23]}} & n32_bit_general_register_2_q0;  // AND_Gate and_36, 24 bits wide
  ROM_part #(.addrWidth(24), .dataWidth(32)) rom_1 (
    .addr(n32_bit_general_register_2_q0), .data(rom_1_data));  // open: sel
  assign and_37_out = {32{and_35_out[23]}} & rom_1_data;  // AND_Gate and_37, 32 bits wide
  assign not_5_out = ~and_36_out;  // NOT_Gate not_5, 24 bits wide
  assign and_38_out = {in_28, in_27, in_26, in_25, in_24, in_23, in_22, in_21, in_20, in_19, in_18, in_17, in_16, in_15, in_14, in_13, in_9, in_8, in_7, in_6, in_5, in_4, in_3, _0} & not_5_out;  // AND_Gate and_38, 24 bits wide
  and and_39 (and_39_out, in_12, and_35_out[23]);
  assign or_3_out = and_36_out | and_38_out;  // OR_Gate or_3, 24 bits wide
  assign or_4_out = and_37_out | in_1;  // OR_Gate or_4, 32 bits wide
  not not_6 (not_6_out, Store_else_Load);
  or or_5 (or_5_out, and_39_out, Store_else_Load);
  RAM_part #(.addrWidth(24), .dataWidth(32), .bus("separate")) ram_1 (
    .addr(or_3_out), .din(or_4_out),
    .data({out_61, out_60, out_59, out_58, out_57, out_56, out_55, out_54, out_53, out_52, out_51, out_50, out_49, out_48, out_47, out_46, out_45, out_44, out_43, out_42, out_41, out_40, out_39, out_38, out_37, out_36, out_35, out_34, out_33, out_32, Data, _0_2}),
    .str(or_5_out), .clk(CLK), .ld(not_6_out), .clr(Start_clear));  // open: sel

  // Notes on the sheet:
  //   Data In
  //   Addr
  //   Load  ROM into RAM
  //   contents of rom_1 (hex, n*v repeats v):
  //   16777215*ffffffff
endmodule

module RAM (
  input  _0,
  input  in_2,
  input  in_3,
  input  in_4,
  input  in_5,
  input  in_6,
  input  in_7,
  input  in_8,
  input  in_9,
  input  in_10,
  input  in_11,
  input  in_12,
  input  in_13,
  input  in_14,
  input  CLK,
  input  Store,
  input  in_17,
  input  in_18,
  input  in_19,
  input  in_20,
  input  in_21,
  input  in_22,
  input  in_23,
  input  in_24,
  input  in_25,
  input  in_26,
  input  _0_2,
  input  in_28,
  input  in_29,
  input  in_30,
  input  in_31,
  input  in_32,
  input  in_33,
  input  in_34,
  input  in_35,
  input  in_36,
  input  in_37,
  input  in_38,
  input  in_39,
  input  in_40,
  input  in_41,
  input  in_42,
  input  in_43,
  input  in_44,
  input  in_45,
  input  in_46,
  input  in_47,
  input  in_48,
  input  in_49,
  input  in_50,
  input  in_51,
  input  in_52,
  input  in_53,
  input  in_54,
  input  in_55,
  input  in_56,
  input  in_57,
  input  in_58,
  output _0_3,
  output Data,
  output out_61,
  output out_62,
  output out_63,
  output out_64,
  output out_65,
  output out_66,
  output out_67,
  output out_68,
  output out_69,
  output out_70,
  output out_71,
  output out_72,
  output out_73,
  output out_74,
  output out_75,
  output out_76,
  output out_77,
  output out_78,
  output out_79,
  output out_80,
  output out_81,
  output out_82,
  output out_83,
  output out_84,
  output out_85,
  output out_86,
  output out_87,
  output out_88,
  output out_89,
  output out_90
);

  wire not_1_out;

  RAM_part #(.addrWidth(24), .dataWidth(32), .bus("separate")) ram_1 (
    .addr({in_26, in_25, in_24, in_23, in_22, in_21, in_20, in_19, in_18, in_17, in_14, in_13, in_12, in_11, in_10, in_9, in_8, in_7, in_6, in_5, in_4, in_3, in_2, _0}),
    .din({in_58, in_57, in_56, in_55, in_54, in_53, in_52, in_51, in_50, in_49, in_48, in_47, in_46, in_45, in_44, in_43, in_42, in_41, in_40, in_39, in_38, in_37, in_36, in_35, in_34, in_33, in_32, in_31, in_30, in_29, in_28, _0_2}),
    .data({out_90, out_89, out_88, out_87, out_86, out_85, out_84, out_83, out_82, out_81, out_80, out_79, out_78, out_77, out_76, out_75, out_74, out_73, out_72, out_71, out_70, out_69, out_68, out_67, out_66, out_65, out_64, out_63, out_62, out_61, Data, _0_3}),
    .str(Store), .clk(CLK), .ld(not_1_out), .clr(1'b0));  // open: sel
  not not_1 (not_1_out, Store);

  // Notes on the sheet:
  //   Address
  //   Data
endmodule
